// Logisim project cpu-finished.circ as structural Verilog: 33 circuits, main circuit ◇单周期RISC-V
module \单周期RISC_V  (
  input  IR1,
  input  IR2,
  input  IR3,
  output RegWrite,
  output MemWrite,
  output [31:0] PC,
  output [31:0] IR,
  output [31:0] RDin,
  output [31:0] MDin,
  output [31:0] LedData
);

  wire AluSrcB, and_1_out, and_2_out, and_3_out, and_4_out, and_6_out, and_7_out, B, Beq, Bltu, Bne, Branch,
       button_3_out, CLK, clock_1_out, comparator_1_eq, comparator_2_eq, comparator_2_lt, d_ff_1_q, ecall,
       equal, Go, I, IR1_t, IR2_t, IR3_t, IRA, IRB, IRC, J, JAL, JALR, less, lh, MemToReg, multiplexer_1_out,
       nand_1_out, not_1_out, not_2_out, or_1_out, or_2_out, or_4_out, or_8_out, RST, S, S_Type, stop,
       System, URET, W1, W2, W3, \继续运行_out ;
  wire [0:0] alu_1_result;
  wire [3:0] AluOP;
  wire [4:0] multiplexer_3_out, multiplexer_4_out;
  wire [12:0] CNT_num;
  wire [15:0] multiplexer_8_out, \总周期数 ;
  wire [30:0] alu_1_result_2;
  wire [31:0] adder_1_out, adder_2_out, bit_extender_1_out, immvaluegen_1_imm, multiplexer_2_out,
       multiplexer_6_out, multiplexer_7_out, multiplexer_9_out, multiplexer_10_out, ram_1_data,
       regfile_for_single_unit_1_r1, shifter_1_out;

  Button \u_继续运行  (.out(\继续运行_out ));
  Button _1 (.out(IRA));
  Button _2 (.out(IRB));
  Button _3 (.out(IRC));
  LED #(.active("true")) led_1 (.in(W1));
  LED #(.active("true")) led_2 (.in(W2));
  LED #(.active("true")) led_3 (.in(W3));
  Button button_1 (.out(Go));
  Button button_2 (.out(RST));
  Button button_3 (.out(button_3_out));
  Hex_Digit_Display hex_digit_display_1 (.value(LedData[31:28]));  // open: dp
  Multiplexer #(.select(1), .width(1), .disabled("Z"), .enable("false")) multiplexer_1 (
    .in0(button_3_out), .in1(1'b1), .out(multiplexer_1_out), .sel(stop));
  Hex_Digit_Display hex_digit_display_2 (.value(LedData[27:24]));  // open: dp
  Hex_Digit_Display hex_digit_display_3 (.value(LedData[23:20]));  // open: dp
  Adder #(.width(32)) adder_1 (.a(32'h4), .b(PC), .out(adder_1_out), .cin(1'b0));  // open: cout
  Hex_Digit_Display hex_digit_display_4 (.value(LedData[15:12]));  // open: dp
  Hex_Digit_Display hex_digit_display_5 (.value(LedData[19:16]));  // open: dp
  not not_1 (not_1_out, 1'b0);
  Multiplexer #(.select(2), .width(32), .disabled("Z"), .enable("false")) multiplexer_2 (
    .in0(adder_1_out), .in1(adder_2_out), .in2({alu_1_result_2, 1'b0}), .out(multiplexer_2_out),
    .sel({JALR, Branch}));  // open: in3
  Hex_Digit_Display hex_digit_display_6 (.value(LedData[7:4]));  // open: dp
  Hex_Digit_Display hex_digit_display_7 (.value(LedData[11:8]));  // open: dp
  // Probe on \总周期数 
  or or_1 (or_1_out, Go, not_1_out);
  Counter #(.width(16), .max('hffff), .ongoal("wrap"), .trigger("rising"), .behavior("new")) counter_1 (
    .D({16{1'b0}}), .count(or_1_out), .Q(\总周期数 ), .clk(CLK), .clr(RST));  // open: load, carry, preset, down
  Register #(.width(32), .trigger("rising"), .Select("low")) u_PC (
    .D(multiplexer_2_out), .en(or_2_out), .Q(PC), .clk(CLK), .clr(RST), .cs(1'b0), .preset(1'b0));
  or or_2 (or_2_out, Go, not_2_out);
  not not_2 (not_2_out, 1'b0);
  Hex_Digit_Display hex_digit_display_8 (.value(LedData[3:0]));  // open: dp
  and and_1 (and_1_out, equal, ~IR[12]);  // AND_Gate
  and and_2 (and_2_out, ~equal, IR[12]);  // AND_Gate
  and and_3 (and_3_out, IR[14], less);
  or or_3 (IR1_t, IR1, IRA);
  Comparator #(.width(16), .mode("twosComplement")) comparator_1 (
    .a(\总周期数 ), .b(16'h140), .eq(comparator_1_eq));  // open: gt, lt
  // RiscV_Probe riscv_probe_1: pin names not known; wires that end beside it: PC, comparator_1_eq, 1'b0, IR
  or or_4 (or_4_out, and_1_out, and_2_out, and_3_out);
  or or_5 (IR2_t, IR2, IRB);
  ROM #(.addrWidth(10), .dataWidth(32), .Select("high")) rom_1 (.addr(PC[11:2]), .data(IR), .sel(1'b1));
  and and_4 (and_4_out, B, or_4_out);
  or or_6 (IR3_t, IR3, IRC);
  \单周期硬布线控制器  \u_单周期硬布线控制器_1  (
    .Funct({IR[30], IR[25], IR[14:12]}), .OP(IR[6:2]), .ALU_OP(AluOP), .MemToReg(MemToReg), .bltu(Bltu),
    .ecall(ecall), .in_3(IR[21]), .uret(URET), .MemWrite(MemWrite), .lh(lh), .BEQ(Bne), .S_Type(S_Type),
    .RegWrite(RegWrite), .ALU_SRC(AluSrcB), .BNE(Beq), .JALR(JALR), .JAL(JAL));  // open: CSR, lw
  Multiplexer #(.select(1), .width(5), .disabled("Z"), .enable("false")) multiplexer_3 (
    .in0(IR[19:15]), .in1(5'b01010), .out(multiplexer_3_out), .sel(ecall));
  Multiplexer #(.select(1), .width(5), .disabled("Z"), .enable("false")) multiplexer_4 (
    .in0(IR[24:20]), .in1(5'b10001), .out(multiplexer_4_out), .sel(ecall));
  or or_7 (Branch, and_4_out, J);
  RegFile_for_Single_Unit regfile_for_single_unit_1 (
    .Din(RDin), .Clk(CLK), .R1(regfile_for_single_unit_1_r1), .R2(MDin), .WE(RegWrite), .W_num(IR[11:7]),
    .R1_num(multiplexer_3_out), .R2_num(multiplexer_4_out));
  Multiplexer #(.select(1), .width(32), .disabled("Z"), .enable("false")) multiplexer_5 (
    .in0(multiplexer_10_out), .in1(adder_1_out), .out(RDin), .sel(or_8_out));
  or or_8 (or_8_out, JALR, J);
  ImmValueGen immvaluegen_1 (
    .Imm(immvaluegen_1_imm), .Type_I_Imm(IR[31:20]), .Type_S_Imm({IR[31:25], IR[11:7]}),
    .Type_B_Imm({IR[31], IR[7], IR[30:25], IR[11:8]}), .Type_J_Imm({IR[31], IR[19:12], IR[20], IR[30:21]}),
    .Op6(IR[6]), .I(I), .Op5(IR[5]), .S(S), .Op4(IR[4]), .B(B), .Op3(IR[3]), .J(J), .Op2(IR[2]),
    .System(System));
  and and_5 (stop, ~equal, ecall);  // AND_Gate
  Multiplexer #(.select(1), .width(32), .disabled("Z"), .enable("false")) multiplexer_6 (
    .in0(regfile_for_single_unit_1_r1), .in1(32'h22), .out(multiplexer_6_out), .sel(ecall));
  Multiplexer #(.select(1), .width(32), .disabled("Z"), .enable("false")) multiplexer_7 (
    .in0(MDin), .in1(immvaluegen_1_imm), .out(multiplexer_7_out), .sel(AluSrcB));
  // Probe on immvaluegen_1_imm
  Register #(.width(32), .trigger("rising"), .Select("low")) register_1 (
    .D(regfile_for_single_unit_1_r1), .en(and_6_out), .Q(LedData), .clk(CLK));  // open: clr
  and and_6 (and_6_out, equal, ecall);
  and and_7 (and_7_out, ~equal, ecall);  // AND_Gate
  ALU alu_1 (
    .X(multiplexer_6_out), .Y(multiplexer_7_out), .AluOP(AluOP), .Equal(equal),
    .Result({alu_1_result_2, alu_1_result[0]}), .out_6(less));  // open: Result_2, out_4
  D_Flip_Flop #(.trigger("high"), .Pre_Clr_Positions("LEGACY"), .NegatePresetClear("false"), .enable("true"), .NewFFLayout("false")) d_ff_1 (.Q(d_ff_1_q));  // open: clk, D, Qn, preset, en, reset
  // Probe on 13'hc
  Shifter #(.width(32), .shift("ll")) shifter_1 (.in(immvaluegen_1_imm), .\dist (5'b00001), .out(shifter_1_out));
  Comparator #(.width(13), .mode("twosComplement")) comparator_2 (
    .a(CNT_num), .b(13'hc), .eq(comparator_2_eq), .lt(comparator_2_lt));  // open: gt
  Clock #(.highDuration(1), .lowDuration(1)) clock_1 (.out(clock_1_out));
  RAM #(.addrWidth(10), .dataWidth(32), .bus("separate"), .Select("high")) ram_1 (
    .addr(alu_1_result_2[10:1]), .din(MDin), .data(ram_1_data), .str(MemWrite), .sel(1'b1), .clk(CLK),
    .ld(1'b1), .clr(RST));
  Adder #(.width(32)) adder_2 (.a(shifter_1_out), .b(PC), .out(adder_2_out), .cin(1'b0));  // open: cout
  Counter #(.width(13), .max('h1fff), .ongoal("stay"), .trigger("rising"), .behavior("old")) counter_2 (
    .count(comparator_2_lt), .Q(CNT_num), .clk(clock_1_out));  // open: load, D, carry, clr, preset
  nand nand_1 (nand_1_out, d_ff_1_q, comparator_2_eq);
  Multiplexer #(.select(1), .width(16), .disabled("Z"), .enable("false")) multiplexer_8 (
    .in0(ram_1_data[15:0]), .in1(ram_1_data[31:16]), .out(multiplexer_8_out), .sel(alu_1_result_2[0]));
  assign bit_extender_1_out = {{16{multiplexer_8_out[15]}}, multiplexer_8_out};  // Bit_Extender bit_extender_1
  assign CLK = nand_1_out ? clock_1_out : 1'bz;  // Controlled_Buffer controlled_buffer_1
  Pull_Resistor #(.pull(1)) pull_resistor_1 (.node(CLK));
  Multiplexer #(.select(1), .width(32), .disabled("Z"), .enable("false")) multiplexer_9 (
    .in0(ram_1_data), .in1(bit_extender_1_out), .out(multiplexer_9_out), .sel(lh));
  Multiplexer #(.select(1), .width(32), .disabled("Z"), .enable("false")) multiplexer_10 (
    .in0({alu_1_result_2, alu_1_result[0]}), .in1(multiplexer_9_out), .out(multiplexer_10_out), .sel(MemToReg));

  // Other names for the same wires on the sheet: funct[4:0] = {IR[30], IR[25], IR[14:12]}; opcode[4:0] = IR[6:2]

  // Notes on the sheet:
  //   中断源
  //   中断等待指示
  //   00: not jumping
  //   10: for JALR jumping
  //   数码管输出应该用寄存器锁存，否则显示数据只能一闪而过
  //   01: branch jumping, for bne, beq, jal & bltu
  //   数码管输出
  //   for JAL
  //   指令探针
  //   指令存储器
  //   Bne, Beq & bltu: func3 of 3 instructions is different, with 000 for Beq, 001 for Bne and 110 for bltu, respectively
  //   Beq
  //   Bne
  //   bltu
  //   指令字
  //   contents of rom_1 (hex, n*v repeats v):
  //   100493 100006f 100493 200913 300993 100006f 100493 200913 300993 100006f 100493 200913 300993
  //   100006f 100493 200913 300993 29c000ef 100413 100493 1f49493 900533 2200893 73 24d493 48463 fedff06f
  //   900533 2200893 73 100493 249493 900533 2200893 73 48463 fedff06f 100493 1f49493 900533 2200893 73
  //   4034d493 900533 2200893 73 4044d493 900533 2200893 73 4044d493 900533 2200893 73 4044d493 900533
  //   2200893 73 4044d493 900533 2200893 73 4044d493 900533 2200893 73 4044d493 900533 2200893 73 4044d493
  //   900533 2200893 73 100413 1f41993 41f9d993 433 c00913 300b13 140413 f47413 800293 100313 499993
  //   89e9b3 1300533 2200893 73 406282b3 fe0294e3 140413 f00f93 1f47433 1c41413 800293 100313 49d993
  //   89e9b3 1300533 2200893 73 406282b3 fe0294e3 1c45413 406b0b33 b0463 f95ff06f 2b3 fff2c293 829293
  //   ff2e293 500533 2200893 73 fff00413 493 84a023 140413 448493 84a023 140413 448493 84a023 140413
  //   448493 84a023 140413 448493 84a023 140413 448493 84a023 140413 448493 84a023 140413 448493 84a023
  //   140413 448493 84a023 140413 448493 84a023 140413 448493 84a023 140413 448493 84a023 140413 448493
  //   84a023 140413 448493 84a023 140413 448493 84a023 140413 448493 84a023 140413 448493 140413 433
  //   3c00493 42983 4aa03 149a2b3 28663 134a023 1442023 ffc48493 fe9412e3 800533 2200893 73 440413 3c00493
  //   fc9416e3 a00893 73 413 140413 800533 2200893 73 240413 800533 2200893 73 340413 800533 2200893 73
  //   440413 800533 2200893 73 540413 800533 2200893 73 640413 800533 2200893 73 740413 800533 2200893 73
  //   840413 800533 2200893 2200893 73 8067
  //   PC+4
  //   OpCode
  //   I-type command
  //   S-type command
  //   B-type command
  //   J-type command
  //   B type jump
  //   J type jump
  //   Only JAL is J-type instruction
  //   IR21
  //   funct
  //   for ecall
  //   OpCode
  //   为方便自动评测，需要输出PC，IR，寄存器堆写如数据RDin
  //   $a0
  //   stop the program while equal is 0
  //   clik RST and then LedData should be clear
  //   RAM写使能MemWrite、RAM写入数据MDin等信号
  //   Update LedData using $a0
  //   SrcA
  //   SrcB
  //   Imm
  //   for B-type jumping
  //   控制位
  //   暂停节拍，不能为0
  //   戳工具置1进入计数暂停模式，ctrl+k时钟自动运行到对应节拍暂停
  //   ctrl+k关闭时钟连续运行，将控制位置零，进入单步调试模式调试
  //   用这个时钟源需要去掉电路中的其他时钟源
  //   数据存储器
  //   for JALR jumping
  //   可计数暂停的时钟源
endmodule

// 单周期硬布线控制器
module \单周期硬布线控制器  (
  input  [4:0] OP,
  input  [4:0] Funct,
  input  in_3,
  output [3:0] ALU_OP,
  output MemToReg,
  output bltu,
  output CSR,
  output MemWrite,
  output lh,
  output ALU_SRC,
  output lw,
  output RegWrite,
  output S_Type,
  output BEQ,
  output BNE,
  output JALR,
  output JAL,
  output uret,
  output ecall
);

  wire and_1_out, and_2_out, nor_1_out;

  nor nor_1 (nor_1_out, OP[0], OP[1]);
  and and_1 (and_1_out, OP[2], OP[3], OP[4]);
  \运算控制器自动生成  \u_运算控制器自动生成_1  (
    .OP2(OP[0]), .OP3(OP[1]), .OP4(OP[2]), .OP5(OP[3]), .OP6(OP[4]), .F12(Funct[0]), .F13(Funct[1]),
    .F14(Funct[2]), .F25(Funct[3]), .F30(Funct[4]), .S0(ALU_OP[0]), .S1(ALU_OP[1]), .S2(ALU_OP[2]),
    .S3(ALU_OP[3]));
  \控制信号自动生成  \u_控制信号自动生成_1  (
    .OP2(OP[0]), .OP3(OP[1]), .OP4(OP[2]), .OP5(OP[3]), .MemToReg(MemToReg), .OP6(OP[4]), .F12(Funct[0]),
    .F13(Funct[1]), .F14(Funct[2]), .F25(Funct[3]), .bltu(bltu), .F30(Funct[4]), .CSR(CSR),
    .MemWrite(MemWrite), .lh(lh), .ALU_SRC(ALU_SRC), .lw(lw), .RegWrite(RegWrite), .S_Type(S_Type),
    .BEQ(BEQ), .BNE(BNE), .JALR(JALR), .JAL(JAL));
  and and_2 (and_2_out, nor_1_out, and_1_out);
  and and_3 (uret, and_2_out, in_3);
  and and_4 (ecall, and_2_out, ~in_3);  // AND_Gate

  // Other names for the same wires on the sheet: IR21 = in_3; OP_CODE[4:0] = OP

  // Notes on the sheet:
  //   opcode of uret & ecall is 11100, the 21st bits of both instruction is different
  //   运算器控制器，根据指令生成运算器功能选择信号
endmodule

// 运算器控制器
module \运算控制器自动生成  (
  input  OP2,
  input  OP3,
  input  OP4,
  input  OP5,
  input  OP6,
  input  F12,
  input  F13,
  input  F14,
  input  F25,
  input  F30,
  output S0,
  output S1,
  output S2,
  output S3
);

  wire and_1_out, and_2_out, and_3_out, and_4_out, and_5_out, and_6_out, and_7_out, and_8_out, and_9_out,
       and_10_out, and_11_out, and_12_out, and_13_out, and_14_out, and_15_out, and_16_out, and_17_out,
       and_18_out, and_19_out, and_20_out, and_21_out, and_22_out, and_23_out, and_24_out, and_25_out,
       and_26_out, and_27_out, and_28_out, and_29_out, and_30_out, and_31_out, and_32_out, and_33_out,
       and_34_out, and_35_out, and_36_out, and_37_out, and_38_out, and_39_out, and_40_out, and_41_out,
       and_42_out, and_43_out, and_44_out, and_45_out, and_46_out, not_1_out, not_2_out, not_3_out,
       not_4_out, not_5_out, not_6_out, not_7_out, not_8_out, not_9_out, not_10_out, not_11_out, not_12_out,
       not_13_out, not_14_out, not_15_out, not_16_out, not_17_out, not_18_out, not_19_out, not_20_out,
       not_21_out, not_22_out, not_23_out, not_24_out, not_25_out, not_26_out, not_27_out, not_28_out,
       not_29_out, not_30_out, not_31_out, not_32_out, not_33_out, not_34_out, not_35_out, not_36_out,
       not_37_out, not_38_out, not_39_out, not_40_out, not_41_out, not_42_out, not_43_out, not_44_out,
       not_45_out, not_46_out, not_47_out, not_48_out, not_49_out, not_50_out, not_51_out, not_52_out,
       not_53_out, not_54_out, not_55_out, not_56_out, not_57_out, not_58_out, not_59_out, not_60_out,
       not_61_out, not_62_out, not_63_out, not_64_out, not_65_out, not_66_out, not_67_out, not_68_out,
       not_69_out, not_70_out, not_71_out, not_72_out, not_73_out, not_74_out, not_75_out, not_76_out,
       not_77_out, not_78_out, not_79_out, not_80_out, not_81_out, not_82_out, not_83_out, not_84_out,
       not_85_out, not_86_out, not_87_out, not_88_out, not_89_out, not_90_out, not_91_out, not_92_out,
       not_93_out, not_94_out, not_95_out, not_96_out, not_97_out, not_98_out, not_99_out, not_100_out,
       not_101_out, not_102_out, not_103_out, not_104_out, not_105_out, not_106_out, not_107_out,
       not_108_out, not_109_out, not_110_out, not_111_out, not_112_out, not_113_out, not_114_out,
       not_115_out, not_116_out, not_117_out, not_118_out, not_119_out, not_120_out, not_121_out,
       not_122_out, not_123_out, not_124_out, not_125_out, not_126_out, not_127_out, not_128_out,
       not_129_out, not_130_out, not_131_out, not_132_out, not_133_out, not_134_out, not_135_out,
       not_136_out, not_137_out, not_138_out, not_139_out, not_140_out, not_141_out, not_142_out,
       not_143_out, not_144_out, not_145_out, not_146_out, not_147_out, not_148_out, not_149_out,
       not_150_out, not_151_out, not_152_out, not_153_out, not_154_out, not_155_out, not_156_out,
       not_157_out, not_158_out, not_159_out, not_160_out, not_161_out, not_162_out, not_163_out,
       not_164_out, not_165_out, not_166_out, not_167_out, not_168_out, not_169_out, not_170_out,
       not_171_out, not_172_out, not_173_out, not_174_out, not_175_out, not_176_out, not_177_out,
       not_178_out, not_179_out, not_180_out, not_181_out, not_182_out, not_183_out, not_184_out,
       not_185_out, not_186_out, not_187_out, not_188_out, not_189_out, not_190_out, not_191_out,
       not_192_out, not_193_out, not_194_out, not_195_out, not_196_out, not_197_out, not_198_out,
       not_199_out, not_200_out, not_201_out, not_202_out, not_203_out, not_204_out, not_205_out,
       not_206_out, not_207_out, not_208_out, not_209_out, not_210_out, not_211_out, not_212_out,
       not_213_out, not_214_out, not_215_out, not_216_out, not_217_out, not_218_out, not_219_out,
       not_220_out, not_221_out, not_222_out, not_223_out, not_224_out, not_225_out, not_226_out,
       not_227_out, not_228_out, not_229_out, not_230_out, not_231_out, not_232_out, not_233_out,
       not_234_out, not_235_out, not_236_out, not_237_out, not_238_out, not_239_out, not_240_out,
       not_241_out, not_242_out, not_243_out, not_244_out, not_245_out, not_246_out, not_247_out,
       not_248_out, not_249_out, not_250_out, not_251_out, not_252_out, not_253_out, not_254_out,
       not_255_out, not_256_out, not_257_out, not_258_out;

  not not_1 (not_1_out, F30);
  not not_2 (not_2_out, F25);
  not not_3 (not_3_out, F14);
  not not_4 (not_4_out, F13);
  not not_5 (not_5_out, F12);
  not not_6 (not_6_out, OP6);
  not not_7 (not_7_out, OP3);
  not not_8 (not_8_out, OP2);
  not not_9 (not_9_out, F30);
  not not_10 (not_10_out, F25);
  not not_11 (not_11_out, OP6);
  not not_12 (not_12_out, OP3);
  not not_13 (not_13_out, OP2);
  not not_14 (not_14_out, F30);
  not not_15 (not_15_out, F25);
  not not_16 (not_16_out, F14);
  not not_17 (not_17_out, F12);
  not not_18 (not_18_out, OP6);
  not not_19 (not_19_out, OP3);
  not not_20 (not_20_out, OP2);
  not not_21 (not_21_out, F14);
  not not_22 (not_22_out, F13);
  not not_23 (not_23_out, F12);
  not not_24 (not_24_out, OP6);
  not not_25 (not_25_out, OP5);
  not not_26 (not_26_out, OP3);
  not not_27 (not_27_out, OP2);
  not not_28 (not_28_out, OP6);
  not not_29 (not_29_out, OP5);
  not not_30 (not_30_out, OP3);
  not not_31 (not_31_out, OP2);
  not not_32 (not_32_out, F13);
  not not_33 (not_33_out, F12);
  not not_34 (not_34_out, OP6);
  not not_35 (not_35_out, OP5);
  not not_36 (not_36_out, OP3);
  not not_37 (not_37_out, OP2);
  not not_38 (not_38_out, F14);
  not not_39 (not_39_out, F12);
  not not_40 (not_40_out, OP6);
  not not_41 (not_41_out, OP5);
  not not_42 (not_42_out, OP3);
  not not_43 (not_43_out, OP2);
  not not_44 (not_44_out, F25);
  not not_45 (not_45_out, F13);
  not not_46 (not_46_out, OP6);
  not not_47 (not_47_out, OP5);
  not not_48 (not_48_out, OP3);
  not not_49 (not_49_out, OP2);
  not not_50 (not_50_out, F14);
  not not_51 (not_51_out, F12);
  not not_52 (not_52_out, OP6);
  not not_53 (not_53_out, OP5);
  not not_54 (not_54_out, OP4);
  not not_55 (not_55_out, OP3);
  not not_56 (not_56_out, OP2);
  not not_57 (not_57_out, F14);
  not not_58 (not_58_out, F12);
  not not_59 (not_59_out, OP6);
  not not_60 (not_60_out, OP4);
  not not_61 (not_61_out, OP3);
  not not_62 (not_62_out, OP2);
  not not_63 (not_63_out, OP3);
  not not_64 (not_64_out, OP2);
  not not_65 (not_65_out, F25);
  not not_66 (not_66_out, F13);
  not not_67 (not_67_out, OP6);
  not not_68 (not_68_out, OP3);
  not not_69 (not_69_out, OP2);
  not not_70 (not_70_out, F14);
  not not_71 (not_71_out, F13);
  not not_72 (not_72_out, OP6);
  not not_73 (not_73_out, OP5);
  not not_74 (not_74_out, OP4);
  not not_75 (not_75_out, OP3);
  not not_76 (not_76_out, OP2);
  not not_77 (not_77_out, F25);
  not not_78 (not_78_out, F14);
  not not_79 (not_79_out, F13);
  not not_80 (not_80_out, F12);
  not not_81 (not_81_out, OP6);
  not not_82 (not_82_out, OP3);
  not not_83 (not_83_out, OP2);
  not not_84 (not_84_out, F30);
  not not_85 (not_85_out, F25);
  not not_86 (not_86_out, OP6);
  not not_87 (not_87_out, OP3);
  not not_88 (not_88_out, OP2);
  not not_89 (not_89_out, F30);
  not not_90 (not_90_out, F25);
  not not_91 (not_91_out, F14);
  not not_92 (not_92_out, F12);
  not not_93 (not_93_out, OP6);
  not not_94 (not_94_out, OP3);
  not not_95 (not_95_out, OP2);
  not not_96 (not_96_out, OP6);
  not not_97 (not_97_out, OP5);
  not not_98 (not_98_out, OP3);
  not not_99 (not_99_out, OP2);
  not not_100 (not_100_out, F14);
  not not_101 (not_101_out, F12);
  not not_102 (not_102_out, OP6);
  not not_103 (not_103_out, OP5);
  not not_104 (not_104_out, OP3);
  not not_105 (not_105_out, OP2);
  not not_106 (not_106_out, F30);
  not not_107 (not_107_out, F25);
  not not_108 (not_108_out, F13);
  not not_109 (not_109_out, OP6);
  not not_110 (not_110_out, OP5);
  not not_111 (not_111_out, OP3);
  not not_112 (not_112_out, OP2);
  not not_113 (not_113_out, F14);
  not not_114 (not_114_out, F13);
  not not_115 (not_115_out, F12);
  not not_116 (not_116_out, OP4);
  not not_117 (not_117_out, OP3);
  not not_118 (not_118_out, OP2);
  not not_119 (not_119_out, F14);
  not not_120 (not_120_out, F13);
  not not_121 (not_121_out, OP4);
  not not_122 (not_122_out, OP3);
  not not_123 (not_123_out, OP2);
  not not_124 (not_124_out, F14);
  not not_125 (not_125_out, F13);
  not not_126 (not_126_out, F12);
  not not_127 (not_127_out, OP4);
  not not_128 (not_128_out, OP3);
  not not_129 (not_129_out, OP3);
  not not_130 (not_130_out, OP2);
  not not_131 (not_131_out, F30);
  not not_132 (not_132_out, F25);
  not not_133 (not_133_out, F13);
  not not_134 (not_134_out, OP6);
  not not_135 (not_135_out, OP3);
  not not_136 (not_136_out, OP2);
  not not_137 (not_137_out, F30);
  not not_138 (not_138_out, F25);
  not not_139 (not_139_out, F14);
  not not_140 (not_140_out, F13);
  not not_141 (not_141_out, F12);
  not not_142 (not_142_out, OP6);
  not not_143 (not_143_out, OP3);
  not not_144 (not_144_out, OP2);
  not not_145 (not_145_out, F25);
  not not_146 (not_146_out, F14);
  not not_147 (not_147_out, F13);
  not not_148 (not_148_out, F12);
  not not_149 (not_149_out, OP6);
  not not_150 (not_150_out, OP3);
  not not_151 (not_151_out, OP2);
  not not_152 (not_152_out, F30);
  not not_153 (not_153_out, F25);
  not not_154 (not_154_out, OP6);
  not not_155 (not_155_out, OP3);
  not not_156 (not_156_out, OP2);
  not not_157 (not_157_out, F30);
  not not_158 (not_158_out, F25);
  not not_159 (not_159_out, F14);
  not not_160 (not_160_out, OP6);
  not not_161 (not_161_out, OP3);
  not not_162 (not_162_out, OP2);
  not not_163 (not_163_out, F14);
  not not_164 (not_164_out, F13);
  not not_165 (not_165_out, F12);
  not not_166 (not_166_out, OP6);
  not not_167 (not_167_out, OP5);
  not not_168 (not_168_out, OP3);
  not not_169 (not_169_out, OP2);
  not not_170 (not_170_out, OP6);
  not not_171 (not_171_out, OP5);
  not not_172 (not_172_out, OP3);
  not not_173 (not_173_out, OP2);
  not not_174 (not_174_out, F14);
  not not_175 (not_175_out, F12);
  not not_176 (not_176_out, OP6);
  not not_177 (not_177_out, OP5);
  not not_178 (not_178_out, OP4);
  not not_179 (not_179_out, OP3);
  not not_180 (not_180_out, OP2);
  not not_181 (not_181_out, F14);
  not not_182 (not_182_out, F12);
  not not_183 (not_183_out, OP6);
  not not_184 (not_184_out, OP4);
  not not_185 (not_185_out, OP3);
  not not_186 (not_186_out, OP2);
  not not_187 (not_187_out, F14);
  not not_188 (not_188_out, F13);
  not not_189 (not_189_out, F12);
  not not_190 (not_190_out, OP4);
  not not_191 (not_191_out, OP3);
  not not_192 (not_192_out, OP2);
  not not_193 (not_193_out, F14);
  not not_194 (not_194_out, F13);
  not not_195 (not_195_out, OP4);
  not not_196 (not_196_out, OP3);
  not not_197 (not_197_out, OP2);
  not not_198 (not_198_out, F14);
  not not_199 (not_199_out, F13);
  not not_200 (not_200_out, F12);
  not not_201 (not_201_out, OP4);
  not not_202 (not_202_out, OP3);
  not not_203 (not_203_out, OP3);
  not not_204 (not_204_out, OP2);
  not not_205 (not_205_out, F14);
  not not_206 (not_206_out, F13);
  not not_207 (not_207_out, OP6);
  not not_208 (not_208_out, OP5);
  not not_209 (not_209_out, OP4);
  not not_210 (not_210_out, OP3);
  not not_211 (not_211_out, OP2);
  not not_212 (not_212_out, F12);
  not not_213 (not_213_out, OP4);
  not not_214 (not_214_out, OP3);
  not not_215 (not_215_out, OP2);
  not not_216 (not_216_out, F30);
  not not_217 (not_217_out, F25);
  not not_218 (not_218_out, F12);
  not not_219 (not_219_out, OP6);
  not not_220 (not_220_out, OP3);
  not not_221 (not_221_out, OP2);
  not not_222 (not_222_out, F30);
  not not_223 (not_223_out, F25);
  not not_224 (not_224_out, F14);
  not not_225 (not_225_out, F12);
  not not_226 (not_226_out, OP6);
  not not_227 (not_227_out, OP3);
  not not_228 (not_228_out, OP2);
  not not_229 (not_229_out, F30);
  not not_230 (not_230_out, F25);
  not not_231 (not_231_out, F14);
  not not_232 (not_232_out, OP6);
  not not_233 (not_233_out, OP3);
  not not_234 (not_234_out, OP2);
  not not_235 (not_235_out, F12);
  not not_236 (not_236_out, OP6);
  not not_237 (not_237_out, OP5);
  not not_238 (not_238_out, OP3);
  not not_239 (not_239_out, OP2);
  not not_240 (not_240_out, F13);
  not not_241 (not_241_out, F12);
  not not_242 (not_242_out, OP6);
  not not_243 (not_243_out, OP5);
  not not_244 (not_244_out, OP3);
  not not_245 (not_245_out, OP2);
  not not_246 (not_246_out, F14);
  not not_247 (not_247_out, F12);
  not not_248 (not_248_out, OP6);
  not not_249 (not_249_out, OP5);
  not not_250 (not_250_out, OP3);
  not not_251 (not_251_out, OP2);
  not not_252 (not_252_out, F12);
  not not_253 (not_253_out, OP3);
  not not_254 (not_254_out, OP2);
  not not_255 (not_255_out, F12);
  not not_256 (not_256_out, OP4);
  not not_257 (not_257_out, OP3);
  not not_258 (not_258_out, OP2);
  and and_1 (and_1_out, not_1_out, not_2_out, not_3_out, not_4_out, not_5_out, not_6_out, OP5, OP4, not_7_out, not_8_out);
  and and_2 (and_2_out, not_9_out, not_10_out, F14, F13, F12, not_11_out, OP5, OP4, not_12_out, not_13_out);
  and and_3 (and_3_out, not_14_out, not_15_out, not_16_out, F13, not_17_out, not_18_out, OP5, OP4, not_19_out, not_20_out);
  and and_4 (and_4_out, not_21_out, not_22_out, not_23_out, not_24_out, not_25_out, OP4, not_26_out, not_27_out);
  and and_5 (and_5_out, F14, F13, F12, not_28_out, not_29_out, OP4, not_30_out, not_31_out);
  and and_6 (and_6_out, F14, not_32_out, not_33_out, not_34_out, not_35_out, OP4, not_36_out, not_37_out);
  and and_7 (and_7_out, not_38_out, F13, not_39_out, not_40_out, not_41_out, OP4, not_42_out, not_43_out);
  and and_8 (and_8_out, F30, not_44_out, F14, not_45_out, F12, not_46_out, not_47_out, OP4, not_48_out, not_49_out);
  and and_9 (and_9_out, not_50_out, F13, not_51_out, not_52_out, not_53_out, not_54_out, not_55_out, not_56_out);
  and and_10 (and_10_out, not_57_out, F13, not_58_out, not_59_out, OP5, not_60_out, not_61_out, not_62_out);
  and and_11 (and_11_out, F14, F13, F12, OP6, OP5, OP4, not_63_out, not_64_out);
  and and_12 (and_12_out, F30, not_65_out, F14, not_66_out, F12, not_67_out, OP5, OP4, not_68_out, not_69_out);
  and and_13 (and_13_out, not_70_out, not_71_out, F12, not_72_out, not_73_out, not_74_out, not_75_out, not_76_out);
  and and_14 (and_14_out, F30, not_77_out, not_78_out, not_79_out, not_80_out, not_81_out, OP5, OP4, not_82_out, not_83_out);
  and and_15 (and_15_out, not_84_out, not_85_out, F14, F13, F12, not_86_out, OP5, OP4, not_87_out, not_88_out);
  and and_16 (and_16_out, not_89_out, not_90_out, not_91_out, F13, not_92_out, not_93_out, OP5, OP4, not_94_out, not_95_out);
  and and_17 (and_17_out, F14, F13, F12, not_96_out, not_97_out, OP4, not_98_out, not_99_out);
  and and_18 (and_18_out, not_100_out, F13, not_101_out, not_102_out, not_103_out, OP4, not_104_out, not_105_out);
  and and_19 (and_19_out, not_106_out, not_107_out, F14, not_108_out, F12, not_109_out, not_110_out, OP4, not_111_out, not_112_out);
  and and_20 (and_20_out, not_113_out, not_114_out, not_115_out, OP6, OP5, not_116_out, not_117_out, not_118_out);
  and and_21 (and_21_out, not_119_out, not_120_out, F12, OP6, OP5, not_121_out, not_122_out, not_123_out);
  and and_22 (and_22_out, not_124_out, not_125_out, not_126_out, OP6, OP5, not_127_out, not_128_out, OP2);
  and and_23 (and_23_out, F14, F13, F12, OP6, OP5, OP4, not_129_out, not_130_out);
  and and_24 (and_24_out, not_131_out, not_132_out, F14, not_133_out, F12, not_134_out, OP5, OP4, not_135_out, not_136_out);
  and and_25 (and_25_out, not_137_out, not_138_out, not_139_out, not_140_out, not_141_out, not_142_out, OP5, OP4, not_143_out, not_144_out);
  and and_26 (and_26_out, F30, not_145_out, not_146_out, not_147_out, not_148_out, not_149_out, OP5, OP4, not_150_out, not_151_out);
  and and_27 (and_27_out, not_152_out, not_153_out, F14, F13, F12, not_154_out, OP5, OP4, not_155_out, not_156_out);
  and and_28 (and_28_out, not_157_out, not_158_out, not_159_out, F13, F12, not_160_out, OP5, OP4, not_161_out, not_162_out);
  and and_29 (and_29_out, not_163_out, not_164_out, not_165_out, not_166_out, not_167_out, OP4, not_168_out, not_169_out);
  and and_30 (and_30_out, F14, F13, F12, not_170_out, not_171_out, OP4, not_172_out, not_173_out);
  and and_31 (and_31_out, not_174_out, F13, not_175_out, not_176_out, not_177_out, not_178_out, not_179_out, not_180_out);
  and and_32 (and_32_out, not_181_out, F13, not_182_out, not_183_out, OP5, not_184_out, not_185_out, not_186_out);
  and and_33 (and_33_out, not_187_out, not_188_out, not_189_out, OP6, OP5, not_190_out, not_191_out, not_192_out);
  and and_34 (and_34_out, not_193_out, not_194_out, F12, OP6, OP5, not_195_out, not_196_out, not_197_out);
  and and_35 (and_35_out, not_198_out, not_199_out, not_200_out, OP6, OP5, not_201_out, not_202_out, OP2);
  and and_36 (and_36_out, F14, F13, F12, OP6, OP5, OP4, not_203_out, not_204_out);
  and and_37 (and_37_out, not_205_out, not_206_out, F12, not_207_out, not_208_out, not_209_out, not_210_out, not_211_out);
  and and_38 (and_38_out, F14, F13, not_212_out, OP6, OP5, not_213_out, not_214_out, not_215_out);
  and and_39 (and_39_out, not_216_out, not_217_out, F14, F13, not_218_out, not_219_out, OP5, OP4, not_220_out, not_221_out);
  and and_40 (and_40_out, not_222_out, not_223_out, not_224_out, F13, not_225_out, not_226_out, OP5, OP4, not_227_out, not_228_out);
  and and_41 (and_41_out, not_229_out, not_230_out, not_231_out, F13, F12, not_232_out, OP5, OP4, not_233_out, not_234_out);
  and and_42 (and_42_out, F14, F13, not_235_out, not_236_out, not_237_out, OP4, not_238_out, not_239_out);
  and and_43 (and_43_out, F14, not_240_out, not_241_out, not_242_out, not_243_out, OP4, not_244_out, not_245_out);
  and and_44 (and_44_out, not_246_out, F13, not_247_out, not_248_out, not_249_out, OP4, not_250_out, not_251_out);
  and and_45 (and_45_out, F14, F13, not_252_out, OP6, OP5, OP4, not_253_out, not_254_out);
  and and_46 (and_46_out, F14, F13, not_255_out, OP6, OP5, not_256_out, not_257_out, not_258_out);
  or or_1 (S0, and_1_out, and_2_out, and_3_out, and_4_out, and_5_out, and_6_out, and_7_out, and_8_out, and_9_out, and_10_out, and_11_out, and_12_out, and_13_out);
  or or_2 (S1, and_14_out, and_15_out, and_16_out, and_17_out, and_18_out, and_19_out, and_20_out, and_21_out, and_22_out, and_23_out, and_24_out);
  or or_3 (S2, and_25_out, and_26_out, and_27_out, and_28_out, and_29_out, and_30_out, and_31_out, and_32_out, and_33_out, and_34_out, and_35_out, and_36_out, and_37_out, and_38_out);
  or or_4 (S3, and_39_out, and_40_out, and_41_out, and_42_out, and_43_out, and_44_out, and_45_out, and_46_out);
endmodule

// 控制信号生成
module \控制信号自动生成  (
  input  OP2,
  input  OP3,
  input  OP4,
  input  OP5,
  input  OP6,
  input  F12,
  input  F13,
  input  F14,
  input  F25,
  input  F30,
  output MemToReg,
  output bltu,
  output CSR,
  output MemWrite,
  output lh,
  output ALU_SRC,
  output lw,
  output RegWrite,
  output S_Type,
  output BEQ,
  output BNE,
  output JALR,
  output JAL
);

  wire and_1_out, and_2_out, and_4_out, and_5_out, and_8_out, and_9_out, and_10_out, and_11_out, and_12_out,
       and_13_out, and_14_out, and_15_out, and_16_out, and_17_out, and_18_out, and_19_out, and_20_out,
       and_21_out, and_23_out, and_24_out, and_25_out, and_26_out, and_27_out, and_28_out, and_29_out,
       and_30_out, and_31_out, and_32_out, and_33_out, and_34_out, and_35_out, and_36_out, and_37_out,
       and_38_out, and_39_out, and_40_out, and_41_out, and_42_out, not_1_out, not_2_out, not_3_out,
       not_4_out, not_5_out, not_6_out, not_7_out, not_8_out, not_9_out, not_10_out, not_11_out, not_12_out,
       not_13_out, not_14_out, not_15_out, not_16_out, not_17_out, not_18_out, not_19_out, not_20_out,
       not_21_out, not_22_out, not_23_out, not_24_out, not_25_out, not_26_out, not_27_out, not_28_out,
       not_29_out, not_30_out, not_31_out, not_32_out, not_33_out, not_34_out, not_35_out, not_36_out,
       not_37_out, not_38_out, not_39_out, not_40_out, not_41_out, not_42_out, not_43_out, not_44_out,
       not_45_out, not_46_out, not_47_out, not_48_out, not_49_out, not_50_out, not_51_out, not_52_out,
       not_53_out, not_54_out, not_55_out, not_56_out, not_57_out, not_58_out, not_59_out, not_60_out,
       not_61_out, not_62_out, not_63_out, not_64_out, not_65_out, not_66_out, not_67_out, not_68_out,
       not_69_out, not_70_out, not_71_out, not_72_out, not_73_out, not_74_out, not_75_out, not_76_out,
       not_77_out, not_78_out, not_79_out, not_80_out, not_81_out, not_82_out, not_83_out, not_84_out,
       not_85_out, not_86_out, not_87_out, not_88_out, not_89_out, not_90_out, not_91_out, not_92_out,
       not_93_out, not_94_out, not_95_out, not_96_out, not_97_out, not_98_out, not_99_out, not_100_out,
       not_101_out, not_102_out, not_103_out, not_104_out, not_105_out, not_106_out, not_107_out,
       not_108_out, not_109_out, not_110_out, not_111_out, not_112_out, not_113_out, not_114_out,
       not_115_out, not_116_out, not_117_out, not_118_out, not_119_out, not_120_out, not_121_out,
       not_122_out, not_123_out, not_124_out, not_125_out, not_126_out, not_127_out, not_128_out,
       not_129_out, not_130_out, not_131_out, not_132_out, not_133_out, not_134_out, not_135_out,
       not_136_out, not_137_out, not_138_out, not_139_out, not_140_out, not_141_out, not_142_out,
       not_143_out, not_144_out, not_145_out, not_146_out, not_147_out, not_148_out, not_149_out,
       not_150_out, not_151_out, not_152_out, not_153_out, not_154_out, not_155_out, not_156_out,
       not_157_out, not_158_out, not_159_out, not_160_out, not_161_out, not_162_out, not_163_out,
       not_164_out, not_165_out, not_166_out, not_167_out, not_168_out, not_169_out, not_170_out,
       not_171_out, not_172_out, not_173_out, not_174_out, not_175_out, not_176_out, not_177_out,
       not_178_out, not_179_out, not_180_out, not_181_out, not_182_out, not_183_out, not_184_out,
       not_185_out, not_186_out, not_187_out, not_188_out, not_189_out, not_190_out, not_191_out,
       not_192_out, not_193_out, not_194_out, not_195_out, not_196_out, not_197_out, not_198_out,
       not_199_out, not_200_out, not_201_out, not_202_out, not_203_out, not_204_out, not_205_out,
       not_206_out, not_207_out, not_208_out, not_209_out, not_210_out, not_211_out, not_212_out,
       not_213_out, not_214_out, not_215_out, not_216_out, not_217_out, not_218_out, not_219_out,
       not_220_out, not_221_out, not_222_out, not_223_out, not_224_out, not_225_out, not_226_out,
       not_227_out, not_228_out, not_229_out, not_230_out, not_231_out, not_232_out, not_233_out,
       not_234_out, not_235_out, not_236_out, not_237_out, not_238_out, not_239_out, not_240_out,
       not_241_out, not_242_out, not_243_out, not_244_out, not_245_out, not_246_out, not_247_out,
       not_248_out, not_249_out, not_250_out, not_251_out, not_252_out, not_253_out, not_254_out,
       not_255_out, not_256_out, not_257_out, not_258_out, not_259_out, not_260_out, not_261_out,
       not_262_out, not_263_out, not_264_out;

  not not_1 (not_1_out, F14);
  not not_2 (not_2_out, F12);
  not not_3 (not_3_out, OP6);
  not not_4 (not_4_out, OP5);
  not not_5 (not_5_out, OP4);
  not not_6 (not_6_out, OP3);
  not not_7 (not_7_out, OP2);
  not not_8 (not_8_out, F14);
  not not_9 (not_9_out, F13);
  not not_10 (not_10_out, OP6);
  not not_11 (not_11_out, OP5);
  not not_12 (not_12_out, OP4);
  not not_13 (not_13_out, OP3);
  not not_14 (not_14_out, OP2);
  not not_15 (not_15_out, F12);
  not not_16 (not_16_out, OP4);
  not not_17 (not_17_out, OP3);
  not not_18 (not_18_out, OP2);
  not not_19 (not_19_out, F12);
  not not_20 (not_20_out, OP3);
  not not_21 (not_21_out, OP2);
  not not_22 (not_22_out, OP3);
  not not_23 (not_23_out, OP2);
  not not_24 (not_24_out, F14);
  not not_25 (not_25_out, F12);
  not not_26 (not_26_out, OP6);
  not not_27 (not_27_out, OP4);
  not not_28 (not_28_out, OP3);
  not not_29 (not_29_out, OP2);
  not not_30 (not_30_out, F14);
  not not_31 (not_31_out, F13);
  not not_32 (not_32_out, OP6);
  not not_33 (not_33_out, OP5);
  not not_34 (not_34_out, OP4);
  not not_35 (not_35_out, OP3);
  not not_36 (not_36_out, OP2);
  not not_37 (not_37_out, F14);
  not not_38 (not_38_out, F13);
  not not_39 (not_39_out, F12);
  not not_40 (not_40_out, OP6);
  not not_41 (not_41_out, OP5);
  not not_42 (not_42_out, OP3);
  not not_43 (not_43_out, OP2);
  not not_44 (not_44_out, OP6);
  not not_45 (not_45_out, OP5);
  not not_46 (not_46_out, OP3);
  not not_47 (not_47_out, OP2);
  not not_48 (not_48_out, F12);
  not not_49 (not_49_out, OP6);
  not not_50 (not_50_out, OP5);
  not not_51 (not_51_out, OP3);
  not not_52 (not_52_out, OP2);
  not not_53 (not_53_out, F13);
  not not_54 (not_54_out, F12);
  not not_55 (not_55_out, OP6);
  not not_56 (not_56_out, OP5);
  not not_57 (not_57_out, OP3);
  not not_58 (not_58_out, OP2);
  not not_59 (not_59_out, F14);
  not not_60 (not_60_out, F12);
  not not_61 (not_61_out, OP6);
  not not_62 (not_62_out, OP5);
  not not_63 (not_63_out, OP3);
  not not_64 (not_64_out, OP2);
  not not_65 (not_65_out, F30);
  not not_66 (not_66_out, F25);
  not not_67 (not_67_out, F14);
  not not_68 (not_68_out, F13);
  not not_69 (not_69_out, OP6);
  not not_70 (not_70_out, OP5);
  not not_71 (not_71_out, OP3);
  not not_72 (not_72_out, OP2);
  not not_73 (not_73_out, F30);
  not not_74 (not_74_out, F25);
  not not_75 (not_75_out, F13);
  not not_76 (not_76_out, OP6);
  not not_77 (not_77_out, OP5);
  not not_78 (not_78_out, OP3);
  not not_79 (not_79_out, OP2);
  not not_80 (not_80_out, F25);
  not not_81 (not_81_out, F13);
  not not_82 (not_82_out, OP6);
  not not_83 (not_83_out, OP5);
  not not_84 (not_84_out, OP3);
  not not_85 (not_85_out, OP2);
  not not_86 (not_86_out, F14);
  not not_87 (not_87_out, F12);
  not not_88 (not_88_out, OP6);
  not not_89 (not_89_out, OP5);
  not not_90 (not_90_out, OP4);
  not not_91 (not_91_out, OP3);
  not not_92 (not_92_out, OP2);
  not not_93 (not_93_out, F14);
  not not_94 (not_94_out, F12);
  not not_95 (not_95_out, OP6);
  not not_96 (not_96_out, OP4);
  not not_97 (not_97_out, OP3);
  not not_98 (not_98_out, OP2);
  not not_99 (not_99_out, F14);
  not not_100 (not_100_out, F13);
  not not_101 (not_101_out, F12);
  not not_102 (not_102_out, OP4);
  not not_103 (not_103_out, OP3);
  not not_104 (not_104_out, F12);
  not not_105 (not_105_out, OP3);
  not not_106 (not_106_out, OP2);
  not not_107 (not_107_out, OP3);
  not not_108 (not_108_out, OP2);
  not not_109 (not_109_out, F14);
  not not_110 (not_110_out, F13);
  not not_111 (not_111_out, OP6);
  not not_112 (not_112_out, OP5);
  not not_113 (not_113_out, OP4);
  not not_114 (not_114_out, OP3);
  not not_115 (not_115_out, OP2);
  not not_116 (not_116_out, F14);
  not not_117 (not_117_out, F12);
  not not_118 (not_118_out, OP6);
  not not_119 (not_119_out, OP5);
  not not_120 (not_120_out, OP4);
  not not_121 (not_121_out, OP3);
  not not_122 (not_122_out, OP2);
  not not_123 (not_123_out, F30);
  not not_124 (not_124_out, F25);
  not not_125 (not_125_out, F14);
  not not_126 (not_126_out, F13);
  not not_127 (not_127_out, F12);
  not not_128 (not_128_out, OP6);
  not not_129 (not_129_out, OP3);
  not not_130 (not_130_out, OP2);
  not not_131 (not_131_out, F25);
  not not_132 (not_132_out, F14);
  not not_133 (not_133_out, F13);
  not not_134 (not_134_out, F12);
  not not_135 (not_135_out, OP6);
  not not_136 (not_136_out, OP3);
  not not_137 (not_137_out, OP2);
  not not_138 (not_138_out, F30);
  not not_139 (not_139_out, F25);
  not not_140 (not_140_out, OP6);
  not not_141 (not_141_out, OP3);
  not not_142 (not_142_out, OP2);
  not not_143 (not_143_out, F30);
  not not_144 (not_144_out, F25);
  not not_145 (not_145_out, F12);
  not not_146 (not_146_out, OP6);
  not not_147 (not_147_out, OP3);
  not not_148 (not_148_out, OP2);
  not not_149 (not_149_out, F30);
  not not_150 (not_150_out, F25);
  not not_151 (not_151_out, F14);
  not not_152 (not_152_out, F12);
  not not_153 (not_153_out, OP6);
  not not_154 (not_154_out, OP3);
  not not_155 (not_155_out, OP2);
  not not_156 (not_156_out, F30);
  not not_157 (not_157_out, F25);
  not not_158 (not_158_out, F14);
  not not_159 (not_159_out, OP6);
  not not_160 (not_160_out, OP3);
  not not_161 (not_161_out, OP2);
  not not_162 (not_162_out, F14);
  not not_163 (not_163_out, F13);
  not not_164 (not_164_out, F12);
  not not_165 (not_165_out, OP6);
  not not_166 (not_166_out, OP5);
  not not_167 (not_167_out, OP3);
  not not_168 (not_168_out, OP2);
  not not_169 (not_169_out, OP6);
  not not_170 (not_170_out, OP5);
  not not_171 (not_171_out, OP3);
  not not_172 (not_172_out, OP2);
  not not_173 (not_173_out, F12);
  not not_174 (not_174_out, OP6);
  not not_175 (not_175_out, OP5);
  not not_176 (not_176_out, OP3);
  not not_177 (not_177_out, OP2);
  not not_178 (not_178_out, F13);
  not not_179 (not_179_out, F12);
  not not_180 (not_180_out, OP6);
  not not_181 (not_181_out, OP5);
  not not_182 (not_182_out, OP3);
  not not_183 (not_183_out, OP2);
  not not_184 (not_184_out, F14);
  not not_185 (not_185_out, F12);
  not not_186 (not_186_out, OP6);
  not not_187 (not_187_out, OP5);
  not not_188 (not_188_out, OP3);
  not not_189 (not_189_out, OP2);
  not not_190 (not_190_out, F30);
  not not_191 (not_191_out, F25);
  not not_192 (not_192_out, F14);
  not not_193 (not_193_out, F13);
  not not_194 (not_194_out, OP6);
  not not_195 (not_195_out, OP5);
  not not_196 (not_196_out, OP3);
  not not_197 (not_197_out, OP2);
  not not_198 (not_198_out, F30);
  not not_199 (not_199_out, F25);
  not not_200 (not_200_out, F13);
  not not_201 (not_201_out, OP6);
  not not_202 (not_202_out, OP5);
  not not_203 (not_203_out, OP3);
  not not_204 (not_204_out, OP2);
  not not_205 (not_205_out, F25);
  not not_206 (not_206_out, F13);
  not not_207 (not_207_out, OP6);
  not not_208 (not_208_out, OP5);
  not not_209 (not_209_out, OP3);
  not not_210 (not_210_out, OP2);
  not not_211 (not_211_out, F14);
  not not_212 (not_212_out, F12);
  not not_213 (not_213_out, OP6);
  not not_214 (not_214_out, OP5);
  not not_215 (not_215_out, OP4);
  not not_216 (not_216_out, OP3);
  not not_217 (not_217_out, OP2);
  not not_218 (not_218_out, OP4);
  not not_219 (not_219_out, F14);
  not not_220 (not_220_out, F13);
  not not_221 (not_221_out, F12);
  not not_222 (not_222_out, OP4);
  not not_223 (not_223_out, OP3);
  not not_224 (not_224_out, F30);
  not not_225 (not_225_out, F25);
  not not_226 (not_226_out, F13);
  not not_227 (not_227_out, OP6);
  not not_228 (not_228_out, OP3);
  not not_229 (not_229_out, OP2);
  not not_230 (not_230_out, F25);
  not not_231 (not_231_out, F13);
  not not_232 (not_232_out, OP6);
  not not_233 (not_233_out, OP3);
  not not_234 (not_234_out, OP2);
  not not_235 (not_235_out, F14);
  not not_236 (not_236_out, F13);
  not not_237 (not_237_out, OP6);
  not not_238 (not_238_out, OP5);
  not not_239 (not_239_out, OP4);
  not not_240 (not_240_out, OP3);
  not not_241 (not_241_out, OP2);
  not not_242 (not_242_out, F14);
  not not_243 (not_243_out, F12);
  not not_244 (not_244_out, OP6);
  not not_245 (not_245_out, OP4);
  not not_246 (not_246_out, OP3);
  not not_247 (not_247_out, OP2);
  not not_248 (not_248_out, F14);
  not not_249 (not_249_out, F13);
  not not_250 (not_250_out, F12);
  not not_251 (not_251_out, OP4);
  not not_252 (not_252_out, OP3);
  not not_253 (not_253_out, OP2);
  not not_254 (not_254_out, F14);
  not not_255 (not_255_out, F13);
  not not_256 (not_256_out, OP4);
  not not_257 (not_257_out, OP3);
  not not_258 (not_258_out, OP2);
  not not_259 (not_259_out, F14);
  not not_260 (not_260_out, F13);
  not not_261 (not_261_out, F12);
  not not_262 (not_262_out, OP4);
  not not_263 (not_263_out, OP3);
  not not_264 (not_264_out, OP4);
  and and_1 (and_1_out, not_1_out, F13, not_2_out, not_3_out, not_4_out, not_5_out, not_6_out, not_7_out);
  and and_2 (and_2_out, not_8_out, not_9_out, F12, not_10_out, not_11_out, not_12_out, not_13_out, not_14_out);
  and and_3 (bltu, F14, F13, not_15_out, OP6, OP5, not_16_out, not_17_out, not_18_out);
  and and_4 (and_4_out, F14, F13, not_19_out, OP6, OP5, OP4, not_20_out, not_21_out);
  and and_5 (and_5_out, F14, F13, F12, OP6, OP5, OP4, not_22_out, not_23_out);
  and and_6 (MemWrite, not_24_out, F13, not_25_out, not_26_out, OP5, not_27_out, not_28_out, not_29_out);
  and and_7 (lh, not_30_out, not_31_out, F12, not_32_out, not_33_out, not_34_out, not_35_out, not_36_out);
  and and_8 (and_8_out, not_37_out, not_38_out, not_39_out, not_40_out, not_41_out, OP4, not_42_out, not_43_out);
  and and_9 (and_9_out, F14, F13, F12, not_44_out, not_45_out, OP4, not_46_out, not_47_out);
  and and_10 (and_10_out, F14, F13, not_48_out, not_49_out, not_50_out, OP4, not_51_out, not_52_out);
  and and_11 (and_11_out, F14, not_53_out, not_54_out, not_55_out, not_56_out, OP4, not_57_out, not_58_out);
  and and_12 (and_12_out, not_59_out, F13, not_60_out, not_61_out, not_62_out, OP4, not_63_out, not_64_out);
  and and_13 (and_13_out, not_65_out, not_66_out, not_67_out, not_68_out, F12, not_69_out, not_70_out, OP4, not_71_out, not_72_out);
  and and_14 (and_14_out, not_73_out, not_74_out, F14, not_75_out, F12, not_76_out, not_77_out, OP4, not_78_out, not_79_out);
  and and_15 (and_15_out, F30, not_80_out, F14, not_81_out, F12, not_82_out, not_83_out, OP4, not_84_out, not_85_out);
  and and_16 (and_16_out, not_86_out, F13, not_87_out, not_88_out, not_89_out, not_90_out, not_91_out, not_92_out);
  and and_17 (and_17_out, not_93_out, F13, not_94_out, not_95_out, OP5, not_96_out, not_97_out, not_98_out);
  and and_18 (and_18_out, not_99_out, not_100_out, not_101_out, OP6, OP5, not_102_out, not_103_out, OP2);
  and and_19 (and_19_out, F14, F13, not_104_out, OP6, OP5, OP4, not_105_out, not_106_out);
  and and_20 (and_20_out, F14, F13, F12, OP6, OP5, OP4, not_107_out, not_108_out);
  and and_21 (and_21_out, not_109_out, not_110_out, F12, not_111_out, not_112_out, not_113_out, not_114_out, not_115_out);
  and and_22 (lw, not_116_out, F13, not_117_out, not_118_out, not_119_out, not_120_out, not_121_out, not_122_out);
  and and_23 (and_23_out, not_123_out, not_124_out, not_125_out, not_126_out, not_127_out, not_128_out, OP5, OP4, not_129_out, not_130_out);
  and and_24 (and_24_out, F30, not_131_out, not_132_out, not_133_out, not_134_out, not_135_out, OP5, OP4, not_136_out, not_137_out);
  and and_25 (and_25_out, not_138_out, not_139_out, F14, F13, F12, not_140_out, OP5, OP4, not_141_out, not_142_out);
  and and_26 (and_26_out, not_143_out, not_144_out, F14, F13, not_145_out, not_146_out, OP5, OP4, not_147_out, not_148_out);
  and and_27 (and_27_out, not_149_out, not_150_out, not_151_out, F13, not_152_out, not_153_out, OP5, OP4, not_154_out, not_155_out);
  and and_28 (and_28_out, not_156_out, not_157_out, not_158_out, F13, F12, not_159_out, OP5, OP4, not_160_out, not_161_out);
  and and_29 (and_29_out, not_162_out, not_163_out, not_164_out, not_165_out, not_166_out, OP4, not_167_out, not_168_out);
  and and_30 (and_30_out, F14, F13, F12, not_169_out, not_170_out, OP4, not_171_out, not_172_out);
  and and_31 (and_31_out, F14, F13, not_173_out, not_174_out, not_175_out, OP4, not_176_out, not_177_out);
  and and_32 (and_32_out, F14, not_178_out, not_179_out, not_180_out, not_181_out, OP4, not_182_out, not_183_out);
  and and_33 (and_33_out, not_184_out, F13, not_185_out, not_186_out, not_187_out, OP4, not_188_out, not_189_out);
  and and_34 (and_34_out, not_190_out, not_191_out, not_192_out, not_193_out, F12, not_194_out, not_195_out, OP4, not_196_out, not_197_out);
  and and_35 (and_35_out, not_198_out, not_199_out, F14, not_200_out, F12, not_201_out, not_202_out, OP4, not_203_out, not_204_out);
  and and_36 (and_36_out, F30, not_205_out, F14, not_206_out, F12, not_207_out, not_208_out, OP4, not_209_out, not_210_out);
  and and_37 (and_37_out, not_211_out, F13, not_212_out, not_213_out, not_214_out, not_215_out, not_216_out, not_217_out);
  and and_38 (and_38_out, OP6, OP5, not_218_out, OP3, OP2);
  and and_39 (and_39_out, not_219_out, not_220_out, not_221_out, OP6, OP5, not_222_out, not_223_out, OP2);
  and and_40 (and_40_out, not_224_out, not_225_out, F14, not_226_out, F12, not_227_out, OP5, OP4, not_228_out, not_229_out);
  and and_41 (and_41_out, F30, not_230_out, F14, not_231_out, F12, not_232_out, OP5, OP4, not_233_out, not_234_out);
  and and_42 (and_42_out, not_235_out, not_236_out, F12, not_237_out, not_238_out, not_239_out, not_240_out, not_241_out);
  and and_43 (S_Type, not_242_out, F13, not_243_out, not_244_out, OP5, not_245_out, not_246_out, not_247_out);
  and and_44 (BEQ, not_248_out, not_249_out, not_250_out, OP6, OP5, not_251_out, not_252_out, not_253_out);
  and and_45 (BNE, not_254_out, not_255_out, F12, OP6, OP5, not_256_out, not_257_out, not_258_out);
  and and_46 (JALR, not_259_out, not_260_out, not_261_out, OP6, OP5, not_262_out, not_263_out, OP2);
  and and_47 (JAL, OP6, OP5, not_264_out, OP3, OP2);
  or or_1 (MemToReg, and_1_out, and_2_out);
  or or_2 (CSR, and_4_out, and_5_out);
  or or_3 (ALU_SRC, and_8_out, and_9_out, and_10_out, and_11_out, and_12_out, and_13_out, and_14_out, and_15_out, and_16_out, and_17_out, and_18_out, and_19_out, and_20_out, and_21_out);
  or or_4 (RegWrite, and_23_out, and_24_out, and_25_out, and_26_out, and_27_out, and_28_out, and_29_out, and_30_out, and_31_out, and_32_out, and_33_out, and_34_out, and_35_out, and_36_out, and_37_out, and_38_out, and_39_out, and_40_out, and_41_out, and_42_out);
endmodule

// ALU
module ALU (
  input  [31:0] X,
  input  [31:0] Y,
  input  [3:0] AluOP,
  output out_4,
  output Equal,
  output out_6,
  output [31:0] Result,
  output [31:0] Result_2
);

  wire [0:0] comparator_1_lt, comparator_2_lt;
  wire [31:0] adder_1_out, AND_out, divider_1_out, divider_1_rem, multiplier_1_cout, multiplier_1_out,
       NOR_out, OR_out, shifter_1_out, shifter_2_out, shifter_3_out, subtractor_1_out, XOR_out;

  assign AND_out = X & Y;  // AND_Gate AND, 32 bits wide
  assign OR_out = X | Y;  // OR_Gate OR, 32 bits wide
  Shifter #(.width(32), .shift("ll")) shifter_1 (.in(X), .\dist (Y[4:0]), .out(shifter_1_out));
  Shifter #(.width(32), .shift("ar")) shifter_2 (.in(X), .\dist (Y[4:0]), .out(shifter_2_out));
  Shifter #(.width(32), .shift("lr")) shifter_3 (.in(X), .\dist (Y[4:0]), .out(shifter_3_out));
  Multiplier #(.width(32)) multiplier_1 (.a(X), .b(Y), .out(multiplier_1_out), .cout(multiplier_1_cout));  // open: cin
  Divider #(.width(32)) divider_1 (.a(X), .b(Y), .out(divider_1_out), .rem(divider_1_rem));  // open: upper
  Adder #(.width(32)) adder_1 (.a(X), .b(Y), .out(adder_1_out));  // open: cin, cout
  Subtractor #(.width(32)) subtractor_1 (.a(X), .b(Y), .out(subtractor_1_out));  // open: bin, bout
  assign XOR_out = X ^ Y;  // XOR_Gate XOR, 32 bits wide
  assign NOR_out = ~(X | Y);  // NOR_Gate NOR, 32 bits wide
  Comparator #(.width(32), .mode("twosComplement")) comparator_1 (
    .a(X), .b(Y), .eq(Equal), .lt(comparator_1_lt[0]));  // open: gt
  Comparator #(.width(32), .mode("unsigned")) comparator_2 (.a(X), .b(Y), .lt(comparator_2_lt[0]));  // open: gt, eq
  Multiplexer #(.select(4), .width(32), .disabled("Z"), .enable("false")) multiplexer_1 (
    .in0(shifter_1_out), .in1(shifter_2_out), .in2(shifter_3_out), .in3(multiplier_1_out),
    .in4(divider_1_out), .in5(adder_1_out), .in6(subtractor_1_out), .in7(AND_out), .in8(OR_out),
    .in9(XOR_out), .in10(NOR_out), .in11({{31{1'b0}}, comparator_1_lt[0]}),
    .in12({{31{1'b0}}, comparator_2_lt[0]}), .in13({32{1'b0}}), .in14({32{1'b0}}), .in15({32{1'b0}}),
    .out(Result), .sel(AluOP));
  Multiplexer #(.select(4), .width(32), .disabled("Z"), .enable("false")) multiplexer_2 (
    .in0({32{1'b0}}), .in1({32{1'b0}}), .in2({32{1'b0}}), .in3(multiplier_1_cout), .in4(divider_1_rem),
    .in5({32{1'b0}}), .in6({32{1'b0}}), .in7({32{1'b0}}), .in8({32{1'b0}}), .in9({32{1'b0}}),
    .in10({32{1'b0}}), .in11({32{1'b0}}), .in12({32{1'b0}}), .in13({32{1'b0}}), .in14({32{1'b0}}),
    .in15({32{1'b0}}), .out(Result_2), .sel(AluOP));
  Multiplexer #(.select(4), .width(1), .disabled("Z"), .enable("false")) multiplexer_3 (
    .in0(1'b0), .in1(1'b0), .in2(1'b0), .in3(1'b0), .in4(1'b0), .in5(1'b0), .in6(1'b0), .in7(1'b0),
    .in8(1'b0), .in9(1'b0), .in10(1'b0), .in11(comparator_1_lt[0]), .in12(comparator_2_lt[0]), .in13(1'b0),
    .in14(1'b0), .in15(1'b0), .out(out_6), .sel(AluOP));
  not not_1 (out_4, out_6);

  // Other names for the same wires on the sheet: Result2[31:0] = Result_2; S[3:0] = AluOP; tunnel = out_6;
  //   tunnel_t = out_4

  // Notes on the sheet:
  //   不要改变此引脚区域内容，也不要改变ALU封装形式
  //   输入引脚
  //   输出引脚
endmodule

module Regifile (
  input  [31:0] Din,
  input  Clk,
  input  WE,
  input  [4:0] R1_num,
  input  [4:0] W_num,
  input  [4:0] R2_num,
  output [31:0] R1,
  output [31:0] R2
);

  // RegisterFile registerfile_1: pin names not known; wires that end beside it: Din, Clk, WE, W_num, R1_num, R2_num, R1, R2
endmodule

module RegFile_for_Single_Unit (
  input  [31:0] Din,
  input  Clk,
  input  WE,
  input  [4:0] R1_num,
  input  [4:0] W_num,
  input  [4:0] R2_num,
  output [31:0] R1,
  output [31:0] R2
);

  // RegisterFile registerfile_1: pin names not known; wires that end beside it: Din, Clk, WE, W_num, R1_num, R2_num, R1, R2
endmodule

module \理想流水线  (
  output RegWrite,
  output MemWrite,
  output [31:0] IF_PC,
  output [31:0] ID_PC,
  output [31:0] EX_PC,
  output [31:0] M_PC,
  output [31:0] WB_PC,
  output [31:0] RDin,
  output [31:0] MDin,
  output [31:0] LedData
);

  wire and_1_out, and_2_out, and_3_out, and_4_out, and_5_out, Branch, CLK, clock_1_out, comparator_1_eq,
       comparator_1_lt, d_ff_1_q, EX_B, ex_equal, EX_J, ex_less, Go, halt, IF_B, IF_I, IF_J, IF_S, IR1, IR2,
       IR3, mul_cmdreg_1_alu_src_2, mul_cmdreg_1_beq_2, mul_cmdreg_1_bne_2, mul_cmdreg_1_ecall_2,
       mul_cmdreg_1_jal_2, mul_cmdreg_1_jalr_2, mul_cmdreg_1_lh_2, mul_cmdreg_1_memtoreg_2,
       mul_cmdreg_1_memwrite_2, mul_cmdreg_1_regwrite_2, mul_cmdreg_1_s_type_2, mul_cmdreg_1_uret_2,
       mul_cmdreg_2_alu_src_2, mul_cmdreg_2_beq_2, mul_cmdreg_2_bne_2, mul_cmdreg_2_ecall_2,
       mul_cmdreg_2_jal_2, mul_cmdreg_2_jalr_2, mul_cmdreg_2_lh_2, mul_cmdreg_2_memtoreg_2,
       mul_cmdreg_2_regwrite_2, mul_cmdreg_2_s_type_2, mul_cmdreg_2_uret_2, mul_cmdreg_3_alu_src_2,
       mul_cmdreg_3_beq_2, mul_cmdreg_3_bne_2, mul_cmdreg_3_ecall_2, mul_cmdreg_3_jal_2, mul_cmdreg_3_jalr_2,
       mul_cmdreg_3_lh_2, mul_cmdreg_3_memtoreg_2, mul_cmdreg_3_memwrite_2, mul_cmdreg_3_s_type_2,
       mul_cmdreg_3_uret_2, nand_1_out, not_1_out, not_2_out, or_1_out, or_2_out, or_3_out, RST, System, W1,
       W2, W3, \单周期硬布线控制器_1_alu_src , \单周期硬布线控制器_1_beq , \单周期硬布线控制器_1_bne , \单周期硬布线控制器_1_ecall ,
       \单周期硬布线控制器_1_jal , \单周期硬布线控制器_1_jalr , \单周期硬布线控制器_1_lh , \单周期硬布线控制器_1_memtoreg ,
       \单周期硬布线控制器_1_memwrite , \单周期硬布线控制器_1_regwrite , \单周期硬布线控制器_1_s_type , \单周期硬布线控制器_1_uret ;
  wire [3:0] mul_cmdreg_1_alu_op_2, mul_cmdreg_2_alu_op_2, mul_cmdreg_3_alu_op_2, \单周期硬布线控制器_1_alu_op ;
  wire [4:0] funct, multiplexer_2_out, multiplexer_3_out, register_7_q, register_16_q, register_21_q;
  wire [12:0] CNT_num;
  wire [15:0] \LoadUse次数 , multiplexer_7_out, \总周期数 , \插入气泡数 , \无条件分支数 , \条件分支成功数 ;
  wire [31:0] adder_1_out, alu_1_result, bit_extender_1_out, EX_IR, ID_IR, IF_IR, immvaluegen_1_imm, MEM_IR,
       multiplexer_1_out, multiplexer_4_out, multiplexer_5_out, multiplexer_8_out, offset,
       pc_jumpingunit_1_ir_2, pc_jumpingunit_1_pc_2, pc_jumpingunit_2_ir_2, pc_jumpingunit_2_pc_2,
       pc_jumpingunit_3_ir_2, pc_jumpingunit_3_pc_2, ram_1_data, regifile_1_r1, regifile_1_r2, register_5_q,
       register_6_q, register_8_q, register_14_q, register_19_q, register_20_q, shifter_1_out, WB_IR;

  Button \u_总复位  (.out(RST));
  Button _1 (.out(IR1));
  Button _2 (.out(IR2));
  Button _3 (.out(IR3));
  // Probe on \总周期数 
  // Probe on \总周期数 
  Button \u_继续运行  (.out(Go));
  LED #(.active("true")) led_1 (.in(W1));
  LED #(.active("true")) led_2 (.in(W2));
  LED #(.active("true")) led_3 (.in(W3));
  not not_1 (not_1_out, halt);
  Hex_Digit_Display hex_digit_display_1 (.value(LedData[31:28]));  // open: dp
  // Probe on IF_PC[19:0]
  // RiscV_Probe riscv_probe_1: pin names not known; wires that end beside it: IF_IR
  Button button_1 (.out(halt));
  Adder #(.width(32)) adder_1 (.a(IF_PC), .b(32'h4), .out(adder_1_out), .cin(1'b0));  // open: cout
  or or_1 (or_1_out, Go, not_1_out);
  Counter #(.width(16), .max('hffff), .ongoal("wrap"), .trigger("rising"), .behavior("new")) counter_1 (
    .D({16{1'b0}}), .count(or_1_out), .Q(\总周期数 ), .clk(CLK), .clr(RST));  // open: load, carry, preset, down
  Hex_Digit_Display hex_digit_display_2 (.value(LedData[27:24]));  // open: dp
  Hex_Digit_Display hex_digit_display_3 (.value(LedData[23:20]));  // open: dp
  // Probe on ID_PC[19:0]
  // RiscV_Probe riscv_probe_2: pin names not known; wires that end beside it: {ID_IR[31], funct[4], ID_IR[29:26], funct[3], ID_IR[24:15], funct[2:0], ID_IR[11:0]}
  Multiplexer #(.select(1), .width(32), .disabled("Z"), .enable("false")) multiplexer_1 (
    .in0(adder_1_out), .in1(offset), .out(multiplexer_1_out), .sel(Branch));
  or or_2 (or_2_out, Go, not_2_out);
  not not_2 (not_2_out, halt);
  Hex_Digit_Display hex_digit_display_4 (.value(LedData[19:16]));  // open: dp
  Hex_Digit_Display hex_digit_display_5 (.value(LedData[15:12]));  // open: dp
  Register #(.width(32), .trigger("rising"), .Select("low")) PC (
    .D(multiplexer_1_out), .en(or_2_out), .Q(IF_PC), .clk(CLK), .clr(RST), .cs(1'b0), .preset(1'b0));
  Hex_Digit_Display hex_digit_display_6 (.value(LedData[11:8]));  // open: dp
  Hex_Digit_Display hex_digit_display_7 (.value(LedData[7:4]));  // open: dp
  // Probe on EX_PC[19:0]
  // RiscV_Probe riscv_probe_3: pin names not known; wires that end beside it: EX_IR
  Hex_Digit_Display hex_digit_display_8 (.value(LedData[3:0]));  // open: dp
  ROM #(.addrWidth(10), .dataWidth(32), .Select("high")) Instruction_Memory (
    .addr(IF_PC[11:2]), .data(IF_IR), .sel(1'b1));
  // Probe on \总周期数 
  // Probe on M_PC[19:0]
  // RiscV_Probe riscv_probe_4: pin names not known; wires that end beside it: MEM_IR, offset
  // Probe on \总周期数 
  // Probe on \无条件分支数 
  // Probe on \条件分支成功数 
  // Probe on \插入气泡数 
  // Probe on \LoadUse次数 
  PC_JumpingUnit pc_jumpingunit_1 (
    .Branch(Branch), .PC(IF_PC), .offset(offset), .PC_2(pc_jumpingunit_1_pc_2), .IR_2(pc_jumpingunit_1_ir_2),
    .IR(IF_IR));
  // Probe on IF_PC[11:0]
  // Probe on WB_PC[19:0]
  // RiscV_Probe riscv_probe_5: pin names not known; wires that end beside it: WB_IR
  // Probe on EX_PC[11:0]
  // Probe on ID_PC[11:0]
  Register #(.width(32), .trigger("rising"), .Select("low")) register_1 (
    .D(pc_jumpingunit_1_pc_2), .en(or_2_out), .Q(ID_PC), .clk(CLK), .clr(RST), .cs(1'b0), .preset(1'b0));
  Register #(.width(32), .trigger("rising"), .Select("low")) register_2 (
    .D(pc_jumpingunit_1_ir_2), .en(or_2_out),
    .Q({ID_IR[31], funct[4], ID_IR[29:26], funct[3], ID_IR[24:15], funct[2:0], ID_IR[11:0]}), .clk(CLK),
    .clr(RST), .cs(1'b0), .preset(1'b0));
  // Probe on M_PC[11:0]
  D_Flip_Flop #(.trigger("high"), .Pre_Clr_Positions("LEGACY"), .NegatePresetClear("false"), .enable("true"), .NewFFLayout("false")) d_ff_1 (.Q(d_ff_1_q));  // open: clk, D, Qn, preset, en, reset
  // Probe on 13'hc
  // Probe on WB_PC[11:0]
  Comparator #(.width(13), .mode("twosComplement")) comparator_1 (
    .a(CNT_num), .b(13'hc), .eq(comparator_1_eq), .lt(comparator_1_lt));  // open: gt
  Clock #(.highDuration(1), .lowDuration(1)) clock_1 (.out(clock_1_out));
  Multiplexer #(.select(1), .width(5), .disabled("Z"), .enable("false")) multiplexer_2 (
    .in0(ID_IR[19:15]), .in1(5'b01010), .out(multiplexer_2_out), .sel(\单周期硬布线控制器_1_ecall ));
  Multiplexer #(.select(1), .width(5), .disabled("Z"), .enable("false")) multiplexer_3 (
    .in0(ID_IR[24:20]), .in1(5'b10001), .out(multiplexer_3_out), .sel(\单周期硬布线控制器_1_ecall ));
  nand nand_1 (nand_1_out, d_ff_1_q, comparator_1_eq);
  Counter #(.width(13), .max('h1fff), .ongoal("stay"), .trigger("rising"), .behavior("old")) counter_2 (
    .count(comparator_1_lt), .Q(CNT_num), .clk(clock_1_out));  // open: load, D, carry, clr, preset
  assign CLK = nand_1_out ? clock_1_out : 1'bz;  // Controlled_Buffer controlled_buffer_1
  PC_JumpingUnit pc_jumpingunit_2 (
    .Branch(Branch), .PC(ID_PC), .offset(offset), .PC_2(pc_jumpingunit_2_pc_2), .IR_2(pc_jumpingunit_2_ir_2),
    .IR({ID_IR[31], funct[4], ID_IR[29:26], funct[3], ID_IR[24:15], funct[2:0], ID_IR[11:0]}));
  \单周期硬布线控制器  \u_单周期硬布线控制器_1  (
    .Funct(funct), .OP(ID_IR[6:2]), .ALU_OP(\单周期硬布线控制器_1_alu_op ), .MemToReg(\单周期硬布线控制器_1_memtoreg ),
    .ecall(\单周期硬布线控制器_1_ecall ), .in_3(ID_IR[21]), .uret(\单周期硬布线控制器_1_uret ),
    .MemWrite(\单周期硬布线控制器_1_memwrite ), .lh(\单周期硬布线控制器_1_lh ), .BEQ(\单周期硬布线控制器_1_beq ),
    .S_Type(\单周期硬布线控制器_1_s_type ), .RegWrite(\单周期硬布线控制器_1_regwrite ), .ALU_SRC(\单周期硬布线控制器_1_alu_src ),
    .BNE(\单周期硬布线控制器_1_bne ), .JALR(\单周期硬布线控制器_1_jalr ), .JAL(\单周期硬布线控制器_1_jal ));  // open: bltu, CSR, lw
  ImmValueGen immvaluegen_1 (
    .Imm(immvaluegen_1_imm), .Type_I_Imm({ID_IR[31], funct[4], ID_IR[29:26], funct[3], ID_IR[24:20]}),
    .Type_S_Imm({ID_IR[31], funct[4], ID_IR[29:26], funct[3], ID_IR[11:7]}),
    .Type_B_Imm({ID_IR[31], ID_IR[7], funct[4], ID_IR[29:26], funct[3], ID_IR[11:8]}),
    .Type_J_Imm({ID_IR[31], ID_IR[19:15], funct[2:0], ID_IR[20], funct[4], ID_IR[29:26], funct[3], ID_IR[24:21]}),
    .Op6(ID_IR[6]), .I(IF_I), .Op5(ID_IR[5]), .S(IF_S), .Op4(ID_IR[4]), .B(IF_B), .Op3(ID_IR[3]), .J(IF_J),
    .Op2(ID_IR[2]), .System(System));
  Pull_Resistor #(.pull(1)) pull_resistor_1 (.node(CLK));
  Regifile regifile_1 (
    .Din(RDin), .Clk(CLK), .R1(regifile_1_r1), .R2(regifile_1_r2), .WE(RegWrite), .W_num(register_21_q),
    .R1_num(multiplexer_2_out), .R2_num(multiplexer_3_out));
  Register #(.width(32), .trigger("rising"), .Select("low")) register_3 (
    .D(pc_jumpingunit_2_pc_2), .en(or_2_out), .Q(EX_PC), .clk(CLK), .clr(RST), .cs(1'b0), .preset(1'b0));
  Register #(.width(32), .trigger("rising"), .Select("low")) register_4 (
    .D(pc_jumpingunit_2_ir_2), .en(or_2_out), .Q(EX_IR), .clk(CLK), .clr(RST), .cs(1'b0), .preset(1'b0));
  Mul_cmdReg mul_cmdreg_1 (
    .lh(\单周期硬布线控制器_1_lh ), .Bne(\单周期硬布线控制器_1_bne ), .Alu_OP(\单周期硬布线控制器_1_alu_op ), .uret(\单周期硬布线控制器_1_uret ),
    .Beq(\单周期硬布线控制器_1_beq ), .Alu_Src(\单周期硬布线控制器_1_alu_src ), .JALR(\单周期硬布线控制器_1_jalr ),
    .MemToReg(\单周期硬布线控制器_1_memtoreg ), .RegWrite(\单周期硬布线控制器_1_regwrite ), .JAL(\单周期硬布线控制器_1_jal ),
    .MemWrite(\单周期硬布线控制器_1_memwrite ), .S_Type(\单周期硬布线控制器_1_s_type ), .ecall(\单周期硬布线控制器_1_ecall ), .CLK(CLK),
    .lh_2(mul_cmdreg_1_lh_2), .Bne_2(mul_cmdreg_1_bne_2), .Alu_OP_2(mul_cmdreg_1_alu_op_2),
    .uret_2(mul_cmdreg_1_uret_2), .Beq_2(mul_cmdreg_1_beq_2), .Alu_Src_2(mul_cmdreg_1_alu_src_2),
    .JALR_2(mul_cmdreg_1_jalr_2), .MemToReg_2(mul_cmdreg_1_memtoreg_2), .RegWrite_2(mul_cmdreg_1_regwrite_2),
    .JAL_2(mul_cmdreg_1_jal_2), .MemWrite_2(mul_cmdreg_1_memwrite_2), .S_Type_2(mul_cmdreg_1_s_type_2),
    .ecall_2(mul_cmdreg_1_ecall_2), .RST(RST));  // open: bltu, bltu_2, lw_2, lw, CSR_2, CSR
  Register #(.width(32), .trigger("rising"), .Select("low")) register_5 (
    .D(regifile_1_r1), .en(1'b1), .Q(register_5_q), .clk(CLK), .clr(RST), .cs(1'b0), .preset(1'b0));
  Register #(.width(32), .trigger("rising"), .Select("low")) register_6 (
    .D(regifile_1_r2), .en(1'b1), .Q(register_6_q), .clk(CLK), .clr(RST), .cs(1'b0), .preset(1'b0));
  Register #(.width(5), .trigger("rising"), .Select("low")) register_7 (
    .D(ID_IR[11:7]), .en(1'b1), .Q(register_7_q), .clk(CLK), .clr(RST), .cs(RST), .preset(RST));
  Register #(.width(32), .trigger("rising"), .Select("low")) register_8 (
    .D(immvaluegen_1_imm), .en(1'b1), .Q(register_8_q), .clk(CLK), .clr(RST), .cs(1'b0), .preset(1'b0));
  Register #(.width(1), .trigger("rising"), .Select("low")) register_9 (
    .D(IF_J), .en(1'b1), .Q(EX_J), .clk(CLK), .clr(RST), .cs(1'b0), .preset(1'b0));
  Register #(.width(1), .trigger("rising"), .Select("low")) register_10 (
    .D(IF_B), .en(1'b1), .Q(EX_B), .clk(CLK), .clr(RST), .cs(1'b0), .preset(1'b0));
  and and_1 (and_1_out, mul_cmdreg_1_ecall_2, ex_equal);
  Shifter #(.width(32), .shift("ll")) shifter_1 (.in(register_8_q), .\dist (5'b00001), .out(shifter_1_out));
  and and_2 (and_2_out, ex_equal, ~funct[0]);  // AND_Gate
  and and_3 (and_3_out, ~ex_equal, funct[0]);  // AND_Gate
  and and_4 (and_4_out, funct[2], ex_less);
  Multiplexer #(.select(1), .width(32), .disabled("Z"), .enable("false")) multiplexer_4 (
    .in0(register_5_q), .in1(32'h22), .out(multiplexer_4_out), .sel(mul_cmdreg_1_ecall_2));
  Register #(.width(32), .trigger("rising"), .Select("low")) register_11 (
    .D(register_5_q), .en(and_1_out), .Q(LedData), .clk(CLK), .clr(RST), .cs(1'b0), .preset(1'b0));
  or or_3 (or_3_out, and_2_out, and_3_out, and_4_out);
  PC_JumpingUnit pc_jumpingunit_3 (
    .Branch(Branch), .PC(EX_PC), .offset(offset), .PC_2(pc_jumpingunit_3_pc_2), .IR_2(pc_jumpingunit_3_ir_2),
    .IR(EX_IR));
  Multiplexer #(.select(1), .width(32), .disabled("Z"), .enable("false")) multiplexer_5 (
    .in0(register_6_q), .in1(register_8_q), .out(multiplexer_5_out), .sel(mul_cmdreg_1_alu_src_2));
  Multiplexer #(.select(1), .width(32), .disabled("Z"), .enable("false")) multiplexer_6 (
    .in0({alu_1_result[31:1], 1'b0}), .in1(shifter_1_out), .out(offset), .sel(mul_cmdreg_1_jalr_2));
  and and_5 (and_5_out, EX_B, or_3_out);
  ALU alu_1 (
    .X(multiplexer_4_out), .Y(multiplexer_5_out), .AluOP(mul_cmdreg_1_alu_op_2), .Equal(ex_equal),
    .Result(alu_1_result), .out_6(ex_less));  // open: Result_2, out_4
  or or_4 (Branch, and_5_out, EX_J);
  Register #(.width(32), .trigger("rising"), .Select("low")) register_12 (
    .D(pc_jumpingunit_3_pc_2), .en(or_2_out), .Q(M_PC), .clk(CLK), .clr(RST), .cs(1'b0), .preset(1'b0));
  Register #(.width(32), .trigger("rising"), .Select("low")) register_13 (
    .D(pc_jumpingunit_3_ir_2), .en(or_2_out), .Q(MEM_IR), .clk(CLK), .clr(RST), .cs(1'b0), .preset(1'b0));
  Mul_cmdReg mul_cmdreg_2 (
    .lh(mul_cmdreg_1_lh_2), .Bne(mul_cmdreg_1_bne_2), .Alu_OP(mul_cmdreg_1_alu_op_2),
    .uret(mul_cmdreg_1_uret_2), .Beq(mul_cmdreg_1_beq_2), .Alu_Src(mul_cmdreg_1_alu_src_2),
    .JALR(mul_cmdreg_1_jalr_2), .MemToReg(mul_cmdreg_1_memtoreg_2), .RegWrite(mul_cmdreg_1_regwrite_2),
    .JAL(mul_cmdreg_1_jal_2), .MemWrite(mul_cmdreg_1_memwrite_2), .S_Type(mul_cmdreg_1_s_type_2),
    .ecall(mul_cmdreg_1_ecall_2), .CLK(CLK), .lh_2(mul_cmdreg_2_lh_2), .Bne_2(mul_cmdreg_2_bne_2),
    .Alu_OP_2(mul_cmdreg_2_alu_op_2), .uret_2(mul_cmdreg_2_uret_2), .Beq_2(mul_cmdreg_2_beq_2),
    .Alu_Src_2(mul_cmdreg_2_alu_src_2), .JALR_2(mul_cmdreg_2_jalr_2), .MemToReg_2(mul_cmdreg_2_memtoreg_2),
    .RegWrite_2(mul_cmdreg_2_regwrite_2), .JAL_2(mul_cmdreg_2_jal_2), .MemWrite_2(MemWrite),
    .S_Type_2(mul_cmdreg_2_s_type_2), .ecall_2(mul_cmdreg_2_ecall_2), .RST(RST));  // open: bltu, bltu_2, lw_2, lw, CSR_2, CSR
  Register #(.width(32), .trigger("rising"), .Select("low")) register_14 (
    .D(alu_1_result), .en(1'b1), .Q(register_14_q), .clk(CLK), .clr(RST), .cs(1'b0), .preset(1'b0));
  Register #(.width(32), .trigger("rising"), .Select("low")) register_15 (
    .D(register_6_q), .en(1'b1), .Q(MDin), .clk(CLK), .clr(RST), .cs(1'b0), .preset(1'b0));
  Register #(.width(5), .trigger("rising"), .Select("low")) register_16 (
    .D(register_7_q), .en(1'b1), .Q(register_16_q), .clk(CLK), .clr(RST), .cs(1'b0), .preset(1'b0));
  RAM #(.addrWidth(10), .dataWidth(32), .bus("separate"), .Select("high")) ram_1 (
    .addr(register_14_q[11:2]), .din(MDin), .data(ram_1_data), .str(MemWrite), .sel(1'b1), .clk(CLK),
    .ld(1'b1), .clr(RST));
  Multiplexer #(.select(1), .width(16), .disabled("Z"), .enable("false")) multiplexer_7 (
    .in0(ram_1_data[15:0]), .in1(ram_1_data[31:16]), .out(multiplexer_7_out), .sel(register_14_q[1]));
  Register #(.width(32), .trigger("rising"), .Select("low")) register_17 (
    .D(M_PC), .en(or_2_out), .Q(WB_PC), .clk(CLK), .clr(RST), .cs(1'b0), .preset(1'b0));
  Register #(.width(32), .trigger("rising"), .Select("low")) register_18 (
    .D(MEM_IR), .en(or_2_out), .Q(WB_IR), .clk(CLK), .clr(RST), .cs(1'b0), .preset(1'b0));
  assign bit_extender_1_out = {{16{multiplexer_7_out[15]}}, multiplexer_7_out};  // Bit_Extender bit_extender_1
  Multiplexer #(.select(1), .width(32), .disabled("Z"), .enable("false")) multiplexer_8 (
    .in0(ram_1_data), .in1(bit_extender_1_out), .out(multiplexer_8_out), .sel(mul_cmdreg_2_lh_2));
  Mul_cmdReg mul_cmdreg_3 (
    .lh(mul_cmdreg_2_lh_2), .Bne(mul_cmdreg_2_bne_2), .Alu_OP(mul_cmdreg_2_alu_op_2),
    .uret(mul_cmdreg_2_uret_2), .Beq(mul_cmdreg_2_beq_2), .Alu_Src(mul_cmdreg_2_alu_src_2),
    .JALR(mul_cmdreg_2_jalr_2), .MemToReg(mul_cmdreg_2_memtoreg_2), .RegWrite(mul_cmdreg_2_regwrite_2),
    .JAL(mul_cmdreg_2_jal_2), .MemWrite(MemWrite), .S_Type(mul_cmdreg_2_s_type_2),
    .ecall(mul_cmdreg_2_ecall_2), .CLK(CLK), .lh_2(mul_cmdreg_3_lh_2), .Bne_2(mul_cmdreg_3_bne_2),
    .Alu_OP_2(mul_cmdreg_3_alu_op_2), .uret_2(mul_cmdreg_3_uret_2), .Beq_2(mul_cmdreg_3_beq_2),
    .Alu_Src_2(mul_cmdreg_3_alu_src_2), .JALR_2(mul_cmdreg_3_jalr_2), .MemToReg_2(mul_cmdreg_3_memtoreg_2),
    .RegWrite_2(RegWrite), .JAL_2(mul_cmdreg_3_jal_2), .MemWrite_2(mul_cmdreg_3_memwrite_2),
    .S_Type_2(mul_cmdreg_3_s_type_2), .ecall_2(mul_cmdreg_3_ecall_2), .RST(RST));  // open: bltu, bltu_2, lw_2, lw, CSR_2, CSR
  Register #(.width(32), .trigger("rising"), .Select("low")) register_19 (
    .D(register_14_q), .en(1'b1), .Q(register_19_q), .clk(CLK), .clr(RST), .cs(1'b0), .preset(1'b0));
  Register #(.width(32), .trigger("rising"), .Select("low")) register_20 (
    .D(multiplexer_8_out), .en(1'b1), .Q(register_20_q), .clk(CLK), .clr(RST), .cs(1'b0), .preset(1'b0));
  Register #(.width(5), .trigger("rising"), .Select("low")) register_21 (
    .D(register_16_q), .en(1'b1), .Q(register_21_q), .clk(CLK), .clr(RST), .cs(1'b0), .preset(1'b0));
  Multiplexer #(.select(1), .width(32), .disabled("Z"), .enable("false")) multiplexer_9 (
    .in0(register_19_q), .in1(register_20_q), .out(RDin), .sel(mul_cmdreg_3_memtoreg_2));
  Register #(.width(32), .trigger("rising"), .Select("low")) register_22 (
    .D(WB_PC), .en(or_2_out), .clk(CLK), .clr(RST), .cs(1'b0), .preset(1'b0));  // open: Q
  Register #(.width(32), .trigger("rising"), .Select("low")) register_23 (
    .D(WB_IR), .en(or_2_out), .clk(CLK), .clr(RST), .cs(1'b0), .preset(1'b0));  // open: Q

  // Other names for the same wires on the sheet: IR21 = ID_IR[21]; ID_IR (some bits) = funct;
  //   opcode[4:0] = ID_IR[6:2]; MEM_PC[31:0] = M_PC

  // Notes on the sheet:
  //   中断源
  //   时空图监测，可删除
  //   中断等待指示
  //   PC+4
  //   数码管输出
  //   contents of Instruction_Memory (hex, n*v repeats v):
  //   ff100493 900533 2200893 73 148493 fe9068e3 900533 2200893 73 a00893 73
  //   PC Buffer Reg
  //   控制位
  //   流水调试日志用
  //   暂停节拍，不能为0
  //   PC
  //   IR
  //   Run
  //   CLK
  //   RST
  //   I-type command
  //   S-type command
  //   戳工具置1进入计数暂停模式，ctrl+k时钟自动运行到对应节拍暂停
  //   ctrl+k关闭时钟连续运行，将控制位置零，进入单步调试模式调试
  //   用这个时钟源需要去掉电路中的其他时钟源
  //   especailly for ecall
  //   B-type command
  //   J-type command
  //   IR21
  //   opcode
  //   funct
  //   可计数暂停的时钟源
  //   lh
  //   uret
  //   JALR
  //   JAL
  //   Bne
  //   Beq
  //   MemToReg
  //   MemWrite
  //   Alu_OP
  //   Alu_Src
  //   RegWrite
  //   S_Type
  //   ecall
  //   OpCode
  //   PC Buffer Reg
  //   R1
  //   R2
  //   Imm
  //   PC
  //   IR
  //   Run
  //   CLK
  //   RST
  //   为方便自动评测，需要输出流水线各段保存的PC值，注意是PC不是PC+4，另外ID段寄存器写入信息，Mem段内存写入信息也要输出
  //   lh
  //   uret
  //   JALR
  //   JAL
  //   Bne
  //   Beq
  //   ecall
  //   Imm
  //   J
  //   B
  //   MemToReg
  //   MemWrite
  //   Alu_OP
  //   Alu_Src
  //   RegWrite
  //   S_Type
  //   R1
  //   especailly for ecall
  //   especailly for ecall
  //   write Address
  //   Beq
  //   Bne
  //   bltu
  //   R2
  //   Imm
  //   JALR Jumping
  //   B-Type Jumping
  //   SrcA
  //   SrcB
  //   Bne, Beq & bltu: func3 of 3 instructions is different
  //   with 000 for Beq, 001 for Bne and 110 for bltu, respectively
  //   B type jump
  //   J type jump
  //   Only JAL is J-type instruction
  //   PC Buffer Reg
  //   PC
  //   IR
  //   Run
  //   CLK
  //   RST
  //   lh
  //   uret
  //   JALR
  //   JAL
  //   Bne
  //   Beq
  //   ecall
  //   Result
  //   R2
  //   write Address
  //   MemToReg
  //   MemWrite
  //   Alu_OP
  //   Alu_Src
  //   RegWrite
  //   S_Type
  //   Data
  //   PC Buffer Reg
  //   PC
  //   IR
  //   Run
  //   CLK
  //   RST
  //   lh
  //   uret
  //   JALR
  //   JAL
  //   Bne
  //   Beq
  //   ecall
  //   Result
  //   Data
  //   write Address
  //   MemToReg
  //   MemWrite
  //   Alu_OP
  //   Alu_Src
  //   RegWrite
  //   S_Type
  //   WriteData
  //   PC Buffer Reg
endmodule

module \气泡流水线  (
  output RegWrite,
  output MemWrite,
  output [31:0] IF_PC,
  output [31:0] ID_PC,
  output [31:0] EX_PC,
  output [31:0] M_PC,
  output [31:0] WB_PC,
  output [31:0] RDin,
  output [31:0] MDin,
  output [31:0] LedData
);

  wire and_1_out, and_2_out, and_4_out, and_5_out, and_6_out, Branch, BranchClear, button_1_out, CLK,
       clock_1_out, comparator_2_eq, comparator_2_lt, Conflict, ConflictClear, d_ff_1_q, EX_B, ex_equal,
       EX_J, EX_JALR, ex_less, EX_RegWrite, Go, halt, IF_Alu_Src, IF_B, IF_I, IF_J, IF_S, IR1, IR2, IR3,
       MEM_RegWrite, mul_cmdclear_1_p17, mul_cmdclear_1_p18, mul_cmdclear_1_p20, mul_cmdclear_1_p21,
       mul_cmdclear_1_p22, mul_cmdclear_1_p23, mul_cmdclear_1_p24, mul_cmdclear_1_p26, mul_cmdclear_1_p28,
       mul_cmdclear_1_p29, mul_cmdclear_1_p30, mul_cmdreg_1_alu_src_2, mul_cmdreg_1_beq_2,
       mul_cmdreg_1_bltu_2, mul_cmdreg_1_bne_2, mul_cmdreg_1_ecall_2, mul_cmdreg_1_jal_2,
       mul_cmdreg_1_jalr_2, mul_cmdreg_1_lh_2, mul_cmdreg_1_memtoreg_2, mul_cmdreg_1_memwrite_2,
       mul_cmdreg_1_regwrite_2, mul_cmdreg_1_s_type_2, mul_cmdreg_1_uret_2, mul_cmdreg_2_alu_src_2,
       mul_cmdreg_2_beq_2, mul_cmdreg_2_bltu_2, mul_cmdreg_2_bne_2, mul_cmdreg_2_ecall_2, mul_cmdreg_2_jal_2,
       mul_cmdreg_2_jalr_2, mul_cmdreg_2_lh_2, mul_cmdreg_2_memtoreg_2, mul_cmdreg_2_s_type_2,
       mul_cmdreg_2_uret_2, mul_cmdreg_3_alu_src_2, mul_cmdreg_3_beq_2, mul_cmdreg_3_bltu_2,
       mul_cmdreg_3_bne_2, mul_cmdreg_3_ecall_2, mul_cmdreg_3_jal_2, mul_cmdreg_3_jalr_2, mul_cmdreg_3_lh_2,
       mul_cmdreg_3_memtoreg_2, mul_cmdreg_3_memwrite_2, mul_cmdreg_3_s_type_2, mul_cmdreg_3_uret_2,
       multiplexer_13_out, multiplexer_14_out, nand_1_out, not_1_out, not_2_out, or_1_out, or_2_out,
       or_3_out, or_4_out, or_5_out, or_6_out, or_7_out, or_8_out, or_9_out, RST, System, W1, W2, W3,
       \单周期硬布线控制器_1_beq , \单周期硬布线控制器_1_bltu , \单周期硬布线控制器_1_bne , \单周期硬布线控制器_1_ecall , \单周期硬布线控制器_1_jal ,
       \单周期硬布线控制器_1_jalr , \单周期硬布线控制器_1_lh , \单周期硬布线控制器_1_memtoreg , \单周期硬布线控制器_1_memwrite ,
       \单周期硬布线控制器_1_regwrite , \单周期硬布线控制器_1_s_type , \单周期硬布线控制器_1_uret ;
  wire [0:0] alu_1_result_2;
  wire [3:0] mul_cmdclear_1_p25, mul_cmdreg_1_alu_op_2, mul_cmdreg_2_alu_op_2, mul_cmdreg_3_alu_op_2,
       \单周期硬布线控制器_1_alu_op ;
  wire [4:0] EX_Reg, funct, MEM_Reg, multiplexer_5_out, multiplexer_6_out, multiplexer_11_out, register_21_q;
  wire [12:0] CNT_num;
  wire [15:0] \LoadUse次数 , \总周期数 , \插入气泡数 , \无条件分支数 , \条件分支成功数 ;
  wire [31:0] adder_1_out, adder_3_out, EX_IR, ID_IR, IF_IR, immvaluegen_1_imm, MEM_IR, multiplexer_1_out,
       multiplexer_2_out, multiplexer_7_out, multiplexer_8_out, multiplexer_9_out, multiplexer_10_out,
       multiplexer_12_out, multiplexer_15_out, multiplexer_16_out, multiplexer_17_out, multiplexer_18_out,
       multiplexer_20_out, offset, ram_1_data, regifile_1_r1, regifile_1_r2, register_1_q, register_2_q,
       register_5_q, register_6_q, register_8_q, register_14_q, register_19_q, register_20_q, register_22_q,
       register_23_q, shifter_1_out, WB_IR;
  wire [31:1] alu_1_result;

  Button \u_总复位  (.out(RST));
  Button _1 (.out(IR1));
  Button _2 (.out(IR2));
  Button _3 (.out(IR3));
  // Probe on \总周期数 
  // Probe on \总周期数 
  Button \u_继续运行  (.out(Go));
  LED #(.active("true")) led_1 (.in(W1));
  LED #(.active("true")) led_2 (.in(W2));
  LED #(.active("true")) led_3 (.in(W3));
  Adder #(.width(32)) adder_1 (.a(IF_PC), .b(32'h4), .out(adder_1_out), .cin(1'b0));  // open: cout
  Hex_Digit_Display hex_digit_display_1 (.value(LedData[31:28]));  // open: dp
  // Probe on IF_PC[19:0]
  // RiscV_Probe riscv_probe_1: pin names not known; wires that end beside it: IF_IR
  Button button_1 (.out(button_1_out));
  Multiplexer #(.select(1), .width(32), .disabled("Z"), .enable("false")) multiplexer_1 (
    .in0(adder_1_out), .in1(offset), .out(multiplexer_1_out), .sel(Branch));
  Hex_Digit_Display hex_digit_display_2 (.value(LedData[23:20]));  // open: dp
  Hex_Digit_Display hex_digit_display_3 (.value(LedData[27:24]));  // open: dp
  // Probe on ID_PC[19:0]
  // RiscV_Probe riscv_probe_2: pin names not known; wires that end beside it: {ID_IR[31], funct[4], ID_IR[29:26], funct[3], ID_IR[24:15], funct[2:0], ID_IR[11:0]}, button_1_out, halt
  Multiplexer #(.select(1), .width(32), .disabled("Z"), .enable("false")) multiplexer_2 (
    .in0(multiplexer_1_out), .in1(IF_PC), .out(multiplexer_2_out), .sel(Conflict));
  or or_1 (or_1_out, Go, not_1_out);
  not not_1 (not_1_out, halt);
  Hex_Digit_Display hex_digit_display_4 (.value(LedData[15:12]));  // open: dp
  Hex_Digit_Display hex_digit_display_5 (.value(LedData[19:16]));  // open: dp
  Register #(.width(32), .trigger("rising"), .Select("low")) PC (
    .D(multiplexer_2_out), .en(or_1_out), .Q(IF_PC), .clk(CLK), .clr(RST), .cs(1'b0), .preset(1'b0));
  Hex_Digit_Display hex_digit_display_6 (.value(LedData[11:8]));  // open: dp
  Hex_Digit_Display hex_digit_display_7 (.value(LedData[7:4]));  // open: dp
  // Probe on EX_PC[19:0]
  // RiscV_Probe riscv_probe_3: pin names not known; wires that end beside it: EX_IR
  Hex_Digit_Display hex_digit_display_8 (.value(LedData[3:0]));  // open: dp
  Comparator #(.width(16), .mode("twosComplement")) comparator_1 (.a(\总周期数 ), .b(16'h120));  // open: gt, eq, lt
  ROM #(.addrWidth(10), .dataWidth(32), .Select("high")) Instruction_Memory (
    .addr(IF_PC[11:2]), .data(IF_IR), .sel(1'b1));
  // Probe on \总周期数 
  // Probe on M_PC[19:0]
  // RiscV_Probe riscv_probe_4: pin names not known; wires that end beside it: halt, MEM_IR
  // Probe on \总周期数 
  // Probe on \无条件分支数 
  // Probe on \条件分支成功数 
  // Probe on \插入气泡数 
  // Probe on \LoadUse次数 
  // Probe on IF_PC[11:0]
  // Probe on WB_PC[19:0]
  // RiscV_Probe riscv_probe_5: pin names not known; wires that end beside it: WB_IR
  // Probe on ID_PC[11:0]
  // Probe on EX_PC[11:0]
  Register #(.width(32), .trigger("rising"), .Select("low")) register_1 (
    .D(IF_PC), .en(or_1_out), .Q(register_1_q), .clk(CLK), .clr(or_2_out));
  Register #(.width(32), .trigger("rising"), .Select("low")) register_2 (
    .D(IF_IR), .en(or_1_out), .Q(register_2_q), .clk(CLK), .clr(or_2_out));
  or or_2 (or_2_out, RST, and_1_out);
  and and_1 (and_1_out, BranchClear, Branch);
  // Probe on M_PC[11:0]
  D_Flip_Flop #(.trigger("high"), .Pre_Clr_Positions("LEGACY"), .NegatePresetClear("false"), .enable("true"), .NewFFLayout("false")) d_ff_1 (.Q(d_ff_1_q));  // open: clk, D, Qn, preset, en, reset
  // Probe on 13'hc
  // Probe on WB_PC[11:0]
  Comparator #(.width(13), .mode("twosComplement")) comparator_2 (
    .a(CNT_num), .b(13'hc), .eq(comparator_2_eq), .lt(comparator_2_lt));  // open: gt
  Clock #(.highDuration(1), .lowDuration(1)) clock_1 (.out(clock_1_out));
  DataConflict dataconflict_1 (
    .Alu_Src(IF_Alu_Src), .rs(multiplexer_5_out), .rt(multiplexer_6_out), .EX_Reg(EX_Reg), .MEM_Reg(MEM_Reg),
    .EX_RegWrite(EX_RegWrite), .MEM_RegWrite(MEM_RegWrite), .hazzard(Conflict));
  nand nand_1 (nand_1_out, d_ff_1_q, comparator_2_eq);
  Counter #(.width(13), .max('h1fff), .ongoal("stay"), .trigger("rising"), .behavior("old")) counter_1 (
    .count(comparator_2_lt), .Q(CNT_num), .clk(clock_1_out));  // open: load, D, carry, clr, preset
  Multiplexer #(.select(1), .width(32), .disabled("Z"), .enable("false")) multiplexer_3 (
    .in0(register_1_q), .in1(ID_PC), .out(ID_PC), .sel(ConflictClear));
  Multiplexer #(.select(1), .width(32), .disabled("Z"), .enable("false")) multiplexer_4 (
    .in0(register_2_q),
    .in1({ID_IR[31], funct[4], ID_IR[29:26], funct[3], ID_IR[24:15], funct[2:0], ID_IR[11:0]}),
    .out({ID_IR[31], funct[4], ID_IR[29:26], funct[3], ID_IR[24:15], funct[2:0], ID_IR[11:0]}),
    .sel(ConflictClear));
  Multiplexer #(.select(1), .width(5), .disabled("Z"), .enable("false")) multiplexer_5 (
    .in0(ID_IR[19:15]), .in1(5'b01010), .out(multiplexer_5_out), .sel(\单周期硬布线控制器_1_ecall ));
  Multiplexer #(.select(1), .width(5), .disabled("Z"), .enable("false")) multiplexer_6 (
    .in0(ID_IR[24:20]), .in1(5'b10001), .out(multiplexer_6_out), .sel(\单周期硬布线控制器_1_ecall ));
  assign CLK = nand_1_out ? clock_1_out : 1'bz;  // Controlled_Buffer controlled_buffer_1
  \单周期硬布线控制器  \u_单周期硬布线控制器_1  (
    .Funct(funct), .OP(ID_IR[6:2]), .ALU_OP(\单周期硬布线控制器_1_alu_op ), .MemToReg(\单周期硬布线控制器_1_memtoreg ),
    .bltu(\单周期硬布线控制器_1_bltu ), .ecall(\单周期硬布线控制器_1_ecall ), .in_3(ID_IR[21]), .uret(\单周期硬布线控制器_1_uret ),
    .MemWrite(\单周期硬布线控制器_1_memwrite ), .lh(\单周期硬布线控制器_1_lh ), .BEQ(\单周期硬布线控制器_1_beq ),
    .S_Type(\单周期硬布线控制器_1_s_type ), .RegWrite(\单周期硬布线控制器_1_regwrite ), .ALU_SRC(IF_Alu_Src),
    .BNE(\单周期硬布线控制器_1_bne ), .JALR(\单周期硬布线控制器_1_jalr ), .JAL(\单周期硬布线控制器_1_jal ));  // open: CSR, lw
  ImmValueGen immvaluegen_1 (
    .Imm(immvaluegen_1_imm), .Type_I_Imm({ID_IR[31], funct[4], ID_IR[29:26], funct[3], ID_IR[24:20]}),
    .Type_S_Imm({ID_IR[31], funct[4], ID_IR[29:26], funct[3], ID_IR[11:7]}),
    .Type_B_Imm({ID_IR[31], ID_IR[7], funct[4], ID_IR[29:26], funct[3], ID_IR[11:8]}),
    .Type_J_Imm({ID_IR[31], ID_IR[19:15], funct[2:0], ID_IR[20], funct[4], ID_IR[29:26], funct[3], ID_IR[24:21]}),
    .Op6(ID_IR[6]), .I(IF_I), .Op5(ID_IR[5]), .S(IF_S), .Op4(ID_IR[4]), .B(IF_B), .Op3(ID_IR[3]), .J(IF_J),
    .Op2(ID_IR[2]), .System(System));
  Pull_Resistor #(.pull(1)) pull_resistor_1 (.node(CLK));
  Multiplexer #(.select(1), .width(32), .disabled("Z"), .enable("false")) multiplexer_7 (
    .in0(ID_PC), .in1({32{1'b0}}), .out(multiplexer_7_out), .sel(Conflict));
  Multiplexer #(.select(1), .width(32), .disabled("Z"), .enable("false")) multiplexer_8 (
    .in0({ID_IR[31], funct[4], ID_IR[29:26], funct[3], ID_IR[24:15], funct[2:0], ID_IR[11:0]}),
    .in1({32{1'b0}}), .out(multiplexer_8_out), .sel(Conflict));
  Regifile regifile_1 (
    .Din(RDin), .Clk(CLK), .R1(regifile_1_r1), .R2(regifile_1_r2), .WE(RegWrite), .W_num(register_21_q),
    .R1_num(multiplexer_5_out), .R2_num(multiplexer_6_out));
  Register #(.width(32), .trigger("rising"), .Select("low")) register_3 (
    .D(multiplexer_7_out), .en(or_1_out), .Q(EX_PC), .clk(CLK), .clr(or_3_out));
  Register #(.width(32), .trigger("rising"), .Select("low")) register_4 (
    .D(multiplexer_8_out), .en(or_1_out), .Q(EX_IR), .clk(CLK), .clr(or_3_out));
  or or_3 (or_3_out, BranchClear, RST);
  D_Flip_Flop #(.trigger("rising"), .Pre_Clr_Positions("ABOVE_BELOW"), .NegatePresetClear("false"), .enable("false"), .NewFFLayout("true")) d_ff_2 (
    .clk(CLK), .D(Branch), .Q(BranchClear), .preset(1'b0), .reset(1'b0));  // open: Qn
  D_Flip_Flop #(.trigger("rising"), .Pre_Clr_Positions("ABOVE_BELOW"), .NegatePresetClear("false"), .enable("false"), .NewFFLayout("true")) d_ff_3 (
    .clk(CLK), .D(Conflict), .Q(ConflictClear), .preset(1'b0), .reset(1'b0));  // open: Qn
  Multiplexer #(.select(1), .width(32), .disabled("Z"), .enable("false")) multiplexer_9 (
    .in0(regifile_1_r1), .in1({32{1'b0}}), .out(multiplexer_9_out), .sel(Conflict));
  Multiplexer #(.select(1), .width(32), .disabled("Z"), .enable("false")) multiplexer_10 (
    .in0(regifile_1_r2), .in1({32{1'b0}}), .out(multiplexer_10_out), .sel(Conflict));
  Multiplexer #(.select(1), .width(5), .disabled("Z"), .enable("false")) multiplexer_11 (
    .in0(ID_IR[11:7]), .in1({5{1'b0}}), .out(multiplexer_11_out), .sel(Conflict));
  Multiplexer #(.select(1), .width(32), .disabled("Z"), .enable("false")) multiplexer_12 (
    .in0(immvaluegen_1_imm), .in1({32{1'b0}}), .out(multiplexer_12_out), .sel(Conflict));
  Multiplexer #(.select(1), .width(1), .disabled("Z"), .enable("false")) multiplexer_13 (
    .in0(IF_J), .in1(1'b0), .out(multiplexer_13_out), .sel(Conflict));
  Multiplexer #(.select(1), .width(1), .disabled("Z"), .enable("false")) multiplexer_14 (
    .in0(IF_B), .in1(1'b0), .out(multiplexer_14_out), .sel(Conflict));
  Mul_cmdReg mul_cmdreg_1 (
    .lh(\单周期硬布线控制器_1_lh ), .Bne(\单周期硬布线控制器_1_bne ), .Alu_OP(\单周期硬布线控制器_1_alu_op ), .uret(\单周期硬布线控制器_1_uret ),
    .Beq(\单周期硬布线控制器_1_beq ), .Alu_Src(IF_Alu_Src), .JALR(\单周期硬布线控制器_1_jalr ),
    .MemToReg(\单周期硬布线控制器_1_memtoreg ), .RegWrite(\单周期硬布线控制器_1_regwrite ), .JAL(\单周期硬布线控制器_1_jal ),
    .MemWrite(\单周期硬布线控制器_1_memwrite ), .S_Type(\单周期硬布线控制器_1_s_type ), .ecall(\单周期硬布线控制器_1_ecall ), .CLK(CLK),
    .lh_2(mul_cmdreg_1_lh_2), .Bne_2(mul_cmdreg_1_bne_2), .Alu_OP_2(mul_cmdreg_1_alu_op_2),
    .uret_2(mul_cmdreg_1_uret_2), .Beq_2(mul_cmdreg_1_beq_2), .Alu_Src_2(mul_cmdreg_1_alu_src_2),
    .JALR_2(mul_cmdreg_1_jalr_2), .MemToReg_2(mul_cmdreg_1_memtoreg_2), .RegWrite_2(mul_cmdreg_1_regwrite_2),
    .JAL_2(mul_cmdreg_1_jal_2), .MemWrite_2(mul_cmdreg_1_memwrite_2), .S_Type_2(mul_cmdreg_1_s_type_2),
    .ecall_2(mul_cmdreg_1_ecall_2), .RST(RST), .bltu(\单周期硬布线控制器_1_bltu ), .bltu_2(mul_cmdreg_1_bltu_2));  // open: lw_2, lw, CSR_2, CSR
  Register #(.width(32), .trigger("rising"), .Select("low")) register_5 (
    .D(multiplexer_9_out), .Q(register_5_q), .clk(CLK), .clr(or_3_out));  // open: en
  Register #(.width(32), .trigger("rising"), .Select("low")) register_6 (
    .D(multiplexer_10_out), .Q(register_6_q), .clk(CLK), .clr(or_3_out));  // open: en
  Register #(.width(5), .trigger("rising"), .Select("low")) register_7 (
    .D(multiplexer_11_out), .Q(EX_Reg), .clk(CLK), .clr(or_3_out));  // open: en
  Register #(.width(32), .trigger("rising"), .Select("low")) register_8 (
    .D(multiplexer_12_out), .Q(register_8_q), .clk(CLK), .clr(or_3_out));  // open: en
  Register #(.width(1), .trigger("rising"), .Select("low")) register_9 (
    .D(multiplexer_13_out), .Q(EX_J), .clk(CLK), .clr(or_3_out));  // open: en
  Register #(.width(1), .trigger("rising"), .Select("low")) register_10 (
    .D(multiplexer_14_out), .Q(EX_B), .clk(CLK), .clr(or_3_out));  // open: en
  or or_4 (or_4_out, RST, BranchClear);
  // Mul_cmdClear mul_cmdclear_1: pin names not known; wires that end beside it: mul_cmdreg_1_lh_2, mul_cmdreg_1_uret_2, mul_cmdreg_1_jalr_2, mul_cmdreg_1_jal_2, mul_cmdreg_1_bne_2, mul_cmdreg_1_beq_2, mul_cmdreg_1_memtoreg_2, mul_cmdreg_1_memwrite_2, mul_cmdreg_1_alu_op_2, mul_cmdreg_1_alu_src_2, mul_cmdreg_1_regwrite_2, mul_cmdreg_1_bltu_2, mul_cmdreg_1_s_type_2, mul_cmdreg_1_ecall_2, or_4_out, ConflictClear, mul_cmdclear_1_p17, mul_cmdclear_1_p18, EX_JALR, mul_cmdclear_1_p20, mul_cmdclear_1_p21, mul_cmdclear_1_p22, mul_cmdclear_1_p23, mul_cmdclear_1_p24, mul_cmdclear_1_p25, mul_cmdclear_1_p26, EX_RegWrite, mul_cmdclear_1_p28, mul_cmdclear_1_p29, mul_cmdclear_1_p30
  and and_2 (and_2_out, mul_cmdclear_1_p30, ex_equal);
  and and_3 (halt, mul_cmdclear_1_p30, ~ex_equal);  // AND_Gate
  Shifter #(.width(32), .shift("ll")) shifter_1 (.in(register_8_q), .\dist (5'b00001), .out(shifter_1_out));
  and and_4 (and_4_out, ex_equal, mul_cmdclear_1_p22);
  and and_5 (and_5_out, ~ex_equal, mul_cmdclear_1_p21);  // AND_Gate
  and and_6 (and_6_out, mul_cmdclear_1_p28, ex_less);
  Multiplexer #(.select(1), .width(32), .disabled("Z"), .enable("false")) multiplexer_15 (
    .in0(register_5_q), .in1(32'h22), .out(multiplexer_15_out), .sel(mul_cmdclear_1_p30));
  Register #(.width(32), .trigger("rising"), .Select("low")) register_11 (
    .D(register_5_q), .en(and_2_out), .Q(LedData), .clk(CLK), .clr(or_3_out));
  or or_5 (or_5_out, and_4_out, and_5_out, and_6_out);
  Multiplexer #(.select(1), .width(32), .disabled("Z"), .enable("false")) multiplexer_16 (
    .in0(register_6_q), .in1(register_8_q), .out(multiplexer_16_out), .sel(mul_cmdclear_1_p26));
  Multiplexer #(.select(1), .width(32), .disabled("Z"), .enable("false")) multiplexer_17 (
    .in0({alu_1_result, 1'b0}), .in1(shifter_1_out), .out(multiplexer_17_out), .sel(or_6_out));
  Multiplexer #(.select(1), .width(32), .disabled("Z"), .enable("false")) multiplexer_18 (
    .in0(EX_PC), .in1({32{1'b0}}), .out(multiplexer_18_out), .sel(EX_JALR));
  or or_6 (or_6_out, EX_B, mul_cmdclear_1_p20);
  ALU alu_1 (
    .X(multiplexer_15_out), .Y(multiplexer_16_out), .AluOP(mul_cmdclear_1_p25), .Equal(ex_equal),
    .Result({alu_1_result, alu_1_result_2[0]}), .out_6(ex_less));  // open: Result_2, out_4
  Adder #(.width(32)) adder_2 (.a(multiplexer_17_out), .b(multiplexer_18_out), .out(offset), .cin(1'b0));  // open: cout
  or or_7 (or_7_out, or_5_out, EX_JALR, EX_J);
  Register #(.width(32), .trigger("rising"), .Select("low")) register_12 (
    .D(EX_PC), .en(or_1_out), .Q(M_PC), .clk(CLK), .clr(RST));
  Register #(.width(32), .trigger("rising"), .Select("low")) register_13 (
    .D(EX_IR), .en(or_1_out), .Q(MEM_IR), .clk(CLK), .clr(RST));
  Multiplexer #(.select(1), .width(1), .disabled("Z"), .enable("false")) multiplexer_19 (
    .in0(or_7_out), .in1(1'b0), .out(Branch), .sel(Conflict));
  Mul_cmdReg mul_cmdreg_2 (
    .lh(mul_cmdclear_1_p17), .Bne(mul_cmdclear_1_p21), .Alu_OP(mul_cmdclear_1_p25),
    .uret(mul_cmdclear_1_p18), .Beq(mul_cmdclear_1_p22), .Alu_Src(mul_cmdclear_1_p26), .JALR(EX_JALR),
    .MemToReg(mul_cmdclear_1_p23), .RegWrite(EX_RegWrite), .JAL(mul_cmdclear_1_p20),
    .MemWrite(mul_cmdclear_1_p24), .S_Type(mul_cmdclear_1_p29), .ecall(mul_cmdclear_1_p30), .CLK(CLK),
    .lh_2(mul_cmdreg_2_lh_2), .Bne_2(mul_cmdreg_2_bne_2), .Alu_OP_2(mul_cmdreg_2_alu_op_2),
    .uret_2(mul_cmdreg_2_uret_2), .Beq_2(mul_cmdreg_2_beq_2), .Alu_Src_2(mul_cmdreg_2_alu_src_2),
    .JALR_2(mul_cmdreg_2_jalr_2), .MemToReg_2(mul_cmdreg_2_memtoreg_2), .RegWrite_2(MEM_RegWrite),
    .JAL_2(mul_cmdreg_2_jal_2), .MemWrite_2(MemWrite), .S_Type_2(mul_cmdreg_2_s_type_2),
    .ecall_2(mul_cmdreg_2_ecall_2), .RST(RST), .bltu(mul_cmdclear_1_p28), .bltu_2(mul_cmdreg_2_bltu_2));  // open: lw_2, lw, CSR_2, CSR
  Register #(.width(32), .trigger("rising"), .Select("low")) register_14 (
    .D({alu_1_result, alu_1_result_2[0]}), .en(1'b1), .Q(register_14_q), .clk(CLK), .clr(RST), .cs(1'b0),
    .preset(1'b0));
  Register #(.width(32), .trigger("rising"), .Select("low")) register_15 (
    .D(register_6_q), .en(1'b1), .Q(MDin), .clk(CLK), .clr(RST), .cs(1'b0), .preset(1'b0));
  Register #(.width(5), .trigger("rising"), .Select("low")) register_16 (
    .D(EX_Reg), .en(1'b1), .Q(MEM_Reg), .clk(CLK), .clr(RST), .cs(1'b0), .preset(1'b0));
  RAM #(.addrWidth(10), .dataWidth(32), .bus("separate"), .Select("high")) ram_1 (
    .addr(register_14_q[11:2]), .din(MDin), .data(ram_1_data), .str(MemWrite), .sel(1'b1), .clk(CLK),
    .ld(1'b1), .clr(RST));
  Register #(.width(32), .trigger("rising"), .Select("low")) register_17 (
    .D(M_PC), .en(or_1_out), .Q(WB_PC), .clk(CLK), .clr(RST));
  Register #(.width(32), .trigger("rising"), .Select("low")) register_18 (
    .D(MEM_IR), .en(or_1_out), .Q(WB_IR), .clk(CLK), .clr(RST));
  Mul_cmdReg mul_cmdreg_3 (
    .lh(mul_cmdreg_2_lh_2), .Bne(mul_cmdreg_2_bne_2), .Alu_OP(mul_cmdreg_2_alu_op_2),
    .uret(mul_cmdreg_2_uret_2), .Beq(mul_cmdreg_2_beq_2), .Alu_Src(mul_cmdreg_2_alu_src_2),
    .JALR(mul_cmdreg_2_jalr_2), .MemToReg(mul_cmdreg_2_memtoreg_2), .RegWrite(MEM_RegWrite),
    .JAL(mul_cmdreg_2_jal_2), .MemWrite(MemWrite), .S_Type(mul_cmdreg_2_s_type_2),
    .ecall(mul_cmdreg_2_ecall_2), .CLK(CLK), .lh_2(mul_cmdreg_3_lh_2), .Bne_2(mul_cmdreg_3_bne_2),
    .Alu_OP_2(mul_cmdreg_3_alu_op_2), .uret_2(mul_cmdreg_3_uret_2), .Beq_2(mul_cmdreg_3_beq_2),
    .Alu_Src_2(mul_cmdreg_3_alu_src_2), .JALR_2(mul_cmdreg_3_jalr_2), .MemToReg_2(mul_cmdreg_3_memtoreg_2),
    .RegWrite_2(RegWrite), .JAL_2(mul_cmdreg_3_jal_2), .MemWrite_2(mul_cmdreg_3_memwrite_2),
    .S_Type_2(mul_cmdreg_3_s_type_2), .ecall_2(mul_cmdreg_3_ecall_2), .RST(RST), .bltu(mul_cmdreg_2_bltu_2),
    .bltu_2(mul_cmdreg_3_bltu_2));  // open: lw_2, lw, CSR_2, CSR
  Register #(.width(32), .trigger("rising"), .Select("low")) register_19 (
    .D(register_14_q), .en(1'b1), .Q(register_19_q), .clk(CLK), .clr(RST), .cs(1'b0), .preset(1'b0));
  Register #(.width(32), .trigger("rising"), .Select("low")) register_20 (
    .D(ram_1_data), .en(1'b1), .Q(register_20_q), .clk(CLK), .clr(RST), .cs(1'b0), .preset(1'b0));
  Register #(.width(5), .trigger("rising"), .Select("low")) register_21 (
    .D(MEM_Reg), .en(1'b1), .Q(register_21_q), .clk(CLK), .clr(RST), .cs(1'b0), .preset(1'b0));
  Multiplexer #(.select(1), .width(32), .disabled("Z"), .enable("false")) multiplexer_20 (
    .in0(register_19_q), .in1(register_20_q), .out(multiplexer_20_out), .sel(mul_cmdreg_3_memtoreg_2));
  Adder #(.width(32)) adder_3 (.a(WB_PC), .b(32'h4), .out(adder_3_out));  // open: cin, cout
  Multiplexer #(.select(1), .width(32), .disabled("Z"), .enable("false")) multiplexer_21 (
    .in0(multiplexer_20_out), .in1(adder_3_out), .out(RDin), .sel(or_8_out));
  or or_8 (or_8_out, mul_cmdreg_3_jal_2, mul_cmdreg_3_jalr_2, mul_cmdreg_3_uret_2);
  Register #(.width(32), .trigger("rising"), .Select("low")) register_22 (
    .D(WB_PC), .en(or_1_out), .Q(register_22_q), .clk(CLK), .clr(RST));
  Register #(.width(32), .trigger("rising"), .Select("low")) register_23 (
    .D(WB_IR), .en(or_1_out), .Q(register_23_q), .clk(CLK), .clr(RST));
  or or_9 (or_9_out, Go, not_2_out);
  not not_2 (not_2_out, halt);
  Counter #(.width(16), .max('hffff), .ongoal("wrap"), .trigger("rising"), .behavior("new")) counter_2 (
    .D({16{1'b0}}), .count(or_9_out), .Q(\总周期数 ), .clk(CLK), .clr(RST));  // open: load, carry, preset, down

  // Other names for the same wires on the sheet: IR21 = ID_IR[21]; ID_IR (some bits) = funct;
  //   opcode[4:0] = ID_IR[6:2]; MEM_PC[31:0] = M_PC

  // Notes on the sheet:
  //   中断源
  //   时空图监测，可删除
  //   中断等待指示
  //   PC+4
  //   数码管输出
  //   contents of Instruction_Memory (hex, n*v repeats v):
  //   100493 100006f 100493 200913 300993 100006f 100493 200913 300993 100006f 100493 200913 300993
  //   100006f 100493 200913 300993 29c000ef 100413 100493 1f49493 900533 2200893 73 24d493 48463 fedff06f
  //   900533 2200893 73 100493 249493 900533 2200893 73 48463 fedff06f 100493 1f49493 900533 2200893 73
  //   4034d493 900533 2200893 73 4044d493 900533 2200893 73 4044d493 900533 2200893 73 4044d493 900533
  //   2200893 73 4044d493 900533 2200893 73 4044d493 900533 2200893 73 4044d493 900533 2200893 73 4044d493
  //   900533 2200893 73 100413 1f41993 41f9d993 433 c00913 300b13 140413 f47413 800293 100313 499993
  //   89e9b3 1300533 2200893 73 406282b3 fe0294e3 140413 f00f93 1f47433 1c41413 800293 100313 49d993
  //   89e9b3 1300533 2200893 73 406282b3 fe0294e3 1c45413 406b0b33 b0463 f95ff06f 2b3 fff2c293 829293
  //   ff2e293 500533 2200893 73 fff00413 493 84a023 140413 448493 84a023 140413 448493 84a023 140413
  //   448493 84a023 140413 448493 84a023 140413 448493 84a023 140413 448493 84a023 140413 448493 84a023
  //   140413 448493 84a023 140413 448493 84a023 140413 448493 84a023 140413 448493 84a023 140413 448493
  //   84a023 140413 448493 84a023 140413 448493 84a023 140413 448493 84a023 140413 448493 140413 433
  //   3c00493 42983 4aa03 149a2b3 28663 134a023 1442023 ffc48493 fe9412e3 800533 2200893 73 440413 3c00493
  //   fc9416e3 a00893 73 413 140413 800533 2200893 73 240413 800533 2200893 73 340413 800533 2200893 73
  //   440413 800533 2200893 73 540413 800533 2200893 73 640413 800533 2200893 73 740413 800533 2200893 73
  //   840413 800533 2200893 2200893 73 8067
  //   PC Buffer Reg
  //   控制位
  //   流水调试日志用
  //   暂停节拍，不能为0
  //   PC
  //   IR
  //   ConflictClear
  //   Run
  //   CLK
  //   RST
  //   especailly for ecall
  //   I-type command
  //   S-type command
  //   B-type command
  //   J-type command
  //   Data Conflict Hazzard
  //   IR21
  //   opcode
  //   funct
  //   OpCode
  //   ecall
  //   可计数暂停的时钟源
  //   lh
  //   uret
  //   JALR
  //   JAL
  //   Bne
  //   Beq
  //   MemToReg
  //   MemWrite
  //   Alu_OP
  //   Alu_Src
  //   RegWrite
  //   S_Type
  //   ecall
  //   R1
  //   R2
  //   Imm
  //   Jump-cmd Clear
  //   PC Buffer Reg
  //   PC
  //   IR
  //   Run
  //   CLK
  //   RST
  //   为方便自动评测，需要输出流水线各段保存的PC值，注意是PC不是PC+4，另外ID段寄存器写入信息，Mem段内存写入信息也要输出
  //   conflict
  //   J
  //   B
  //   lh
  //   uret
  //   JALR
  //   JAL
  //   Bne
  //   Beq
  //   MemWrite
  //   Alu_OP
  //   Alu_Src
  //   RegWrite
  //   bltu
  //   S_Type
  //   ecall
  //   R1
  //   especailly for ecall
  //   especailly for ecall
  //   write Address
  //   Imm
  //   Beq
  //   Bne
  //   bltu
  //   MemToReg
  //   R2
  //   Imm
  //   JALR Jumping
  //   B-Type Jumping
  //   Bne
  //   Beq
  //   bltu
  //   SrcA
  //   SrcB
  //   Bne, Beq & bltu: func3 of 3 instructions is different
  //   with 000 for Beq, 001 for Bne and 110 for bltu, respectively
  //   B type jump
  //   J type jump
  //   Only JAL is J-type instruction
  //   PC Buffer Reg
  //   PC
  //   IR
  //   Run
  //   CLK
  //   RST
  //   conflict
  //   Result
  //   R2
  //   write Address
  //   lh
  //   uret
  //   JALR
  //   JAL
  //   Bne
  //   Beq
  //   MemWrite
  //   Alu_OP
  //   Alu_Src
  //   RegWrite
  //   S_Type
  //   ecall
  //   In EX part, only branch would need to clear
  //   MemToReg
  //   Data
  //   PC Buffer Reg
  //   PC
  //   IR
  //   conflict
  //   Run
  //   CLK
  //   RST
  //   lh
  //   uret
  //   JAL
  //   Bne
  //   Beq
  //   Result
  //   Data
  //   write Address
  //   JALR
  //   MemToReg
  //   MemWrite
  //   Alu_OP
  //   Alu_Src
  //   RegWrite
  //   S_Type
  //   ecall
  //   WriteData
  //   set $rd while jumping
  //   PC Buffer Reg
endmodule
module \重定向流水线  (
  output RegWrite,
  output MemWrite,
  output [31:0] IF_PC,
  output [31:0] ID_PC,
  output [31:0] EX_PC,
  output [31:0] M_PC,
  output [31:0] WB_PC,
  output [31:0] RDin,
  output [31:0] MDin,
  output [31:0] LedData
);

  wire and_1_out, and_2_out, and_3_out, and_4_out, and_5_out, Branch, button_1_out, CLK, clock_1_out,
       comparator_1_eq, comparator_2_eq, comparator_2_lt, Conflict, d_ff_1_q, EX_B, EX_Beq, EX_bltu, EX_Bne,
       EX_ecall, ex_equal, EX_J, EX_JAL, EX_JALR, ex_less, EX_MemToReg, EX_RegWrite, Go, Halt, halt_t,
       IF_Alu_Src, IF_B, IF_I, IF_J, IF_S, IF_S_Type, IR1, IR2, IR3, LoadConflict, MEM_RegWrite,
       mul_cmdclear_1_alu_src_2, mul_cmdclear_1_beq_2, mul_cmdclear_1_bltu_2, mul_cmdclear_1_bne_2,
       mul_cmdclear_1_csr_2, mul_cmdclear_1_ecall_2, mul_cmdclear_1_jal_2, mul_cmdclear_1_jalr_2,
       mul_cmdclear_1_lh_2, mul_cmdclear_1_lw_2, mul_cmdclear_1_memtoreg_2, mul_cmdclear_1_memwrite_2,
       mul_cmdclear_1_regwrite_2, mul_cmdclear_1_s_type_2, mul_cmdclear_1_uret_2, mul_cmdreg_1_alu_src_2,
       mul_cmdreg_1_lh_2, mul_cmdreg_1_lw_2, mul_cmdreg_1_memwrite_2, mul_cmdreg_1_s_type_2,
       mul_cmdreg_1_uret_2, mul_cmdreg_2_alu_src_2, mul_cmdreg_2_beq_2, mul_cmdreg_2_bltu_2,
       mul_cmdreg_2_bne_2, mul_cmdreg_2_ecall_2, mul_cmdreg_2_jal_2, mul_cmdreg_2_jalr_2, mul_cmdreg_2_lh_2,
       mul_cmdreg_2_lw_2, mul_cmdreg_2_memtoreg_2, mul_cmdreg_2_s_type_2, mul_cmdreg_2_uret_2,
       mul_cmdreg_3_alu_src_2, mul_cmdreg_3_beq_2, mul_cmdreg_3_bltu_2, mul_cmdreg_3_bne_2,
       mul_cmdreg_3_ecall_2, mul_cmdreg_3_jal_2, mul_cmdreg_3_jalr_2, mul_cmdreg_3_lh_2, mul_cmdreg_3_lw_2,
       mul_cmdreg_3_memtoreg_2, mul_cmdreg_3_memwrite_2, mul_cmdreg_3_s_type_2, mul_cmdreg_3_uret_2,
       multiplexer_9_out, multiplexer_10_out, nand_1_out, not_1_out, not_2_out, not_3_out, not_4_out,
       or_1_out, or_2_out, or_3_out, or_4_out, or_5_out, or_6_out, or_7_out, or_8_out, or_9_out, or_10_out,
       or_11_out, RST, System, W1, W2, W3, \单周期硬布线控制器_1_p1 , \单周期硬布线控制器_1_p2 , \单周期硬布线控制器_1_p3 ,
       \单周期硬布线控制器_1_p4 , \单周期硬布线控制器_1_p5 , \单周期硬布线控制器_1_p9 , \单周期硬布线控制器_1_p11 , \单周期硬布线控制器_1_p12 ,
       \单周期硬布线控制器_1_p13 , \单周期硬布线控制器_1_p14 , \单周期硬布线控制器_1_p17 , \单周期硬布线控制器_1_p18 ;
  wire [0:0] alu_1_result_2;
  wire [1:0] redirectionconflict_1_rsfoward, redirectionconflict_1_rtfoward, RsFoward, RtFoward;
  wire [3:0] mul_cmdclear_1_alu_op_2, mul_cmdreg_1_alu_op_2, mul_cmdreg_2_alu_op_2, mul_cmdreg_3_alu_op_2,
       \单周期硬布线控制器_1_p15 ;
  wire [4:0] ex_mem_wd_cmdreg_2_c_5_2, EX_Reg, funct, MEM_Reg, multiplexer_7_out, Rs, Rt;
  wire [12:0] CNT_num;
  wire [15:0] \LoadUse次数 , multiplexer_18_out, \总周期数 , \插入气泡数 , \无条件分支数 , \条件分支成功数 ;
  wire [31:0] adder_1_out, adder_3_out, bit_extender_1_out, EX_IR, ex_mem_wd_cmdreg_1_a_32_2,
       ex_mem_wd_cmdreg_2_a_32_2, ex_mem_wd_cmdreg_2_b_32_2, ID_IR, if_ex_cmdreg_1_imm_2,
       if_ex_cmdreg_1_r1_2, if_ex_cmdreg_1_r2_2, IF_IR, immvaluegen_1_imm, MEM_IR, multiplexer_1_out,
       multiplexer_2_out, multiplexer_5_out, multiplexer_6_out, multiplexer_8_out, multiplexer_11_out,
       multiplexer_12_out, multiplexer_13_out, multiplexer_14_out, multiplexer_15_out, multiplexer_16_out,
       multiplexer_17_out, multiplexer_19_out, multiplexer_20_out, offset, pc_ir_cmdreg_1_ir_2,
       pc_ir_cmdreg_1_pc_2, ram_1_data, regifile_1_r1, regifile_1_r2, shifter_1_out, WB_IR;
  wire [31:1] alu_1_result;

  Button \u_总复位  (.out(RST));
  Button _1 (.out(IR1));
  Button _2 (.out(IR2));
  Button _3 (.out(IR3));
  // Probe on \总周期数 
  // Probe on \总周期数 
  Button \u_继续运行  (.out(Go));
  LED #(.active("true")) led_1 (.in(W1));
  LED #(.active("true")) led_2 (.in(W2));
  LED #(.active("true")) led_3 (.in(W3));
  Adder #(.width(32)) adder_1 (.a(IF_PC), .b(32'h4), .out(adder_1_out));  // open: cin, cout
  Hex_Digit_Display hex_digit_display_1 (.value(LedData[31:28]));  // open: dp
  // Probe on IF_PC[19:0]
  // RiscV_Probe riscv_probe_1: pin names not known; wires that end beside it: IF_IR
  Button button_1 (.out(button_1_out));
  Multiplexer #(.select(1), .width(32), .disabled("Z"), .enable("false")) multiplexer_1 (
    .in0(adder_1_out), .in1(offset), .out(multiplexer_1_out), .sel(Branch));
  Hex_Digit_Display hex_digit_display_2 (.value(LedData[27:24]));  // open: dp
  Hex_Digit_Display hex_digit_display_3 (.value(LedData[23:20]));  // open: dp
  // Probe on ID_PC[19:0]
  // RiscV_Probe riscv_probe_2: pin names not known; wires that end beside it: {ID_IR[31], funct[4], ID_IR[29:26], funct[3], ID_IR[24:15], funct[2:0], ID_IR[11:0]}, button_1_out, halt_t
  Multiplexer #(.select(1), .width(32), .disabled("Z"), .enable("false")) multiplexer_2 (
    .in0(multiplexer_1_out), .in1(IF_PC), .out(multiplexer_2_out), .sel(LoadConflict));
  Hex_Digit_Display hex_digit_display_4 (.value(LedData[15:12]));  // open: dp
  Hex_Digit_Display hex_digit_display_5 (.value(LedData[19:16]));  // open: dp
  Hex_Digit_Display hex_digit_display_6 (.value(LedData[7:4]));  // open: dp
  Hex_Digit_Display hex_digit_display_7 (.value(LedData[11:8]));  // open: dp
  // Probe on EX_PC[19:0]
  // RiscV_Probe riscv_probe_3: pin names not known; wires that end beside it: EX_IR
  Hex_Digit_Display hex_digit_display_8 (.value(LedData[3:0]));  // open: dp
  Comparator #(.width(16), .mode("twosComplement")) comparator_1 (
    .a(\总周期数 ), .b(16'h1b0), .eq(comparator_1_eq));  // open: gt, lt
  Register #(.width(32), .trigger("rising"), .Select("low")) PC (
    .D(multiplexer_2_out), .en(or_1_out), .Q(IF_PC), .clk(CLK), .clr(RST));
  or or_1 (or_1_out, Go, not_1_out);
  not not_1 (not_1_out, halt_t);
  // Probe on \总周期数 
  // Probe on M_PC[19:0]
  // RiscV_Probe riscv_probe_4: pin names not known; wires that end beside it: comparator_1_eq, halt_t, MEM_IR
  // Probe on \总周期数 
  // Probe on \无条件分支数 
  // Probe on \条件分支成功数 
  // Probe on \插入气泡数 
  // Probe on \LoadUse次数 
  // Probe on IF_PC[11:0]
  // Probe on WB_PC[19:0]
  // RiscV_Probe riscv_probe_5: pin names not known; wires that end beside it: WB_IR
  ROM #(.addrWidth(10), .dataWidth(32), .Select("high")) Instruction_Memory (
    .addr(IF_PC[11:2]), .data(IF_IR), .sel(1'b1));
  // Probe on ID_PC[11:0]
  // Probe on EX_PC[11:0]
  PC_IR_cmdReg pc_ir_cmdreg_1 (
    .PC(IF_PC), .IR(IF_IR), .PC_2(pc_ir_cmdreg_1_pc_2), .IR_2(pc_ir_cmdreg_1_ir_2), .Run(or_1_out),
    .CLK(CLK), .Clear(RST), .AsyClear(Branch));
  // Probe on M_PC[11:0]
  D_Flip_Flop #(.trigger("high"), .Pre_Clr_Positions("LEGACY"), .NegatePresetClear("false"), .enable("true"), .NewFFLayout("false")) d_ff_1 (.Q(d_ff_1_q));  // open: clk, D, Qn, preset, en, reset
  // Probe on 13'hc
  // Probe on WB_PC[11:0]
  Comparator #(.width(13), .mode("twosComplement")) comparator_2 (
    .a(CNT_num), .b(13'hc), .eq(comparator_2_eq), .lt(comparator_2_lt));  // open: gt
  Clock #(.highDuration(1), .lowDuration(1)) clock_1 (.out(clock_1_out));
  DataConflict dataconflict_1 (
    .Alu_Src(IF_Alu_Src), .rs(Rs), .rt(Rt), .EX_Reg(EX_Reg), .MEM_Reg(MEM_Reg), .EX_RegWrite(EX_RegWrite),
    .MEM_RegWrite(MEM_RegWrite), .hazzard(Conflict));
  nand nand_1 (nand_1_out, d_ff_1_q, comparator_2_eq);
  Counter #(.width(13), .max('h1fff), .ongoal("stay"), .trigger("rising"), .behavior("old")) counter_1 (
    .count(comparator_2_lt), .Q(CNT_num), .clk(clock_1_out));  // open: load, D, carry, clr, preset
  LoadConflictProcessorUnit loadconflictprocessorunit_1 (
    .PC(pc_ir_cmdreg_1_pc_2), .IR(pc_ir_cmdreg_1_ir_2), .PC_2(ID_PC),
    .IR_2({ID_IR[31], funct[4], ID_IR[29:26], funct[3], ID_IR[24:15], funct[2:0], ID_IR[11:0]}),
    .Conflict(LoadConflict), .CLK(CLK));
  Multiplexer #(.select(1), .width(5), .disabled("Z"), .enable("false")) multiplexer_3 (
    .in0(ID_IR[19:15]), .in1(5'b01010), .out(Rs), .sel(\单周期硬布线控制器_1_p9 ));
  Multiplexer #(.select(1), .width(5), .disabled("Z"), .enable("false")) multiplexer_4 (
    .in0(ID_IR[24:20]), .in1(5'b10001), .out(Rt), .sel(\单周期硬布线控制器_1_p9 ));
  assign CLK = nand_1_out ? clock_1_out : 1'bz;  // Controlled_Buffer controlled_buffer_1
  // 单周期硬布线控制器 单周期硬布线控制器_1: pin names not known; wires that end beside it: \单周期硬布线控制器_1_p1 , \单周期硬布线控制器_1_p2 , \单周期硬布线控制器_1_p3 , \单周期硬布线控制器_1_p4 , \单周期硬布线控制器_1_p5 , ID_IR[21], ID_IR[6:2], funct, \单周期硬布线控制器_1_p9 , halt_t, \单周期硬布线控制器_1_p11 , \单周期硬布线控制器_1_p12 , \单周期硬布线控制器_1_p13 , \单周期硬布线控制器_1_p14 , \单周期硬布线控制器_1_p15 , IF_Alu_Src, \单周期硬布线控制器_1_p17 , \单周期硬布线控制器_1_p18 , IF_S_Type
  ImmValueGen immvaluegen_1 (
    .Imm(immvaluegen_1_imm), .Type_I_Imm({ID_IR[31], funct[4], ID_IR[29:26], funct[3], ID_IR[24:20]}),
    .Type_S_Imm({ID_IR[31], funct[4], ID_IR[29:26], funct[3], ID_IR[11:7]}),
    .Type_B_Imm({ID_IR[31], ID_IR[7], funct[4], ID_IR[29:26], funct[3], ID_IR[11:8]}),
    .Type_J_Imm({ID_IR[31], ID_IR[19:15], funct[2:0], ID_IR[20], funct[4], ID_IR[29:26], funct[3], ID_IR[24:21]}),
    .Op6(ID_IR[6]), .I(IF_I), .Op5(ID_IR[5]), .S(IF_S), .Op4(ID_IR[4]), .B(IF_B), .Op3(ID_IR[3]), .J(IF_J),
    .Op2(ID_IR[2]), .System(System));
  Pull_Resistor #(.pull(1)) pull_resistor_1 (.node(CLK));
  Regifile regifile_1 (
    .Din(RDin), .Clk(CLK), .R1(regifile_1_r1), .R2(regifile_1_r2), .WE(RegWrite),
    .W_num(ex_mem_wd_cmdreg_2_c_5_2), .R1_num(Rs), .R2_num(Rt));
  or or_2 (or_2_out, Go, not_2_out);
  not not_2 (not_2_out, halt_t);
  PC_IR_cmdReg pc_ir_cmdreg_2 (
    .PC(ID_PC), .IR({ID_IR[31], funct[4], ID_IR[29:26], funct[3], ID_IR[24:15], funct[2:0], ID_IR[11:0]}),
    .PC_2(EX_PC), .IR_2(EX_IR), .Run(or_1_out), .CLK(CLK), .Clear(RST), .AsyClear(or_4_out));
  or or_3 (or_3_out, Branch, RST);
  Counter #(.width(16), .max('hffff), .ongoal("wrap"), .trigger("rising"), .behavior("new")) counter_2 (
    .D({16{1'b0}}), .count(or_2_out), .Q(\总周期数 ), .clk(CLK), .clr(RST));  // open: load, carry, preset, down
  Multiplexer #(.select(1), .width(32), .disabled("Z"), .enable("false")) multiplexer_5 (
    .in0(regifile_1_r1), .in1({32{1'b0}}), .out(multiplexer_5_out), .sel(LoadConflict));
  Multiplexer #(.select(1), .width(32), .disabled("Z"), .enable("false")) multiplexer_6 (
    .in0(regifile_1_r2), .in1({32{1'b0}}), .out(multiplexer_6_out), .sel(LoadConflict));
  Multiplexer #(.select(1), .width(5), .disabled("Z"), .enable("false")) multiplexer_7 (
    .in0(ID_IR[11:7]), .in1({5{1'b0}}), .out(multiplexer_7_out), .sel(LoadConflict));
  Multiplexer #(.select(1), .width(32), .disabled("Z"), .enable("false")) multiplexer_8 (
    .in0(immvaluegen_1_imm), .in1({32{1'b0}}), .out(multiplexer_8_out), .sel(LoadConflict));
  Multiplexer #(.select(1), .width(1), .disabled("Z"), .enable("false")) multiplexer_9 (
    .in0(IF_J), .in1(1'b0), .out(multiplexer_9_out), .sel(LoadConflict));
  Multiplexer #(.select(1), .width(1), .disabled("Z"), .enable("false")) multiplexer_10 (
    .in0(IF_B), .in1(1'b0), .out(multiplexer_10_out), .sel(LoadConflict));
  or or_4 (or_4_out, RST, LoadConflict, Branch);
  Mul_cmdClear mul_cmdclear_1 (
    .Clear(or_4_out), .lh(\单周期硬布线控制器_1_p4 ), .uret(\单周期硬布线控制器_1_p3 ), .JALR(\单周期硬布线控制器_1_p2 ),
    .JAL(\单周期硬布线控制器_1_p1 ), .Bne(\单周期硬布线控制器_1_p11 ), .Beq(\单周期硬布线控制器_1_p12 ), .MemToReg(\单周期硬布线控制器_1_p13 ),
    .MemWrite(\单周期硬布线控制器_1_p14 ), .Alu_OP(\单周期硬布线控制器_1_p15 ), .Alu_Src(IF_Alu_Src),
    .RegWrite(\单周期硬布线控制器_1_p17 ), .S_Type(IF_S_Type), .ecall(\单周期硬布线控制器_1_p9 ), .lh_2(mul_cmdclear_1_lh_2),
    .uret_2(mul_cmdclear_1_uret_2), .JALR_2(mul_cmdclear_1_jalr_2), .JAL_2(mul_cmdclear_1_jal_2),
    .Bne_2(mul_cmdclear_1_bne_2), .Beq_2(mul_cmdclear_1_beq_2), .MemToReg_2(mul_cmdclear_1_memtoreg_2),
    .MemWrite_2(mul_cmdclear_1_memwrite_2), .Alu_OP_2(mul_cmdclear_1_alu_op_2),
    .Alu_Src_2(mul_cmdclear_1_alu_src_2), .RegWrite_2(mul_cmdclear_1_regwrite_2),
    .S_Type_2(mul_cmdclear_1_s_type_2), .ecall_2(mul_cmdclear_1_ecall_2), .bltu(\单周期硬布线控制器_1_p18 ),
    .bltu_2(mul_cmdclear_1_bltu_2), .lw(\单周期硬布线控制器_1_p5 ), .lw_2(mul_cmdclear_1_lw_2),
    .CSR_2(mul_cmdclear_1_csr_2));  // open: CSR
  Mul_cmdReg mul_cmdreg_1 (
    .lh(mul_cmdclear_1_lh_2), .Bne(mul_cmdclear_1_bne_2), .Alu_OP(mul_cmdclear_1_alu_op_2),
    .uret(mul_cmdclear_1_uret_2), .Beq(mul_cmdclear_1_beq_2), .Alu_Src(mul_cmdclear_1_alu_src_2),
    .JALR(mul_cmdclear_1_jalr_2), .MemToReg(mul_cmdclear_1_memtoreg_2), .RegWrite(mul_cmdclear_1_regwrite_2),
    .JAL(mul_cmdclear_1_jal_2), .MemWrite(mul_cmdclear_1_memwrite_2), .S_Type(mul_cmdclear_1_s_type_2),
    .ecall(mul_cmdclear_1_ecall_2), .CLK(CLK), .lh_2(mul_cmdreg_1_lh_2), .Bne_2(EX_Bne),
    .Alu_OP_2(mul_cmdreg_1_alu_op_2), .uret_2(mul_cmdreg_1_uret_2), .Beq_2(EX_Beq),
    .Alu_Src_2(mul_cmdreg_1_alu_src_2), .JALR_2(EX_JALR), .MemToReg_2(EX_MemToReg), .RegWrite_2(EX_RegWrite),
    .JAL_2(EX_JAL), .MemWrite_2(mul_cmdreg_1_memwrite_2), .S_Type_2(mul_cmdreg_1_s_type_2),
    .ecall_2(EX_ecall), .RST(RST), .bltu(mul_cmdclear_1_bltu_2), .bltu_2(EX_bltu), .lw_2(mul_cmdreg_1_lw_2),
    .lw(mul_cmdclear_1_lw_2), .CSR(mul_cmdclear_1_csr_2));  // open: CSR_2
  IF_EX_cmdReg if_ex_cmdreg_1 (
    .R1(multiplexer_5_out), .R2(multiplexer_6_out), .writeAddr(multiplexer_7_out), .Imm(multiplexer_8_out),
    .J(multiplexer_9_out), .B(multiplexer_10_out), .R1_2(if_ex_cmdreg_1_r1_2), .R2_2(if_ex_cmdreg_1_r2_2),
    .writeAddr_2(EX_Reg), .Imm_2(if_ex_cmdreg_1_imm_2), .J_2(EX_J), .B_2(EX_B), .CLK(CLK), .Clear(or_3_out));
  and and_1 (and_1_out, EX_ecall, ~ex_equal);  // AND_Gate
  Shifter #(.width(32), .shift("ll")) shifter_1 (.in(if_ex_cmdreg_1_imm_2), .\dist (5'b00001), .out(shifter_1_out));
  and and_2 (and_2_out, ex_equal, EX_Beq);
  and and_3 (and_3_out, ~ex_equal, EX_Bne);  // AND_Gate
  and and_4 (and_4_out, EX_bltu, ex_less);
  D_Flip_Flop #(.trigger("falling"), .Pre_Clr_Positions("ABOVE_BELOW"), .NegatePresetClear("false"), .enable("false"), .NewFFLayout("false")) d_ff_2 (
    .clk(CLK), .D(and_1_out), .Q(Halt));  // open: Qn, preset, reset
  and and_5 (and_5_out, EX_ecall, ex_equal);
  or or_5 (or_5_out, and_2_out, and_3_out, and_4_out);
  Multiplexer #(.select(2), .width(32), .disabled("Z"), .enable("false")) multiplexer_11 (
    .in0(if_ex_cmdreg_1_r1_2), .in1(RDin), .in2(ex_mem_wd_cmdreg_1_a_32_2), .in3(ex_mem_wd_cmdreg_1_a_32_2),
    .out(multiplexer_11_out), .sel(RsFoward));
  Multiplexer #(.select(2), .width(32), .disabled("Z"), .enable("false")) multiplexer_12 (
    .in0(if_ex_cmdreg_1_r2_2), .in1(RDin), .in2(ex_mem_wd_cmdreg_1_a_32_2), .in3(ex_mem_wd_cmdreg_1_a_32_2),
    .out(multiplexer_12_out), .sel(RtFoward));
  Multiplexer #(.select(1), .width(32), .disabled("Z"), .enable("false")) multiplexer_13 (
    .in0({alu_1_result, 1'b0}), .in1(shifter_1_out), .out(multiplexer_13_out), .sel(or_6_out));
  Multiplexer #(.select(1), .width(32), .disabled("Z"), .enable("false")) multiplexer_14 (
    .in0(EX_PC), .in1({32{1'b0}}), .out(multiplexer_14_out), .sel(EX_JALR));
  or or_6 (or_6_out, EX_B, EX_JAL);
  Multiplexer #(.select(1), .width(32), .disabled("Z"), .enable("false")) multiplexer_15 (
    .in0(multiplexer_11_out), .in1(32'h22), .out(multiplexer_15_out), .sel(EX_ecall));
  Multiplexer #(.select(1), .width(32), .disabled("Z"), .enable("false")) multiplexer_16 (
    .in0(multiplexer_12_out), .in1(if_ex_cmdreg_1_imm_2), .out(multiplexer_16_out),
    .sel(mul_cmdreg_1_alu_src_2));
  Multiplexer #(.select(1), .width(32), .disabled("Z"), .enable("false")) multiplexer_17 (
    .in0(multiplexer_11_out), .in1({32{1'b0}}), .out(multiplexer_17_out), .sel(or_3_out));
  Register #(.width(32), .trigger("rising"), .Select("low")) register_1 (
    .D(multiplexer_17_out), .en(and_5_out), .Q(LedData), .clk(CLK));  // open: clr
  Adder #(.width(32)) adder_2 (.a(multiplexer_13_out), .b(multiplexer_14_out), .out(offset), .cin(1'b0));  // open: cout
  or or_7 (or_7_out, or_5_out, EX_JALR, EX_J);
  PC_IR_cmdReg pc_ir_cmdreg_3 (
    .PC(EX_PC), .IR(EX_IR), .PC_2(M_PC), .IR_2(MEM_IR), .Run(or_1_out), .CLK(CLK), .Clear(RST),
    .AsyClear(1'b0));
  ALU alu_1 (
    .X(multiplexer_15_out), .Y(multiplexer_16_out), .AluOP(mul_cmdreg_1_alu_op_2), .Equal(ex_equal),
    .Result({alu_1_result, alu_1_result_2[0]}), .out_6(ex_less));  // open: Result_2, out_4
  and and_6 (Branch, or_7_out, ~LoadConflict);  // AND_Gate
  Mul_cmdReg mul_cmdreg_2 (
    .lh(mul_cmdreg_1_lh_2), .Bne(EX_Bne), .Alu_OP(mul_cmdreg_1_alu_op_2), .uret(mul_cmdreg_1_uret_2),
    .Beq(EX_Beq), .Alu_Src(mul_cmdreg_1_alu_src_2), .JALR(EX_JALR), .MemToReg(EX_MemToReg),
    .RegWrite(EX_RegWrite), .JAL(EX_JAL), .MemWrite(mul_cmdreg_1_memwrite_2), .S_Type(mul_cmdreg_1_s_type_2),
    .ecall(EX_ecall), .CLK(CLK), .lh_2(mul_cmdreg_2_lh_2), .Bne_2(mul_cmdreg_2_bne_2),
    .Alu_OP_2(mul_cmdreg_2_alu_op_2), .uret_2(mul_cmdreg_2_uret_2), .Beq_2(mul_cmdreg_2_beq_2),
    .Alu_Src_2(mul_cmdreg_2_alu_src_2), .JALR_2(mul_cmdreg_2_jalr_2), .MemToReg_2(mul_cmdreg_2_memtoreg_2),
    .RegWrite_2(MEM_RegWrite), .JAL_2(mul_cmdreg_2_jal_2), .MemWrite_2(MemWrite),
    .S_Type_2(mul_cmdreg_2_s_type_2), .ecall_2(mul_cmdreg_2_ecall_2), .RST(RST), .bltu(EX_bltu),
    .bltu_2(mul_cmdreg_2_bltu_2), .lw_2(mul_cmdreg_2_lw_2), .lw(mul_cmdreg_1_lw_2));  // open: CSR_2, CSR
  EX_MEM_WD_cmdReg ex_mem_wd_cmdreg_1 (
    .A_32({alu_1_result, alu_1_result_2[0]}), .B_32(multiplexer_12_out), .C_5(EX_Reg),
    .A_32_2(ex_mem_wd_cmdreg_1_a_32_2), .B_32_2(MDin), .C_5_2(MEM_Reg), .CLK(CLK), .Clear(RST));  // open: halt, halt_2
  LoadConflict loadconflict_1 (
    .Rt_Used(or_8_out), .Rs(Rs), .Rt(Rt), .EX_MemRead(EX_MemToReg), .EX_RegWrite(EX_Reg),
    .LoadUsed(LoadConflict));
  or or_8 (or_8_out, IF_S_Type, not_3_out);
  not not_3 (not_3_out, IF_Alu_Src);
  RAM #(.addrWidth(10), .dataWidth(32), .bus("separate"), .Select("high")) ram_1 (
    .addr(ex_mem_wd_cmdreg_1_a_32_2[11:2]), .din(MDin), .data(ram_1_data), .str(MemWrite), .sel(1'b1),
    .clk(CLK), .ld(1'b1), .clr(RST));
  // Probe on redirectionconflict_1_rsfoward
  // Probe on redirectionconflict_1_rtfoward
  RedirectionConflict redirectionconflict_1 (
    .Rt_Used(or_9_out), .RsFoward(redirectionconflict_1_rsfoward), .RtFoward(redirectionconflict_1_rtfoward),
    .EX_RegWrite(EX_RegWrite), .EX_Reg(EX_Reg), .MEM_RegWrite(MEM_RegWrite), .MEM_Reg(MEM_Reg), .Rs(Rs),
    .Rt(Rt));
  Multiplexer #(.select(1), .width(16), .disabled("Z"), .enable("false")) multiplexer_18 (
    .in0(ram_1_data[15:0]), .in1(ram_1_data[31:16]), .out(multiplexer_18_out),
    .sel(ex_mem_wd_cmdreg_1_a_32_2[1]));
  Register #(.width(2), .trigger("rising"), .Select("low")) register_2 (
    .D(redirectionconflict_1_rsfoward), .en(1'b1), .Q(RsFoward), .clk(CLK), .clr(1'b0), .cs(1'b0),
    .preset(1'b0));
  Register #(.width(2), .trigger("rising"), .Select("low")) register_3 (
    .D(redirectionconflict_1_rtfoward), .en(1'b1), .Q(RtFoward), .clk(CLK), .clr(1'b0), .cs(1'b0),
    .preset(1'b0));
  or or_9 (or_9_out, not_4_out, IF_S_Type);
  PC_IR_cmdReg pc_ir_cmdreg_4 (
    .PC(M_PC), .IR(MEM_IR), .PC_2(WB_PC), .IR_2(WB_IR), .Run(or_1_out), .CLK(CLK), .Clear(RST),
    .AsyClear(1'b0));
  assign bit_extender_1_out = {{16{multiplexer_18_out[15]}}, multiplexer_18_out};  // Bit_Extender bit_extender_1
  not not_4 (not_4_out, IF_Alu_Src);
  Multiplexer #(.select(1), .width(32), .disabled("Z"), .enable("false")) multiplexer_19 (
    .in0(ram_1_data), .in1(bit_extender_1_out), .out(multiplexer_19_out), .sel(mul_cmdreg_2_lh_2));
  Mul_cmdReg mul_cmdreg_3 (
    .lh(mul_cmdreg_2_lh_2), .Bne(mul_cmdreg_2_bne_2), .Alu_OP(mul_cmdreg_2_alu_op_2),
    .uret(mul_cmdreg_2_uret_2), .Beq(mul_cmdreg_2_beq_2), .Alu_Src(mul_cmdreg_2_alu_src_2),
    .JALR(mul_cmdreg_2_jalr_2), .MemToReg(mul_cmdreg_2_memtoreg_2), .RegWrite(MEM_RegWrite),
    .JAL(mul_cmdreg_2_jal_2), .MemWrite(MemWrite), .S_Type(mul_cmdreg_2_s_type_2),
    .ecall(mul_cmdreg_2_ecall_2), .CLK(CLK), .lh_2(mul_cmdreg_3_lh_2), .Bne_2(mul_cmdreg_3_bne_2),
    .Alu_OP_2(mul_cmdreg_3_alu_op_2), .uret_2(mul_cmdreg_3_uret_2), .Beq_2(mul_cmdreg_3_beq_2),
    .Alu_Src_2(mul_cmdreg_3_alu_src_2), .JALR_2(mul_cmdreg_3_jalr_2), .MemToReg_2(mul_cmdreg_3_memtoreg_2),
    .RegWrite_2(RegWrite), .JAL_2(mul_cmdreg_3_jal_2), .MemWrite_2(mul_cmdreg_3_memwrite_2),
    .S_Type_2(mul_cmdreg_3_s_type_2), .ecall_2(mul_cmdreg_3_ecall_2), .RST(RST), .bltu(mul_cmdreg_2_bltu_2),
    .bltu_2(mul_cmdreg_3_bltu_2), .lw_2(mul_cmdreg_3_lw_2), .lw(mul_cmdreg_2_lw_2));  // open: CSR_2, CSR
  EX_MEM_WD_cmdReg ex_mem_wd_cmdreg_2 (
    .A_32(ex_mem_wd_cmdreg_1_a_32_2), .B_32(multiplexer_19_out), .C_5(MEM_Reg),
    .A_32_2(ex_mem_wd_cmdreg_2_a_32_2), .B_32_2(ex_mem_wd_cmdreg_2_b_32_2), .C_5_2(ex_mem_wd_cmdreg_2_c_5_2),
    .CLK(CLK), .Clear(RST));  // open: halt, halt_2
  Multiplexer #(.select(1), .width(32), .disabled("Z"), .enable("false")) multiplexer_20 (
    .in0(ex_mem_wd_cmdreg_2_a_32_2), .in1(ex_mem_wd_cmdreg_2_b_32_2), .out(multiplexer_20_out),
    .sel(mul_cmdreg_3_memtoreg_2));
  or or_10 (or_10_out, Halt, halt_t);
  D_Flip_Flop #(.trigger("falling"), .Pre_Clr_Positions("ABOVE_BELOW"), .NegatePresetClear("false"), .enable("false"), .NewFFLayout("false")) d_ff_3 (
    .clk(CLK), .D(or_10_out), .Q(halt_t), .reset(Go));  // open: Qn, preset
  Adder #(.width(32)) adder_3 (.a(WB_PC), .b(32'h4), .out(adder_3_out));  // open: cin, cout
  or or_11 (or_11_out, mul_cmdreg_3_jal_2, mul_cmdreg_3_jalr_2, mul_cmdreg_3_uret_2);
  Multiplexer #(.select(1), .width(32), .disabled("Z"), .enable("false")) multiplexer_21 (
    .in0(multiplexer_20_out), .in1(adder_3_out), .out(RDin), .sel(or_11_out));

  // Other names for the same wires on the sheet: IR21 = ID_IR[21]; ID_IR (some bits) = funct;
  //   opcode[4:0] = ID_IR[6:2]; MEM_PC[31:0] = M_PC

  // Notes on the sheet:
  //   中断源
  //   时空图监测，可删除
  //   中断等待指示
  //   Branch select
  //   PC+4
  //   Keep address
  //   数码管输出
  //   contents of Instruction_Memory (hex, n*v repeats v):
  //   100493 100006f 100493 200913 300993 100006f 100493 200913 300993 100006f 100493 200913 300993
  //   100006f 100493 200913 300993 29c000ef 100413 100493 1f49493 900533 2200893 73 24d493 48463 fedff06f
  //   900533 2200893 73 100493 249493 900533 2200893 73 48463 fedff06f 100493 1f49493 900533 2200893 73
  //   4034d493 900533 2200893 73 4044d493 900533 2200893 73 4044d493 900533 2200893 73 4044d493 900533
  //   2200893 73 4044d493 900533 2200893 73 4044d493 900533 2200893 73 4044d493 900533 2200893 73 4044d493
  //   900533 2200893 73 100413 1f41993 41f9d993 433 c00913 300b13 140413 f47413 800293 100313 499993
  //   89e9b3 1300533 2200893 73 406282b3 fe0294e3 140413 f00f93 1f47433 1c41413 800293 100313 49d993
  //   89e9b3 1300533 2200893 73 406282b3 fe0294e3 1c45413 406b0b33 b0463 f95ff06f 2b3 fff2c293 829293
  //   ff2e293 500533 2200893 73 fff00413 493 84a023 140413 448493 84a023 140413 448493 84a023 140413
  //   448493 84a023 140413 448493 84a023 140413 448493 84a023 140413 448493 84a023 140413 448493 84a023
  //   140413 448493 84a023 140413 448493 84a023 140413 448493 84a023 140413 448493 84a023 140413 448493
  //   84a023 140413 448493 84a023 140413 448493 84a023 140413 448493 84a023 140413 448493 140413 433
  //   3c00493 42983 4aa03 149a2b3 28663 134a023 1442023 ffc48493 fe9412e3 800533 2200893 73 440413 3c00493
  //   fc9416e3 a00893 73 413 140413 800533 2200893 73 240413 800533 2200893 73 340413 800533 2200893 73
  //   440413 800533 2200893 73 540413 800533 2200893 73 640413 800533 2200893 73 740413 800533 2200893 73
  //   840413 800533 2200893 2200893 73 8067
  //   控制位
  //   流水调试日志用
  //   暂停节拍，不能为0
  //   PC
  //   IR
  //   Conflict
  //   Run
  //   CLK
  //   RST
  //   戳工具置1进入计数暂停模式，ctrl+k时钟自动运行到对应节拍暂停
  //   ctrl+k关闭时钟连续运行，将控制位置零，进入单步调试模式调试
  //   especailly for ecall
  //   I-type command
  //   S-type command
  //   B-type command
  //   J-type command
  //   Data Conflict Hazzard
  //   IR21
  //   opcode
  //   funct
  //   OpCode
  //   ecall
  //   可计数暂停的时钟源
  //   lw
  //   lh
  //   uret
  //   JALR
  //   JAL
  //   Bne
  //   Beq
  //   MemToReg
  //   MemWrite
  //   Alu_OP
  //   Alu_Src
  //   RegWrite
  //   bltu
  //   S_Type
  //   ecall
  //   R1
  //   R2
  //   Imm
  //   PC
  //   IR
  //   conflict
  //   Run
  //   CLK
  //   RST
  //   为方便自动评测，需要输出流水线各段保存的PC值，注意是PC不是PC+4，另外ID段寄存器写入信息，Mem段内存写入信息也要输出
  //   J
  //   B
  //   lw
  //   lh
  //   uret
  //   JALR
  //   JAL
  //   Bne
  //   Beq
  //   MemToReg
  //   MemWrite
  //   Alu_OP
  //   Alu_Src
  //   RegWrite
  //   bltu
  //   S_Type
  //   ecall
  //   R1
  //   R2
  //   especailly for ecall
  //   write Address
  //   Imm
  //   Beq
  //   Bne
  //   bltu
  //   JALR Jumping
  //   B-Type Jumping
  //   Imm
  //   Bne, Beq & bltu: func3 of 3 instructions is different
  //   with 000 for Beq, 001 for Bne and 110 for bltu, respectively
  //   B type jump
  //   SrcA
  //   SrcB
  //   J type jump
  //   Only JAL is J-type instruction
  //   PC
  //   IR
  //   Run
  //   CLK
  //   RST
  //   conflict
  //   lw
  //   lh
  //   uret
  //   JALR
  //   JAL
  //   Bne
  //   Beq
  //   MemToReg
  //   MemWrite
  //   Alu_OP
  //   Alu_Src
  //   RegWrite
  //   S_Type
  //   ecall
  //   Result
  //   R2
  //   write Address
  //   Conflict Judgement of lw & lh
  //   S-type cmd use rs&rt
  //   In EX part, only branch would need to clear
  //   Data
  //   PC
  //   IR
  //   conflict
  //   Run
  //   CLK
  //   RST
  //   lw
  //   lh
  //   uret
  //   JAL
  //   Bne
  //   Beq
  //   Result
  //   Data
  //   write Address
  //   JALR
  //   MemToReg
  //   MemWrite
  //   Alu_OP
  //   Alu_Src
  //   RegWrite
  //   S_Type
  //   ecall
  //   WriteData
  //   set $rd while jumping
endmodule

module \中断按键参考电路  (
  input  \同步清零信号 ,
  output \与中断屏蔽位与 
);

  wire \_1号中断_out , and_1_out, clock_1_out, d_ff_1_q, or_1_out, or_2_out;

  Clock #(.highDuration(1), .lowDuration(1)) clock_1 (.out(clock_1_out));
  Button \_1号中断  (.out(\_1号中断_out ));
  LED #(.active("true")) \_1号中断等待指示灯  (.in(or_1_out));
  or or_1 (or_1_out, \与中断屏蔽位与 , d_ff_1_q);
  D_Flip_Flop #(.trigger("rising"), .Pre_Clr_Positions("LEGACY"), .NegatePresetClear("false"), .enable("true"), .NewFFLayout("false")) d_ff_1 (
    .clk(\_1号中断_out ), .D(1'b1), .Q(d_ff_1_q), .reset(\与中断屏蔽位与 ));  // open: Qn, preset, en
  or or_2 (or_2_out, d_ff_1_q, \与中断屏蔽位与 );
  and and_1 (and_1_out, or_2_out, ~\同步清零信号 );  // AND_Gate
  D_Flip_Flop #(.trigger("rising"), .Pre_Clr_Positions("LEGACY"), .NegatePresetClear("false"), .enable("true"), .NewFFLayout("false")) IR1 (
    .clk(clock_1_out), .D(and_1_out), .Q(\与中断屏蔽位与 ));  // open: Qn, preset, en, reset

  // Notes on the sheet:
  //   中断信号采样参考电路
  //   Reset 
endmodule

module \单周期_单级中断  (
  input  IR1,
  input  IR2,
  input  IR3,
  output RegWrite,
  output MemWrite,
  output [31:0] PC,
  output [31:0] IR,
  output [31:0] RDin,
  output [31:0] MDin,
  output [31:0] LedData
);

  wire AluSrcB, and_1_out, and_2_out, and_3_out, and_5_out, and_6_out, and_7_out, and_8_out, and_9_out, B,
       Beq, Bne, Branch, CLK, clock_1_out, CLR1, CLR2, CLR3, comparator_1_eq, comparator_2_eq,
       comparator_3_eq, comparator_4_eq, comparator_5_eq, comparator_6_eq, comparator_6_lt, d_ff_1_q,
       d_ff_2_q, d_ff_3_q, d_ff_7_q, d_ff_8_q, ecall, equal, Go, halt, I, INTR, INTR1, INTR2, INTR3, IR1_t,
       IR2_t, IR3_t, IRA, IRB, IRC, J, JAL, JALR, less, lh, MemToReg, nand_1_out, not_1_out, or_4_out,
       or_5_out, or_6_out, or_7_out, or_8_out, or_11_out, or_12_out, or_14_out, or_15_out, or_16_out,
       pull_resistor_1_node, pull_resistor_2_node, pull_resistor_3_node, RST, S, S_Type, stop, System, URET,
       W1, W2, W3;
  wire [0:0] alu_1_result;
  wire [1:0] priority_encoder_1_out, priority_encoder_2_out, register_1_q;
  wire [3:0] AluOP;
  wire [4:0] multiplexer_4_out, multiplexer_5_out;
  wire [9:0] alu_1_result_3;
  wire [12:0] CNT_num;
  wire [15:0] \总周期数 ;
  wire [30:0] alu_1_result_2;
  wire [31:0] adder_1_out, adder_2_out, immvaluegen_1_imm, INTR_PC, multiplexer_2_out, multiplexer_3_out,
       multiplexer_7_out, multiplexer_8_out, multiplexer_9_out, Orig_PC, ram_1_data,
       regfile_for_single_unit_1_r1, shifter_1_out;

  Button \u_继续运行  (.out(Go));
  Button _1 (.out(IRA));
  Button _2 (.out(IRB));
  Button _3 (.out(IRC));
  or or_1 (W1, INTR1, d_ff_1_q);
  or or_2 (W2, INTR2, d_ff_2_q);
  or or_3 (W3, INTR3, d_ff_3_q);
  LED #(.active("true")) led_1 (.in(W1));
  LED #(.active("true")) led_2 (.in(W2));
  LED #(.active("true")) led_3 (.in(W3));
  or or_4 (or_4_out, Go, not_1_out);
  not not_1 (not_1_out, halt);
  Counter #(.width(16), .max('hffff), .ongoal("wrap"), .trigger("rising"), .behavior("new")) counter_1 (
    .D({16{1'b0}}), .count(or_4_out), .Q(\总周期数 ), .clk(CLK), .clr(RST));  // open: load, carry, preset, down
  D_Flip_Flop #(.trigger("rising"), .Pre_Clr_Positions("LEGACY"), .NegatePresetClear("false"), .enable("true"), .NewFFLayout("false")) d_ff_1 (
    .clk(IRA), .D(1'b1), .Q(d_ff_1_q), .reset(INTR1));  // open: Qn, preset, en
  D_Flip_Flop #(.trigger("rising"), .Pre_Clr_Positions("LEGACY"), .NegatePresetClear("false"), .enable("true"), .NewFFLayout("false")) d_ff_2 (
    .clk(IRB), .D(1'b1), .Q(d_ff_2_q), .reset(INTR2));  // open: Qn, preset, en
  D_Flip_Flop #(.trigger("rising"), .Pre_Clr_Positions("LEGACY"), .NegatePresetClear("false"), .enable("true"), .NewFFLayout("false")) d_ff_3 (
    .clk(IRC), .D(1'b1), .Q(d_ff_3_q), .reset(INTR3));  // open: Qn, preset, en
  Hex_Digit_Display hex_digit_display_1 (.value(LedData[31:28]));  // open: dp
  Comparator #(.width(16), .mode("twosComplement")) comparator_1 (
    .a(16'h23b), .b(\总周期数 ), .eq(comparator_1_eq));  // open: gt, lt
  Comparator #(.width(16), .mode("twosComplement")) comparator_2 (
    .a(\总周期数 ), .b(16'h1), .eq(comparator_2_eq));  // open: gt, lt
  Comparator #(.width(16), .mode("twosComplement")) comparator_3 (
    .a(\总周期数 ), .b(16'h4), .eq(comparator_3_eq));  // open: gt, lt
  Comparator #(.width(16), .mode("twosComplement")) comparator_4 (
    .a(\总周期数 ), .b(16'h7), .eq(comparator_4_eq));  // open: gt, lt
  or or_5 (or_5_out, d_ff_1_q, INTR1);
  or or_6 (or_6_out, d_ff_2_q, INTR2);
  or or_7 (or_7_out, d_ff_3_q, INTR3);
  Multiplexer #(.select(2), .width(32), .disabled("Z"), .enable("false")) multiplexer_1 (
    .in0(32'h30ac), .in1(32'h3150), .in2(32'h31f4), .out(INTR_PC), .sel(priority_encoder_1_out));  // open: in3
  Priority_Encoder #(.select(2), .disabled("Z")) priority_encoder_1 (
    .in0(INTR1), .in1(INTR2), .in2(INTR3), .out(priority_encoder_1_out));  // open: in3, gs, en_out, en_in
  Hex_Digit_Display hex_digit_display_2 (.value(LedData[27:24]));  // open: dp
  Hex_Digit_Display hex_digit_display_3 (.value(LedData[23:20]));  // open: dp
  Button button_1 (.out(halt));
  Button button_2 (.out(RST));
  or or_8 (or_8_out, comparator_1_eq, comparator_2_eq);
  Pull_Resistor #(.pull(0)) pull_resistor_1 (.node(pull_resistor_1_node));
  assign pull_resistor_1_node = or_8_out ? ~CLK : 1'bz;  // Controlled_Inverter controlled_inverter_1
  Pull_Resistor #(.pull(0)) pull_resistor_2 (.node(pull_resistor_2_node));
  assign pull_resistor_2_node = comparator_3_eq ? ~CLK : 1'bz;  // Controlled_Inverter controlled_inverter_2
  Pull_Resistor #(.pull(0)) pull_resistor_3 (.node(pull_resistor_3_node));
  assign pull_resistor_3_node = comparator_4_eq ? ~CLK : 1'bz;  // Controlled_Inverter controlled_inverter_3
  and and_1 (and_1_out, or_5_out, ~CLR1);  // AND_Gate
  and and_2 (and_2_out, or_6_out, ~CLR2);  // AND_Gate
  and and_3 (and_3_out, or_7_out, ~CLR3);  // AND_Gate
  Hex_Digit_Display hex_digit_display_4 (.value(LedData[19:16]));  // open: dp
  Hex_Digit_Display hex_digit_display_5 (.value(LedData[15:12]));  // open: dp
  Comparator #(.width(16), .mode("twosComplement")) comparator_5 (
    .a(\总周期数 ), .b(16'h340), .eq(comparator_5_eq));  // open: gt, lt
  D_Flip_Flop #(.trigger("rising"), .Pre_Clr_Positions("LEGACY"), .NegatePresetClear("false"), .enable("true"), .NewFFLayout("false")) d_ff_4 (
    .clk(CLK), .D(and_1_out), .Q(INTR1));  // open: Qn, preset, en, reset
  D_Flip_Flop #(.trigger("rising"), .Pre_Clr_Positions("LEGACY"), .NegatePresetClear("false"), .enable("true"), .NewFFLayout("false")) d_ff_5 (
    .clk(CLK), .D(and_2_out), .Q(INTR2));  // open: Qn, preset, en, reset
  D_Flip_Flop #(.trigger("rising"), .Pre_Clr_Positions("LEGACY"), .NegatePresetClear("false"), .enable("true"), .NewFFLayout("false")) d_ff_6 (
    .clk(CLK), .D(and_3_out), .Q(INTR3));  // open: Qn, preset, en, reset
  Register #(.width(2), .trigger("rising"), .Select("low")) register_1 (
    .D(priority_encoder_1_out), .en(INTR), .Q(register_1_q), .clk(CLK));  // open: clr
  Hex_Digit_Display hex_digit_display_6 (.value(LedData[11:8]));  // open: dp
  Hex_Digit_Display hex_digit_display_7 (.value(LedData[7:4]));  // open: dp
  // Probe on \总周期数 
  Demultiplexer #(.select(2), .width(1), .tristate("false"), .disabled("Z"), .enable("false")) demultiplexer_1 (
    .out0(CLR1), .out1(CLR2), .out2(CLR3), .in(URET), .sel(register_1_q));  // open: out3
  Hex_Digit_Display hex_digit_display_8 (.value(LedData[3:0]));  // open: dp
  // Probe on multiplexer_3_out
  // Probe on multiplexer_2_out
  Multiplexer #(.select(2), .width(32), .disabled("Z"), .enable("false")) multiplexer_2 (
    .in0(adder_1_out), .in1(adder_2_out),
    .in2({alu_1_result_2[30:11], alu_1_result_3, alu_1_result_2[0], 1'b0}), .out(multiplexer_2_out),
    .sel({JALR, Branch}));  // open: in3
  Adder #(.width(32)) adder_1 (.a(32'h4), .b(PC), .out(adder_1_out), .cin(1'b0));  // open: cout
  or or_9 (IR1_t, IR1, IRA);
  Priority_Encoder #(.select(2), .disabled("Z")) priority_encoder_2 (
    .in0(1'b1), .in1(INTR), .in2(URET), .out(priority_encoder_2_out));  // open: in3, gs, en_out, en_in
  Multiplexer #(.select(2), .width(32), .disabled("Z"), .enable("false")) multiplexer_3 (
    .in0(multiplexer_2_out), .in1(INTR_PC), .in2(Orig_PC), .out(multiplexer_3_out),
    .sel(priority_encoder_2_out));  // open: in3
  Register #(.width(32), .trigger("rising"), .Select("low")) register_2 (
    .D(multiplexer_2_out), .en(INTR), .Q(Orig_PC), .clk(CLK), .cs(1'b0), .preset(1'b0));  // open: clr
  or or_10 (IR2_t, IR2, IRB);
  or or_11 (or_11_out, Go, ~halt);  // OR_Gate
  or or_12 (or_12_out, INTR1, INTR2, INTR3);
  Register #(.width(32), .trigger("rising"), .Select("low")) u_PC (
    .D(multiplexer_3_out), .en(or_11_out), .Q(PC), .clk(CLK), .clr(RST), .cs(1'b0), .preset(1'b0));
  or or_13 (IR3_t, IR3, IRC);
  or or_14 (or_14_out, ~or_12_out, URET);  // OR_Gate
  // RiscV_Probe riscv_probe_1: pin names not known; wires that end beside it: IR
  D_Flip_Flop #(.trigger("rising"), .Pre_Clr_Positions("ABOVE_BELOW"), .NegatePresetClear("false"), .enable("false"), .NewFFLayout("true")) d_ff_7 (
    .clk(CLK), .D(or_14_out), .Q(d_ff_7_q));  // open: Qn, preset, reset
  and and_4 (INTR, d_ff_7_q, or_12_out);
  ROM #(.addrWidth(10), .dataWidth(32), .Select("high")) rom_1 (.addr(PC[11:2]), .data(IR), .sel(1'b1));
  Multiplexer #(.select(1), .width(5), .disabled("Z"), .enable("false")) multiplexer_4 (
    .in0(IR[19:15]), .in1(5'b01010), .out(multiplexer_4_out), .sel(ecall));
  Multiplexer #(.select(1), .width(5), .disabled("Z"), .enable("false")) multiplexer_5 (
    .in0(IR[24:20]), .in1(5'b10001), .out(multiplexer_5_out), .sel(ecall));
  \单周期硬布线控制器  \u_单周期硬布线控制器_1  (
    .Funct({IR[30], IR[25], IR[14:12]}), .OP(IR[6:2]), .ALU_OP(AluOP), .MemToReg(MemToReg), .ecall(ecall),
    .in_3(IR[21]), .uret(URET), .MemWrite(MemWrite), .lh(lh), .BEQ(Bne), .S_Type(S_Type),
    .RegWrite(RegWrite), .ALU_SRC(AluSrcB), .BNE(Beq), .JALR(JALR), .JAL(JAL));  // open: bltu, CSR, lw
  Multiplexer #(.select(1), .width(32), .disabled("Z"), .enable("false")) multiplexer_6 (
    .in0(multiplexer_9_out), .in1(adder_1_out), .out(RDin), .sel(or_15_out));
  RegFile_for_Single_Unit regfile_for_single_unit_1 (
    .Din(RDin), .Clk(CLK), .R1(regfile_for_single_unit_1_r1), .R2(MDin), .WE(RegWrite), .W_num(IR[11:7]),
    .R1_num(multiplexer_4_out), .R2_num(multiplexer_5_out));
  or or_15 (or_15_out, JALR, J);
  ImmValueGen immvaluegen_1 (
    .Imm(immvaluegen_1_imm), .Type_I_Imm(IR[31:20]), .Type_S_Imm({IR[31:25], IR[11:7]}),
    .Type_B_Imm({IR[31], IR[7], IR[30:25], IR[11:8]}), .Type_J_Imm({IR[31], IR[19:12], IR[20], IR[30:21]}),
    .Op6(IR[6]), .I(I), .Op5(IR[5]), .S(S), .Op4(IR[4]), .B(B), .Op3(IR[3]), .J(J), .Op2(IR[2]),
    .System(System));
  D_Flip_Flop #(.trigger("high"), .Pre_Clr_Positions("LEGACY"), .NegatePresetClear("false"), .enable("true"), .NewFFLayout("false")) d_ff_8 (.Q(d_ff_8_q));  // open: clk, D, Qn, preset, en, reset
  // Probe on 13'hc
  Comparator #(.width(13), .mode("twosComplement")) comparator_6 (
    .a(CNT_num), .b(13'hc), .eq(comparator_6_eq), .lt(comparator_6_lt));  // open: gt
  Clock #(.highDuration(1), .lowDuration(1)) clock_1 (.out(clock_1_out));
  Multiplexer #(.select(1), .width(32), .disabled("Z"), .enable("false")) multiplexer_7 (
    .in0(regfile_for_single_unit_1_r1), .in1(32'h22), .out(multiplexer_7_out), .sel(ecall));
  Multiplexer #(.select(1), .width(32), .disabled("Z"), .enable("false")) multiplexer_8 (
    .in0(MDin), .in1(immvaluegen_1_imm), .out(multiplexer_8_out), .sel(AluSrcB));
  // Probe on immvaluegen_1_imm
  Counter #(.width(13), .max('h1fff), .ongoal("stay"), .trigger("rising"), .behavior("old")) counter_2 (
    .count(comparator_6_lt), .Q(CNT_num), .clk(clock_1_out));  // open: load, D, carry, clr, preset
  and and_5 (and_5_out, equal, ecall);
  nand nand_1 (nand_1_out, d_ff_8_q, comparator_6_eq);
  Register #(.width(32), .trigger("rising"), .Select("low")) register_3 (
    .D(regfile_for_single_unit_1_r1), .en(and_5_out), .Q(LedData), .clk(CLK));  // open: clr
  ALU alu_1 (
    .X(multiplexer_7_out), .Y(multiplexer_8_out), .AluOP(AluOP), .Equal(equal),
    .Result({alu_1_result_2[30:11], alu_1_result_3, alu_1_result_2[0], alu_1_result[0]}), .out_6(less));  // open: Result_2, out_4
  and and_6 (and_6_out, equal, ~IR[12]);  // AND_Gate
  and and_7 (and_7_out, ~equal, IR[12]);  // AND_Gate
  and and_8 (and_8_out, IR[14], less);
  assign CLK = nand_1_out ? clock_1_out : 1'bz;  // Controlled_Buffer controlled_buffer_1
  Pull_Resistor #(.pull(1)) pull_resistor_4 (.node(CLK));
  Shifter #(.width(32), .shift("ll")) shifter_1 (.in(immvaluegen_1_imm), .\dist (5'b00001), .out(shifter_1_out));
  or or_16 (or_16_out, and_6_out, and_7_out, and_8_out);
  Adder #(.width(32)) adder_2 (.a(shifter_1_out), .b(PC), .out(adder_2_out), .cin(1'b0));  // open: cout
  and and_9 (and_9_out, B, or_16_out);
  RAM #(.addrWidth(10), .dataWidth(32), .bus("separate"), .Select("high")) ram_1 (
    .addr(alu_1_result_3), .din(MDin), .data(ram_1_data), .str(MemWrite), .sel(1'b1), .clk(CLK), .ld(1'b1),
    .clr(RST));
  and and_10 (stop, ~equal, ecall);  // AND_Gate
  Multiplexer #(.select(1), .width(32), .disabled("Z"), .enable("false")) multiplexer_9 (
    .in0({alu_1_result_2[30:11], alu_1_result_3, alu_1_result_2[0], alu_1_result[0]}), .in1(ram_1_data),
    .out(multiplexer_9_out), .sel(MemToReg));
  or or_17 (Branch, and_9_out, J);

  // Other names for the same wires on the sheet: funct[4:0] = {IR[30], IR[25], IR[14:12]}; opcode[4:0] = IR[6:2]

  // Notes on the sheet:
  //   中断源
  //   avoid repeat signal
  //   中断等待指示
  //   总复位信号应将除ROM以外所有存储组件全部清零
  //   单级中断测试信号模拟器
  //   No CLR request
  //   数码管输出
  //   Select Interrupt-cmd address while triggered
  //   数码管输出应该用寄存器锁存，否则显示数据只能一闪而过
  //   00: not jumping
  //   01: branch jumping, for bne, beq, jal & bltu
  //   10: for JALR jumping
  //   select corresponding CLR signal while excuting URET
  //   Store original address while interrupt happened
  //   Choose address about interrupt
  //   In the non-interrupt program, URET and 3 INTR/ are 0
  //   for JAL
  //   while INTR is true, the circuit should store the original address
  //   指令探针
  //   指令存储器
  //   2nd Or gate is used for distinguish the transform from normal process to interrupt process
  //   指令字
  //   contents of rom_1 (hex, n*v repeats v):
  //   7d000113 100413 1f41993 41f9d993 433 c00913 800b13 140413 f47413 800293 100313 499993 89e9b3 1300533
  //   2200893 73 406282b3 fe0294e3 140413 f00f93 1f47433 1c41413 800293 100313 49d993 89e9b3 1300533
  //   2200893 73 406282b3 fe0294e3 1c45413 406b0b33 b0463 f95ff06f 2b3 fff2c293 1029293 fff2e293 500533
  //   2200893 73 f5dff06f 1112023 410113 a12023 410113 812023 410113 1312023 410113 1412023 410113 1512023
  //   410113 1612023 410113 100b13 300a13 100a93 1600433 441413 14469b3 1300533 2200893 73 fe0416e3
  //   415a0a33 fe0a10e3 ffc10113 12b03 ffc10113 12a83 ffc10113 12a03 ffc10113 12983 ffc10113 12403
  //   ffc10113 12503 ffc10113 12883 200073 1112023 410113 a12023 410113 812023 410113 1312023 410113
  //   1412023 410113 1512023 410113 1612023 410113 200b13 300a13 100a93 1600433 441413 14469b3 1300533
  //   2200893 73 fe0416e3 415a0a33 fe0a10e3 ffc10113 12b03 ffc10113 12a83 ffc10113 12a03 ffc10113 12983
  //   ffc10113 12403 ffc10113 12503 ffc10113 12883 200073 1112023 410113 a12023 410113 812023 410113
  //   1312023 410113 1412023 410113 1512023 410113 1612023 410113 300b13 300a13 100a93 1600433 441413
  //   14469b3 1300533 2200893 73 fe0416e3 415a0a33 fe0a10e3 ffc10113 12b03 ffc10113 12a83 ffc10113 12a03
  //   ffc10113 12983 ffc10113 12403 ffc10113 12503 ffc10113 12883 200073
  //   PC+4
  //   为方便自动评测，需要输出PC，IR，寄存器堆写如数据RDin
  //   I-type command
  //   S-type command
  //   B-type command
  //   J-type command
  //   RAM写使能MemWrite、RAM写入数据MDin等信号
  //   IR21
  //   OpCode
  //   funct
  //   for ecall
  //   OpCode
  //   控制位
  //   暂停节拍，不能为0
  //   $a0
  //   戳工具置1进入计数暂停模式，ctrl+k时钟自动运行到对应节拍暂停
  //   ctrl+k关闭时钟连续运行，将控制位置零，进入单步调试模式调试
  //   Update LedData using $a0
  //   Imm
  //   SrcA
  //   SrcB
  //   for B-type jumping
  //   可计数暂停的时钟源
  //   Bne, Beq & bltu: func3 of 3 instructions is different, with 000 for Beq, 001 for Bne and 110 for bltu, respectively
  //   Beq
  //   Bne
  //   bltu
  //   数据存储器
  //   for JALR jumping
  //   B type jump
  //   J type jump
  //   Only JAL is J-type instruction
  //   stop the program while equal is 0
endmodule

module \单周期_多级中断  (
  input  IR1,
  input  IR2,
  input  IR3,
  output RegWrite,
  output MemWrite,
  output [31:0] PC,
  output [31:0] IR,
  output [31:0] RDin,
  output [31:0] MDin,
  output [31:0] LedData
);

  wire AluSrcB, and_1_out, and_2_out, and_3_out, and_4_out, and_7_out, and_8_out, and_9_out, and_10_out,
       and_12_out, B, Beq, Bne, Branch, CLK, clock_1_out, CLR1, CLR2, CLR3, comparator_1_eq, comparator_2_eq,
       comparator_3_eq, comparator_4_eq, comparator_5_eq, comparator_6_eq, comparator_7_lt, comparator_8_eq,
       comparator_8_lt, controlled_inverter_1_out, controlled_inverter_2_out, controlled_inverter_3_out, CSR,
       CSRRCI, CSRRSI, d_ff_1_q, d_ff_2_q, d_ff_3_q, d_ff_7_q, d_ff_8_q, d_ff_9_q, ecall, equal, Go, halt, I,
       INTR, INTR1, INTR2, INTR3, IR1_t, IR2_t, IR3_t, IRA, IRB, IRC, J, JAL, JALR, less, lh, MemToReg,
       nand_1_out, not_1_out, or_4_out, or_5_out, or_6_out, or_7_out, or_8_out, or_9_out, or_10_out,
       or_12_out, or_14_out, or_15_out, or_17_out, or_18_out, or_20_out, RST, S, S_Type, System, URET, W1,
       W2, W3;
  wire [1:0] multiplexer_2_out, multiplexer_3_out, multiplexer_6_out, NOW_INTR, priority_encoder_1_out,
       priority_encoder_2_out, register_2_q, register_4_q;
  wire [3:0] AluOP;
  wire [4:0] multiplexer_10_out, multiplexer_11_out;
  wire [12:0] CNT_num;
  wire [15:0] \总周期数 ;
  wire [31:0] adder_1_out, adder_2_out, alu_1_result, immvaluegen_1_imm, IR_PC, multiplexer_4_out,
       multiplexer_5_out, multiplexer_7_out, multiplexer_8_out, multiplexer_9_out, multiplexer_13_out,
       multiplexer_14_out, multiplexer_15_out, ram_1_data, regfile_for_single_unit_1_r1, register_3_q,
       register_5_q, register_6_q, shifter_1_out;

  Button \u_继续运行  (.out(Go));
  Button _1 (.out(IRA));
  Button _2 (.out(IRB));
  Button _3 (.out(IRC));
  or or_1 (W1, INTR1, d_ff_1_q);
  or or_2 (W2, INTR2, d_ff_2_q);
  or or_3 (W3, INTR3, d_ff_3_q);
  LED #(.active("true")) led_1 (.in(W1));
  LED #(.active("true")) led_2 (.in(W2));
  LED #(.active("true")) led_3 (.in(W3));
  or or_4 (or_4_out, Go, not_1_out);
  not not_1 (not_1_out, halt);
  Counter #(.width(16), .max('hffff), .ongoal("wrap"), .trigger("rising"), .behavior("new")) counter_1 (
    .D({16{1'b0}}), .count(or_4_out), .Q(\总周期数 ), .clk(CLK), .clr(RST));  // open: load, carry, preset, down
  D_Flip_Flop #(.trigger("rising"), .Pre_Clr_Positions("LEGACY"), .NegatePresetClear("false"), .enable("true"), .NewFFLayout("false")) d_ff_1 (
    .clk(IRA), .D(1'b1), .Q(d_ff_1_q), .reset(INTR1));  // open: Qn, preset, en
  D_Flip_Flop #(.trigger("rising"), .Pre_Clr_Positions("LEGACY"), .NegatePresetClear("false"), .enable("true"), .NewFFLayout("false")) d_ff_2 (
    .clk(IRB), .D(1'b1), .Q(d_ff_2_q), .reset(INTR2));  // open: Qn, preset, en
  D_Flip_Flop #(.trigger("rising"), .Pre_Clr_Positions("LEGACY"), .NegatePresetClear("false"), .enable("true"), .NewFFLayout("false")) d_ff_3 (
    .clk(IRC), .D(1'b1), .Q(d_ff_3_q), .reset(INTR3));  // open: Qn, preset, en
  Priority_Encoder #(.select(2), .disabled("Z")) priority_encoder_1 (
    .in0(1'b1), .in1(INTR1), .in2(INTR2), .in3(INTR3), .out(priority_encoder_1_out));  // open: gs, en_out, en_in
  Hex_Digit_Display hex_digit_display_1 (.value(LedData[31:28]));  // open: dp
  Comparator #(.width(16), .mode("twosComplement")) comparator_1 (
    .a(16'h258), .b(\总周期数 ), .eq(comparator_1_eq));  // open: gt, lt
  Comparator #(.width(16), .mode("twosComplement")) comparator_2 (
    .a(\总周期数 ), .b(16'h1), .eq(comparator_2_eq));  // open: gt, lt
  Comparator #(.width(16), .mode("twosComplement")) comparator_3 (
    .a(\总周期数 ), .b(16'h4), .eq(comparator_3_eq));  // open: gt, lt
  Comparator #(.width(16), .mode("twosComplement")) comparator_4 (
    .a(\总周期数 ), .b(16'h7), .eq(comparator_4_eq));  // open: gt, lt
  Comparator #(.width(16), .mode("twosComplement")) comparator_5 (
    .a(\总周期数 ), .b(16'h241), .eq(comparator_5_eq));  // open: gt, lt
  or or_5 (or_5_out, d_ff_1_q, INTR1);
  or or_6 (or_6_out, d_ff_2_q, INTR2);
  or or_7 (or_7_out, d_ff_3_q, INTR3);
  Multiplexer #(.select(2), .width(32), .disabled("Z"), .enable("false")) multiplexer_1 (
    .in1(32'h30ac), .in2(32'h3158), .in3(32'h3204), .out(IR_PC), .sel(priority_encoder_1_out));  // open: in0
  Hex_Digit_Display hex_digit_display_2 (.value(LedData[23:20]));  // open: dp
  Hex_Digit_Display hex_digit_display_3 (.value(LedData[27:24]));  // open: dp
  Button button_1 (.out(halt));
  Button button_2 (.out(RST));
  or or_8 (or_8_out, comparator_1_eq, comparator_2_eq);
  assign controlled_inverter_1_out = or_8_out ? ~CLK : 1'bz;  // Controlled_Inverter controlled_inverter_1
  assign controlled_inverter_2_out = comparator_3_eq ? ~CLK : 1'bz;  // Controlled_Inverter controlled_inverter_2
  or or_9 (or_9_out, comparator_4_eq, comparator_5_eq);
  assign controlled_inverter_3_out = or_9_out ? ~CLK : 1'bz;  // Controlled_Inverter controlled_inverter_3
  and and_1 (and_1_out, or_5_out, ~CLR1);  // AND_Gate
  and and_2 (and_2_out, or_6_out, ~CLR2);  // AND_Gate
  and and_3 (and_3_out, or_7_out, ~CLR3);  // AND_Gate
  Multiplexer #(.select(1), .width(2), .disabled("Z"), .enable("false")) multiplexer_2 (
    .in0(priority_encoder_1_out), .in1(register_2_q), .out(multiplexer_2_out), .sel(URET));
  or or_10 (or_10_out, URET, INTR);
  Hex_Digit_Display hex_digit_display_4 (.value(LedData[19:16]));  // open: dp
  Hex_Digit_Display hex_digit_display_5 (.value(LedData[15:12]));  // open: dp
  Comparator #(.width(16), .mode("twosComplement")) comparator_6 (
    .a(\总周期数 ), .b(16'hdd), .eq(comparator_6_eq));  // open: gt, lt
  Pull_Resistor #(.pull(0)) pull_resistor_1 (.node(controlled_inverter_1_out));
  Pull_Resistor #(.pull(0)) pull_resistor_2 (.node(controlled_inverter_2_out));
  Pull_Resistor #(.pull(0)) pull_resistor_3 (.node(controlled_inverter_3_out));
  D_Flip_Flop #(.trigger("rising"), .Pre_Clr_Positions("LEGACY"), .NegatePresetClear("false"), .enable("true"), .NewFFLayout("false")) d_ff_4 (
    .clk(CLK), .D(and_1_out), .Q(INTR1));  // open: Qn, preset, en, reset
  D_Flip_Flop #(.trigger("rising"), .Pre_Clr_Positions("LEGACY"), .NegatePresetClear("false"), .enable("true"), .NewFFLayout("false")) d_ff_5 (
    .clk(CLK), .D(and_2_out), .Q(INTR2));  // open: Qn, preset, en, reset
  D_Flip_Flop #(.trigger("rising"), .Pre_Clr_Positions("LEGACY"), .NegatePresetClear("false"), .enable("true"), .NewFFLayout("false")) d_ff_6 (
    .clk(CLK), .D(and_3_out), .Q(INTR3));  // open: Qn, preset, en, reset
  Register #(.width(2), .trigger("rising"), .Select("low")) register_1 (
    .D(multiplexer_2_out), .en(or_10_out), .Q(NOW_INTR), .clk(CLK));  // open: clr
  Hex_Digit_Display hex_digit_display_6 (.value(LedData[11:8]));  // open: dp
  Hex_Digit_Display hex_digit_display_7 (.value(LedData[7:4]));  // open: dp
  // Probe on \总周期数 
  Demultiplexer #(.select(2), .width(1), .tristate("false"), .disabled("Z"), .enable("false")) demultiplexer_1 (
    .out1(CLR1), .out2(CLR2), .out3(CLR3), .in(URET), .sel(NOW_INTR));  // open: out0
  Multiplexer #(.select(1), .width(2), .disabled("Z"), .enable("false")) multiplexer_3 (
    .in0(NOW_INTR), .in1(register_4_q), .out(multiplexer_3_out), .sel(URET));
  Hex_Digit_Display hex_digit_display_8 (.value(LedData[3:0]));  // open: dp
  Register #(.width(2), .trigger("rising"), .Select("low")) register_2 (
    .D(multiplexer_3_out), .en(or_10_out), .Q(register_2_q), .clk(CLK));  // open: clr
  // Probe on multiplexer_7_out
  // Probe on multiplexer_4_out
  Multiplexer #(.select(2), .width(32), .disabled("Z"), .enable("false")) multiplexer_4 (
    .in0(adder_1_out), .in1(adder_2_out), .in2({alu_1_result[31:1], 1'b0}), .out(multiplexer_4_out),
    .sel({JALR, Branch}));  // open: in3
  Multiplexer #(.select(1), .width(32), .disabled("Z"), .enable("false")) multiplexer_5 (
    .in0(multiplexer_4_out), .in1(register_5_q), .out(multiplexer_5_out), .sel(URET));
  Adder #(.width(32)) adder_1 (.a(32'h4), .b(PC), .out(adder_1_out), .cin(1'b0));  // open: cout
  Multiplexer #(.select(1), .width(2), .disabled("Z"), .enable("false")) multiplexer_6 (
    .in0(register_2_q), .out(multiplexer_6_out), .sel(URET));  // open: in1
  or or_11 (IR1_t, IR1, IRA);
  Multiplexer #(.select(2), .width(32), .disabled("Z"), .enable("false")) multiplexer_7 (
    .in0(multiplexer_4_out), .in1(IR_PC), .in2(register_3_q), .out(multiplexer_7_out), .sel({URET, INTR}));  // open: in3
  Register #(.width(32), .trigger("rising"), .Select("low")) register_3 (
    .D(multiplexer_5_out), .en(or_12_out), .Q(register_3_q), .clk(CLK));  // open: clr
  or or_12 (or_12_out, URET, INTR);
  Register #(.width(2), .trigger("rising"), .Select("low")) register_4 (
    .D(multiplexer_6_out), .en(or_10_out), .Q(register_4_q), .clk(CLK));  // open: clr
  or or_13 (IR2_t, IR2, IRB);
  or or_14 (or_14_out, Go, ~halt);  // OR_Gate
  Multiplexer #(.select(1), .width(32), .disabled("Z"), .enable("false")) multiplexer_8 (
    .in0(register_3_q), .in1(register_6_q), .out(multiplexer_8_out), .sel(URET));
  Register #(.width(32), .trigger("rising"), .Select("low")) u_PC (
    .D(multiplexer_7_out), .en(or_14_out), .Q(PC), .clk(CLK), .clr(RST), .cs(1'b0), .preset(1'b0));
  Register #(.width(32), .trigger("rising"), .Select("low")) register_5 (
    .D(multiplexer_8_out), .en(or_12_out), .Q(register_5_q), .clk(CLK));  // open: clr
  or or_15 (or_15_out, INTR1, INTR2, INTR3);
  or or_16 (IR3_t, IR3, IRC);
  Multiplexer #(.select(1), .width(32), .disabled("Z"), .enable("false")) multiplexer_9 (
    .in0(register_5_q), .out(multiplexer_9_out), .sel(URET));  // open: in1
  D_Flip_Flop #(.trigger("rising"), .Pre_Clr_Positions("LEGACY"), .NegatePresetClear("false"), .enable("true"), .NewFFLayout("false")) d_ff_7 (
    .clk(CLK), .D(CSRRSI), .Q(d_ff_7_q), .en(CSR));  // open: Qn, preset, reset
  and and_4 (and_4_out, d_ff_7_q, ~CSRRCI);  // AND_Gate
  and and_5 (CSRRCI, CSR, ~AluOP[3]);  // AND_Gate
  and and_6 (CSRRSI, AluOP[3], CSR);
  // RiscV_Probe riscv_probe_1: pin names not known; wires that end beside it: IR
  Register #(.width(32), .trigger("rising"), .Select("low")) register_6 (
    .D(multiplexer_9_out), .en(or_12_out), .Q(register_6_q), .clk(CLK));  // open: clr
  and and_7 (and_7_out, equal, ~IR[12]);  // AND_Gate
  and and_8 (and_8_out, ~equal, IR[12]);  // AND_Gate
  and and_9 (and_9_out, IR[14], less);
  or or_17 (or_17_out, ~or_15_out, URET, CSRRSI, and_4_out);  // OR_Gate
  ROM #(.addrWidth(10), .dataWidth(32), .Select("high")) rom_1 (.addr(PC[11:2]), .data(IR), .sel(1'b1));
  or or_18 (or_18_out, and_7_out, and_8_out, and_9_out);
  D_Flip_Flop #(.trigger("rising"), .Pre_Clr_Positions("LEGACY"), .NegatePresetClear("false"), .enable("true"), .NewFFLayout("false")) d_ff_8 (
    .clk(CLK), .D(or_17_out), .Q(d_ff_8_q));  // open: Qn, preset, en, reset
  and and_10 (and_10_out, B, or_18_out);
  Multiplexer #(.select(1), .width(5), .disabled("Z"), .enable("false")) multiplexer_10 (
    .in0(IR[19:15]), .in1(5'b01010), .out(multiplexer_10_out), .sel(ecall));
  Multiplexer #(.select(1), .width(5), .disabled("Z"), .enable("false")) multiplexer_11 (
    .in0(IR[24:20]), .in1(5'b10001), .out(multiplexer_11_out), .sel(ecall));
  or or_19 (Branch, and_10_out, J);
  \单周期硬布线控制器  \u_单周期硬布线控制器_1  (
    .Funct({IR[30], IR[25], IR[14:12]}), .OP(IR[6:2]), .ALU_OP(AluOP), .MemToReg(MemToReg), .ecall(ecall),
    .in_3(IR[21]), .uret(URET), .MemWrite(MemWrite), .CSR(CSR), .lh(lh), .BEQ(Bne), .S_Type(S_Type),
    .RegWrite(RegWrite), .ALU_SRC(AluSrcB), .BNE(Beq), .JALR(JALR), .JAL(JAL));  // open: bltu, lw
  Multiplexer #(.select(1), .width(32), .disabled("Z"), .enable("false")) multiplexer_12 (
    .in0(multiplexer_15_out), .in1(adder_1_out), .out(RDin), .sel(or_20_out));
  Priority_Encoder #(.select(2), .disabled("Z")) priority_encoder_2 (
    .in0(1'b1), .in1(INTR1), .in2(INTR2), .in3(INTR3), .out(priority_encoder_2_out));  // open: gs, en_out, en_in
  RegFile_for_Single_Unit regfile_for_single_unit_1 (
    .Din(RDin), .Clk(CLK), .R1(regfile_for_single_unit_1_r1), .R2(MDin), .WE(RegWrite), .W_num(IR[11:7]),
    .R1_num(multiplexer_10_out), .R2_num(multiplexer_11_out));
  or or_20 (or_20_out, JALR, J);
  ImmValueGen immvaluegen_1 (
    .Imm(immvaluegen_1_imm), .Type_I_Imm(IR[31:20]), .Type_S_Imm({IR[31:25], IR[11:7]}),
    .Type_B_Imm({IR[31], IR[7], IR[30:25], IR[11:8]}), .Type_J_Imm({IR[31], IR[19:12], IR[20], IR[30:21]}),
    .Op6(IR[6]), .I(I), .Op5(IR[5]), .S(S), .Op4(IR[4]), .B(B), .Op3(IR[3]), .J(J), .Op2(IR[2]),
    .System(System));
  Comparator #(.width(2), .mode("unsigned")) comparator_7 (
    .a(NOW_INTR), .b(priority_encoder_2_out), .lt(comparator_7_lt));  // open: gt, eq
  D_Flip_Flop #(.trigger("high"), .Pre_Clr_Positions("LEGACY"), .NegatePresetClear("false"), .enable("true"), .NewFFLayout("false")) d_ff_9 (.Q(d_ff_9_q));  // open: clk, D, Qn, preset, en, reset
  // Probe on 13'hc
  and and_11 (INTR, comparator_7_lt, d_ff_8_q);
  Comparator #(.width(13), .mode("twosComplement")) comparator_8 (
    .a(CNT_num), .b(13'hc), .eq(comparator_8_eq), .lt(comparator_8_lt));  // open: gt
  Clock #(.highDuration(1), .lowDuration(1)) clock_1 (.out(clock_1_out));
  Multiplexer #(.select(1), .width(32), .disabled("Z"), .enable("false")) multiplexer_13 (
    .in0(regfile_for_single_unit_1_r1), .in1(32'h22), .out(multiplexer_13_out), .sel(ecall));
  Multiplexer #(.select(1), .width(32), .disabled("Z"), .enable("false")) multiplexer_14 (
    .in0(MDin), .in1(immvaluegen_1_imm), .out(multiplexer_14_out), .sel(AluSrcB));
  // Probe on immvaluegen_1_imm
  Counter #(.width(13), .max('h1fff), .ongoal("stay"), .trigger("rising"), .behavior("old")) counter_2 (
    .count(comparator_8_lt), .Q(CNT_num), .clk(clock_1_out));  // open: load, D, carry, clr, preset
  and and_12 (and_12_out, equal, ecall);
  nand nand_1 (nand_1_out, d_ff_9_q, comparator_8_eq);
  Register #(.width(32), .trigger("rising"), .Select("low")) register_7 (
    .D(regfile_for_single_unit_1_r1), .en(and_12_out), .Q(LedData), .clk(CLK));  // open: clr
  ALU alu_1 (
    .X(multiplexer_13_out), .Y(multiplexer_14_out), .AluOP(AluOP), .Equal(equal), .Result(alu_1_result),
    .out_6(less));  // open: Result_2, out_4
  assign CLK = nand_1_out ? clock_1_out : 1'bz;  // Controlled_Buffer controlled_buffer_1
  Pull_Resistor #(.pull(1)) pull_resistor_4 (.node(CLK));
  Shifter #(.width(32), .shift("ll")) shifter_1 (.in(immvaluegen_1_imm), .\dist (5'b00001), .out(shifter_1_out));
  Adder #(.width(32)) adder_2 (.a(shifter_1_out), .b(PC), .out(adder_2_out), .cin(1'b0));  // open: cout
  RAM #(.addrWidth(10), .dataWidth(32), .bus("separate"), .Select("high")) ram_1 (
    .addr(alu_1_result[11:2]), .din(MDin), .data(ram_1_data), .str(MemWrite), .sel(1'b1), .clk(CLK),
    .ld(1'b1), .clr(RST));
  Multiplexer #(.select(1), .width(32), .disabled("Z"), .enable("false")) multiplexer_15 (
    .in0(alu_1_result), .in1(ram_1_data), .out(multiplexer_15_out), .sel(MemToReg));

  // Other names for the same wires on the sheet: funct[4:0] = {IR[30], IR[25], IR[14:12]}; opcode[4:0] = IR[6:2]

  // Notes on the sheet:
  //   中断源
  //   Interruption Stack
  //   中断等待指示
  //   总复位信号应将除ROM以外所有存储组件全部清零
  //   多级中断测试信号模拟器
  //   数码管输出
  //   数码管输出应该用寄存器锁存，否则显示数据只能一闪而过
  //   00: not jumping
  //   01: branch jumping, for bne, beq, jal & bltu
  //   10: for JALR jumping
  //   for JAL
  //   指令探针
  //   指令存储器
  //   Beq
  //   Bne
  //   bltu
  //   指令字
  //   contents of rom_1 (hex, n*v repeats v):
  //   7d000113 100413 1f41993 41f9d993 433 c00913 800b13 140413 f47413 800293 100313 499993 89e9b3 1300533
  //   2200893 73 406282b3 fe0294e3 140413 f00f93 1f47433 1c41413 800293 100313 49d993 89e9b3 1300533
  //   2200893 73 406282b3 fe0294e3 1c45413 406b0b33 b0463 f95ff06f 2b3 fff2c293 1029293 fff2e293 500533
  //   2200893 73 f5dff06f 1112023 410113 a12023 410113 812023 410113 1312023 410113 1412023 410113 1512023
  //   410113 1612023 410113 40e073 100b13 300a13 100a93 1600433 441413 14469b3 1300533 2200893 73 fe0416e3
  //   415a0a33 fe0a10e3 40f073 ffc10113 12b03 ffc10113 12a83 ffc10113 12a03 ffc10113 12983 ffc10113 12403
  //   ffc10113 12503 ffc10113 12883 200073 1112023 410113 a12023 410113 812023 410113 1312023 410113
  //   1412023 410113 1512023 410113 1612023 410113 40e073 200b13 300a13 100a93 1600433 441413 14469b3
  //   1300533 2200893 73 fe0416e3 415a0a33 fe0a10e3 40f073 ffc10113 12b03 ffc10113 12a83 ffc10113 12a03
  //   ffc10113 12983 ffc10113 12403 ffc10113 12503 ffc10113 12883 200073 1112023 410113 a12023 410113
  //   812023 410113 1312023 410113 1412023 410113 1512023 410113 1612023 410113 40e073 300b13 300a13
  //   100a93 1600433 441413 14469b3 1300533 2200893 73 fe0416e3 415a0a33 fe0a10e3 40f073 ffc10113 12b03
  //   ffc10113 12a83 ffc10113 12a03 ffc10113 12983 ffc10113 12403 ffc10113 12503 ffc10113 12883 200073
  //   PC+4
  //   Bne, Beq & bltu: func3 of 3 instructions is different, with 000 for Beq, 001 for Bne and 110 for bltu, respectively
  //   为方便自动评测，需要输出PC，IR，寄存器堆写如数据RDin
  //   I-type command
  //   S-type command
  //   B-type command
  //   J-type command
  //   J type jump
  //   RAM写使能MemWrite、RAM写入数据MDin等信号
  //   IR21
  //   OpCode
  //   funct
  //   for ecall
  //   B type jump
  //   Only JAL is J-type instruction
  //   stop the program while equal is 0
  //   OpCode
  //   控制位
  //   暂停节拍，不能为0
  //   $a0
  //   戳工具置1进入计数暂停模式，ctrl+k时钟自动运行到对应节拍暂停
  //   ctrl+k关闭时钟连续运行，将控制位置零，进入单步调试模式调试
  //   Update LedData using $a0
  //   Imm
  //   SrcA
  //   SrcB
  //   for B-type jumping
  //   可计数暂停的时钟源
  //   数据存储器
  //   for JALR jumping
endmodule

module \封装正确性测试  (
);

  wire IR1, IR2, IR3, MemW, RegW;
  wire [31:0] EX_PC, ID_PC, IF_PC, IR, LED, MDin, MDinr, MEM_PC, PC, RDin, RDinr, WB_PC;

  \单周期RISC_V  \u_单周期risc_v_1  (
    .IR1(IR1), .IR2(IR2), .IR3(IR3), .RegWrite(RegW), .MemWrite(MemW), .PC(PC), .IR(IR), .RDin(RDin),
    .MDin(MDin), .LedData(LED));
  \气泡流水线  \u_气泡流水线_1  (
    .RegWrite(RegW), .MemWrite(MemW), .IF_PC(IF_PC), .ID_PC(ID_PC), .EX_PC(EX_PC), .M_PC(MEM_PC),
    .WB_PC(WB_PC), .RDin(RDinr), .MDin(MDinr), .LedData(LED));
  \单周期_单级中断  \u_单周期_单级中断_1  (
    .IR1(IR1), .IR2(IR2), .IR3(IR3), .RegWrite(RegW), .MemWrite(MemW), .PC(PC), .IR(IR), .RDin(RDin),
    .MDin(MDin), .LedData(LED));
  \理想流水线  \u_理想流水线_1  (
    .RegWrite(RegW), .MemWrite(MemW), .IF_PC(IF_PC), .ID_PC(ID_PC), .EX_PC(EX_PC), .M_PC(MEM_PC),
    .WB_PC(WB_PC), .RDin(RDinr), .MDin(MDinr), .LedData(LED));
  \重定向流水线  \u_重定向流水线_1  (
    .RegWrite(RegW), .MemWrite(MemW), .IF_PC(IF_PC), .ID_PC(ID_PC), .EX_PC(EX_PC), .M_PC(MEM_PC),
    .WB_PC(WB_PC), .RDin(RDinr), .MDin(MDinr), .LedData(LED));
  \单周期_多级中断  \u_单周期_多级中断_1  (
    .IR1(IR1), .IR2(IR2), .IR3(IR3), .RegWrite(RegW), .MemWrite(MemW), .PC(PC), .IR(IR), .RDin(RDin),
    .MDin(MDin), .LedData(LED));

  // Notes on the sheet:
  //   单周期封装测试
  //   气泡流水封装测试
  //   单周期+单级中断封装测试
  //   请检查上面封装有无位宽不匹配，引脚标签是否和连接的标签相对应，否则无法在educoder平台上正确测试
  //   理想流水封装测试
  //   重定向流水封装测试
  //   单周期+多级中断封装测试
endmodule

module \流水线_单级中断_EX阶段  (
  output RegWrite,
  output MemWrite,
  output [31:0] IF_PC,
  output [31:0] ID_PC,
  output [31:0] EX_PC,
  output [31:0] M_PC,
  output [31:0] WB_PC,
  output [31:0] RDin,
  output [31:0] MDin,
  output [31:0] LedData
);

  wire AlreadyINTR, and_2_out, and_3_out, and_4_out, and_5_out, and_6_out, and_7_out, and_9_out, Branch,
       button_1_out, CLK, clock_1_out, CLR1, CLR2, CLR3, comparator_1_eq, comparator_2_eq, comparator_3_eq,
       comparator_4_eq, comparator_5_eq, comparator_6_eq, comparator_6_lt, Conflict,
       controlled_inverter_1_out, controlled_inverter_2_out, controlled_inverter_3_out, d_ff_1_q, d_ff_2_q,
       d_ff_3_q, d_ff_4_q, d_ff_8_q, EX_B, EX_Beq, EX_bltu, EX_Bne, ex_equal, EX_J, EX_JAL, EX_JALR, ex_less,
       EX_MemToReg, EX_RegWrite, EX_URET, Go, Halt, halt_t, IF_Alu_Src, IF_B, IF_I, IF_J, IF_S, IF_S_Type,
       INTR, INTR1, INTR2, INTR3, IRA, IRB, IRC, LoadConflict, MEM_RegWrite, mul_cmdclear_1_alu_src_2,
       mul_cmdclear_1_beq_2, mul_cmdclear_1_bltu_2, mul_cmdclear_1_bne_2, mul_cmdclear_1_csr_2,
       mul_cmdclear_1_ecall_2, mul_cmdclear_1_jal_2, mul_cmdclear_1_jalr_2, mul_cmdclear_1_lh_2,
       mul_cmdclear_1_lw_2, mul_cmdclear_1_memtoreg_2, mul_cmdclear_1_memwrite_2, mul_cmdclear_1_regwrite_2,
       mul_cmdclear_1_s_type_2, mul_cmdclear_1_uret_2, mul_cmdreg_1_alu_src_2, mul_cmdreg_1_ecall_2,
       mul_cmdreg_1_lh_2, mul_cmdreg_1_lw_2, mul_cmdreg_1_memwrite_2, mul_cmdreg_1_s_type_2,
       mul_cmdreg_2_alu_src_2, mul_cmdreg_2_beq_2, mul_cmdreg_2_bltu_2, mul_cmdreg_2_bne_2,
       mul_cmdreg_2_ecall_2, mul_cmdreg_2_jal_2, mul_cmdreg_2_jalr_2, mul_cmdreg_2_lh_2, mul_cmdreg_2_lw_2,
       mul_cmdreg_2_memtoreg_2, mul_cmdreg_2_s_type_2, mul_cmdreg_2_uret_2, mul_cmdreg_3_alu_src_2,
       mul_cmdreg_3_beq_2, mul_cmdreg_3_bltu_2, mul_cmdreg_3_bne_2, mul_cmdreg_3_ecall_2, mul_cmdreg_3_jal_2,
       mul_cmdreg_3_jalr_2, mul_cmdreg_3_lh_2, mul_cmdreg_3_lw_2, mul_cmdreg_3_memtoreg_2,
       mul_cmdreg_3_memwrite_2, mul_cmdreg_3_s_type_2, mul_cmdreg_3_uret_2, multiplexer_13_out,
       multiplexer_14_out, nand_1_out, not_1_out, not_2_out, not_3_out, not_4_out, not_5_out, or_1_out,
       or_2_out, or_4_out, or_5_out, or_9_out, or_10_out, or_11_out, or_12_out, or_13_out, or_14_out,
       or_15_out, or_16_out, or_17_out, or_18_out, or_19_out, or_20_out, or_21_out, or_22_out, register_1_q,
       register_2_q, register_3_q, RST, System, W1, W2, W3, \单周期硬布线控制器_1_beq , \单周期硬布线控制器_1_bltu ,
       \单周期硬布线控制器_1_bne , \单周期硬布线控制器_1_ecall , \单周期硬布线控制器_1_jal , \单周期硬布线控制器_1_jalr , \单周期硬布线控制器_1_lh ,
       \单周期硬布线控制器_1_lw , \单周期硬布线控制器_1_memtoreg , \单周期硬布线控制器_1_memwrite , \单周期硬布线控制器_1_regwrite ,
       \单周期硬布线控制器_1_uret ;
  wire [0:0] alu_1_result_2;
  wire [1:0] priority_encoder_1_out, priority_encoder_2_out, redirectionconflict_1_rsfoward,
       redirectionconflict_1_rtfoward, register_4_q, RsFoward, RtFoward;
  wire [3:0] mul_cmdclear_1_alu_op_2, mul_cmdreg_1_alu_op_2, mul_cmdreg_2_alu_op_2, mul_cmdreg_3_alu_op_2,
       \单周期硬布线控制器_1_alu_op ;
  wire [4:0] ex_mem_wd_cmdreg_2_c_5_2, EX_Reg, funct, MEM_Reg, multiplexer_11_out, Rs, Rt;
  wire [12:0] CNT_num;
  wire [15:0] \LoadUse次数 , \总周期数 , \插入气泡数 , \无条件分支数 , \条件分支成功数 ;
  wire [31:0] adder_1_out, adder_3_out, EX_IR, ex_mem_wd_cmdreg_1_a_32_2, ex_mem_wd_cmdreg_2_a_32_2,
       ex_mem_wd_cmdreg_2_b_32_2, ID_IR, if_ex_cmdreg_1_imm_2, if_ex_cmdreg_1_r1_2, if_ex_cmdreg_1_r2_2,
       IF_IR, immvaluegen_1_imm, INTR_PC, MEM_IR, multiplexer_1_out, multiplexer_2_out, multiplexer_4_out,
       multiplexer_5_out, multiplexer_6_out, multiplexer_9_out, multiplexer_10_out, multiplexer_12_out,
       multiplexer_15_out, multiplexer_16_out, multiplexer_17_out, multiplexer_18_out, multiplexer_19_out,
       multiplexer_20_out, multiplexer_21_out, multiplexer_22_out, offset, Orig_PC, pc_ir_cmdreg_1_ir_2,
       pc_ir_cmdreg_1_pc_2, ram_1_data, regifile_1_r1, regifile_1_r2, shifter_1_out, WB_IR;
  wire [31:1] alu_1_result;

  Button \u_总复位  (.out(RST));
  Button _1 (.out(IRA));
  Button _2 (.out(IRB));
  Button _3 (.out(IRC));
  // Probe on \总周期数 
  // Probe on \总周期数 
  Button \u_继续运行  (.out(Go));
  LED #(.active("true")) led_1 (.in(W1));
  LED #(.active("true")) led_2 (.in(W2));
  LED #(.active("true")) led_3 (.in(W3));
  Adder #(.width(32)) adder_1 (.a(IF_PC), .b(32'h4), .out(adder_1_out));  // open: cin, cout
  Hex_Digit_Display hex_digit_display_1 (.value(LedData[31:28]));  // open: dp
  // Probe on IF_PC[19:0]
  // RiscV_Probe riscv_probe_1: pin names not known; wires that end beside it: IF_IR
  Button button_1 (.out(button_1_out));
  Multiplexer #(.select(1), .width(32), .disabled("Z"), .enable("false")) multiplexer_1 (
    .in0(adder_1_out), .in1(offset), .out(multiplexer_1_out), .sel(Branch));
  Multiplexer #(.select(1), .width(32), .disabled("Z"), .enable("false")) multiplexer_2 (
    .in0(ID_PC), .in1(multiplexer_4_out), .out(multiplexer_2_out), .sel(Branch));
  not not_1 (not_1_out, AlreadyINTR);
  Comparator #(.width(16), .mode("twosComplement")) comparator_1 (
    .a(16'h23b), .b(\总周期数 ), .eq(comparator_1_eq));  // open: gt, lt
  Comparator #(.width(16), .mode("twosComplement")) comparator_2 (
    .a(\总周期数 ), .b(16'h1), .eq(comparator_2_eq));  // open: gt, lt
  Comparator #(.width(16), .mode("twosComplement")) comparator_3 (
    .a(\总周期数 ), .b(16'h4), .eq(comparator_3_eq));  // open: gt, lt
  Comparator #(.width(16), .mode("twosComplement")) comparator_4 (
    .a(\总周期数 ), .b(16'h7), .eq(comparator_4_eq));  // open: gt, lt
  Multiplexer #(.select(2), .width(32), .disabled("Z"), .enable("false")) multiplexer_3 (
    .in0(32'h30ac), .in1(32'h3150), .in2(32'h31f4), .out(INTR_PC), .sel(priority_encoder_1_out));  // open: in3
  Priority_Encoder #(.select(2), .disabled("Z")) priority_encoder_1 (
    .in0(INTR1), .in1(INTR2), .in2(INTR3), .out(priority_encoder_1_out));  // open: in3, gs, en_out, en_in
  Register #(.width(1), .trigger("rising"), .Select("low")) register_1 (
    .D(INTR1), .Q(register_1_q), .clk(CLK));  // open: en, clr
  Register #(.width(1), .trigger("rising"), .Select("low")) register_2 (
    .D(INTR2), .Q(register_2_q), .clk(CLK));  // open: en, clr
  Register #(.width(1), .trigger("rising"), .Select("low")) register_3 (
    .D(INTR3), .Q(register_3_q), .clk(CLK));  // open: en, clr
  Hex_Digit_Display hex_digit_display_2 (.value(LedData[27:24]));  // open: dp
  Hex_Digit_Display hex_digit_display_3 (.value(LedData[23:20]));  // open: dp
  // Probe on ID_PC[19:0]
  // RiscV_Probe riscv_probe_2: pin names not known; wires that end beside it: {ID_IR[31], funct[4], ID_IR[29:26], funct[3], ID_IR[24:15], funct[2:0], ID_IR[11:0]}, button_1_out, halt_t
  Multiplexer #(.select(1), .width(32), .disabled("Z"), .enable("false")) multiplexer_4 (
    .in0(multiplexer_1_out), .in1(IF_PC), .out(multiplexer_4_out), .sel(LoadConflict));
  Multiplexer #(.select(1), .width(32), .disabled("Z"), .enable("false")) multiplexer_5 (
    .in0(Orig_PC), .in1(multiplexer_2_out), .out(multiplexer_5_out), .sel(not_1_out));
  or or_1 (or_1_out, comparator_1_eq, comparator_2_eq);
  assign controlled_inverter_1_out = or_1_out ? ~CLK : 1'bz;  // Controlled_Inverter controlled_inverter_1
  assign controlled_inverter_2_out = comparator_3_eq ? ~CLK : 1'bz;  // Controlled_Inverter controlled_inverter_2
  assign controlled_inverter_3_out = comparator_4_eq ? ~CLK : 1'bz;  // Controlled_Inverter controlled_inverter_3
  or or_2 (or_2_out, INTR1, INTR2, INTR3);
  or or_3 (AlreadyINTR, register_1_q, register_2_q, register_3_q);
  Hex_Digit_Display hex_digit_display_4 (.value(LedData[19:16]));  // open: dp
  Hex_Digit_Display hex_digit_display_5 (.value(LedData[15:12]));  // open: dp
  Register #(.width(32), .trigger("rising"), .Select("low")) PC (
    .D(multiplexer_5_out), .en(INTR), .Q(Orig_PC), .clk(CLK));  // open: clr
  Pull_Resistor #(.pull(0)) pull_resistor_1 (.node(controlled_inverter_1_out));
  Pull_Resistor #(.pull(0)) pull_resistor_2 (.node(controlled_inverter_2_out));
  Pull_Resistor #(.pull(0)) pull_resistor_3 (.node(controlled_inverter_3_out));
  Register #(.width(2), .trigger("rising"), .Select("low")) register_4 (
    .D(priority_encoder_1_out), .en(INTR), .Q(register_4_q), .clk(CLK));  // open: clr
  Hex_Digit_Display hex_digit_display_6 (.value(LedData[11:8]));  // open: dp
  Hex_Digit_Display hex_digit_display_7 (.value(LedData[7:4]));  // open: dp
  // Probe on EX_PC[19:0]
  // RiscV_Probe riscv_probe_3: pin names not known; wires that end beside it: EX_IR
  Priority_Encoder #(.select(2), .disabled("Z")) priority_encoder_2 (
    .in0(1'b1), .in1(INTR), .in2(EX_URET), .out(priority_encoder_2_out));  // open: in3, gs, en_out, en_in
  Multiplexer #(.select(2), .width(32), .disabled("Z"), .enable("false")) multiplexer_6 (
    .in0(multiplexer_4_out), .in1(INTR_PC), .in2(Orig_PC), .out(multiplexer_6_out),
    .sel(priority_encoder_2_out));  // open: in3
  Demultiplexer #(.select(2), .width(1), .tristate("false"), .disabled("Z"), .enable("false")) demultiplexer_1 (
    .out0(CLR1), .out1(CLR2), .out2(CLR3), .in(EX_URET), .sel(register_4_q));  // open: out3
  or or_4 (or_4_out, ~or_2_out, EX_URET);  // OR_Gate
  Hex_Digit_Display hex_digit_display_8 (.value(LedData[3:0]));  // open: dp
  Comparator #(.width(16), .mode("twosComplement")) comparator_5 (
    .a(\总周期数 ), .b(16'h378), .eq(comparator_5_eq));  // open: gt, lt
  Register #(.width(32), .trigger("rising"), .Select("low")) PC_2 (
    .D(multiplexer_6_out), .en(or_5_out), .Q(IF_PC), .clk(CLK), .clr(RST));
  or or_5 (or_5_out, Go, not_2_out);
  not not_2 (not_2_out, halt_t);
  D_Flip_Flop #(.trigger("rising"), .Pre_Clr_Positions("LEGACY"), .NegatePresetClear("false"), .enable("true"), .NewFFLayout("false")) d_ff_1 (
    .clk(IRA), .D(1'b1), .Q(d_ff_1_q), .reset(INTR1));  // open: Qn, preset, en
  or or_6 (W1, INTR1, d_ff_1_q);
  D_Flip_Flop #(.trigger("rising"), .Pre_Clr_Positions("LEGACY"), .NegatePresetClear("false"), .enable("true"), .NewFFLayout("false")) d_ff_2 (
    .clk(IRB), .D(1'b1), .Q(d_ff_2_q), .reset(INTR2));  // open: Qn, preset, en
  or or_7 (W2, INTR2, d_ff_2_q);
  D_Flip_Flop #(.trigger("rising"), .Pre_Clr_Positions("LEGACY"), .NegatePresetClear("false"), .enable("true"), .NewFFLayout("false")) d_ff_3 (
    .clk(IRC), .D(1'b1), .Q(d_ff_3_q), .reset(INTR3));  // open: Qn, preset, en
  or or_8 (W3, INTR3, d_ff_3_q);
  D_Flip_Flop #(.trigger("rising"), .Pre_Clr_Positions("ABOVE_BELOW"), .NegatePresetClear("false"), .enable("false"), .NewFFLayout("true")) d_ff_4 (
    .clk(CLK), .D(or_4_out), .Q(d_ff_4_q));  // open: Qn, preset, reset
  // Probe on \总周期数 
  // Probe on M_PC[19:0]
  // RiscV_Probe riscv_probe_4: pin names not known; wires that end beside it: comparator_5_eq, halt_t, MEM_IR
  or or_9 (or_9_out, d_ff_1_q, INTR1);
  or or_10 (or_10_out, d_ff_2_q, INTR2);
  or or_11 (or_11_out, d_ff_3_q, INTR3);
  and and_1 (INTR, d_ff_4_q, or_2_out);
  // Probe on \总周期数 
  // Probe on \无条件分支数 
  // Probe on \条件分支成功数 
  // Probe on \插入气泡数 
  // Probe on \LoadUse次数 
  and and_2 (and_2_out, or_9_out, ~CLR1);  // AND_Gate
  and and_3 (and_3_out, or_10_out, ~CLR2);  // AND_Gate
  and and_4 (and_4_out, or_11_out, ~CLR3);  // AND_Gate
  // Probe on IF_PC[11:0]
  // Probe on WB_PC[19:0]
  // RiscV_Probe riscv_probe_5: pin names not known; wires that end beside it: WB_IR
  ROM #(.addrWidth(10), .dataWidth(32), .Select("high")) Instruction_Memory (
    .addr(IF_PC[11:2]), .data(IF_IR), .sel(1'b1));
  D_Flip_Flop #(.trigger("rising"), .Pre_Clr_Positions("LEGACY"), .NegatePresetClear("false"), .enable("true"), .NewFFLayout("false")) d_ff_5 (
    .clk(CLK), .D(and_2_out), .Q(INTR1));  // open: Qn, preset, en, reset
  D_Flip_Flop #(.trigger("rising"), .Pre_Clr_Positions("LEGACY"), .NegatePresetClear("false"), .enable("true"), .NewFFLayout("false")) d_ff_6 (
    .clk(CLK), .D(and_3_out), .Q(INTR2));  // open: Qn, preset, en, reset
  D_Flip_Flop #(.trigger("rising"), .Pre_Clr_Positions("LEGACY"), .NegatePresetClear("false"), .enable("true"), .NewFFLayout("false")) d_ff_7 (
    .clk(CLK), .D(and_4_out), .Q(INTR3));  // open: Qn, preset, en, reset
  // Probe on ID_PC[11:0]
  // Probe on EX_PC[11:0]
  PC_IR_cmdReg pc_ir_cmdreg_1 (
    .PC(IF_PC), .IR(IF_IR), .PC_2(pc_ir_cmdreg_1_pc_2), .IR_2(pc_ir_cmdreg_1_ir_2), .Run(or_5_out),
    .CLK(CLK), .Clear(RST), .AsyClear(or_12_out));
  or or_12 (or_12_out, Branch, INTR);
  // Probe on M_PC[11:0]
  D_Flip_Flop #(.trigger("high"), .Pre_Clr_Positions("LEGACY"), .NegatePresetClear("false"), .enable("true"), .NewFFLayout("false")) d_ff_8 (.Q(d_ff_8_q));  // open: clk, D, Qn, preset, en, reset
  // Probe on 13'hc
  // Probe on WB_PC[11:0]
  Comparator #(.width(13), .mode("twosComplement")) comparator_6 (
    .a(CNT_num), .b(13'hc), .eq(comparator_6_eq), .lt(comparator_6_lt));  // open: gt
  Clock #(.highDuration(1), .lowDuration(1)) clock_1 (.out(clock_1_out));
  DataConflict dataconflict_1 (
    .Alu_Src(IF_Alu_Src), .rs(Rs), .rt(Rt), .EX_Reg(EX_Reg), .MEM_Reg(MEM_Reg), .EX_RegWrite(EX_RegWrite),
    .MEM_RegWrite(MEM_RegWrite), .hazzard(Conflict));
  nand nand_1 (nand_1_out, d_ff_8_q, comparator_6_eq);
  Counter #(.width(13), .max('h1fff), .ongoal("stay"), .trigger("rising"), .behavior("old")) counter_1 (
    .count(comparator_6_lt), .Q(CNT_num), .clk(clock_1_out));  // open: load, D, carry, clr, preset
  LoadConflictProcessorUnit loadconflictprocessorunit_1 (
    .PC(pc_ir_cmdreg_1_pc_2), .IR(pc_ir_cmdreg_1_ir_2), .PC_2(ID_PC),
    .IR_2({ID_IR[31], funct[4], ID_IR[29:26], funct[3], ID_IR[24:15], funct[2:0], ID_IR[11:0]}),
    .Conflict(LoadConflict), .CLK(CLK));
  Multiplexer #(.select(1), .width(5), .disabled("Z"), .enable("false")) multiplexer_7 (
    .in0(ID_IR[19:15]), .in1(5'b01010), .out(Rs), .sel(\单周期硬布线控制器_1_ecall ));
  Multiplexer #(.select(1), .width(5), .disabled("Z"), .enable("false")) multiplexer_8 (
    .in0(ID_IR[24:20]), .in1(5'b10001), .out(Rt), .sel(\单周期硬布线控制器_1_ecall ));
  assign CLK = nand_1_out ? clock_1_out : 1'bz;  // Controlled_Buffer controlled_buffer_1
  \单周期硬布线控制器  \u_单周期硬布线控制器_1  (
    .Funct(funct), .OP(ID_IR[6:2]), .ALU_OP(\单周期硬布线控制器_1_alu_op ), .MemToReg(\单周期硬布线控制器_1_memtoreg ),
    .bltu(\单周期硬布线控制器_1_bltu ), .ecall(\单周期硬布线控制器_1_ecall ), .in_3(ID_IR[21]), .uret(\单周期硬布线控制器_1_uret ),
    .MemWrite(\单周期硬布线控制器_1_memwrite ), .lh(\单周期硬布线控制器_1_lh ), .BEQ(\单周期硬布线控制器_1_beq ), .S_Type(IF_S_Type),
    .RegWrite(\单周期硬布线控制器_1_regwrite ), .lw(\单周期硬布线控制器_1_lw ), .ALU_SRC(IF_Alu_Src), .BNE(\单周期硬布线控制器_1_bne ),
    .JALR(\单周期硬布线控制器_1_jalr ), .JAL(\单周期硬布线控制器_1_jal ));  // open: CSR
  ImmValueGen immvaluegen_1 (
    .Imm(immvaluegen_1_imm), .Type_I_Imm({ID_IR[31], funct[4], ID_IR[29:26], funct[3], ID_IR[24:20]}),
    .Type_S_Imm({ID_IR[31], funct[4], ID_IR[29:26], funct[3], ID_IR[11:7]}),
    .Type_B_Imm({ID_IR[31], ID_IR[7], funct[4], ID_IR[29:26], funct[3], ID_IR[11:8]}),
    .Type_J_Imm({ID_IR[31], ID_IR[19:15], funct[2:0], ID_IR[20], funct[4], ID_IR[29:26], funct[3], ID_IR[24:21]}),
    .Op6(ID_IR[6]), .I(IF_I), .Op5(ID_IR[5]), .S(IF_S), .Op4(ID_IR[4]), .B(IF_B), .Op3(ID_IR[3]), .J(IF_J),
    .Op2(ID_IR[2]), .System(System));
  Pull_Resistor #(.pull(1)) pull_resistor_4 (.node(CLK));
  Regifile regifile_1 (
    .Din(RDin), .Clk(CLK), .R1(regifile_1_r1), .R2(regifile_1_r2), .WE(RegWrite),
    .W_num(ex_mem_wd_cmdreg_2_c_5_2), .R1_num(Rs), .R2_num(Rt));
  or or_13 (or_13_out, Go, not_3_out);
  not not_3 (not_3_out, halt_t);
  PC_IR_cmdReg pc_ir_cmdreg_2 (
    .PC(ID_PC), .IR({ID_IR[31], funct[4], ID_IR[29:26], funct[3], ID_IR[24:15], funct[2:0], ID_IR[11:0]}),
    .PC_2(EX_PC), .IR_2(EX_IR), .Run(or_5_out), .CLK(CLK), .Clear(RST), .AsyClear(or_15_out));
  or or_14 (or_14_out, Branch, RST);
  Counter #(.width(16), .max('hffff), .ongoal("wrap"), .trigger("rising"), .behavior("new")) counter_2 (
    .D({16{1'b0}}), .count(or_13_out), .Q(\总周期数 ), .clk(CLK), .clr(RST));  // open: load, carry, preset, down
  Multiplexer #(.select(1), .width(32), .disabled("Z"), .enable("false")) multiplexer_9 (
    .in0(regifile_1_r1), .in1({32{1'b0}}), .out(multiplexer_9_out), .sel(LoadConflict));
  Multiplexer #(.select(1), .width(32), .disabled("Z"), .enable("false")) multiplexer_10 (
    .in0(regifile_1_r2), .in1({32{1'b0}}), .out(multiplexer_10_out), .sel(LoadConflict));
  Multiplexer #(.select(1), .width(5), .disabled("Z"), .enable("false")) multiplexer_11 (
    .in0(ID_IR[11:7]), .in1({5{1'b0}}), .out(multiplexer_11_out), .sel(LoadConflict));
  Multiplexer #(.select(1), .width(32), .disabled("Z"), .enable("false")) multiplexer_12 (
    .in0(immvaluegen_1_imm), .in1({32{1'b0}}), .out(multiplexer_12_out), .sel(LoadConflict));
  Multiplexer #(.select(1), .width(1), .disabled("Z"), .enable("false")) multiplexer_13 (
    .in0(IF_J), .in1(1'b0), .out(multiplexer_13_out), .sel(LoadConflict));
  Multiplexer #(.select(1), .width(1), .disabled("Z"), .enable("false")) multiplexer_14 (
    .in0(IF_B), .in1(1'b0), .out(multiplexer_14_out), .sel(LoadConflict));
  or or_15 (or_15_out, INTR, RST, LoadConflict, Branch);
  Mul_cmdClear mul_cmdclear_1 (
    .Clear(or_15_out), .lh(\单周期硬布线控制器_1_lh ), .uret(\单周期硬布线控制器_1_uret ), .JALR(\单周期硬布线控制器_1_jalr ),
    .JAL(\单周期硬布线控制器_1_jal ), .Bne(\单周期硬布线控制器_1_bne ), .Beq(\单周期硬布线控制器_1_beq ),
    .MemToReg(\单周期硬布线控制器_1_memtoreg ), .MemWrite(\单周期硬布线控制器_1_memwrite ), .Alu_OP(\单周期硬布线控制器_1_alu_op ),
    .Alu_Src(IF_Alu_Src), .RegWrite(\单周期硬布线控制器_1_regwrite ), .S_Type(IF_S_Type), .ecall(\单周期硬布线控制器_1_ecall ),
    .lh_2(mul_cmdclear_1_lh_2), .uret_2(mul_cmdclear_1_uret_2), .JALR_2(mul_cmdclear_1_jalr_2),
    .JAL_2(mul_cmdclear_1_jal_2), .Bne_2(mul_cmdclear_1_bne_2), .Beq_2(mul_cmdclear_1_beq_2),
    .MemToReg_2(mul_cmdclear_1_memtoreg_2), .MemWrite_2(mul_cmdclear_1_memwrite_2),
    .Alu_OP_2(mul_cmdclear_1_alu_op_2), .Alu_Src_2(mul_cmdclear_1_alu_src_2),
    .RegWrite_2(mul_cmdclear_1_regwrite_2), .S_Type_2(mul_cmdclear_1_s_type_2),
    .ecall_2(mul_cmdclear_1_ecall_2), .bltu(\单周期硬布线控制器_1_bltu ), .bltu_2(mul_cmdclear_1_bltu_2),
    .lw(\单周期硬布线控制器_1_lw ), .lw_2(mul_cmdclear_1_lw_2), .CSR_2(mul_cmdclear_1_csr_2));  // open: CSR
  Mul_cmdReg mul_cmdreg_1 (
    .lh(mul_cmdclear_1_lh_2), .Bne(mul_cmdclear_1_bne_2), .Alu_OP(mul_cmdclear_1_alu_op_2),
    .uret(mul_cmdclear_1_uret_2), .Beq(mul_cmdclear_1_beq_2), .Alu_Src(mul_cmdclear_1_alu_src_2),
    .JALR(mul_cmdclear_1_jalr_2), .MemToReg(mul_cmdclear_1_memtoreg_2), .RegWrite(mul_cmdclear_1_regwrite_2),
    .JAL(mul_cmdclear_1_jal_2), .MemWrite(mul_cmdclear_1_memwrite_2), .S_Type(mul_cmdclear_1_s_type_2),
    .ecall(mul_cmdclear_1_ecall_2), .CLK(CLK), .lh_2(mul_cmdreg_1_lh_2), .Bne_2(EX_Bne),
    .Alu_OP_2(mul_cmdreg_1_alu_op_2), .uret_2(EX_URET), .Beq_2(EX_Beq), .Alu_Src_2(mul_cmdreg_1_alu_src_2),
    .JALR_2(EX_JALR), .MemToReg_2(EX_MemToReg), .RegWrite_2(EX_RegWrite), .JAL_2(EX_JAL),
    .MemWrite_2(mul_cmdreg_1_memwrite_2), .S_Type_2(mul_cmdreg_1_s_type_2), .ecall_2(mul_cmdreg_1_ecall_2),
    .RST(RST), .bltu(mul_cmdclear_1_bltu_2), .bltu_2(EX_bltu), .lw_2(mul_cmdreg_1_lw_2),
    .lw(mul_cmdclear_1_lw_2), .CSR(mul_cmdclear_1_csr_2));  // open: CSR_2
  IF_EX_cmdReg if_ex_cmdreg_1 (
    .R1(multiplexer_9_out), .R2(multiplexer_10_out), .writeAddr(multiplexer_11_out),
    .Imm(multiplexer_12_out), .J(multiplexer_13_out), .B(multiplexer_14_out), .R1_2(if_ex_cmdreg_1_r1_2),
    .R2_2(if_ex_cmdreg_1_r2_2), .writeAddr_2(EX_Reg), .Imm_2(if_ex_cmdreg_1_imm_2), .J_2(EX_J), .B_2(EX_B),
    .CLK(CLK), .Clear(or_14_out));
  Shifter #(.width(32), .shift("ll")) shifter_1 (.in(if_ex_cmdreg_1_imm_2), .\dist (5'b00001), .out(shifter_1_out));
  and and_5 (and_5_out, ex_equal, EX_Beq);
  and and_6 (and_6_out, ~ex_equal, EX_Bne);  // AND_Gate
  and and_7 (and_7_out, EX_bltu, ex_less);
  and and_8 (Halt, mul_cmdreg_1_ecall_2, ~ex_equal);  // AND_Gate
  and and_9 (and_9_out, mul_cmdreg_1_ecall_2, ex_equal);
  or or_16 (or_16_out, and_5_out, and_6_out, and_7_out);
  Multiplexer #(.select(2), .width(32), .disabled("Z"), .enable("false")) multiplexer_15 (
    .in0(if_ex_cmdreg_1_r1_2), .in1(RDin), .in2(ex_mem_wd_cmdreg_1_a_32_2), .in3(ex_mem_wd_cmdreg_1_a_32_2),
    .out(multiplexer_15_out), .sel(RsFoward));
  Multiplexer #(.select(2), .width(32), .disabled("Z"), .enable("false")) multiplexer_16 (
    .in0(if_ex_cmdreg_1_r2_2), .in1(RDin), .in2(ex_mem_wd_cmdreg_1_a_32_2), .in3(ex_mem_wd_cmdreg_1_a_32_2),
    .out(multiplexer_16_out), .sel(RtFoward));
  Multiplexer #(.select(1), .width(32), .disabled("Z"), .enable("false")) multiplexer_17 (
    .in0({alu_1_result, 1'b0}), .in1(shifter_1_out), .out(multiplexer_17_out), .sel(or_17_out));
  Multiplexer #(.select(1), .width(32), .disabled("Z"), .enable("false")) multiplexer_18 (
    .in0(EX_PC), .in1({32{1'b0}}), .out(multiplexer_18_out), .sel(EX_JALR));
  or or_17 (or_17_out, EX_B, EX_JAL);
  Multiplexer #(.select(1), .width(32), .disabled("Z"), .enable("false")) multiplexer_19 (
    .in0(multiplexer_15_out), .in1(32'h22), .out(multiplexer_19_out), .sel(mul_cmdreg_1_ecall_2));
  Multiplexer #(.select(1), .width(32), .disabled("Z"), .enable("false")) multiplexer_20 (
    .in0(multiplexer_16_out), .in1(if_ex_cmdreg_1_imm_2), .out(multiplexer_20_out),
    .sel(mul_cmdreg_1_alu_src_2));
  Register #(.width(32), .trigger("rising"), .Select("low")) register_5 (
    .D(multiplexer_21_out), .en(and_9_out), .Q(LedData), .clk(CLK));  // open: clr
  Multiplexer #(.select(1), .width(32), .disabled("Z"), .enable("false")) multiplexer_21 (
    .in0(multiplexer_15_out), .in1({32{1'b0}}), .out(multiplexer_21_out), .sel(or_14_out));
  Adder #(.width(32)) adder_2 (.a(multiplexer_17_out), .b(multiplexer_18_out), .out(offset), .cin(1'b0));  // open: cout
  or or_18 (or_18_out, or_16_out, EX_JALR, EX_J);
  PC_IR_cmdReg pc_ir_cmdreg_3 (
    .PC(EX_PC), .IR(EX_IR), .PC_2(M_PC), .IR_2(MEM_IR), .Run(or_5_out), .CLK(CLK), .Clear(RST),
    .AsyClear(1'b0));
  ALU alu_1 (
    .X(multiplexer_19_out), .Y(multiplexer_20_out), .AluOP(mul_cmdreg_1_alu_op_2), .Equal(ex_equal),
    .Result({alu_1_result, alu_1_result_2[0]}), .out_6(ex_less));  // open: Result_2, out_4
  and and_10 (Branch, or_18_out, ~LoadConflict);  // AND_Gate
  Mul_cmdReg mul_cmdreg_2 (
    .lh(mul_cmdreg_1_lh_2), .Bne(EX_Bne), .Alu_OP(mul_cmdreg_1_alu_op_2), .uret(EX_URET), .Beq(EX_Beq),
    .Alu_Src(mul_cmdreg_1_alu_src_2), .JALR(EX_JALR), .MemToReg(EX_MemToReg), .RegWrite(EX_RegWrite),
    .JAL(EX_JAL), .MemWrite(mul_cmdreg_1_memwrite_2), .S_Type(mul_cmdreg_1_s_type_2),
    .ecall(mul_cmdreg_1_ecall_2), .CLK(CLK), .lh_2(mul_cmdreg_2_lh_2), .Bne_2(mul_cmdreg_2_bne_2),
    .Alu_OP_2(mul_cmdreg_2_alu_op_2), .uret_2(mul_cmdreg_2_uret_2), .Beq_2(mul_cmdreg_2_beq_2),
    .Alu_Src_2(mul_cmdreg_2_alu_src_2), .JALR_2(mul_cmdreg_2_jalr_2), .MemToReg_2(mul_cmdreg_2_memtoreg_2),
    .RegWrite_2(MEM_RegWrite), .JAL_2(mul_cmdreg_2_jal_2), .MemWrite_2(MemWrite),
    .S_Type_2(mul_cmdreg_2_s_type_2), .ecall_2(mul_cmdreg_2_ecall_2), .RST(RST), .bltu(EX_bltu),
    .bltu_2(mul_cmdreg_2_bltu_2), .lw_2(mul_cmdreg_2_lw_2), .lw(mul_cmdreg_1_lw_2));  // open: CSR_2, CSR
  EX_MEM_WD_cmdReg ex_mem_wd_cmdreg_1 (
    .A_32({alu_1_result, alu_1_result_2[0]}), .B_32(multiplexer_16_out), .C_5(EX_Reg),
    .A_32_2(ex_mem_wd_cmdreg_1_a_32_2), .B_32_2(MDin), .C_5_2(MEM_Reg), .CLK(CLK), .Clear(RST));  // open: halt, halt_2
  LoadConflict loadconflict_1 (
    .Rt_Used(or_19_out), .Rs(Rs), .Rt(Rt), .EX_MemRead(EX_MemToReg), .EX_RegWrite(EX_Reg),
    .LoadUsed(LoadConflict));
  or or_19 (or_19_out, IF_S_Type, not_4_out);
  not not_4 (not_4_out, IF_Alu_Src);
  RAM #(.addrWidth(10), .dataWidth(32), .bus("separate"), .Select("high")) ram_1 (
    .addr(ex_mem_wd_cmdreg_1_a_32_2[11:2]), .din(MDin), .data(ram_1_data), .str(MemWrite), .sel(1'b1),
    .clk(CLK), .ld(1'b1), .clr(RST));
  // Probe on redirectionconflict_1_rsfoward
  // Probe on redirectionconflict_1_rtfoward
  RedirectionConflict redirectionconflict_1 (
    .Rt_Used(or_20_out), .RsFoward(redirectionconflict_1_rsfoward),
    .RtFoward(redirectionconflict_1_rtfoward), .EX_RegWrite(EX_RegWrite), .EX_Reg(EX_Reg),
    .MEM_RegWrite(MEM_RegWrite), .MEM_Reg(MEM_Reg), .Rs(Rs), .Rt(Rt));
  Register #(.width(2), .trigger("rising"), .Select("low")) register_6 (
    .D(redirectionconflict_1_rsfoward), .en(1'b1), .Q(RsFoward), .clk(CLK), .clr(1'b0), .cs(1'b0),
    .preset(1'b0));
  Register #(.width(2), .trigger("rising"), .Select("low")) register_7 (
    .D(redirectionconflict_1_rtfoward), .en(1'b1), .Q(RtFoward), .clk(CLK), .clr(1'b0), .cs(1'b0),
    .preset(1'b0));
  or or_20 (or_20_out, not_5_out, IF_S_Type);
  PC_IR_cmdReg pc_ir_cmdreg_4 (
    .PC(M_PC), .IR(MEM_IR), .PC_2(WB_PC), .IR_2(WB_IR), .Run(or_5_out), .CLK(CLK), .Clear(RST),
    .AsyClear(1'b0));
  not not_5 (not_5_out, IF_Alu_Src);
  Mul_cmdReg mul_cmdreg_3 (
    .lh(mul_cmdreg_2_lh_2), .Bne(mul_cmdreg_2_bne_2), .Alu_OP(mul_cmdreg_2_alu_op_2),
    .uret(mul_cmdreg_2_uret_2), .Beq(mul_cmdreg_2_beq_2), .Alu_Src(mul_cmdreg_2_alu_src_2),
    .JALR(mul_cmdreg_2_jalr_2), .MemToReg(mul_cmdreg_2_memtoreg_2), .RegWrite(MEM_RegWrite),
    .JAL(mul_cmdreg_2_jal_2), .MemWrite(MemWrite), .S_Type(mul_cmdreg_2_s_type_2),
    .ecall(mul_cmdreg_2_ecall_2), .CLK(CLK), .lh_2(mul_cmdreg_3_lh_2), .Bne_2(mul_cmdreg_3_bne_2),
    .Alu_OP_2(mul_cmdreg_3_alu_op_2), .uret_2(mul_cmdreg_3_uret_2), .Beq_2(mul_cmdreg_3_beq_2),
    .Alu_Src_2(mul_cmdreg_3_alu_src_2), .JALR_2(mul_cmdreg_3_jalr_2), .MemToReg_2(mul_cmdreg_3_memtoreg_2),
    .RegWrite_2(RegWrite), .JAL_2(mul_cmdreg_3_jal_2), .MemWrite_2(mul_cmdreg_3_memwrite_2),
    .S_Type_2(mul_cmdreg_3_s_type_2), .ecall_2(mul_cmdreg_3_ecall_2), .RST(RST), .bltu(mul_cmdreg_2_bltu_2),
    .bltu_2(mul_cmdreg_3_bltu_2), .lw_2(mul_cmdreg_3_lw_2), .lw(mul_cmdreg_2_lw_2));  // open: CSR_2, CSR
  EX_MEM_WD_cmdReg ex_mem_wd_cmdreg_2 (
    .A_32(ex_mem_wd_cmdreg_1_a_32_2), .B_32(ram_1_data), .C_5(MEM_Reg), .A_32_2(ex_mem_wd_cmdreg_2_a_32_2),
    .B_32_2(ex_mem_wd_cmdreg_2_b_32_2), .C_5_2(ex_mem_wd_cmdreg_2_c_5_2), .CLK(CLK), .Clear(RST));  // open: halt, halt_2
  Multiplexer #(.select(1), .width(32), .disabled("Z"), .enable("false")) multiplexer_22 (
    .in0(ex_mem_wd_cmdreg_2_a_32_2), .in1(ex_mem_wd_cmdreg_2_b_32_2), .out(multiplexer_22_out),
    .sel(mul_cmdreg_3_memtoreg_2));
  or or_21 (or_21_out, Halt, halt_t);
  Adder #(.width(32)) adder_3 (.a(WB_PC), .b(32'h4), .out(adder_3_out));  // open: cin, cout
  Multiplexer #(.select(1), .width(32), .disabled("Z"), .enable("false")) multiplexer_23 (
    .in0(multiplexer_22_out), .in1(adder_3_out), .out(RDin), .sel(or_22_out));
  D_Flip_Flop #(.trigger("falling"), .Pre_Clr_Positions("ABOVE_BELOW"), .NegatePresetClear("false"), .enable("false"), .NewFFLayout("false")) d_ff_9 (
    .clk(CLK), .D(or_21_out), .Q(halt_t), .reset(Go));  // open: Qn, preset
  or or_22 (or_22_out, mul_cmdreg_3_jal_2, mul_cmdreg_3_jalr_2, mul_cmdreg_3_uret_2);

  // Other names for the same wires on the sheet: IR21 = ID_IR[21]; ID_IR (some bits) = funct;
  //   opcode[4:0] = ID_IR[6:2]; MEM_PC[31:0] = M_PC

  // Notes on the sheet:
  //   中断源
  //   时空图监测，可删除
  //   中断等待指示
  //   Branch select
  //   PC+4
  //   Keep address
  //   Do not update original PC
  //   In the non-interrupt program, URET and 3 INTR/ are 0
  //   while INTR is true, the circuit should store the original address
  //   数码管输出
  //   Select Interrupt-cmd address while triggered
  //   2nd Or gate is used for distinguish the transform from normal process to interrupt process
  //   select corresponding CLR signal while excuting URET
  //   No CLR request
  //   contents of Instruction_Memory (hex, n*v repeats v):
  //   7d000113 100413 1f41993 41f9d993 433 c00913 800b13 140413 f47413 800293 100313 499993 89e9b3 1300533
  //   2200893 73 406282b3 fe0294e3 140413 f00f93 1f47433 1c41413 800293 100313 49d993 89e9b3 1300533
  //   2200893 73 406282b3 fe0294e3 1c45413 406b0b33 b0463 f95ff06f 2b3 fff2c293 1029293 fff2e293 500533
  //   2200893 73 f5dff06f 1112023 410113 a12023 410113 812023 410113 1312023 410113 1412023 410113 1512023
  //   410113 1612023 410113 100b13 300a13 100a93 1600433 441413 14469b3 1300533 2200893 73 fe0416e3
  //   415a0a33 fe0a10e3 ffc10113 12b03 ffc10113 12a83 ffc10113 12a03 ffc10113 12983 ffc10113 12403
  //   ffc10113 12503 ffc10113 12883 200073 1112023 410113 a12023 410113 812023 410113 1312023 410113
  //   1412023 410113 1512023 410113 1612023 410113 200b13 300a13 100a93 1600433 441413 14469b3 1300533
  //   2200893 73 fe0416e3 415a0a33 fe0a10e3 ffc10113 12b03 ffc10113 12a83 ffc10113 12a03 ffc10113 12983
  //   ffc10113 12403 ffc10113 12503 ffc10113 12883 200073 1112023 410113 a12023 410113 812023 410113
  //   1312023 410113 1412023 410113 1512023 410113 1612023 410113 300b13 300a13 100a93 1600433 441413
  //   14469b3 1300533 2200893 73 fe0416e3 415a0a33 fe0a10e3 ffc10113 12b03 ffc10113 12a83 ffc10113 12a03
  //   ffc10113 12983 ffc10113 12403 ffc10113 12503 ffc10113 12883 200073
  //   控制位
  //   流水调试日志用
  //   暂停节拍，不能为0
  //   PC
  //   IR
  //   Conflict
  //   Run
  //   CLK
  //   RST
  //   戳工具置1进入计数暂停模式，ctrl+k时钟自动运行到对应节拍暂停
  //   ctrl+k关闭时钟连续运行，将控制位置零，进入单步调试模式调试
  //   especailly for ecall
  //   I-type command
  //   S-type command
  //   B-type command
  //   J-type command
  //   Data Conflict Hazzard
  //   IR21
  //   opcode
  //   funct
  //   OpCode
  //   ecall
  //   可计数暂停的时钟源
  //   lw
  //   lh
  //   uret
  //   JALR
  //   JAL
  //   Bne
  //   Beq
  //   MemToReg
  //   MemWrite
  //   Alu_OP
  //   Alu_Src
  //   RegWrite
  //   bltu
  //   S_Type
  //   ecall
  //   R1
  //   R2
  //   Imm
  //   PC
  //   IR
  //   conflict
  //   Run
  //   CLK
  //   RST
  //   为方便自动评测，需要输出流水线各段保存的PC值，注意是PC不是PC+4，另外ID段寄存器写入信息，Mem段内存写入信息也要输出
  //   J
  //   B
  //   lw
  //   lh
  //   uret
  //   JALR
  //   JAL
  //   Bne
  //   Beq
  //   MemToReg
  //   MemWrite
  //   Alu_OP
  //   Alu_Src
  //   RegWrite
  //   bltu
  //   S_Type
  //   ecall
  //   R1
  //   R2
  //   especailly for ecall
  //   write Address
  //   Imm
  //   Beq
  //   Bne
  //   bltu
  //   JALR Jumping
  //   B-Type Jumping
  //   Imm
  //   Bne, Beq & bltu: func3 of 3 instructions is different
  //   with 000 for Beq, 001 for Bne and 110 for bltu, respectively
  //   B type jump
  //   SrcA
  //   SrcB
  //   J type jump
  //   Only JAL is J-type instruction
  //   PC
  //   IR
  //   Run
  //   CLK
  //   RST
  //   conflict
  //   lw
  //   lh
  //   uret
  //   JALR
  //   JAL
  //   Bne
  //   Beq
  //   MemToReg
  //   MemWrite
  //   Alu_OP
  //   Alu_Src
  //   RegWrite
  //   S_Type
  //   ecall
  //   Result
  //   R2
  //   write Address
  //   Conflict Judgement of lw & lh
  //   S-type cmd use rs&rt
  //   In EX part, only branch would need to clear
  //   Data
  //   PC
  //   IR
  //   conflict
  //   Run
  //   CLK
  //   RST
  //   lw
  //   lh
  //   uret
  //   JAL
  //   Bne
  //   Beq
  //   Result
  //   Data
  //   write Address
  //   JALR
  //   MemToReg
  //   MemWrite
  //   Alu_OP
  //   Alu_Src
  //   RegWrite
  //   S_Type
  //   ecall
  //   WriteData
  //   set $rd while jumping
endmodule
module \流水线_多级中断_EX阶段  (
  output RegWrite,
  output MemWrite,
  output [31:0] IF_PC,
  output [31:0] ID_PC,
  output [31:0] EX_PC,
  output [31:0] M_PC,
  output [31:0] WB_PC,
  output [31:0] RDin,
  output [31:0] MDin,
  output [31:0] LedData
);

  wire and_1_out, and_2_out, and_3_out, and_4_out, and_8_out, and_9_out, and_10_out, and_11_out, Branch, CLK,
       clock_1_out, CLR1, CLR2, CLR3, comparator_1_eq, comparator_2_lt, comparator_3_eq, comparator_3_lt,
       Conflict, d_ff_1_q, d_ff_2_q, d_ff_3_q, d_ff_4_q, d_ff_5_q, d_ff_9_q, EX_B, EX_Beq, EX_bltu, EX_Bne,
       EX_CSR, EX_CSRRCI, EX_CSRRSI, ex_equal, EX_J, EX_JAL, EX_JALR, ex_less, EX_MemToReg, EX_RegWrite,
       EX_URET, Go, halt, ID_URET, IF_Alu_Src, IF_B, IF_I, IF_J, IF_S, IF_S_Type, INTR, INTR1, INTR2, INTR3,
       IR1, IR2, IR3, LoadConflict, MEM_RegWrite, mul_cmdclear_1_alu_src_2, mul_cmdclear_1_beq_2,
       mul_cmdclear_1_bltu_2, mul_cmdclear_1_bne_2, mul_cmdclear_1_csr_2, mul_cmdclear_1_ecall_2,
       mul_cmdclear_1_jal_2, mul_cmdclear_1_jalr_2, mul_cmdclear_1_lh_2, mul_cmdclear_1_lw_2,
       mul_cmdclear_1_memtoreg_2, mul_cmdclear_1_memwrite_2, mul_cmdclear_1_regwrite_2,
       mul_cmdclear_1_s_type_2, mul_cmdclear_1_uret_2, mul_cmdreg_1_alu_src_2, mul_cmdreg_1_ecall_2,
       mul_cmdreg_1_lh_2, mul_cmdreg_1_lw_2, mul_cmdreg_1_memwrite_2, mul_cmdreg_1_s_type_2,
       mul_cmdreg_2_alu_src_2, mul_cmdreg_2_beq_2, mul_cmdreg_2_bltu_2, mul_cmdreg_2_bne_2,
       mul_cmdreg_2_csr_2, mul_cmdreg_2_ecall_2, mul_cmdreg_2_jal_2, mul_cmdreg_2_jalr_2, mul_cmdreg_2_lh_2,
       mul_cmdreg_2_lw_2, mul_cmdreg_2_memtoreg_2, mul_cmdreg_2_s_type_2, mul_cmdreg_2_uret_2,
       mul_cmdreg_3_alu_src_2, mul_cmdreg_3_beq_2, mul_cmdreg_3_bltu_2, mul_cmdreg_3_bne_2,
       mul_cmdreg_3_csr_2, mul_cmdreg_3_ecall_2, mul_cmdreg_3_jal_2, mul_cmdreg_3_jalr_2, mul_cmdreg_3_lh_2,
       mul_cmdreg_3_lw_2, mul_cmdreg_3_memtoreg_2, mul_cmdreg_3_memwrite_2, mul_cmdreg_3_s_type_2,
       mul_cmdreg_3_uret_2, multiplexer_18_out, multiplexer_19_out, nand_1_out, not_1_out, not_2_out,
       not_3_out, not_4_out, or_1_out, or_2_out, or_3_out, or_4_out, or_5_out, or_9_out, or_10_out,
       or_11_out, or_12_out, or_13_out, or_14_out, or_15_out, or_16_out, or_17_out, or_18_out, or_19_out,
       or_20_out, or_21_out, RST, System, W1, W2, W3, \单周期硬布线控制器_1_beq , \单周期硬布线控制器_1_bltu ,
       \单周期硬布线控制器_1_bne , \单周期硬布线控制器_1_csr , \单周期硬布线控制器_1_ecall , \单周期硬布线控制器_1_jal , \单周期硬布线控制器_1_jalr ,
       \单周期硬布线控制器_1_lh , \单周期硬布线控制器_1_lw , \单周期硬布线控制器_1_memtoreg , \单周期硬布线控制器_1_memwrite ,
       \单周期硬布线控制器_1_regwrite ;
  wire [0:0] alu_1_result_2;
  wire [1:0] CUR_INTR, multiplexer_7_out, multiplexer_10_out, multiplexer_11_out, priority_encoder_1_out,
       priority_encoder_2_out, priority_encoder_3_out, redirectionconflict_1_rsfoward,
       redirectionconflict_1_rtfoward, register_5_q, register_6_q, RsFoward, RtFoward;
  wire [3:0] EX_Alu_OP, mul_cmdclear_1_alu_op_2, mul_cmdreg_2_alu_op_2, mul_cmdreg_3_alu_op_2,
       \单周期硬布线控制器_1_alu_op ;
  wire [4:0] ex_mem_wd_cmdreg_2_c_5_2, EX_Reg, funct, MEM_Reg, multiplexer_16_out, Rs, Rt;
  wire [12:0] CNT_num;
  wire [15:0] \LoadUse次数 , \总周期数 , \插入气泡数 , \无条件分支数 , \条件分支成功数 ;
  wire [31:0] adder_1_out, adder_3_out, EX_IR, ex_mem_wd_cmdreg_1_a_32_2, ex_mem_wd_cmdreg_2_a_32_2,
       ex_mem_wd_cmdreg_2_b_32_2, ID_IR, if_ex_cmdreg_1_imm_2, if_ex_cmdreg_1_r1_2, if_ex_cmdreg_1_r2_2,
       IF_IR, immvaluegen_1_imm, INTR_PC, MEM_IR, multiplexer_1_out, multiplexer_2_out, multiplexer_3_out,
       multiplexer_5_out, multiplexer_6_out, multiplexer_8_out, multiplexer_9_out, multiplexer_14_out,
       multiplexer_15_out, multiplexer_17_out, multiplexer_20_out, multiplexer_21_out, multiplexer_22_out,
       multiplexer_23_out, multiplexer_24_out, multiplexer_25_out, multiplexer_26_out, multiplexer_27_out,
       offset, pc_ir_cmdreg_1_ir_2, pc_ir_cmdreg_1_pc_2, ram_1_data, regifile_1_r1, regifile_1_r2,
       register_1_q, register_2_q, register_4_q, shifter_1_out, WB_IR;
  wire [31:1] alu_1_result;

  Button \u_总复位  (.out(RST));
  Button _1 (.out(IR1));
  Button _2 (.out(IR2));
  Button _3 (.out(IR3));
  // Probe on \总周期数 
  // Probe on \总周期数 
  Button \u_继续运行  (.out(Go));
  LED #(.active("true")) led_1 (.in(W1));
  LED #(.active("true")) led_2 (.in(W2));
  LED #(.active("true")) led_3 (.in(W3));
  Adder #(.width(32)) adder_1 (.a(IF_PC), .b(32'h4), .out(adder_1_out));  // open: cin, cout
  Multiplexer #(.select(1), .width(32), .disabled("Z"), .enable("false")) multiplexer_1 (
    .in0(multiplexer_3_out), .in1(register_2_q), .out(multiplexer_1_out), .sel(EX_URET));
  Hex_Digit_Display hex_digit_display_1 (.value(LedData[31:28]));  // open: dp
  // Probe on IF_PC[19:0]
  // RiscV_Probe riscv_probe_1: pin names not known; wires that end beside it: IF_IR
  Button button_1 (.out(halt));
  Multiplexer #(.select(1), .width(32), .disabled("Z"), .enable("false")) multiplexer_2 (
    .in0(adder_1_out), .in1(offset), .out(multiplexer_2_out), .sel(Branch));
  Multiplexer #(.select(1), .width(32), .disabled("Z"), .enable("false")) multiplexer_3 (
    .in0(ID_PC), .in1(multiplexer_5_out), .out(multiplexer_3_out), .sel(Branch));
  Register #(.width(32), .trigger("rising"), .Select("low")) register_1 (
    .D(multiplexer_1_out), .en(or_1_out), .Q(register_1_q), .clk(CLK));  // open: clr
  or or_1 (or_1_out, EX_URET, INTR);
  Multiplexer #(.select(2), .width(32), .disabled("Z"), .enable("false")) multiplexer_4 (
    .in1(32'h30ac), .in2(32'h3158), .in3(32'h3204), .out(INTR_PC), .sel(priority_encoder_1_out));  // open: in0
  Priority_Encoder #(.select(2), .disabled("Z")) priority_encoder_1 (
    .in0(1'b1), .in1(INTR1), .in2(INTR2), .in3(INTR3), .out(priority_encoder_1_out));  // open: gs, en_out, en_in
  or or_2 (or_2_out, INTR1, INTR2, INTR3);
  D_Flip_Flop #(.trigger("rising"), .Pre_Clr_Positions("LEGACY"), .NegatePresetClear("false"), .enable("true"), .NewFFLayout("false")) d_ff_1 (
    .clk(CLK), .D(EX_CSRRSI), .Q(d_ff_1_q), .en(EX_CSR));  // open: Qn, preset, reset
  Hex_Digit_Display hex_digit_display_2 (.value(LedData[23:20]));  // open: dp
  Hex_Digit_Display hex_digit_display_3 (.value(LedData[27:24]));  // open: dp
  // Probe on ID_PC[19:0]
  // RiscV_Probe riscv_probe_2: pin names not known; wires that end beside it: {ID_IR[31], funct[4], ID_IR[29:26], funct[3], ID_IR[24:15], funct[2:0], ID_IR[11:0]}
  Multiplexer #(.select(1), .width(32), .disabled("Z"), .enable("false")) multiplexer_5 (
    .in0(multiplexer_2_out), .in1(IF_PC), .out(multiplexer_5_out), .sel(LoadConflict));
  Multiplexer #(.select(1), .width(32), .disabled("Z"), .enable("false")) multiplexer_6 (
    .in0(register_1_q), .in1(register_4_q), .out(multiplexer_6_out), .sel(EX_URET));
  Multiplexer #(.select(1), .width(2), .disabled("Z"), .enable("false")) multiplexer_7 (
    .in0(priority_encoder_1_out), .in1(register_5_q), .out(multiplexer_7_out), .sel(EX_URET));
  or or_3 (or_3_out, EX_URET, INTR);
  or or_4 (or_4_out, ~or_2_out, EX_URET, EX_CSRRSI, and_1_out);  // OR_Gate
  and and_1 (and_1_out, d_ff_1_q, ~EX_CSRRCI);  // AND_Gate
  Hex_Digit_Display hex_digit_display_4 (.value(LedData[19:16]));  // open: dp
  Hex_Digit_Display hex_digit_display_5 (.value(LedData[15:12]));  // open: dp
  Register #(.width(32), .trigger("rising"), .Select("low")) register_2 (
    .D(multiplexer_6_out), .en(or_1_out), .Q(register_2_q), .clk(CLK));  // open: clr
  Multiplexer #(.select(1), .width(32), .disabled("Z"), .enable("false")) multiplexer_8 (
    .in0(register_2_q), .out(multiplexer_8_out), .sel(EX_URET));  // open: in1
  Register #(.width(2), .trigger("rising"), .Select("low")) register_3 (
    .D(multiplexer_7_out), .en(or_3_out), .Q(CUR_INTR), .clk(CLK));  // open: clr
  D_Flip_Flop #(.trigger("rising"), .Pre_Clr_Positions("LEGACY"), .NegatePresetClear("false"), .enable("true"), .NewFFLayout("false")) d_ff_2 (
    .clk(CLK), .D(or_4_out), .Q(d_ff_2_q));  // open: Qn, preset, en, reset
  Hex_Digit_Display hex_digit_display_6 (.value(LedData[7:4]));  // open: dp
  Hex_Digit_Display hex_digit_display_7 (.value(LedData[11:8]));  // open: dp
  // Probe on EX_PC[19:0]
  // RiscV_Probe riscv_probe_3: pin names not known; wires that end beside it: EX_IR
  Multiplexer #(.select(2), .width(32), .disabled("Z"), .enable("false")) multiplexer_9 (
    .in0(multiplexer_5_out), .in1(INTR_PC), .in2(register_1_q), .out(multiplexer_9_out),
    .sel(priority_encoder_2_out));  // open: in3
  Priority_Encoder #(.select(2), .disabled("Z")) priority_encoder_2 (
    .in0(1'b1), .in1(INTR), .in2(EX_URET), .out(priority_encoder_2_out));  // open: in3, gs, en_out, en_in
  Register #(.width(32), .trigger("rising"), .Select("low")) register_4 (
    .D(multiplexer_8_out), .en(or_1_out), .Q(register_4_q), .clk(CLK));  // open: clr
  Multiplexer #(.select(1), .width(2), .disabled("Z"), .enable("false")) multiplexer_10 (
    .in0(CUR_INTR), .in1(register_6_q), .out(multiplexer_10_out), .sel(EX_URET));
  Hex_Digit_Display hex_digit_display_8 (.value(LedData[3:0]));  // open: dp
  Comparator #(.width(16), .mode("twosComplement")) comparator_1 (
    .a(\总周期数 ), .b(16'h378), .eq(comparator_1_eq));  // open: gt, lt
  Register #(.width(32), .trigger("rising"), .Select("low")) PC (
    .D(multiplexer_9_out), .en(or_5_out), .Q(IF_PC), .clk(CLK), .clr(RST));
  or or_5 (or_5_out, Go, not_1_out);
  not not_1 (not_1_out, halt);
  D_Flip_Flop #(.trigger("rising"), .Pre_Clr_Positions("LEGACY"), .NegatePresetClear("false"), .enable("true"), .NewFFLayout("false")) d_ff_3 (
    .clk(IR1), .D(1'b1), .Q(d_ff_3_q), .reset(INTR1));  // open: Qn, preset, en
  or or_6 (W1, INTR1, d_ff_3_q);
  D_Flip_Flop #(.trigger("rising"), .Pre_Clr_Positions("LEGACY"), .NegatePresetClear("false"), .enable("true"), .NewFFLayout("false")) d_ff_4 (
    .clk(IR2), .D(1'b1), .Q(d_ff_4_q), .reset(INTR2));  // open: Qn, preset, en
  or or_7 (W2, INTR2, d_ff_4_q);
  D_Flip_Flop #(.trigger("rising"), .Pre_Clr_Positions("LEGACY"), .NegatePresetClear("false"), .enable("true"), .NewFFLayout("false")) d_ff_5 (
    .clk(IR3), .D(1'b1), .Q(d_ff_5_q), .reset(INTR3));  // open: Qn, preset, en
  or or_8 (W3, INTR3, d_ff_5_q);
  Register #(.width(2), .trigger("rising"), .Select("low")) register_5 (
    .D(multiplexer_10_out), .en(or_3_out), .Q(register_5_q), .clk(CLK));  // open: clr
  // Probe on \总周期数 
  // Probe on M_PC[19:0]
  // RiscV_Probe riscv_probe_4: pin names not known; wires that end beside it: comparator_1_eq, halt, MEM_IR
  or or_9 (or_9_out, d_ff_3_q, INTR1);
  or or_10 (or_10_out, d_ff_4_q, INTR2);
  or or_11 (or_11_out, d_ff_5_q, INTR3);
  Multiplexer #(.select(1), .width(2), .disabled("Z"), .enable("false")) multiplexer_11 (
    .in0(register_5_q), .out(multiplexer_11_out), .sel(EX_URET));  // open: in1
  Priority_Encoder #(.select(2), .disabled("Z")) priority_encoder_3 (
    .in0(1'b1), .in1(INTR1), .in2(INTR2), .in3(INTR3), .out(priority_encoder_3_out));  // open: gs, en_out, en_in
  // Probe on \总周期数 
  // Probe on \无条件分支数 
  // Probe on \条件分支成功数 
  // Probe on \插入气泡数 
  // Probe on \LoadUse次数 
  and and_2 (and_2_out, or_9_out, ~CLR1);  // AND_Gate
  and and_3 (and_3_out, or_10_out, ~CLR2);  // AND_Gate
  and and_4 (and_4_out, or_11_out, ~CLR3);  // AND_Gate
  Demultiplexer #(.select(2), .width(1), .tristate("false"), .disabled("Z"), .enable("false")) demultiplexer_1 (
    .out1(CLR1), .out2(CLR2), .out3(CLR3), .in(EX_URET), .sel(CUR_INTR));  // open: out0
  Register #(.width(2), .trigger("rising"), .Select("low")) register_6 (
    .D(multiplexer_11_out), .en(or_3_out), .Q(register_6_q), .clk(CLK));  // open: clr
  Comparator #(.width(2), .mode("unsigned")) comparator_2 (
    .a(CUR_INTR), .b(priority_encoder_3_out), .lt(comparator_2_lt));  // open: gt, eq
  and and_5 (EX_CSRRCI, EX_CSR, ~EX_Alu_OP[3]);  // AND_Gate
  and and_6 (EX_CSRRSI, EX_CSR, EX_Alu_OP[3]);
  // Probe on IF_PC[11:0]
  // Probe on WB_PC[19:0]
  // RiscV_Probe riscv_probe_5: pin names not known; wires that end beside it: WB_IR
  ROM #(.addrWidth(10), .dataWidth(32), .Select("high")) Instruction_Memory (
    .addr(IF_PC[11:2]), .data(IF_IR), .sel(1'b1));
  D_Flip_Flop #(.trigger("rising"), .Pre_Clr_Positions("LEGACY"), .NegatePresetClear("false"), .enable("true"), .NewFFLayout("false")) d_ff_6 (
    .clk(CLK), .D(and_2_out), .Q(INTR1));  // open: Qn, preset, en, reset
  D_Flip_Flop #(.trigger("rising"), .Pre_Clr_Positions("LEGACY"), .NegatePresetClear("false"), .enable("true"), .NewFFLayout("false")) d_ff_7 (
    .clk(CLK), .D(and_3_out), .Q(INTR2));  // open: Qn, preset, en, reset
  D_Flip_Flop #(.trigger("rising"), .Pre_Clr_Positions("LEGACY"), .NegatePresetClear("false"), .enable("true"), .NewFFLayout("false")) d_ff_8 (
    .clk(CLK), .D(and_4_out), .Q(INTR3));  // open: Qn, preset, en, reset
  and and_7 (INTR, comparator_2_lt, d_ff_2_q);
  // Probe on EX_PC[11:0]
  // Probe on ID_PC[11:0]
  PC_IR_cmdReg pc_ir_cmdreg_1 (
    .PC(IF_PC), .IR(IF_IR), .PC_2(pc_ir_cmdreg_1_pc_2), .IR_2(pc_ir_cmdreg_1_ir_2), .Run(or_5_out),
    .CLK(CLK), .Clear(RST), .AsyClear(or_12_out));
  or or_12 (or_12_out, Branch, INTR);
  // Probe on M_PC[11:0]
  D_Flip_Flop #(.trigger("high"), .Pre_Clr_Positions("LEGACY"), .NegatePresetClear("false"), .enable("true"), .NewFFLayout("false")) d_ff_9 (.Q(d_ff_9_q));  // open: clk, D, Qn, preset, en, reset
  // Probe on 13'hc
  // Probe on WB_PC[11:0]
  Comparator #(.width(13), .mode("twosComplement")) comparator_3 (
    .a(CNT_num), .b(13'hc), .eq(comparator_3_eq), .lt(comparator_3_lt));  // open: gt
  Clock #(.highDuration(1), .lowDuration(1)) clock_1 (.out(clock_1_out));
  DataConflict dataconflict_1 (
    .Alu_Src(IF_Alu_Src), .rs(Rs), .rt(Rt), .EX_Reg(EX_Reg), .MEM_Reg(MEM_Reg), .EX_RegWrite(EX_RegWrite),
    .MEM_RegWrite(MEM_RegWrite), .hazzard(Conflict));
  nand nand_1 (nand_1_out, d_ff_9_q, comparator_3_eq);
  Counter #(.width(13), .max('h1fff), .ongoal("stay"), .trigger("rising"), .behavior("old")) counter_1 (
    .count(comparator_3_lt), .Q(CNT_num), .clk(clock_1_out));  // open: load, D, carry, clr, preset
  LoadConflictProcessorUnit loadconflictprocessorunit_1 (
    .PC(pc_ir_cmdreg_1_pc_2), .IR(pc_ir_cmdreg_1_ir_2), .PC_2(ID_PC),
    .IR_2({ID_IR[31], funct[4], ID_IR[29:26], funct[3], ID_IR[24:15], funct[2:0], ID_IR[11:0]}),
    .Conflict(LoadConflict), .CLK(CLK));
  Multiplexer #(.select(1), .width(5), .disabled("Z"), .enable("false")) multiplexer_12 (
    .in0(ID_IR[19:15]), .in1(5'b01010), .out(Rs), .sel(\单周期硬布线控制器_1_ecall ));
  Multiplexer #(.select(1), .width(5), .disabled("Z"), .enable("false")) multiplexer_13 (
    .in0(ID_IR[24:20]), .in1(5'b10001), .out(Rt), .sel(\单周期硬布线控制器_1_ecall ));
  assign CLK = nand_1_out ? clock_1_out : 1'bz;  // Controlled_Buffer controlled_buffer_1
  \单周期硬布线控制器  \u_单周期硬布线控制器_1  (
    .Funct(funct), .OP(ID_IR[6:2]), .ALU_OP(\单周期硬布线控制器_1_alu_op ), .MemToReg(\单周期硬布线控制器_1_memtoreg ),
    .bltu(\单周期硬布线控制器_1_bltu ), .ecall(\单周期硬布线控制器_1_ecall ), .in_3(ID_IR[21]), .uret(ID_URET),
    .MemWrite(\单周期硬布线控制器_1_memwrite ), .CSR(\单周期硬布线控制器_1_csr ), .lh(\单周期硬布线控制器_1_lh ),
    .BEQ(\单周期硬布线控制器_1_beq ), .S_Type(IF_S_Type), .RegWrite(\单周期硬布线控制器_1_regwrite ), .lw(\单周期硬布线控制器_1_lw ),
    .ALU_SRC(IF_Alu_Src), .BNE(\单周期硬布线控制器_1_bne ), .JALR(\单周期硬布线控制器_1_jalr ), .JAL(\单周期硬布线控制器_1_jal ));
  ImmValueGen immvaluegen_1 (
    .Imm(immvaluegen_1_imm), .Type_I_Imm({ID_IR[31], funct[4], ID_IR[29:26], funct[3], ID_IR[24:20]}),
    .Type_S_Imm({ID_IR[31], funct[4], ID_IR[29:26], funct[3], ID_IR[11:7]}),
    .Type_B_Imm({ID_IR[31], ID_IR[7], funct[4], ID_IR[29:26], funct[3], ID_IR[11:8]}),
    .Type_J_Imm({ID_IR[31], ID_IR[19:15], funct[2:0], ID_IR[20], funct[4], ID_IR[29:26], funct[3], ID_IR[24:21]}),
    .Op6(ID_IR[6]), .I(IF_I), .Op5(ID_IR[5]), .S(IF_S), .Op4(ID_IR[4]), .B(IF_B), .Op3(ID_IR[3]), .J(IF_J),
    .Op2(ID_IR[2]), .System(System));
  Pull_Resistor #(.pull(1)) pull_resistor_1 (.node(CLK));
  Regifile regifile_1 (
    .Din(RDin), .Clk(CLK), .R1(regifile_1_r1), .R2(regifile_1_r2), .WE(RegWrite),
    .W_num(ex_mem_wd_cmdreg_2_c_5_2), .R1_num(Rs), .R2_num(Rt));
  or or_13 (or_13_out, Go, not_2_out);
  not not_2 (not_2_out, halt);
  PC_IR_cmdReg pc_ir_cmdreg_2 (
    .PC(ID_PC), .IR({ID_IR[31], funct[4], ID_IR[29:26], funct[3], ID_IR[24:15], funct[2:0], ID_IR[11:0]}),
    .PC_2(EX_PC), .IR_2(EX_IR), .Run(or_5_out), .CLK(CLK), .Clear(RST), .AsyClear(or_15_out));
  or or_14 (or_14_out, Branch, RST);
  Counter #(.width(16), .max('hffff), .ongoal("wrap"), .trigger("rising"), .behavior("new")) counter_2 (
    .D({16{1'b0}}), .count(or_13_out), .Q(\总周期数 ), .clk(CLK), .clr(RST));  // open: load, carry, preset, down
  Multiplexer #(.select(1), .width(32), .disabled("Z"), .enable("false")) multiplexer_14 (
    .in0(regifile_1_r1), .in1({32{1'b0}}), .out(multiplexer_14_out), .sel(LoadConflict));
  Multiplexer #(.select(1), .width(32), .disabled("Z"), .enable("false")) multiplexer_15 (
    .in0(regifile_1_r2), .in1({32{1'b0}}), .out(multiplexer_15_out), .sel(LoadConflict));
  Multiplexer #(.select(1), .width(5), .disabled("Z"), .enable("false")) multiplexer_16 (
    .in0(ID_IR[11:7]), .in1({5{1'b0}}), .out(multiplexer_16_out), .sel(LoadConflict));
  Multiplexer #(.select(1), .width(32), .disabled("Z"), .enable("false")) multiplexer_17 (
    .in0(immvaluegen_1_imm), .in1({32{1'b0}}), .out(multiplexer_17_out), .sel(LoadConflict));
  Multiplexer #(.select(1), .width(1), .disabled("Z"), .enable("false")) multiplexer_18 (
    .in0(IF_J), .in1(1'b0), .out(multiplexer_18_out), .sel(LoadConflict));
  Multiplexer #(.select(1), .width(1), .disabled("Z"), .enable("false")) multiplexer_19 (
    .in0(IF_B), .in1(1'b0), .out(multiplexer_19_out), .sel(LoadConflict));
  or or_15 (or_15_out, INTR, RST, LoadConflict, Branch);
  Mul_cmdReg mul_cmdreg_1 (
    .lh(mul_cmdclear_1_lh_2), .Bne(mul_cmdclear_1_bne_2), .Alu_OP(mul_cmdclear_1_alu_op_2),
    .uret(mul_cmdclear_1_uret_2), .Beq(mul_cmdclear_1_beq_2), .Alu_Src(mul_cmdclear_1_alu_src_2),
    .JALR(mul_cmdclear_1_jalr_2), .MemToReg(mul_cmdclear_1_memtoreg_2), .RegWrite(mul_cmdclear_1_regwrite_2),
    .JAL(mul_cmdclear_1_jal_2), .MemWrite(mul_cmdclear_1_memwrite_2), .S_Type(mul_cmdclear_1_s_type_2),
    .ecall(mul_cmdclear_1_ecall_2), .CLK(CLK), .lh_2(mul_cmdreg_1_lh_2), .Bne_2(EX_Bne),
    .Alu_OP_2(EX_Alu_OP), .uret_2(EX_URET), .Beq_2(EX_Beq), .Alu_Src_2(mul_cmdreg_1_alu_src_2),
    .JALR_2(EX_JALR), .MemToReg_2(EX_MemToReg), .RegWrite_2(EX_RegWrite), .JAL_2(EX_JAL),
    .MemWrite_2(mul_cmdreg_1_memwrite_2), .S_Type_2(mul_cmdreg_1_s_type_2), .ecall_2(mul_cmdreg_1_ecall_2),
    .RST(RST), .bltu(mul_cmdclear_1_bltu_2), .bltu_2(EX_bltu), .lw_2(mul_cmdreg_1_lw_2),
    .lw(mul_cmdclear_1_lw_2), .CSR_2(EX_CSR), .CSR(mul_cmdclear_1_csr_2));
  Mul_cmdClear mul_cmdclear_1 (
    .Clear(or_15_out), .lh(\单周期硬布线控制器_1_lh ), .uret(ID_URET), .JALR(\单周期硬布线控制器_1_jalr ),
    .JAL(\单周期硬布线控制器_1_jal ), .Bne(\单周期硬布线控制器_1_bne ), .Beq(\单周期硬布线控制器_1_beq ),
    .MemToReg(\单周期硬布线控制器_1_memtoreg ), .MemWrite(\单周期硬布线控制器_1_memwrite ), .Alu_OP(\单周期硬布线控制器_1_alu_op ),
    .Alu_Src(IF_Alu_Src), .RegWrite(\单周期硬布线控制器_1_regwrite ), .S_Type(IF_S_Type), .ecall(\单周期硬布线控制器_1_ecall ),
    .lh_2(mul_cmdclear_1_lh_2), .uret_2(mul_cmdclear_1_uret_2), .JALR_2(mul_cmdclear_1_jalr_2),
    .JAL_2(mul_cmdclear_1_jal_2), .Bne_2(mul_cmdclear_1_bne_2), .Beq_2(mul_cmdclear_1_beq_2),
    .MemToReg_2(mul_cmdclear_1_memtoreg_2), .MemWrite_2(mul_cmdclear_1_memwrite_2),
    .Alu_OP_2(mul_cmdclear_1_alu_op_2), .Alu_Src_2(mul_cmdclear_1_alu_src_2),
    .RegWrite_2(mul_cmdclear_1_regwrite_2), .S_Type_2(mul_cmdclear_1_s_type_2),
    .ecall_2(mul_cmdclear_1_ecall_2), .bltu(\单周期硬布线控制器_1_bltu ), .bltu_2(mul_cmdclear_1_bltu_2),
    .lw(\单周期硬布线控制器_1_lw ), .lw_2(mul_cmdclear_1_lw_2), .CSR(\单周期硬布线控制器_1_csr ), .CSR_2(mul_cmdclear_1_csr_2));
  IF_EX_cmdReg if_ex_cmdreg_1 (
    .R1(multiplexer_14_out), .R2(multiplexer_15_out), .writeAddr(multiplexer_16_out),
    .Imm(multiplexer_17_out), .J(multiplexer_18_out), .B(multiplexer_19_out), .R1_2(if_ex_cmdreg_1_r1_2),
    .R2_2(if_ex_cmdreg_1_r2_2), .writeAddr_2(EX_Reg), .Imm_2(if_ex_cmdreg_1_imm_2), .J_2(EX_J), .B_2(EX_B),
    .CLK(CLK), .Clear(or_14_out));
  Shifter #(.width(32), .shift("ll")) shifter_1 (.in(if_ex_cmdreg_1_imm_2), .\dist (5'b00001), .out(shifter_1_out));
  and and_8 (and_8_out, ex_equal, EX_Beq);
  and and_9 (and_9_out, ~ex_equal, EX_Bne);  // AND_Gate
  and and_10 (and_10_out, EX_bltu, ex_less);
  and and_11 (and_11_out, mul_cmdreg_1_ecall_2, ex_equal);
  or or_16 (or_16_out, and_8_out, and_9_out, and_10_out);
  Multiplexer #(.select(2), .width(32), .disabled("Z"), .enable("false")) multiplexer_20 (
    .in0(if_ex_cmdreg_1_r1_2), .in1(RDin), .in2(ex_mem_wd_cmdreg_1_a_32_2), .in3(ex_mem_wd_cmdreg_1_a_32_2),
    .out(multiplexer_20_out), .sel(RsFoward));
  Multiplexer #(.select(2), .width(32), .disabled("Z"), .enable("false")) multiplexer_21 (
    .in0(if_ex_cmdreg_1_r2_2), .in1(RDin), .in2(ex_mem_wd_cmdreg_1_a_32_2), .in3(ex_mem_wd_cmdreg_1_a_32_2),
    .out(multiplexer_21_out), .sel(RtFoward));
  Multiplexer #(.select(1), .width(32), .disabled("Z"), .enable("false")) multiplexer_22 (
    .in0({alu_1_result, 1'b0}), .in1(shifter_1_out), .out(multiplexer_22_out), .sel(or_17_out));
  Multiplexer #(.select(1), .width(32), .disabled("Z"), .enable("false")) multiplexer_23 (
    .in0(EX_PC), .in1({32{1'b0}}), .out(multiplexer_23_out), .sel(EX_JALR));
  or or_17 (or_17_out, EX_B, EX_JAL);
  Multiplexer #(.select(1), .width(32), .disabled("Z"), .enable("false")) multiplexer_24 (
    .in0(multiplexer_20_out), .in1(32'h22), .out(multiplexer_24_out), .sel(mul_cmdreg_1_ecall_2));
  Multiplexer #(.select(1), .width(32), .disabled("Z"), .enable("false")) multiplexer_25 (
    .in0(multiplexer_21_out), .in1(if_ex_cmdreg_1_imm_2), .out(multiplexer_25_out),
    .sel(mul_cmdreg_1_alu_src_2));
  Register #(.width(32), .trigger("rising"), .Select("low")) register_7 (
    .D(multiplexer_26_out), .en(and_11_out), .Q(LedData), .clk(CLK));  // open: clr
  Multiplexer #(.select(1), .width(32), .disabled("Z"), .enable("false")) multiplexer_26 (
    .in0(multiplexer_20_out), .in1({32{1'b0}}), .out(multiplexer_26_out), .sel(or_14_out));
  Adder #(.width(32)) adder_2 (.a(multiplexer_22_out), .b(multiplexer_23_out), .out(offset), .cin(1'b0));  // open: cout
  or or_18 (or_18_out, or_16_out, EX_JALR, EX_J);
  PC_IR_cmdReg pc_ir_cmdreg_3 (
    .PC(EX_PC), .IR(EX_IR), .PC_2(M_PC), .IR_2(MEM_IR), .Run(or_5_out), .CLK(CLK), .Clear(RST),
    .AsyClear(1'b0));
  ALU alu_1 (
    .X(multiplexer_24_out), .Y(multiplexer_25_out), .AluOP(EX_Alu_OP), .Equal(ex_equal),
    .Result({alu_1_result, alu_1_result_2[0]}), .out_6(ex_less));  // open: Result_2, out_4
  and and_12 (Branch, or_18_out, ~LoadConflict);  // AND_Gate
  Mul_cmdReg mul_cmdreg_2 (
    .lh(mul_cmdreg_1_lh_2), .Bne(EX_Bne), .Alu_OP(EX_Alu_OP), .uret(EX_URET), .Beq(EX_Beq),
    .Alu_Src(mul_cmdreg_1_alu_src_2), .JALR(EX_JALR), .MemToReg(EX_MemToReg), .RegWrite(EX_RegWrite),
    .JAL(EX_JAL), .MemWrite(mul_cmdreg_1_memwrite_2), .S_Type(mul_cmdreg_1_s_type_2),
    .ecall(mul_cmdreg_1_ecall_2), .CLK(CLK), .lh_2(mul_cmdreg_2_lh_2), .Bne_2(mul_cmdreg_2_bne_2),
    .Alu_OP_2(mul_cmdreg_2_alu_op_2), .uret_2(mul_cmdreg_2_uret_2), .Beq_2(mul_cmdreg_2_beq_2),
    .Alu_Src_2(mul_cmdreg_2_alu_src_2), .JALR_2(mul_cmdreg_2_jalr_2), .MemToReg_2(mul_cmdreg_2_memtoreg_2),
    .RegWrite_2(MEM_RegWrite), .JAL_2(mul_cmdreg_2_jal_2), .MemWrite_2(MemWrite),
    .S_Type_2(mul_cmdreg_2_s_type_2), .ecall_2(mul_cmdreg_2_ecall_2), .RST(RST), .bltu(EX_bltu),
    .bltu_2(mul_cmdreg_2_bltu_2), .lw_2(mul_cmdreg_2_lw_2), .lw(mul_cmdreg_1_lw_2),
    .CSR_2(mul_cmdreg_2_csr_2), .CSR(EX_CSR));
  EX_MEM_WD_cmdReg ex_mem_wd_cmdreg_1 (
    .A_32({alu_1_result, alu_1_result_2[0]}), .B_32(multiplexer_21_out), .C_5(EX_Reg),
    .A_32_2(ex_mem_wd_cmdreg_1_a_32_2), .B_32_2(MDin), .C_5_2(MEM_Reg), .CLK(CLK), .Clear(RST));  // open: halt, halt_2
  LoadConflict loadconflict_1 (
    .Rt_Used(or_19_out), .Rs(Rs), .Rt(Rt), .EX_MemRead(EX_MemToReg), .EX_RegWrite(EX_Reg),
    .LoadUsed(LoadConflict));
  or or_19 (or_19_out, IF_S_Type, not_3_out);
  not not_3 (not_3_out, IF_Alu_Src);
  RAM #(.addrWidth(10), .dataWidth(32), .bus("separate"), .Select("high")) ram_1 (
    .addr(ex_mem_wd_cmdreg_1_a_32_2[11:2]), .din(MDin), .data(ram_1_data), .str(MemWrite), .sel(1'b1),
    .clk(CLK), .ld(1'b1), .clr(RST));
  // Probe on redirectionconflict_1_rsfoward
  // Probe on redirectionconflict_1_rtfoward
  RedirectionConflict redirectionconflict_1 (
    .Rt_Used(or_20_out), .RsFoward(redirectionconflict_1_rsfoward),
    .RtFoward(redirectionconflict_1_rtfoward), .EX_RegWrite(EX_RegWrite), .EX_Reg(EX_Reg),
    .MEM_RegWrite(MEM_RegWrite), .MEM_Reg(MEM_Reg), .Rs(Rs), .Rt(Rt));
  Register #(.width(2), .trigger("rising"), .Select("low")) register_8 (
    .D(redirectionconflict_1_rsfoward), .en(1'b1), .Q(RsFoward), .clk(CLK), .clr(1'b0), .cs(1'b0),
    .preset(1'b0));
  Register #(.width(2), .trigger("rising"), .Select("low")) register_9 (
    .D(redirectionconflict_1_rtfoward), .en(1'b1), .Q(RtFoward), .clk(CLK), .clr(1'b0), .cs(1'b0),
    .preset(1'b0));
  or or_20 (or_20_out, not_4_out, IF_S_Type);
  PC_IR_cmdReg pc_ir_cmdreg_4 (
    .PC(M_PC), .IR(MEM_IR), .PC_2(WB_PC), .IR_2(WB_IR), .Run(or_5_out), .CLK(CLK), .Clear(RST),
    .AsyClear(1'b0));
  not not_4 (not_4_out, IF_Alu_Src);
  Mul_cmdReg mul_cmdreg_3 (
    .lh(mul_cmdreg_2_lh_2), .Bne(mul_cmdreg_2_bne_2), .Alu_OP(mul_cmdreg_2_alu_op_2),
    .uret(mul_cmdreg_2_uret_2), .Beq(mul_cmdreg_2_beq_2), .Alu_Src(mul_cmdreg_2_alu_src_2),
    .JALR(mul_cmdreg_2_jalr_2), .MemToReg(mul_cmdreg_2_memtoreg_2), .RegWrite(MEM_RegWrite),
    .JAL(mul_cmdreg_2_jal_2), .MemWrite(MemWrite), .S_Type(mul_cmdreg_2_s_type_2),
    .ecall(mul_cmdreg_2_ecall_2), .CLK(CLK), .lh_2(mul_cmdreg_3_lh_2), .Bne_2(mul_cmdreg_3_bne_2),
    .Alu_OP_2(mul_cmdreg_3_alu_op_2), .uret_2(mul_cmdreg_3_uret_2), .Beq_2(mul_cmdreg_3_beq_2),
    .Alu_Src_2(mul_cmdreg_3_alu_src_2), .JALR_2(mul_cmdreg_3_jalr_2), .MemToReg_2(mul_cmdreg_3_memtoreg_2),
    .RegWrite_2(RegWrite), .JAL_2(mul_cmdreg_3_jal_2), .MemWrite_2(mul_cmdreg_3_memwrite_2),
    .S_Type_2(mul_cmdreg_3_s_type_2), .ecall_2(mul_cmdreg_3_ecall_2), .RST(RST), .bltu(mul_cmdreg_2_bltu_2),
    .bltu_2(mul_cmdreg_3_bltu_2), .lw_2(mul_cmdreg_3_lw_2), .lw(mul_cmdreg_2_lw_2),
    .CSR_2(mul_cmdreg_3_csr_2), .CSR(mul_cmdreg_2_csr_2));
  EX_MEM_WD_cmdReg ex_mem_wd_cmdreg_2 (
    .A_32(ex_mem_wd_cmdreg_1_a_32_2), .B_32(ram_1_data), .C_5(MEM_Reg), .A_32_2(ex_mem_wd_cmdreg_2_a_32_2),
    .B_32_2(ex_mem_wd_cmdreg_2_b_32_2), .C_5_2(ex_mem_wd_cmdreg_2_c_5_2), .CLK(CLK), .Clear(RST));  // open: halt, halt_2
  Multiplexer #(.select(1), .width(32), .disabled("Z"), .enable("false")) multiplexer_27 (
    .in0(ex_mem_wd_cmdreg_2_a_32_2), .in1(ex_mem_wd_cmdreg_2_b_32_2), .out(multiplexer_27_out),
    .sel(mul_cmdreg_3_memtoreg_2));
  Adder #(.width(32)) adder_3 (.a(WB_PC), .b(32'h4), .out(adder_3_out));  // open: cin, cout
  Multiplexer #(.select(1), .width(32), .disabled("Z"), .enable("false")) multiplexer_28 (
    .in0(multiplexer_27_out), .in1(adder_3_out), .out(RDin), .sel(or_21_out));
  or or_21 (or_21_out, mul_cmdreg_3_jal_2, mul_cmdreg_3_jalr_2, mul_cmdreg_3_uret_2);

  // Other names for the same wires on the sheet: IR21 = ID_IR[21]; ID_IR (some bits) = funct;
  //   opcode[4:0] = ID_IR[6:2]; MEM_PC[31:0] = M_PC

  // Notes on the sheet:
  //   中断源
  //   时空图监测，可删除
  //   中断等待指示
  //   Branch select
  //   PC+4
  //   Keep address
  //   数码管输出
  //   contents of Instruction_Memory (hex, n*v repeats v):
  //   7d000113 100413 1f41993 41f9d993 433 c00913 800b13 140413 f47413 800293 100313 499993 89e9b3 1300533
  //   2200893 73 406282b3 fe0294e3 140413 f00f93 1f47433 1c41413 800293 100313 49d993 89e9b3 1300533
  //   2200893 73 406282b3 fe0294e3 1c45413 406b0b33 b0463 f95ff06f 2b3 fff2c293 1029293 fff2e293 500533
  //   2200893 73 f5dff06f 1112023 410113 a12023 410113 812023 410113 1312023 410113 1412023 410113 1512023
  //   410113 1612023 410113 40e073 100b13 300a13 100a93 1600433 441413 14469b3 1300533 2200893 73 fe0416e3
  //   415a0a33 fe0a10e3 40f073 ffc10113 12b03 ffc10113 12a83 ffc10113 12a03 ffc10113 12983 ffc10113 12403
  //   ffc10113 12503 ffc10113 12883 200073 1112023 410113 a12023 410113 812023 410113 1312023 410113
  //   1412023 410113 1512023 410113 1612023 410113 40e073 200b13 300a13 100a93 1600433 441413 14469b3
  //   1300533 2200893 73 fe0416e3 415a0a33 fe0a10e3 40f073 ffc10113 12b03 ffc10113 12a83 ffc10113 12a03
  //   ffc10113 12983 ffc10113 12403 ffc10113 12503 ffc10113 12883 200073 1112023 410113 a12023 410113
  //   812023 410113 1312023 410113 1412023 410113 1512023 410113 1612023 410113 40e073 300b13 300a13
  //   100a93 1600433 441413 14469b3 1300533 2200893 73 fe0416e3 415a0a33 fe0a10e3 40f073 ffc10113 12b03
  //   ffc10113 12a83 ffc10113 12a03 ffc10113 12983 ffc10113 12403 ffc10113 12503 ffc10113 12883 200073
  //   控制位
  //   流水调试日志用
  //   暂停节拍，不能为0
  //   PC
  //   IR
  //   Conflict
  //   Run
  //   CLK
  //   RST
  //   戳工具置1进入计数暂停模式，ctrl+k时钟自动运行到对应节拍暂停
  //   ctrl+k关闭时钟连续运行，将控制位置零，进入单步调试模式调试
  //   especailly for ecall
  //   I-type command
  //   S-type command
  //   B-type command
  //   J-type command
  //   Data Conflict Hazzard
  //   IR21
  //   opcode
  //   funct
  //   OpCode
  //   ecall
  //   可计数暂停的时钟源
  //   lw
  //   lh
  //   uret
  //   JALR
  //   JAL
  //   Bne
  //   Beq
  //   MemToReg
  //   MemWrite
  //   Alu_OP
  //   Alu_Src
  //   RegWrite
  //   bltu
  //   S_Type
  //   ecall
  //   R1
  //   R2
  //   Imm
  //   PC
  //   IR
  //   conflict
  //   Run
  //   CLK
  //   RST
  //   为方便自动评测，需要输出流水线各段保存的PC值，注意是PC不是PC+4，另外ID段寄存器写入信息，Mem段内存写入信息也要输出
  //   J
  //   B
  //   lw
  //   lh
  //   uret
  //   JALR
  //   JAL
  //   Bne
  //   Beq
  //   MemToReg
  //   MemWrite
  //   Alu_OP
  //   Alu_Src
  //   RegWrite
  //   bltu
  //   S_Type
  //   ecall
  //   R1
  //   R2
  //   especailly for ecall
  //   write Address
  //   Imm
  //   Beq
  //   Bne
  //   bltu
  //   JALR Jumping
  //   B-Type Jumping
  //   Imm
  //   Bne, Beq & bltu: func3 of 3 instructions is different
  //   with 000 for Beq, 001 for Bne and 110 for bltu, respectively
  //   B type jump
  //   SrcA
  //   SrcB
  //   J type jump
  //   Only JAL is J-type instruction
  //   PC
  //   IR
  //   Run
  //   CLK
  //   RST
  //   conflict
  //   lw
  //   lh
  //   uret
  //   JALR
  //   JAL
  //   Bne
  //   Beq
  //   MemToReg
  //   MemWrite
  //   Alu_OP
  //   Alu_Src
  //   RegWrite
  //   S_Type
  //   ecall
  //   Result
  //   R2
  //   write Address
  //   Conflict Judgement of lw & lh
  //   S-type cmd use rs&rt
  //   In EX part, only branch would need to clear
  //   Data
  //   PC
  //   IR
  //   conflict
  //   Run
  //   CLK
  //   RST
  //   lw
  //   lh
  //   uret
  //   JAL
  //   Bne
  //   Beq
  //   Result
  //   Data
  //   write Address
  //   JALR
  //   MemToReg
  //   MemWrite
  //   Alu_OP
  //   Alu_Src
  //   RegWrite
  //   S_Type
  //   ecall
  //   WriteData
  //   set $rd while jumping
endmodule

module \动态预测  (
  output RegWrite,
  output MemWrite,
  output [31:0] IF_PC,
  output [31:0] ID_PC,
  output [31:0] EX_PC,
  output [31:0] M_PC,
  output [31:0] WB_PC,
  output [31:0] RDin,
  output [31:0] MDin,
  output [31:0] LedData
);

  wire and_1_out, and_2_out, and_3_out, and_5_out, Branch, BranchTaken, btb_1_failure, button_1_out, CLK,
       clock_1_out, comparator_1_eq, comparator_2_eq, comparator_2_lt, comparator_3_eq, comparator_4_eq,
       Conflict, d_ff_1_q, d_ff_2_q, EX_B, EX_Beq, EX_bltu, EX_Bne, EX_ecall, ex_equal, EX_J, EX_JAL,
       EX_JALR, ex_less, EX_MemToReg, EX_RegWrite, Go, Halt, halt_t, IF_Alu_Src, IF_B, IF_I, IF_J, IF_S,
       IF_S_Type, IR1, IR2, IR3, IsBranch, LoadConflict, MEM_RegWrite, mul_cmdclear_1_alu_src_2,
       mul_cmdclear_1_beq_2, mul_cmdclear_1_bltu_2, mul_cmdclear_1_bne_2, mul_cmdclear_1_csr_2,
       mul_cmdclear_1_ecall_2, mul_cmdclear_1_jal_2, mul_cmdclear_1_jalr_2, mul_cmdclear_1_lh_2,
       mul_cmdclear_1_lw_2, mul_cmdclear_1_memtoreg_2, mul_cmdclear_1_memwrite_2, mul_cmdclear_1_regwrite_2,
       mul_cmdclear_1_s_type_2, mul_cmdclear_1_uret_2, mul_cmdreg_1_alu_src_2, mul_cmdreg_1_lh_2,
       mul_cmdreg_1_lw_2, mul_cmdreg_1_memwrite_2, mul_cmdreg_1_s_type_2, mul_cmdreg_1_uret_2,
       mul_cmdreg_2_alu_src_2, mul_cmdreg_2_beq_2, mul_cmdreg_2_bltu_2, mul_cmdreg_2_bne_2,
       mul_cmdreg_2_ecall_2, mul_cmdreg_2_jal_2, mul_cmdreg_2_jalr_2, mul_cmdreg_2_lh_2, mul_cmdreg_2_lw_2,
       mul_cmdreg_2_memtoreg_2, mul_cmdreg_2_s_type_2, mul_cmdreg_2_uret_2, mul_cmdreg_3_alu_src_2,
       mul_cmdreg_3_beq_2, mul_cmdreg_3_bltu_2, mul_cmdreg_3_bne_2, mul_cmdreg_3_ecall_2, mul_cmdreg_3_jal_2,
       mul_cmdreg_3_jalr_2, mul_cmdreg_3_lh_2, mul_cmdreg_3_lw_2, mul_cmdreg_3_memtoreg_2,
       mul_cmdreg_3_memwrite_2, mul_cmdreg_3_s_type_2, mul_cmdreg_3_uret_2, multiplexer_8_out,
       multiplexer_9_out, nand_1_out, not_1_out, not_2_out, not_3_out, not_4_out, or_1_out, or_2_out,
       or_3_out, or_4_out, or_6_out, or_7_out, or_8_out, or_9_out, or_10_out, or_11_out, or_12_out, RST,
       System, W1, W2, W3, \单周期硬布线控制器_1_beq , \单周期硬布线控制器_1_bltu , \单周期硬布线控制器_1_bne , \单周期硬布线控制器_1_ecall ,
       \单周期硬布线控制器_1_jal , \单周期硬布线控制器_1_jalr , \单周期硬布线控制器_1_lh , \单周期硬布线控制器_1_lw , \单周期硬布线控制器_1_memtoreg ,
       \单周期硬布线控制器_1_memwrite , \单周期硬布线控制器_1_regwrite , \单周期硬布线控制器_1_uret ;
  wire [0:0] alu_1_result_2;
  wire [1:0] redirectionconflict_1_rsfoward, redirectionconflict_1_rtfoward, RsFoward, RtFoward;
  wire [3:0] mul_cmdclear_1_alu_op_2, mul_cmdreg_1_alu_op_2, mul_cmdreg_2_alu_op_2, mul_cmdreg_3_alu_op_2,
       \单周期硬布线控制器_1_alu_op ;
  wire [4:0] ex_mem_wd_cmdreg_2_c_5_2, EX_Reg, funct, MEM_Reg, multiplexer_6_out, Rs, Rt;
  wire [11:0] multiplexer_1_out;
  wire [12:0] CNT_num;
  wire [15:0] \LoadUse次数 , multiplexer_18_out, \总周期数 , \插入气泡数 , \无条件分支数 , \条件分支成功数 ;
  wire [31:0] adder_1_out, adder_2_out, adder_3_out, bit_extender_1_out, btb_1_target_pc, EX_IR,
       ex_mem_wd_cmdreg_1_a_32_2, ex_mem_wd_cmdreg_2_a_32_2, ex_mem_wd_cmdreg_2_b_32_2, ID_IR,
       if_ex_cmdreg_1_imm_2, if_ex_cmdreg_1_r1_2, if_ex_cmdreg_1_r2_2, IF_IR, immvaluegen_1_imm, MEM_IR,
       multiplexer_4_out, multiplexer_5_out, multiplexer_7_out, multiplexer_10_out, multiplexer_11_out,
       multiplexer_12_out, multiplexer_13_out, multiplexer_14_out, multiplexer_15_out, multiplexer_16_out,
       multiplexer_19_out, multiplexer_20_out, offset, pc_ir_cmdreg_1_ir_2, pc_ir_cmdreg_1_pc_2, ram_1_data,
       regifile_1_r1, regifile_1_r2, shifter_1_out, WB_IR;
  wire [31:1] alu_1_result;
  wire [31:12] multiplexer_1_out_2;

  Button \u_总复位  (.out(RST));
  Button _1 (.out(IR1));
  Button _2 (.out(IR2));
  Button _3 (.out(IR3));
  // Probe on \总周期数 
  // Probe on \总周期数 
  Button \u_继续运行  (.out(Go));
  LED #(.active("true")) led_1 (.in(W1));
  LED #(.active("true")) led_2 (.in(W2));
  LED #(.active("true")) led_3 (.in(W3));
  Hex_Digit_Display hex_digit_display_1 (.value(LedData[31:28]));  // open: dp
  // Probe on IF_PC[19:0]
  // RiscV_Probe riscv_probe_1: pin names not known; wires that end beside it: IF_IR
  Button button_1 (.out(button_1_out));
  BTB btb_1 (
    .isBranch(IsBranch), .BranchPC(EX_PC), .BranchTargetPC(offset), .BranchTaken(BranchTaken), .CLK(CLK),
    .RST(RST), .Target_PC(btb_1_target_pc), .cmdPC(IF_PC), .Failure(btb_1_failure));
  Hex_Digit_Display hex_digit_display_2 (.value(LedData[27:24]));  // open: dp
  Hex_Digit_Display hex_digit_display_3 (.value(LedData[23:20]));  // open: dp
  // Probe on ID_PC[19:0]
  // RiscV_Probe riscv_probe_2: pin names not known; wires that end beside it: {ID_IR[31], funct[4], ID_IR[29:26], funct[3], ID_IR[24:15], funct[2:0], ID_IR[11:0]}, button_1_out, halt_t
  D_Flip_Flop #(.trigger("rising"), .Pre_Clr_Positions("ABOVE_BELOW"), .NegatePresetClear("false"), .enable("false"), .NewFFLayout("true")) d_ff_1 (
    .clk(EX_ecall), .D(1'b1), .Q(d_ff_1_q));  // open: Qn, preset, reset
  Hex_Digit_Display hex_digit_display_4 (.value(LedData[19:16]));  // open: dp
  Hex_Digit_Display hex_digit_display_5 (.value(LedData[15:12]));  // open: dp
  Multiplexer #(.select(1), .width(32), .disabled("Z"), .enable("false")) multiplexer_1 (
    .in0(btb_1_target_pc), .in1(IF_PC), .out({multiplexer_1_out_2, multiplexer_1_out}), .sel(LoadConflict));
  Hex_Digit_Display hex_digit_display_6 (.value(LedData[7:4]));  // open: dp
  Hex_Digit_Display hex_digit_display_7 (.value(LedData[11:8]));  // open: dp
  // Probe on EX_PC[19:0]
  // RiscV_Probe riscv_probe_3: pin names not known; wires that end beside it: EX_IR
  // Probe on multiplexer_1_out
  Hex_Digit_Display hex_digit_display_8 (.value(LedData[3:0]));  // open: dp
  Comparator #(.width(16), .mode("twosComplement")) comparator_1 (
    .a(\总周期数 ), .b(16'h16c), .eq(comparator_1_eq));  // open: gt, lt
  Register #(.width(32), .trigger("rising"), .Select("low")) PC (
    .D({multiplexer_1_out_2, multiplexer_1_out}), .en(or_1_out), .Q(IF_PC), .clk(CLK), .clr(RST));
  or or_1 (or_1_out, Go, not_1_out);
  not not_1 (not_1_out, halt_t);
  // Probe on \总周期数 
  // Probe on M_PC[19:0]
  // RiscV_Probe riscv_probe_4: pin names not known; wires that end beside it: comparator_1_eq, halt_t, MEM_IR
  // Probe on IF_PC
  // Probe on \总周期数 
  // Probe on \无条件分支数 
  // Probe on \条件分支成功数 
  // Probe on \插入气泡数 
  // Probe on \LoadUse次数 
  // Probe on IF_PC[11:0]
  // Probe on WB_PC[19:0]
  // RiscV_Probe riscv_probe_5: pin names not known; wires that end beside it: WB_IR
  ROM #(.addrWidth(10), .dataWidth(32), .Select("high")) Instruction_Memory (
    .addr(IF_PC[11:2]), .data(IF_IR), .sel(1'b1));
  // Probe on ID_PC[11:0]
  // Probe on EX_PC[11:0]
  PC_IR_cmdReg pc_ir_cmdreg_1 (
    .PC(IF_PC), .IR(IF_IR), .PC_2(pc_ir_cmdreg_1_pc_2), .IR_2(pc_ir_cmdreg_1_ir_2), .Run(or_1_out),
    .CLK(CLK), .Clear(RST), .AsyClear(btb_1_failure));
  // Probe on M_PC[11:0]
  D_Flip_Flop #(.trigger("high"), .Pre_Clr_Positions("LEGACY"), .NegatePresetClear("false"), .enable("true"), .NewFFLayout("false")) d_ff_2 (.Q(d_ff_2_q));  // open: clk, D, Qn, preset, en, reset
  // Probe on 13'hc
  // Probe on WB_PC[11:0]
  Comparator #(.width(13), .mode("twosComplement")) comparator_2 (
    .a(CNT_num), .b(13'hc), .eq(comparator_2_eq), .lt(comparator_2_lt));  // open: gt
  Clock #(.highDuration(1), .lowDuration(1)) clock_1 (.out(clock_1_out));
  DataConflict dataconflict_1 (
    .Alu_Src(IF_Alu_Src), .rs(Rs), .rt(Rt), .EX_Reg(EX_Reg), .MEM_Reg(MEM_Reg), .EX_RegWrite(EX_RegWrite),
    .MEM_RegWrite(MEM_RegWrite), .hazzard(Conflict));
  nand nand_1 (nand_1_out, d_ff_2_q, comparator_2_eq);
  Counter #(.width(13), .max('h1fff), .ongoal("stay"), .trigger("rising"), .behavior("old")) counter_1 (
    .count(comparator_2_lt), .Q(CNT_num), .clk(clock_1_out));  // open: load, D, carry, clr, preset
  LoadConflictProcessorUnit loadconflictprocessorunit_1 (
    .PC(pc_ir_cmdreg_1_pc_2), .IR(pc_ir_cmdreg_1_ir_2), .PC_2(ID_PC),
    .IR_2({ID_IR[31], funct[4], ID_IR[29:26], funct[3], ID_IR[24:15], funct[2:0], ID_IR[11:0]}),
    .Conflict(LoadConflict), .CLK(CLK));
  Multiplexer #(.select(1), .width(5), .disabled("Z"), .enable("false")) multiplexer_2 (
    .in0(ID_IR[19:15]), .in1(5'b01010), .out(Rs), .sel(\单周期硬布线控制器_1_ecall ));
  Multiplexer #(.select(1), .width(5), .disabled("Z"), .enable("false")) multiplexer_3 (
    .in0(ID_IR[24:20]), .in1(5'b10001), .out(Rt), .sel(\单周期硬布线控制器_1_ecall ));
  assign CLK = nand_1_out ? clock_1_out : 1'bz;  // Controlled_Buffer controlled_buffer_1
  \单周期硬布线控制器  \u_单周期硬布线控制器_1  (
    .Funct(funct), .OP(ID_IR[6:2]), .ALU_OP(\单周期硬布线控制器_1_alu_op ), .MemToReg(\单周期硬布线控制器_1_memtoreg ),
    .bltu(\单周期硬布线控制器_1_bltu ), .ecall(\单周期硬布线控制器_1_ecall ), .in_3(ID_IR[21]), .uret(\单周期硬布线控制器_1_uret ),
    .MemWrite(\单周期硬布线控制器_1_memwrite ), .lh(\单周期硬布线控制器_1_lh ), .BEQ(\单周期硬布线控制器_1_beq ), .S_Type(IF_S_Type),
    .RegWrite(\单周期硬布线控制器_1_regwrite ), .lw(\单周期硬布线控制器_1_lw ), .ALU_SRC(IF_Alu_Src), .BNE(\单周期硬布线控制器_1_bne ),
    .JALR(\单周期硬布线控制器_1_jalr ), .JAL(\单周期硬布线控制器_1_jal ));  // open: CSR
  ImmValueGen immvaluegen_1 (
    .Imm(immvaluegen_1_imm), .Type_I_Imm({ID_IR[31], funct[4], ID_IR[29:26], funct[3], ID_IR[24:20]}),
    .Type_S_Imm({ID_IR[31], funct[4], ID_IR[29:26], funct[3], ID_IR[11:7]}),
    .Type_B_Imm({ID_IR[31], ID_IR[7], funct[4], ID_IR[29:26], funct[3], ID_IR[11:8]}),
    .Type_J_Imm({ID_IR[31], ID_IR[19:15], funct[2:0], ID_IR[20], funct[4], ID_IR[29:26], funct[3], ID_IR[24:21]}),
    .Op6(ID_IR[6]), .I(IF_I), .Op5(ID_IR[5]), .S(IF_S), .Op4(ID_IR[4]), .B(IF_B), .Op3(ID_IR[3]), .J(IF_J),
    .Op2(ID_IR[2]), .System(System));
  Pull_Resistor #(.pull(1)) pull_resistor_1 (.node(CLK));
  Regifile regifile_1 (
    .Din(RDin), .Clk(CLK), .R1(regifile_1_r1), .R2(regifile_1_r2), .WE(RegWrite),
    .W_num(ex_mem_wd_cmdreg_2_c_5_2), .R1_num(Rs), .R2_num(Rt));
  or or_2 (or_2_out, Go, not_2_out);
  not not_2 (not_2_out, halt_t);
  PC_IR_cmdReg pc_ir_cmdreg_2 (
    .PC(ID_PC), .IR({ID_IR[31], funct[4], ID_IR[29:26], funct[3], ID_IR[24:15], funct[2:0], ID_IR[11:0]}),
    .PC_2(EX_PC), .IR_2(EX_IR), .Run(or_1_out), .CLK(CLK), .Clear(RST), .AsyClear(or_4_out));
  or or_3 (or_3_out, btb_1_failure, RST);
  Counter #(.width(16), .max('hffff), .ongoal("wrap"), .trigger("rising"), .behavior("new")) counter_2 (
    .D({16{1'b0}}), .count(or_2_out), .Q(\总周期数 ), .clk(CLK), .clr(RST));  // open: load, carry, preset, down
  Multiplexer #(.select(1), .width(32), .disabled("Z"), .enable("false")) multiplexer_4 (
    .in0(regifile_1_r1), .in1({32{1'b0}}), .out(multiplexer_4_out), .sel(LoadConflict));
  Multiplexer #(.select(1), .width(32), .disabled("Z"), .enable("false")) multiplexer_5 (
    .in0(regifile_1_r2), .in1({32{1'b0}}), .out(multiplexer_5_out), .sel(LoadConflict));
  Multiplexer #(.select(1), .width(5), .disabled("Z"), .enable("false")) multiplexer_6 (
    .in0(ID_IR[11:7]), .in1({5{1'b0}}), .out(multiplexer_6_out), .sel(LoadConflict));
  Multiplexer #(.select(1), .width(32), .disabled("Z"), .enable("false")) multiplexer_7 (
    .in0(immvaluegen_1_imm), .in1({32{1'b0}}), .out(multiplexer_7_out), .sel(LoadConflict));
  Multiplexer #(.select(1), .width(1), .disabled("Z"), .enable("false")) multiplexer_8 (
    .in0(IF_J), .in1(1'b0), .out(multiplexer_8_out), .sel(LoadConflict));
  Multiplexer #(.select(1), .width(1), .disabled("Z"), .enable("false")) multiplexer_9 (
    .in0(IF_B), .in1(1'b0), .out(multiplexer_9_out), .sel(LoadConflict));
  or or_4 (or_4_out, RST, LoadConflict, btb_1_failure);
  Mul_cmdReg mul_cmdreg_1 (
    .lh(mul_cmdclear_1_lh_2), .Bne(mul_cmdclear_1_bne_2), .Alu_OP(mul_cmdclear_1_alu_op_2),
    .uret(mul_cmdclear_1_uret_2), .Beq(mul_cmdclear_1_beq_2), .Alu_Src(mul_cmdclear_1_alu_src_2),
    .JALR(mul_cmdclear_1_jalr_2), .MemToReg(mul_cmdclear_1_memtoreg_2), .RegWrite(mul_cmdclear_1_regwrite_2),
    .JAL(mul_cmdclear_1_jal_2), .MemWrite(mul_cmdclear_1_memwrite_2), .S_Type(mul_cmdclear_1_s_type_2),
    .ecall(mul_cmdclear_1_ecall_2), .CLK(CLK), .lh_2(mul_cmdreg_1_lh_2), .Bne_2(EX_Bne),
    .Alu_OP_2(mul_cmdreg_1_alu_op_2), .uret_2(mul_cmdreg_1_uret_2), .Beq_2(EX_Beq),
    .Alu_Src_2(mul_cmdreg_1_alu_src_2), .JALR_2(EX_JALR), .MemToReg_2(EX_MemToReg), .RegWrite_2(EX_RegWrite),
    .JAL_2(EX_JAL), .MemWrite_2(mul_cmdreg_1_memwrite_2), .S_Type_2(mul_cmdreg_1_s_type_2),
    .ecall_2(EX_ecall), .RST(RST), .bltu(mul_cmdclear_1_bltu_2), .bltu_2(EX_bltu), .lw_2(mul_cmdreg_1_lw_2),
    .lw(mul_cmdclear_1_lw_2), .CSR(mul_cmdclear_1_csr_2));  // open: CSR_2
  Mul_cmdClear mul_cmdclear_1 (
    .Clear(or_4_out), .lh(\单周期硬布线控制器_1_lh ), .uret(\单周期硬布线控制器_1_uret ), .JALR(\单周期硬布线控制器_1_jalr ),
    .JAL(\单周期硬布线控制器_1_jal ), .Bne(\单周期硬布线控制器_1_bne ), .Beq(\单周期硬布线控制器_1_beq ),
    .MemToReg(\单周期硬布线控制器_1_memtoreg ), .MemWrite(\单周期硬布线控制器_1_memwrite ), .Alu_OP(\单周期硬布线控制器_1_alu_op ),
    .Alu_Src(IF_Alu_Src), .RegWrite(\单周期硬布线控制器_1_regwrite ), .S_Type(IF_S_Type), .ecall(\单周期硬布线控制器_1_ecall ),
    .lh_2(mul_cmdclear_1_lh_2), .uret_2(mul_cmdclear_1_uret_2), .JALR_2(mul_cmdclear_1_jalr_2),
    .JAL_2(mul_cmdclear_1_jal_2), .Bne_2(mul_cmdclear_1_bne_2), .Beq_2(mul_cmdclear_1_beq_2),
    .MemToReg_2(mul_cmdclear_1_memtoreg_2), .MemWrite_2(mul_cmdclear_1_memwrite_2),
    .Alu_OP_2(mul_cmdclear_1_alu_op_2), .Alu_Src_2(mul_cmdclear_1_alu_src_2),
    .RegWrite_2(mul_cmdclear_1_regwrite_2), .S_Type_2(mul_cmdclear_1_s_type_2),
    .ecall_2(mul_cmdclear_1_ecall_2), .bltu(\单周期硬布线控制器_1_bltu ), .bltu_2(mul_cmdclear_1_bltu_2),
    .lw(\单周期硬布线控制器_1_lw ), .lw_2(mul_cmdclear_1_lw_2), .CSR_2(mul_cmdclear_1_csr_2));  // open: CSR
  IF_EX_cmdReg if_ex_cmdreg_1 (
    .R1(multiplexer_4_out), .R2(multiplexer_5_out), .writeAddr(multiplexer_6_out), .Imm(multiplexer_7_out),
    .J(multiplexer_8_out), .B(multiplexer_9_out), .R1_2(if_ex_cmdreg_1_r1_2), .R2_2(if_ex_cmdreg_1_r2_2),
    .writeAddr_2(EX_Reg), .Imm_2(if_ex_cmdreg_1_imm_2), .J_2(EX_J), .B_2(EX_B), .CLK(CLK), .Clear(or_3_out));
  Shifter #(.width(32), .shift("ll")) shifter_1 (.in(if_ex_cmdreg_1_imm_2), .\dist (5'b00001), .out(shifter_1_out));
  and and_1 (and_1_out, ex_equal, EX_Beq);
  and and_2 (and_2_out, ~ex_equal, EX_Bne);  // AND_Gate
  and and_3 (and_3_out, EX_bltu, ex_less);
  or or_5 (IsBranch, EX_Beq, EX_Bne, EX_bltu, EX_JALR, EX_J);
  and and_4 (Halt, EX_ecall, ~ex_equal);  // AND_Gate
  and and_5 (and_5_out, EX_ecall, ex_equal);
  or or_6 (or_6_out, and_1_out, and_2_out, and_3_out);
  Multiplexer #(.select(2), .width(32), .disabled("Z"), .enable("false")) multiplexer_10 (
    .in0(if_ex_cmdreg_1_r1_2), .in1(RDin), .in2(ex_mem_wd_cmdreg_1_a_32_2), .in3(ex_mem_wd_cmdreg_1_a_32_2),
    .out(multiplexer_10_out), .sel(RsFoward));
  Multiplexer #(.select(2), .width(32), .disabled("Z"), .enable("false")) multiplexer_11 (
    .in0(if_ex_cmdreg_1_r2_2), .in1(RDin), .in2(ex_mem_wd_cmdreg_1_a_32_2), .in3(ex_mem_wd_cmdreg_1_a_32_2),
    .out(multiplexer_11_out), .sel(RtFoward));
  Multiplexer #(.select(1), .width(32), .disabled("Z"), .enable("false")) multiplexer_12 (
    .in0({alu_1_result, 1'b0}), .in1(shifter_1_out), .out(multiplexer_12_out), .sel(or_7_out));
  Multiplexer #(.select(1), .width(32), .disabled("Z"), .enable("false")) multiplexer_13 (
    .in0(EX_PC), .in1({32{1'b0}}), .out(multiplexer_13_out), .sel(EX_JALR));
  or or_7 (or_7_out, EX_B, EX_JAL);
  Multiplexer #(.select(1), .width(32), .disabled("Z"), .enable("false")) multiplexer_14 (
    .in0(multiplexer_10_out), .in1(32'h22), .out(multiplexer_14_out), .sel(EX_ecall));
  Multiplexer #(.select(1), .width(32), .disabled("Z"), .enable("false")) multiplexer_15 (
    .in0(multiplexer_11_out), .in1(if_ex_cmdreg_1_imm_2), .out(multiplexer_15_out),
    .sel(mul_cmdreg_1_alu_src_2));
  Multiplexer #(.select(1), .width(32), .disabled("Z"), .enable("false")) multiplexer_16 (
    .in0(multiplexer_10_out), .in1({32{1'b0}}), .out(multiplexer_16_out), .sel(or_3_out));
  Register #(.width(32), .trigger("rising"), .Select("low")) register_1 (
    .D(multiplexer_16_out), .en(and_5_out), .Q(LedData), .clk(CLK));  // open: clr
  Adder #(.width(32)) adder_1 (
    .a(multiplexer_12_out), .b(multiplexer_13_out), .out(adder_1_out), .cin(1'b0));  // open: cout
  or or_8 (or_8_out, or_6_out, EX_JALR, EX_J);
  PC_IR_cmdReg pc_ir_cmdreg_3 (
    .PC(EX_PC), .IR(EX_IR), .PC_2(M_PC), .IR_2(MEM_IR), .Run(or_1_out), .CLK(CLK), .Clear(RST),
    .AsyClear(1'b0));
  ALU alu_1 (
    .X(multiplexer_14_out), .Y(multiplexer_15_out), .AluOP(mul_cmdreg_1_alu_op_2), .Equal(ex_equal),
    .Result({alu_1_result, alu_1_result_2[0]}), .out_6(ex_less));  // open: Result_2, out_4
  and and_6 (Branch, or_8_out, ~LoadConflict);  // AND_Gate
  Adder #(.width(32)) adder_2 (.a(EX_PC), .b(32'h4), .out(adder_2_out));  // open: cin, cout
  Mul_cmdReg mul_cmdreg_2 (
    .lh(mul_cmdreg_1_lh_2), .Bne(EX_Bne), .Alu_OP(mul_cmdreg_1_alu_op_2), .uret(mul_cmdreg_1_uret_2),
    .Beq(EX_Beq), .Alu_Src(mul_cmdreg_1_alu_src_2), .JALR(EX_JALR), .MemToReg(EX_MemToReg),
    .RegWrite(EX_RegWrite), .JAL(EX_JAL), .MemWrite(mul_cmdreg_1_memwrite_2), .S_Type(mul_cmdreg_1_s_type_2),
    .ecall(EX_ecall), .CLK(CLK), .lh_2(mul_cmdreg_2_lh_2), .Bne_2(mul_cmdreg_2_bne_2),
    .Alu_OP_2(mul_cmdreg_2_alu_op_2), .uret_2(mul_cmdreg_2_uret_2), .Beq_2(mul_cmdreg_2_beq_2),
    .Alu_Src_2(mul_cmdreg_2_alu_src_2), .JALR_2(mul_cmdreg_2_jalr_2), .MemToReg_2(mul_cmdreg_2_memtoreg_2),
    .RegWrite_2(MEM_RegWrite), .JAL_2(mul_cmdreg_2_jal_2), .MemWrite_2(MemWrite),
    .S_Type_2(mul_cmdreg_2_s_type_2), .ecall_2(mul_cmdreg_2_ecall_2), .RST(RST), .bltu(EX_bltu),
    .bltu_2(mul_cmdreg_2_bltu_2), .lw_2(mul_cmdreg_2_lw_2), .lw(mul_cmdreg_1_lw_2));  // open: CSR_2, CSR
  EX_MEM_WD_cmdReg ex_mem_wd_cmdreg_1 (
    .A_32({alu_1_result, alu_1_result_2[0]}), .B_32(multiplexer_11_out), .C_5(EX_Reg),
    .A_32_2(ex_mem_wd_cmdreg_1_a_32_2), .B_32_2(MDin), .C_5_2(MEM_Reg), .CLK(CLK), .Clear(RST));  // open: halt, halt_2
  Multiplexer #(.select(1), .width(32), .disabled("Z"), .enable("false")) multiplexer_17 (
    .in0(adder_2_out), .in1(adder_1_out), .out(offset), .sel(Branch));
  LoadConflict loadconflict_1 (
    .Rt_Used(or_9_out), .Rs(Rs), .Rt(Rt), .EX_MemRead(EX_MemToReg), .EX_RegWrite(EX_Reg),
    .LoadUsed(LoadConflict));
  or or_9 (or_9_out, IF_S_Type, not_3_out);
  not not_3 (not_3_out, IF_Alu_Src);
  Comparator #(.width(32), .mode("twosComplement")) comparator_3 (
    .a(offset), .b(ID_PC), .eq(comparator_3_eq));  // open: gt, lt
  Comparator #(.width(32), .mode("twosComplement")) comparator_4 (
    .a(ID_PC), .b({32{1'b0}}), .eq(comparator_4_eq));  // open: gt, lt
  RAM #(.addrWidth(10), .dataWidth(32), .bus("separate"), .Select("high")) ram_1 (
    .addr(ex_mem_wd_cmdreg_1_a_32_2[11:2]), .din(MDin), .data(ram_1_data), .str(MemWrite), .sel(1'b1),
    .clk(CLK), .ld(1'b1), .clr(RST));
  and and_7 (BranchTaken, comparator_3_eq, ~comparator_4_eq);  // AND_Gate
  // Probe on redirectionconflict_1_rsfoward
  // Probe on redirectionconflict_1_rtfoward
  RedirectionConflict redirectionconflict_1 (
    .Rt_Used(or_10_out), .RsFoward(redirectionconflict_1_rsfoward),
    .RtFoward(redirectionconflict_1_rtfoward), .EX_RegWrite(EX_RegWrite), .EX_Reg(EX_Reg),
    .MEM_RegWrite(MEM_RegWrite), .MEM_Reg(MEM_Reg), .Rs(Rs), .Rt(Rt));
  Multiplexer #(.select(1), .width(16), .disabled("Z"), .enable("false")) multiplexer_18 (
    .in0(ram_1_data[15:0]), .in1(ram_1_data[31:16]), .out(multiplexer_18_out),
    .sel(ex_mem_wd_cmdreg_1_a_32_2[1]));
  Register #(.width(2), .trigger("rising"), .Select("low")) register_2 (
    .D(redirectionconflict_1_rsfoward), .en(1'b1), .Q(RsFoward), .clk(CLK), .clr(1'b0), .cs(1'b0),
    .preset(1'b0));
  Register #(.width(2), .trigger("rising"), .Select("low")) register_3 (
    .D(redirectionconflict_1_rtfoward), .en(1'b1), .Q(RtFoward), .clk(CLK), .clr(1'b0), .cs(1'b0),
    .preset(1'b0));
  or or_10 (or_10_out, not_4_out, IF_S_Type);
  PC_IR_cmdReg pc_ir_cmdreg_4 (
    .PC(M_PC), .IR(MEM_IR), .PC_2(WB_PC), .IR_2(WB_IR), .Run(or_1_out), .CLK(CLK), .Clear(RST),
    .AsyClear(1'b0));
  assign bit_extender_1_out = {{16{multiplexer_18_out[15]}}, multiplexer_18_out};  // Bit_Extender bit_extender_1
  not not_4 (not_4_out, IF_Alu_Src);
  Multiplexer #(.select(1), .width(32), .disabled("Z"), .enable("false")) multiplexer_19 (
    .in0(ram_1_data), .in1(bit_extender_1_out), .out(multiplexer_19_out), .sel(mul_cmdreg_2_lh_2));
  Mul_cmdReg mul_cmdreg_3 (
    .lh(mul_cmdreg_2_lh_2), .Bne(mul_cmdreg_2_bne_2), .Alu_OP(mul_cmdreg_2_alu_op_2),
    .uret(mul_cmdreg_2_uret_2), .Beq(mul_cmdreg_2_beq_2), .Alu_Src(mul_cmdreg_2_alu_src_2),
    .JALR(mul_cmdreg_2_jalr_2), .MemToReg(mul_cmdreg_2_memtoreg_2), .RegWrite(MEM_RegWrite),
    .JAL(mul_cmdreg_2_jal_2), .MemWrite(MemWrite), .S_Type(mul_cmdreg_2_s_type_2),
    .ecall(mul_cmdreg_2_ecall_2), .CLK(CLK), .lh_2(mul_cmdreg_3_lh_2), .Bne_2(mul_cmdreg_3_bne_2),
    .Alu_OP_2(mul_cmdreg_3_alu_op_2), .uret_2(mul_cmdreg_3_uret_2), .Beq_2(mul_cmdreg_3_beq_2),
    .Alu_Src_2(mul_cmdreg_3_alu_src_2), .JALR_2(mul_cmdreg_3_jalr_2), .MemToReg_2(mul_cmdreg_3_memtoreg_2),
    .RegWrite_2(RegWrite), .JAL_2(mul_cmdreg_3_jal_2), .MemWrite_2(mul_cmdreg_3_memwrite_2),
    .S_Type_2(mul_cmdreg_3_s_type_2), .ecall_2(mul_cmdreg_3_ecall_2), .RST(RST), .bltu(mul_cmdreg_2_bltu_2),
    .bltu_2(mul_cmdreg_3_bltu_2), .lw_2(mul_cmdreg_3_lw_2), .lw(mul_cmdreg_2_lw_2));  // open: CSR_2, CSR
  EX_MEM_WD_cmdReg ex_mem_wd_cmdreg_2 (
    .A_32(ex_mem_wd_cmdreg_1_a_32_2), .B_32(multiplexer_19_out), .C_5(MEM_Reg),
    .A_32_2(ex_mem_wd_cmdreg_2_a_32_2), .B_32_2(ex_mem_wd_cmdreg_2_b_32_2), .C_5_2(ex_mem_wd_cmdreg_2_c_5_2),
    .CLK(CLK), .Clear(RST));  // open: halt, halt_2
  Multiplexer #(.select(1), .width(32), .disabled("Z"), .enable("false")) multiplexer_20 (
    .in0(ex_mem_wd_cmdreg_2_a_32_2), .in1(ex_mem_wd_cmdreg_2_b_32_2), .out(multiplexer_20_out),
    .sel(mul_cmdreg_3_memtoreg_2));
  or or_11 (or_11_out, Halt, halt_t);
  D_Flip_Flop #(.trigger("falling"), .Pre_Clr_Positions("ABOVE_BELOW"), .NegatePresetClear("false"), .enable("false"), .NewFFLayout("false")) d_ff_3 (
    .clk(CLK), .D(or_11_out), .Q(halt_t), .reset(Go));  // open: Qn, preset
  Adder #(.width(32)) adder_3 (.a(WB_PC), .b(32'h4), .out(adder_3_out));  // open: cin, cout
  or or_12 (or_12_out, mul_cmdreg_3_jal_2, mul_cmdreg_3_jalr_2, mul_cmdreg_3_uret_2);
  Multiplexer #(.select(1), .width(32), .disabled("Z"), .enable("false")) multiplexer_21 (
    .in0(multiplexer_20_out), .in1(adder_3_out), .out(RDin), .sel(or_12_out));

  // Other names for the same wires on the sheet: IR21 = ID_IR[21]; ID_IR (some bits) = funct;
  //   opcode[4:0] = ID_IR[6:2]; MEM_PC[31:0] = M_PC

  // Notes on the sheet:
  //   中断源
  //   时空图监测，可删除
  //   中断等待指示
  //   数码管输出
  //   contents of Instruction_Memory (hex, n*v repeats v):
  //   100493 100006f 100493 200913 300993 100006f 100493 200913 300993 100006f 100493 200913 300993
  //   100006f 100493 200913 300993 29c000ef 100413 100493 1f49493 900533 2200893 73 24d493 48463 fedff06f
  //   900533 2200893 73 100493 249493 900533 2200893 73 48463 fedff06f 100493 1f49493 900533 2200893 73
  //   4034d493 900533 2200893 73 4044d493 900533 2200893 73 4044d493 900533 2200893 73 4044d493 900533
  //   2200893 73 4044d493 900533 2200893 73 4044d493 900533 2200893 73 4044d493 900533 2200893 73 4044d493
  //   900533 2200893 73 100413 1f41993 41f9d993 433 c00913 300b13 140413 f47413 800293 100313 499993
  //   89e9b3 1300533 2200893 73 406282b3 fe0294e3 140413 f00f93 1f47433 1c41413 800293 100313 49d993
  //   89e9b3 1300533 2200893 73 406282b3 fe0294e3 1c45413 406b0b33 b0463 f95ff06f 2b3 fff2c293 829293
  //   ff2e293 500533 2200893 73 fff00413 493 84a023 140413 448493 84a023 140413 448493 84a023 140413
  //   448493 84a023 140413 448493 84a023 140413 448493 84a023 140413 448493 84a023 140413 448493 84a023
  //   140413 448493 84a023 140413 448493 84a023 140413 448493 84a023 140413 448493 84a023 140413 448493
  //   84a023 140413 448493 84a023 140413 448493 84a023 140413 448493 84a023 140413 448493 140413 433
  //   3c00493 42983 4aa03 149a2b3 28663 134a023 1442023 ffc48493 fe9412e3 800533 2200893 73 440413 3c00493
  //   fc9416e3 a00893 73 413 140413 800533 2200893 73 240413 800533 2200893 73 340413 800533 2200893 73
  //   440413 800533 2200893 73 540413 800533 2200893 73 640413 800533 2200893 73 740413 800533 2200893 73
  //   840413 800533 2200893 2200893 73 8067
  //   控制位
  //   流水调试日志用
  //   暂停节拍，不能为0
  //   PC
  //   IR
  //   Conflict
  //   Run
  //   CLK
  //   RST
  //   戳工具置1进入计数暂停模式，ctrl+k时钟自动运行到对应节拍暂停
  //   ctrl+k关闭时钟连续运行，将控制位置零，进入单步调试模式调试
  //   especailly for ecall
  //   I-type command
  //   S-type command
  //   B-type command
  //   J-type command
  //   Data Conflict Hazzard
  //   IR21
  //   opcode
  //   funct
  //   OpCode
  //   ecall
  //   可计数暂停的时钟源
  //   lw
  //   lh
  //   uret
  //   JALR
  //   JAL
  //   Bne
  //   Beq
  //   MemToReg
  //   MemWrite
  //   Alu_OP
  //   Alu_Src
  //   RegWrite
  //   bltu
  //   S_Type
  //   ecall
  //   R1
  //   R2
  //   Imm
  //   PC
  //   IR
  //   conflict
  //   Run
  //   CLK
  //   RST
  //   为方便自动评测，需要输出流水线各段保存的PC值，注意是PC不是PC+4，另外ID段寄存器写入信息，Mem段内存写入信息也要输出
  //   J
  //   B
  //   lw
  //   lh
  //   uret
  //   JALR
  //   JAL
  //   Bne
  //   Beq
  //   MemToReg
  //   MemWrite
  //   Alu_OP
  //   Alu_Src
  //   RegWrite
  //   bltu
  //   S_Type
  //   ecall
  //   R1
  //   R2
  //   especailly for ecall
  //   write Address
  //   Imm
  //   Beq
  //   Bne
  //   bltu
  //   JALR Jumping
  //   B-Type Jumping
  //   especailly for ecall
  //   Imm
  //   Bne, Beq & bltu: func3 of 3 instructions is different
  //   with 000 for Beq, 001 for Bne and 110 for bltu, respectively
  //   B type jump
  //   SrcA
  //   SrcB
  //   J type jump
  //   Only JAL is J-type instruction
  //   PC
  //   IR
  //   Run
  //   CLK
  //   RST
  //   conflict
  //   lw
  //   lh
  //   uret
  //   JALR
  //   JAL
  //   Bne
  //   Beq
  //   MemToReg
  //   MemWrite
  //   Alu_OP
  //   Alu_Src
  //   RegWrite
  //   S_Type
  //   ecall
  //   Result
  //   R2
  //   write Address
  //   Conflict Judgement of lw & lh
  //   S-type cmd use rs&rt
  //   In EX part, only branch would need to clear
  //   Data
  //   PC
  //   IR
  //   conflict
  //   Run
  //   CLK
  //   RST
  //   lw
  //   lh
  //   uret
  //   JAL
  //   Bne
  //   Beq
  //   Result
  //   Data
  //   write Address
  //   JALR
  //   MemToReg
  //   MemWrite
  //   Alu_OP
  //   Alu_Src
  //   RegWrite
  //   S_Type
  //   ecall
  //   WriteData
  //   set $rd while jumping
endmodule

module ImmValueGen (
  input  Op6,
  input  [11:0] Type_I_Imm,
  input  Op5,
  input  [11:0] Type_S_Imm,
  input  Op4,
  input  [11:0] Type_B_Imm,
  input  Op3,
  input  [19:0] Type_J_Imm,
  input  Op2,
  output I,
  output S,
  output B,
  output J,
  output System,
  output [31:0] Imm
);

  wire and_2_out, not_1_out, not_2_out, not_3_out, not_4_out, not_5_out;
  wire [0:0] or_2_out;
  wire [31:0] bit_extender_1_out, bit_extender_2_out, bit_extender_3_out, bit_extender_4_out;

  assign bit_extender_1_out = {{20{Type_I_Imm[11]}}, Type_I_Imm};  // Bit_Extender bit_extender_1
  assign bit_extender_2_out = {{20{Type_S_Imm[11]}}, Type_S_Imm};  // Bit_Extender bit_extender_2
  assign bit_extender_3_out = {{20{Type_B_Imm[11]}}, Type_B_Imm};  // Bit_Extender bit_extender_3
  assign bit_extender_4_out = {{12{Type_J_Imm[19]}}, Type_J_Imm};  // Bit_Extender bit_extender_4
  Multiplexer #(.select(4), .width(32), .disabled("Z"), .enable("false")) multiplexer_1 (
    .in1(bit_extender_1_out), .in2(bit_extender_2_out), .in4(bit_extender_3_out), .in8(bit_extender_4_out),
    .out(Imm), .sel({Op3, B, S, or_2_out[0]}));  // open: in0, in3, in5, in6, in7, in9, in10, in11, in12, in13, in14, in15
  not not_1 (not_1_out, Op3);
  not not_2 (not_2_out, Op6);
  not not_3 (not_3_out, Op4);
  not not_4 (not_4_out, Op2);
  and and_1 (System, Op6, Op4);
  not not_5 (not_5_out, Op5);
  and and_2 (and_2_out, not_1_out, Op2);
  and and_3 (S, not_2_out, Op5);
  and and_4 (B, Op6, not_3_out, not_4_out);
  or or_1 (I, not_5_out, and_2_out);
  or or_2 (or_2_out[0], I, System);

  assign J = Op3;

  // Other names for the same wires on the sheet: B_Type[11:0] = Type_B_Imm; I_Type[11:0] = Type_I_Imm;
  //   J_Type[19:0] = Type_J_Imm; S_Type[11:0] = Type_S_Imm
endmodule

module ValueLockUnit (
  input  stop,
  input  Bottom,
  output Output
);

  wire not_1_out;

  not not_1 (not_1_out, Output);
  D_Flip_Flop #(.trigger("rising"), .Pre_Clr_Positions("ABOVE_BELOW"), .NegatePresetClear("false"), .enable("false"), .NewFFLayout("true")) d_ff_1 (
    .clk(Bottom), .D(not_1_out), .Q(Output), .preset(stop));  // open: Qn, reset
endmodule

module Mul_cmdReg (
  input  [3:0] Alu_OP,
  input  lh,
  input  Bne,
  input  uret,
  input  Beq,
  input  Alu_Src,
  input  JALR,
  input  MemToReg,
  input  RegWrite,
  input  JAL,
  input  MemWrite,
  input  S_Type,
  input  lw,
  input  bltu,
  input  ecall,
  input  CLK,
  input  RST,
  input  CSR,
  output lh_2,
  output Bne_2,
  output [3:0] Alu_OP_2,
  output uret_2,
  output Beq_2,
  output Alu_Src_2,
  output JALR_2,
  output MemToReg_2,
  output RegWrite_2,
  output JAL_2,
  output MemWrite_2,
  output S_Type_2,
  output lw_2,
  output bltu_2,
  output ecall_2,
  output CSR_2
);

  D_Flip_Flop #(.trigger("rising"), .Pre_Clr_Positions("ABOVE_BELOW"), .NegatePresetClear("false"), .enable("false"), .NewFFLayout("true")) d_ff_1 (
    .clk(CLK), .D(lh), .Q(lh_2), .reset(RST));  // open: Qn, preset
  D_Flip_Flop #(.trigger("rising"), .Pre_Clr_Positions("ABOVE_BELOW"), .NegatePresetClear("false"), .enable("false"), .NewFFLayout("true")) d_ff_2 (
    .clk(CLK), .D(uret), .Q(uret_2), .reset(RST));  // open: Qn, preset
  D_Flip_Flop #(.trigger("rising"), .Pre_Clr_Positions("ABOVE_BELOW"), .NegatePresetClear("false"), .enable("false"), .NewFFLayout("true")) d_ff_3 (
    .clk(CLK), .D(JALR), .Q(JALR_2), .reset(RST));  // open: Qn, preset
  D_Flip_Flop #(.trigger("rising"), .Pre_Clr_Positions("ABOVE_BELOW"), .NegatePresetClear("false"), .enable("false"), .NewFFLayout("true")) d_ff_4 (
    .clk(CLK), .D(JAL), .Q(JAL_2), .reset(RST));  // open: Qn, preset
  D_Flip_Flop #(.trigger("rising"), .Pre_Clr_Positions("ABOVE_BELOW"), .NegatePresetClear("false"), .enable("false"), .NewFFLayout("true")) d_ff_5 (
    .clk(CLK), .D(lw), .Q(lw_2), .reset(RST));  // open: Qn, preset
  D_Flip_Flop #(.trigger("rising"), .Pre_Clr_Positions("ABOVE_BELOW"), .NegatePresetClear("false"), .enable("false"), .NewFFLayout("true")) d_ff_6 (
    .clk(CLK), .D(Bne), .Q(Bne_2), .reset(RST));  // open: Qn, preset
  D_Flip_Flop #(.trigger("rising"), .Pre_Clr_Positions("ABOVE_BELOW"), .NegatePresetClear("false"), .enable("false"), .NewFFLayout("true")) d_ff_7 (
    .clk(CLK), .D(Beq), .Q(Beq_2), .reset(RST));  // open: Qn, preset
  D_Flip_Flop #(.trigger("rising"), .Pre_Clr_Positions("ABOVE_BELOW"), .NegatePresetClear("false"), .enable("false"), .NewFFLayout("true")) d_ff_8 (
    .clk(CLK), .D(MemToReg), .Q(MemToReg_2), .reset(RST));  // open: Qn, preset
  D_Flip_Flop #(.trigger("rising"), .Pre_Clr_Positions("ABOVE_BELOW"), .NegatePresetClear("false"), .enable("false"), .NewFFLayout("true")) d_ff_9 (
    .clk(CLK), .D(MemWrite), .Q(MemWrite_2), .reset(RST));  // open: Qn, preset
  D_Flip_Flop #(.trigger("rising"), .Pre_Clr_Positions("ABOVE_BELOW"), .NegatePresetClear("false"), .enable("false"), .NewFFLayout("true")) d_ff_10 (
    .clk(CLK), .D(bltu), .Q(bltu_2), .reset(RST));  // open: Qn, preset
  Register #(.width(4), .trigger("rising"), .Select("low")) register_1 (
    .D(Alu_OP), .en(1'b1), .Q(Alu_OP_2), .clk(CLK), .clr(RST), .cs(1'b0), .preset(1'b0));
  D_Flip_Flop #(.trigger("rising"), .Pre_Clr_Positions("ABOVE_BELOW"), .NegatePresetClear("false"), .enable("false"), .NewFFLayout("true")) d_ff_11 (
    .clk(CLK), .D(Alu_Src), .Q(Alu_Src_2), .reset(RST));  // open: Qn, preset
  D_Flip_Flop #(.trigger("rising"), .Pre_Clr_Positions("ABOVE_BELOW"), .NegatePresetClear("false"), .enable("false"), .NewFFLayout("true")) d_ff_12 (
    .clk(CLK), .D(RegWrite), .Q(RegWrite_2), .reset(RST));  // open: Qn, preset
  D_Flip_Flop #(.trigger("rising"), .Pre_Clr_Positions("ABOVE_BELOW"), .NegatePresetClear("false"), .enable("false"), .NewFFLayout("true")) d_ff_13 (
    .clk(CLK), .D(S_Type), .Q(S_Type_2), .reset(RST));  // open: Qn, preset
  D_Flip_Flop #(.trigger("rising"), .Pre_Clr_Positions("ABOVE_BELOW"), .NegatePresetClear("false"), .enable("false"), .NewFFLayout("true")) d_ff_14 (
    .clk(CLK), .D(ecall), .Q(ecall_2), .reset(RST));  // open: Qn, preset
  D_Flip_Flop #(.trigger("rising"), .Pre_Clr_Positions("ABOVE_BELOW"), .NegatePresetClear("false"), .enable("false"), .NewFFLayout("true")) d_ff_15 (
    .clk(CLK), .D(CSR), .Q(CSR_2), .reset(RST));  // open: Qn, preset
endmodule

module IF_EX_cmdReg (
  input  CLK,
  input  Clear,
  input  [31:0] R1,
  input  [31:0] R2,
  input  [4:0] writeAddr,
  input  [31:0] Imm,
  input  J,
  input  B,
  output [31:0] R1_2,
  output [31:0] R2_2,
  output [4:0] writeAddr_2,
  output [31:0] Imm_2,
  output J_2,
  output B_2
);

  wire register_1_q;

  Register #(.width(1), .trigger("rising"), .Select("low")) register_1 (
    .D(Clear), .Q(register_1_q), .clk(CLK));  // open: en, clr
  Register #(.width(32), .trigger("rising"), .Select("low")) register_2 (
    .D(R1), .en(1'b1), .Q(R1_2), .clk(CLK), .clr(register_1_q), .cs(1'b0), .preset(1'b0));
  Register #(.width(32), .trigger("rising"), .Select("low")) register_3 (
    .D(R2), .en(1'b1), .Q(R2_2), .clk(CLK), .clr(register_1_q), .cs(1'b0), .preset(1'b0));
  Register #(.width(5), .trigger("rising"), .Select("low")) register_4 (
    .D(writeAddr), .en(1'b1), .Q(writeAddr_2), .clk(CLK), .clr(register_1_q), .cs(register_1_q),
    .preset(register_1_q));
  Register #(.width(32), .trigger("rising"), .Select("low")) register_5 (
    .D(Imm), .en(1'b1), .Q(Imm_2), .clk(CLK), .clr(register_1_q), .cs(1'b0), .preset(1'b0));
  Register #(.width(1), .trigger("rising"), .Select("low")) register_6 (
    .D(J), .en(1'b1), .Q(J_2), .clk(CLK), .clr(register_1_q), .cs(1'b0), .preset(1'b0));
  Register #(.width(1), .trigger("rising"), .Select("low")) register_7 (
    .D(B), .en(1'b1), .Q(B_2), .clk(CLK), .clr(register_1_q), .cs(1'b0), .preset(1'b0));
endmodule

module EX_MEM_WD_cmdReg (
  input  CLK,
  input  Clear,
  input  [31:0] A_32,
  input  [31:0] B_32,
  input  [4:0] C_5,
  input  halt,
  output [31:0] A_32_2,
  output [31:0] B_32_2,
  output [4:0] C_5_2,
  output halt_2
);

  Register #(.width(32), .trigger("rising"), .Select("low")) register_1 (
    .D(A_32), .Q(A_32_2), .clk(CLK), .clr(Clear));  // open: en
  Register #(.width(32), .trigger("rising"), .Select("low")) register_2 (
    .D(B_32), .Q(B_32_2), .clk(CLK), .clr(Clear));  // open: en
  Register #(.width(5), .trigger("rising"), .Select("low")) register_3 (
    .D(C_5), .Q(C_5_2), .clk(CLK), .clr(Clear));  // open: en
  Register #(.width(1), .trigger("rising"), .Select("low")) register_4 (
    .D(halt), .Q(halt_2), .clk(CLK), .clr(Clear));  // open: en
endmodule

module PC_IR_cmdReg (
  input  [31:0] PC,
  input  [31:0] IR,
  input  AsyClear,
  input  Run,
  input  CLK,
  input  Clear,
  output [31:0] PC_2,
  output [31:0] IR_2
);

  wire [31:0] multiplexer_1_out, multiplexer_2_out;

  Multiplexer #(.select(1), .width(32), .disabled("Z"), .enable("false")) multiplexer_1 (
    .in0(PC), .in1({32{1'b0}}), .out(multiplexer_1_out), .sel(AsyClear));
  Multiplexer #(.select(1), .width(32), .disabled("Z"), .enable("false")) multiplexer_2 (
    .in0(IR), .in1({32{1'b0}}), .out(multiplexer_2_out), .sel(AsyClear));
  Register #(.width(32), .trigger("rising"), .Select("low")) register_1 (
    .D(multiplexer_1_out), .en(Run), .Q(PC_2), .clk(CLK), .clr(Clear));
  Register #(.width(32), .trigger("rising"), .Select("low")) register_2 (
    .D(multiplexer_2_out), .en(Run), .Q(IR_2), .clk(CLK), .clr(Clear));
endmodule

module Mul_cmdClear (
  input  Clear,
  input  lw,
  input  lh,
  input  uret,
  input  JALR,
  input  JAL,
  input  Bne,
  input  Beq,
  input  MemToReg,
  input  MemWrite,
  input  [3:0] Alu_OP,
  input  Alu_Src,
  input  RegWrite,
  input  bltu,
  input  S_Type,
  input  ecall,
  input  CSR,
  output lw_2,
  output lh_2,
  output uret_2,
  output JALR_2,
  output JAL_2,
  output Bne_2,
  output Beq_2,
  output MemToReg_2,
  output MemWrite_2,
  output [3:0] Alu_OP_2,
  output Alu_Src_2,
  output RegWrite_2,
  output bltu_2,
  output S_Type_2,
  output ecall_2,
  output CSR_2
);

  Multiplexer #(.select(1), .width(1), .disabled("Z"), .enable("false")) multiplexer_1 (
    .in0(lw), .in1(1'b0), .out(lw_2), .sel(Clear));
  Multiplexer #(.select(1), .width(1), .disabled("Z"), .enable("false")) multiplexer_2 (
    .in0(lh), .in1(1'b0), .out(lh_2), .sel(Clear));
  Multiplexer #(.select(1), .width(1), .disabled("Z"), .enable("false")) multiplexer_3 (
    .in0(uret), .in1(1'b0), .out(uret_2), .sel(Clear));
  Multiplexer #(.select(1), .width(1), .disabled("Z"), .enable("false")) multiplexer_4 (
    .in0(JALR), .in1(1'b0), .out(JALR_2), .sel(Clear));
  Multiplexer #(.select(1), .width(1), .disabled("Z"), .enable("false")) multiplexer_5 (
    .in0(JAL), .in1(1'b0), .out(JAL_2), .sel(Clear));
  Multiplexer #(.select(1), .width(1), .disabled("Z"), .enable("false")) multiplexer_6 (
    .in0(Bne), .in1(1'b0), .out(Bne_2), .sel(Clear));
  Multiplexer #(.select(1), .width(1), .disabled("Z"), .enable("false")) multiplexer_7 (
    .in0(Beq), .in1(1'b0), .out(Beq_2), .sel(Clear));
  Multiplexer #(.select(1), .width(1), .disabled("Z"), .enable("false")) multiplexer_8 (
    .in0(MemToReg), .in1(1'b0), .out(MemToReg_2), .sel(Clear));
  Multiplexer #(.select(1), .width(1), .disabled("Z"), .enable("false")) multiplexer_9 (
    .in0(MemWrite), .in1(1'b0), .out(MemWrite_2), .sel(Clear));
  Multiplexer #(.select(1), .width(4), .disabled("Z"), .enable("false")) multiplexer_10 (
    .in0(Alu_OP), .in1(4'b0000), .out(Alu_OP_2), .sel(Clear));
  Multiplexer #(.select(1), .width(1), .disabled("Z"), .enable("false")) multiplexer_11 (
    .in0(Alu_Src), .in1(1'b0), .out(Alu_Src_2), .sel(Clear));
  Multiplexer #(.select(1), .width(1), .disabled("Z"), .enable("false")) multiplexer_12 (
    .in0(RegWrite), .in1(1'b0), .out(RegWrite_2), .sel(Clear));
  Multiplexer #(.select(1), .width(1), .disabled("Z"), .enable("false")) multiplexer_13 (
    .in0(bltu), .in1(1'b0), .out(bltu_2), .sel(Clear));
  Multiplexer #(.select(1), .width(1), .disabled("Z"), .enable("false")) multiplexer_14 (
    .in0(S_Type), .in1(1'b0), .out(S_Type_2), .sel(Clear));
  Multiplexer #(.select(1), .width(1), .disabled("Z"), .enable("false")) multiplexer_15 (
    .in0(ecall), .in1(1'b0), .out(ecall_2), .sel(Clear));
  Multiplexer #(.select(1), .width(1), .disabled("Z"), .enable("false")) multiplexer_16 (
    .in0(CSR), .in1(1'b0), .out(CSR_2), .sel(Clear));
endmodule

module PC_JumpingUnit (
  input  Branch,
  input  [31:0] PC,
  input  [31:0] offset,
  input  [31:0] IR,
  output [31:0] PC_2,
  output [31:0] IR_2
);

  wire [31:0] adder_1_out, Instruction_Memory_data;

  Adder #(.width(32)) adder_1 (.a(PC), .b(offset), .out(adder_1_out), .cin(1'b0));  // open: cout
  Multiplexer #(.select(1), .width(32), .disabled("Z"), .enable("false")) multiplexer_1 (
    .in0(PC), .in1(adder_1_out), .out(PC_2), .sel(Branch));
  ROM #(.addrWidth(10), .dataWidth(32), .Select("high")) Instruction_Memory (
    .addr(adder_1_out[11:2]), .data(Instruction_Memory_data), .sel(1'b1));
  Multiplexer #(.select(1), .width(32), .disabled("Z"), .enable("false")) multiplexer_2 (
    .in0(IR), .in1(Instruction_Memory_data), .out(IR_2), .sel(Branch));

  // Notes on the sheet:
  //   contents of Instruction_Memory (hex, n*v repeats v):
  //   100413 ff00913 100493 300993 1240a63 840863 100493 200913 300993 800533 2200893 73 949a63 1249863
  //   100493 200913 300993 1300533 2200893 73 a00893 73
endmodule

module DataConflict (
  input  EX_RegWrite,
  input  [4:0] rs,
  input  [4:0] rt,
  input  [4:0] EX_Reg,
  input  [4:0] MEM_Reg,
  input  MEM_RegWrite,
  input  Alu_Src,
  output hazzard
);

  wire and_1_out, and_2_out, and_3_out, and_4_out, and_5_out, and_6_out, comparator_1_eq, comparator_2_eq,
       comparator_3_eq, comparator_4_eq, comparator_5_eq, comparator_6_eq, or_1_out, or_2_out, used_rt;

  Comparator #(.width(5), .mode("twosComplement")) comparator_1 (
    .a({5{1'b0}}), .b(EX_Reg), .eq(comparator_1_eq));  // open: gt, lt
  Comparator #(.width(5), .mode("twosComplement")) comparator_2 (
    .a(EX_Reg), .b(rs), .eq(comparator_2_eq));  // open: gt, lt
  Comparator #(.width(5), .mode("twosComplement")) comparator_3 (
    .a(EX_Reg), .b(rt), .eq(comparator_3_eq));  // open: gt, lt
  Comparator #(.width(5), .mode("twosComplement")) comparator_4 (
    .a(rs), .b(MEM_Reg), .eq(comparator_4_eq));  // open: gt, lt
  Comparator #(.width(5), .mode("twosComplement")) comparator_5 (
    .a(MEM_Reg), .b(rt), .eq(comparator_5_eq));  // open: gt, lt
  Comparator #(.width(5), .mode("twosComplement")) comparator_6 (
    .a(MEM_Reg), .b({5{1'b0}}), .eq(comparator_6_eq));  // open: gt, lt
  not not_1 (used_rt, Alu_Src);
  and and_1 (and_1_out, 1'b1, comparator_2_eq);
  and and_2 (and_2_out, used_rt, comparator_3_eq);
  and and_3 (and_3_out, 1'b1, comparator_4_eq);
  and and_4 (and_4_out, used_rt, comparator_5_eq);
  or or_1 (or_1_out, and_1_out, and_2_out);
  or or_2 (or_2_out, and_3_out, and_4_out);
  and and_5 (and_5_out, ~comparator_1_eq, EX_RegWrite, or_1_out);  // AND_Gate
  or or_3 (hazzard, and_5_out, and_6_out);
  and and_6 (and_6_out, or_2_out, MEM_RegWrite, ~comparator_6_eq);  // AND_Gate

  // Notes on the sheet:
  //   for rs, usedRs-ecall only has 2 situations, that is 10, 11
  //   10 denotes non-system cmd, rs has been used
  //   11 denotes system cmd ecall, we should replace rs&rt
  //   no usage of rt
  //   no usage of rs
  //   while considering system commands, the enable end would be changed
  //   hazzard
endmodule

module LoadConflict (
  input  Rt_Used,
  input  [4:0] Rs,
  input  [4:0] Rt,
  input  EX_MemRead,
  input  [4:0] EX_RegWrite,
  output LoadUsed
);

  wire and_1_out, and_2_out, comparator_1_eq, comparator_2_eq, comparator_3_eq, comparator_4_eq, not_1_out,
       not_2_out;

  Comparator #(.width(5), .mode("twosComplement")) comparator_1 (
    .a(Rs), .b({5{1'b0}}), .eq(comparator_1_eq));  // open: gt, lt
  Comparator #(.width(5), .mode("twosComplement")) comparator_2 (
    .a(Rs), .b(EX_RegWrite), .eq(comparator_2_eq));  // open: gt, lt
  Comparator #(.width(5), .mode("twosComplement")) comparator_3 (
    .a(Rt), .b({5{1'b0}}), .eq(comparator_3_eq));  // open: gt, lt
  Comparator #(.width(5), .mode("twosComplement")) comparator_4 (
    .a(Rt), .b(EX_RegWrite), .eq(comparator_4_eq));  // open: gt, lt
  not not_1 (not_1_out, comparator_1_eq);
  not not_2 (not_2_out, comparator_3_eq);
  and and_1 (and_1_out, 1'b1, not_1_out, comparator_2_eq, EX_MemRead);
  and and_2 (and_2_out, Rt_Used, not_2_out, comparator_4_eq, EX_MemRead);
  or or_1 (LoadUsed, and_1_out, and_2_out);
endmodule

module LoadConflictProcessorUnit (
  input  [31:0] PC,
  input  [31:0] IR,
  input  Conflict,
  input  CLK,
  output [31:0] PC_2,
  output [31:0] IR_2
);

  wire register_1_q;

  Multiplexer #(.select(1), .width(32), .disabled("Z"), .enable("false")) multiplexer_1 (
    .in0(PC), .in1(PC_2), .out(PC_2), .sel(register_1_q));
  Multiplexer #(.select(1), .width(32), .disabled("Z"), .enable("false")) multiplexer_2 (
    .in0(IR), .in1(IR_2), .out(IR_2), .sel(register_1_q));
  Register #(.width(1), .trigger("rising"), .Select("low")) register_1 (
    .D(Conflict), .Q(register_1_q), .clk(CLK));  // open: en, clr
endmodule

module RedirectionConflict (
  input  Rt_Used,
  input  EX_RegWrite,
  input  MEM_RegWrite,
  input  [4:0] Rs,
  input  [4:0] Rt,
  input  [4:0] EX_Reg,
  input  [4:0] MEM_Reg,
  output [1:0] RsFoward,
  output [1:0] RtFoward
);

  wire comparator_1_eq, comparator_2_eq, comparator_3_eq, comparator_4_eq, comparator_5_eq, comparator_6_eq,
       comparator_7_eq, comparator_8_eq, not_1_out, not_2_out, not_3_out, not_4_out;

  Comparator #(.width(5), .mode("twosComplement")) comparator_1 (
    .a({5{1'b0}}), .b(Rs), .eq(comparator_1_eq));  // open: gt, lt
  Comparator #(.width(5), .mode("twosComplement")) comparator_2 (
    .a(Rs), .b(EX_Reg), .eq(comparator_2_eq));  // open: gt, lt
  Comparator #(.width(5), .mode("twosComplement")) comparator_3 (
    .a({5{1'b0}}), .b(Rs), .eq(comparator_3_eq));  // open: gt, lt
  Comparator #(.width(5), .mode("twosComplement")) comparator_4 (
    .a(Rs), .b(MEM_Reg), .eq(comparator_4_eq));  // open: gt, lt
  not not_1 (not_1_out, comparator_1_eq);
  and and_1 (RsFoward[1], 1'b1, not_1_out, EX_RegWrite, comparator_2_eq);
  not not_2 (not_2_out, comparator_3_eq);
  and and_2 (RsFoward[0], 1'b1, not_2_out, MEM_RegWrite, comparator_4_eq);
  Comparator #(.width(5), .mode("twosComplement")) comparator_5 (
    .a({5{1'b0}}), .b(Rt), .eq(comparator_5_eq));  // open: gt, lt
  not not_3 (not_3_out, comparator_5_eq);
  Comparator #(.width(5), .mode("twosComplement")) comparator_6 (
    .a(Rt), .b(EX_Reg), .eq(comparator_6_eq));  // open: gt, lt
  Comparator #(.width(5), .mode("twosComplement")) comparator_7 (
    .a({5{1'b0}}), .b(Rt), .eq(comparator_7_eq));  // open: gt, lt
  not not_4 (not_4_out, comparator_7_eq);
  Comparator #(.width(5), .mode("twosComplement")) comparator_8 (
    .a(Rt), .b(MEM_Reg), .eq(comparator_8_eq));  // open: gt, lt
  and and_3 (RtFoward[1], Rt_Used, not_3_out, EX_RegWrite, comparator_6_eq);
  and and_4 (RtFoward[0], Rt_Used, not_4_out, MEM_RegWrite, comparator_8_eq);
endmodule

module BTB (
  input  isBranch,
  input  [31:0] BranchPC,
  input  [31:0] BranchTargetPC,
  input  CLK,
  input  BranchTaken,
  input  RST,
  input  [31:0] cmdPC,
  output Failure,
  output [31:0] Target_PC
);

  wire and_9_out, and_10_out, and_11_out, and_12_out, and_13_out, and_14_out, and_15_out, and_16_out,
       and_17_out, and_18_out, and_19_out, and_20_out, and_21_out, and_22_out, and_23_out, and_24_out,
       and_25_out, and_27_out, and_28_out, and_29_out, and_30_out, and_31_out, and_32_out, and_33_out,
       and_34_out, comparator_1_eq, comparator_2_eq, comparator_3_eq, comparator_4_eq, comparator_5_eq,
       comparator_6_eq, comparator_7_eq, comparator_8_eq, comparator_9_eq, comparator_10_eq,
       comparator_11_eq, comparator_12_eq, comparator_13_eq, comparator_14_eq, comparator_15_eq,
       comparator_16_eq, Full, hit_0, hit_1, hit_2, hit_3, hit_4, hit_5, hit_6, hit_7, Initalize,
       lru_unit_1_out_0, lru_unit_1_out_1, lru_unit_1_out_2, lru_unit_1_out_3, lru_unit_1_out_4,
       lru_unit_1_out_5, lru_unit_1_out_6, lru_unit_1_out_7, miss_t, not_1_out, not_2_out, not_3_out,
       not_4_out, not_5_out, not_6_out, not_7_out, not_8_out, or_1_out, or_2_out, or_3_out,
       priority_encoder_2_en_out, valid_0, valid_1, valid_2, valid_3, valid_4, valid_5, valid_6, valid_7,
       write_0, write_1, write_2, write_3, write_4, write_5, write_6, write_7, zero_0, zero_1, zero_2,
       zero_3, zero_4, zero_5, zero_6, zero_7;
  wire [1:0] btb_alu_1_newbit, btb_alu_2_newbit, btb_alu_3_newbit, btb_alu_4_newbit, btb_alu_5_newbit,
       btb_alu_6_newbit, btb_alu_7_newbit, btb_alu_8_newbit, history_0, history_1, history_2, history_3,
       history_4, history_5, history_6, history_7, multiplexer_10_out, multiplexer_11_out;
  wire [2:0] priority_encoder_1_out;
  wire [31:0] adder_1_out, branchPC_0, branchPC_1, branchPC_2, branchPC_3, branchPC_4, branchPC_5,
       branchPC_6, branchPC_7, multiplexer_1_out, multiplexer_2_out, multiplexer_3_out, multiplexer_4_out,
       multiplexer_5_out, multiplexer_6_out, multiplexer_7_out, multiplexer_8_out, multiplexer_9_out,
       multiplexer_12_out, targetPC_0, targetPC_1, targetPC_2, targetPC_3, targetPC_4, targetPC_5,
       targetPC_6, targetPC_7;

  Register #(.width(32), .trigger("rising"), .Select("low")) register_1 (
    .D(BranchPC), .en(write_0), .Q(branchPC_0), .clk(CLK), .clr(RST));
  Register #(.width(32), .trigger("rising"), .Select("low")) register_2 (
    .D(BranchPC), .en(write_1), .Q(branchPC_1), .clk(CLK), .clr(RST));
  Register #(.width(32), .trigger("rising"), .Select("low")) register_3 (
    .D(BranchPC), .en(write_2), .Q(branchPC_2), .clk(CLK), .clr(RST));
  Register #(.width(32), .trigger("rising"), .Select("low")) register_4 (
    .D(BranchPC), .en(write_3), .Q(branchPC_3), .clk(CLK), .clr(RST));
  Register #(.width(32), .trigger("rising"), .Select("low")) register_5 (
    .D(BranchPC), .en(write_4), .Q(branchPC_4), .clk(CLK), .clr(RST));
  Register #(.width(32), .trigger("rising"), .Select("low")) register_6 (
    .D(BranchPC), .en(write_5), .Q(branchPC_5), .clk(CLK), .clr(RST));
  Register #(.width(32), .trigger("rising"), .Select("low")) register_7 (
    .D(BranchPC), .en(write_6), .Q(branchPC_6), .clk(CLK), .clr(RST));
  Register #(.width(32), .trigger("rising"), .Select("low")) register_8 (
    .D(BranchPC), .en(write_7), .Q(branchPC_7), .clk(CLK), .clr(RST));
  Comparator #(.width(32), .mode("twosComplement")) comparator_1 (
    .a(cmdPC), .b(branchPC_0), .eq(comparator_1_eq));  // open: gt, lt
  Comparator #(.width(32), .mode("twosComplement")) comparator_2 (
    .a(cmdPC), .b(branchPC_1), .eq(comparator_2_eq));  // open: gt, lt
  Comparator #(.width(32), .mode("twosComplement")) comparator_3 (
    .a(cmdPC), .b(branchPC_2), .eq(comparator_3_eq));  // open: gt, lt
  Comparator #(.width(32), .mode("twosComplement")) comparator_4 (
    .a(cmdPC), .b(branchPC_3), .eq(comparator_4_eq));  // open: gt, lt
  Comparator #(.width(32), .mode("twosComplement")) comparator_5 (
    .a(cmdPC), .b(branchPC_4), .eq(comparator_5_eq));  // open: gt, lt
  Comparator #(.width(32), .mode("twosComplement")) comparator_6 (
    .a(cmdPC), .b(branchPC_5), .eq(comparator_6_eq));  // open: gt, lt
  Comparator #(.width(32), .mode("twosComplement")) comparator_7 (
    .a(cmdPC), .b(branchPC_6), .eq(comparator_7_eq));  // open: gt, lt
  Comparator #(.width(32), .mode("twosComplement")) comparator_8 (
    .a(cmdPC), .b(branchPC_7), .eq(comparator_8_eq));  // open: gt, lt
  and and_1 (hit_0, valid_0, comparator_1_eq);
  and and_2 (hit_1, valid_1, comparator_2_eq);
  and and_3 (hit_2, valid_2, comparator_3_eq);
  and and_4 (hit_3, valid_3, comparator_4_eq);
  and and_5 (hit_4, valid_4, comparator_5_eq);
  and and_6 (hit_5, valid_5, comparator_6_eq);
  and and_7 (hit_6, valid_6, comparator_7_eq);
  and and_8 (hit_7, valid_7, comparator_8_eq);
  Multiplexer #(.select(1), .width(32), .disabled("Z"), .enable("false")) multiplexer_1 (
    .in0(targetPC_0), .in1(BranchTargetPC), .out(multiplexer_1_out), .sel(Initalize));
  Register #(.width(32), .trigger("rising"), .Select("low")) register_9 (
    .D(multiplexer_1_out), .en(write_0), .Q(targetPC_0), .clk(CLK), .clr(RST));
  Multiplexer #(.select(1), .width(32), .disabled("Z"), .enable("false")) multiplexer_2 (
    .in0(targetPC_1), .in1(BranchTargetPC), .out(multiplexer_2_out), .sel(Initalize));
  Register #(.width(32), .trigger("rising"), .Select("low")) register_10 (
    .D(multiplexer_2_out), .en(write_1), .Q(targetPC_1), .clk(CLK), .clr(RST));
  Multiplexer #(.select(1), .width(32), .disabled("Z"), .enable("false")) multiplexer_3 (
    .in0(targetPC_2), .in1(BranchTargetPC), .out(multiplexer_3_out), .sel(Initalize));
  Register #(.width(32), .trigger("rising"), .Select("low")) register_11 (
    .D(multiplexer_3_out), .en(write_2), .Q(targetPC_2), .clk(CLK), .clr(RST));
  Multiplexer #(.select(1), .width(32), .disabled("Z"), .enable("false")) multiplexer_4 (
    .in0(targetPC_3), .in1(BranchTargetPC), .out(multiplexer_4_out), .sel(Initalize));
  Register #(.width(32), .trigger("rising"), .Select("low")) register_12 (
    .D(multiplexer_4_out), .en(write_3), .Q(targetPC_3), .clk(CLK), .clr(RST));
  Multiplexer #(.select(1), .width(32), .disabled("Z"), .enable("false")) multiplexer_5 (
    .in0(targetPC_4), .in1(BranchTargetPC), .out(multiplexer_5_out), .sel(Initalize));
  Register #(.width(32), .trigger("rising"), .Select("low")) register_13 (
    .D(multiplexer_5_out), .en(write_4), .Q(targetPC_4), .clk(CLK), .clr(RST));
  Multiplexer #(.select(1), .width(32), .disabled("Z"), .enable("false")) multiplexer_6 (
    .in0(targetPC_5), .in1(BranchTargetPC), .out(multiplexer_6_out), .sel(Initalize));
  Register #(.width(32), .trigger("rising"), .Select("low")) register_14 (
    .D(multiplexer_6_out), .en(write_5), .Q(targetPC_5), .clk(CLK), .clr(RST));
  Multiplexer #(.select(1), .width(32), .disabled("Z"), .enable("false")) multiplexer_7 (
    .in0(targetPC_6), .in1(BranchTargetPC), .out(multiplexer_7_out), .sel(Initalize));
  Register #(.width(32), .trigger("rising"), .Select("low")) register_15 (
    .D(multiplexer_7_out), .en(write_6), .Q(targetPC_6), .clk(CLK), .clr(RST));
  Multiplexer #(.select(1), .width(32), .disabled("Z"), .enable("false")) multiplexer_8 (
    .in0(targetPC_7), .in1(BranchTargetPC), .out(multiplexer_8_out), .sel(Initalize));
  Register #(.width(32), .trigger("rising"), .Select("low")) register_16 (
    .D(multiplexer_8_out), .en(write_7), .Q(targetPC_7), .clk(CLK), .clr(RST));
  nor nor_1 (miss_t, hit_0, hit_1, hit_2, hit_3, hit_4, hit_5, hit_6, hit_7);
  and and_9 (and_9_out, Initalize, zero_0);
  and and_10 (and_10_out, Initalize, zero_1);
  and and_11 (and_11_out, Initalize, zero_2);
  and and_12 (and_12_out, Initalize, zero_3);
  and and_13 (and_13_out, Initalize, zero_4);
  and and_14 (and_14_out, Initalize, zero_5);
  and and_15 (and_15_out, Initalize, zero_6);
  and and_16 (and_16_out, Initalize, zero_7);
  BTB_ALU btb_alu_1 (
    .Bit(history_0), .ALU_OP(BranchTaken), .NewBit(btb_alu_1_newbit), .enable(write_0), .RST(and_9_out),
    .Zero(zero_0));
  BTB_ALU btb_alu_2 (
    .Bit(history_1), .ALU_OP(BranchTaken), .NewBit(btb_alu_2_newbit), .enable(write_1), .RST(and_10_out),
    .Zero(zero_1));
  BTB_ALU btb_alu_3 (
    .Bit(history_2), .ALU_OP(BranchTaken), .NewBit(btb_alu_3_newbit), .enable(write_2), .RST(and_11_out),
    .Zero(zero_2));
  BTB_ALU btb_alu_4 (
    .Bit(history_3), .ALU_OP(BranchTaken), .NewBit(btb_alu_4_newbit), .enable(write_3), .RST(and_12_out),
    .Zero(zero_3));
  BTB_ALU btb_alu_5 (
    .Bit(history_4), .ALU_OP(BranchTaken), .NewBit(btb_alu_5_newbit), .enable(write_4), .RST(and_13_out),
    .Zero(zero_4));
  BTB_ALU btb_alu_6 (
    .Bit(history_5), .ALU_OP(BranchTaken), .NewBit(btb_alu_6_newbit), .enable(write_5), .RST(and_14_out),
    .Zero(zero_5));
  BTB_ALU btb_alu_7 (
    .Bit(history_6), .ALU_OP(BranchTaken), .NewBit(btb_alu_7_newbit), .enable(write_6), .RST(and_15_out),
    .Zero(zero_6));
  BTB_ALU btb_alu_8 (
    .Bit(history_7), .ALU_OP(BranchTaken), .NewBit(btb_alu_8_newbit), .enable(write_7), .RST(and_16_out),
    .Zero(zero_7));
  Multiplexer #(.select(3), .width(32), .disabled("Z"), .enable("false")) multiplexer_9 (
    .in0(targetPC_0), .in1(targetPC_1), .in2(targetPC_2), .in3(targetPC_3), .in4(targetPC_4),
    .in5(targetPC_5), .in6(targetPC_6), .in7(targetPC_7), .out(multiplexer_9_out),
    .sel(priority_encoder_1_out));
  Priority_Encoder #(.select(3), .disabled("Z")) priority_encoder_1 (
    .in0(hit_0), .in1(hit_1), .in2(hit_2), .in3(hit_3), .in4(hit_4), .in5(hit_5), .in6(hit_6), .in7(hit_7),
    .out(priority_encoder_1_out));  // open: gs, en_out, en_in
  Multiplexer #(.select(3), .width(2), .disabled("Z"), .enable("false")) multiplexer_10 (
    .in0(history_0), .in1(history_1), .in2(history_2), .in3(history_3), .in4(history_4), .in5(history_5),
    .in6(history_6), .in7(history_7), .out(multiplexer_10_out), .sel(priority_encoder_1_out));
  Register #(.width(2), .trigger("rising"), .Select("low")) register_17 (
    .D(btb_alu_1_newbit), .Q(history_0), .clk(CLK), .clr(RST));  // open: en
  Register #(.width(2), .trigger("rising"), .Select("low")) register_18 (
    .D(btb_alu_2_newbit), .Q(history_1), .clk(CLK), .clr(RST));  // open: en
  Register #(.width(2), .trigger("rising"), .Select("low")) register_19 (
    .D(btb_alu_3_newbit), .Q(history_2), .clk(CLK), .clr(RST));  // open: en
  Register #(.width(2), .trigger("rising"), .Select("low")) register_20 (
    .D(btb_alu_4_newbit), .Q(history_3), .clk(CLK), .clr(RST));  // open: en
  Register #(.width(2), .trigger("rising"), .Select("low")) register_21 (
    .D(btb_alu_5_newbit), .Q(history_4), .clk(CLK), .clr(RST));  // open: en
  Register #(.width(2), .trigger("rising"), .Select("low")) register_22 (
    .D(btb_alu_6_newbit), .Q(history_5), .clk(CLK), .clr(RST));  // open: en
  Register #(.width(2), .trigger("rising"), .Select("low")) register_23 (
    .D(btb_alu_7_newbit), .Q(history_6), .clk(CLK), .clr(RST));  // open: en
  Register #(.width(2), .trigger("rising"), .Select("low")) register_24 (
    .D(btb_alu_8_newbit), .Q(history_7), .clk(CLK), .clr(RST));  // open: en
  Multiplexer #(.select(1), .width(2), .disabled("Z"), .enable("false")) multiplexer_11 (
    .in0(multiplexer_10_out), .in1(2'b00), .out(multiplexer_11_out), .sel(miss_t));
  not not_1 (not_1_out, zero_0);
  not not_2 (not_2_out, zero_1);
  not not_3 (not_3_out, zero_2);
  not not_4 (not_4_out, zero_3);
  not not_5 (not_5_out, zero_4);
  not not_6 (not_6_out, zero_5);
  not not_7 (not_7_out, zero_6);
  not not_8 (not_8_out, zero_7);
  Adder #(.width(32)) adder_1 (.a(cmdPC), .b(32'h4), .out(adder_1_out));  // open: cin, cout
  Register #(.width(1), .trigger("falling"), .Select("low")) register_25 (
    .D(not_1_out), .Q(valid_0), .clk(CLK));  // open: en, clr
  Register #(.width(1), .trigger("falling"), .Select("low")) register_26 (
    .D(not_2_out), .Q(valid_1), .clk(CLK));  // open: en, clr
  Register #(.width(1), .trigger("falling"), .Select("low")) register_27 (
    .D(not_3_out), .Q(valid_2), .clk(CLK));  // open: en, clr
  Register #(.width(1), .trigger("falling"), .Select("low")) register_28 (
    .D(not_4_out), .Q(valid_3), .clk(CLK));  // open: en, clr
  Register #(.width(1), .trigger("falling"), .Select("low")) register_29 (
    .D(not_5_out), .Q(valid_4), .clk(CLK));  // open: en, clr
  Register #(.width(1), .trigger("falling"), .Select("low")) register_30 (
    .D(not_6_out), .Q(valid_5), .clk(CLK));  // open: en, clr
  Register #(.width(1), .trigger("falling"), .Select("low")) register_31 (
    .D(not_7_out), .Q(valid_6), .clk(CLK));  // open: en, clr
  Register #(.width(1), .trigger("falling"), .Select("low")) register_32 (
    .D(not_8_out), .Q(valid_7), .clk(CLK));  // open: en, clr
  Multiplexer #(.select(1), .width(32), .disabled("Z"), .enable("false")) multiplexer_12 (
    .in0(adder_1_out), .in1(multiplexer_9_out), .out(multiplexer_12_out), .sel(multiplexer_11_out[1]));
  Adder #(.width(32)) adder_2 (.a(32'h4), .b(BranchPC));  // open: out, cin, cout
  or or_1 (or_1_out, Initalize, and_17_out);
  Multiplexer #(.select(1), .width(32), .disabled("Z"), .enable("false")) multiplexer_13 (
    .in0(multiplexer_12_out), .in1(BranchTargetPC), .out(Target_PC), .sel(or_1_out));
  and and_17 (and_17_out, isBranch, ~BranchTaken);  // AND_Gate
  and and_18 (and_18_out, zero_0, write_0);
  and and_19 (and_19_out, zero_1, write_1);
  and and_20 (and_20_out, zero_2, write_2);
  and and_21 (and_21_out, zero_3, write_3);
  and and_22 (and_22_out, zero_4, write_4);
  and and_23 (and_23_out, zero_5, write_5);
  and and_24 (and_24_out, zero_6, write_6);
  and and_25 (and_25_out, zero_7, write_7);
  and and_26 (Initalize, isBranch, priority_encoder_2_en_out);
  or or_2 (or_2_out, and_18_out, and_19_out, and_20_out, and_21_out, and_22_out, and_23_out, and_24_out, and_25_out);
  Comparator #(.width(32), .mode("twosComplement")) comparator_9 (
    .a(BranchPC), .b(branchPC_0), .eq(comparator_9_eq));  // open: gt, lt
  Comparator #(.width(32), .mode("twosComplement")) comparator_10 (
    .a(BranchPC), .b(branchPC_1), .eq(comparator_10_eq));  // open: gt, lt
  Comparator #(.width(32), .mode("twosComplement")) comparator_11 (
    .a(BranchPC), .b(branchPC_2), .eq(comparator_11_eq));  // open: gt, lt
  Comparator #(.width(32), .mode("twosComplement")) comparator_12 (
    .a(BranchPC), .b(branchPC_3), .eq(comparator_12_eq));  // open: gt, lt
  Comparator #(.width(32), .mode("twosComplement")) comparator_13 (
    .a(BranchPC), .b(branchPC_4), .eq(comparator_13_eq));  // open: gt, lt
  Comparator #(.width(32), .mode("twosComplement")) comparator_14 (
    .a(BranchPC), .b(branchPC_5), .eq(comparator_14_eq));  // open: gt, lt
  Comparator #(.width(32), .mode("twosComplement")) comparator_15 (
    .a(BranchPC), .b(branchPC_6), .eq(comparator_15_eq));  // open: gt, lt
  Comparator #(.width(32), .mode("twosComplement")) comparator_16 (
    .a(BranchPC), .b(branchPC_7), .eq(comparator_16_eq));  // open: gt, lt
  Priority_Encoder #(.select(3), .disabled("Z")) priority_encoder_2 (
    .in0(and_27_out), .in1(and_28_out), .in2(and_29_out), .in3(and_30_out), .in4(and_31_out),
    .in5(and_32_out), .in6(and_33_out), .in7(and_34_out), .en_out(priority_encoder_2_en_out));  // open: out, gs, en_in
  and and_27 (and_27_out, valid_0, isBranch, comparator_9_eq);
  and and_28 (and_28_out, valid_1, isBranch, comparator_10_eq);
  and and_29 (and_29_out, valid_2, isBranch, comparator_11_eq);
  and and_30 (and_30_out, valid_3, isBranch, comparator_12_eq);
  and and_31 (and_31_out, valid_4, isBranch, comparator_13_eq);
  and and_32 (and_32_out, valid_5, isBranch, comparator_14_eq);
  and and_33 (and_33_out, valid_6, isBranch, comparator_15_eq);
  and and_34 (and_34_out, valid_7, isBranch, comparator_16_eq);
  LRU_Unit lru_unit_1 (
    .enable(Initalize), .CLK(CLK), .Clear(RST), .Out_0(lru_unit_1_out_0), .Out_1(lru_unit_1_out_1),
    .Out_2(lru_unit_1_out_2), .Out_3(lru_unit_1_out_3), .Out_4(lru_unit_1_out_4), .Out_5(lru_unit_1_out_5),
    .Out_6(lru_unit_1_out_6), .Out_7(lru_unit_1_out_7), ._0(and_27_out), ._1(and_28_out), ._2(and_29_out),
    ._5(and_32_out), ._6(and_33_out), ._7(and_34_out), ._3(and_30_out), ._4(and_31_out));
  and and_35 (Full, valid_0, valid_1, valid_2, valid_3, valid_4, valid_5, valid_6, valid_7);
  or or_3 (or_3_out, ~BranchTaken, Initalize);  // OR_Gate
  and and_36 (Failure, or_3_out, isBranch);
  or or_4 (write_0, and_27_out, lru_unit_1_out_0);
  or or_5 (write_1, and_28_out, lru_unit_1_out_1);
  or or_6 (write_2, and_29_out, lru_unit_1_out_2);
  or or_7 (write_3, and_30_out, lru_unit_1_out_3);
  or or_8 (write_4, and_31_out, lru_unit_1_out_4);
  or or_9 (write_5, and_32_out, lru_unit_1_out_5);
  or or_10 (write_6, and_33_out, lru_unit_1_out_6);
  or or_11 (write_7, and_34_out, lru_unit_1_out_7);

  // Other names for the same wires on the sheet: Miss = Initalize

  // Notes on the sheet:
  //   This part functions for comparing
  //   Memory Section
  //   Select compared target PC
  //   Signal out-x can replace table data according to LRU
  //   cmdPC can be updated right now
  //   valid-x and replace-x will be set as initial value
  //   if user wants to update data while comparing stage, update-x will be TRUE
  //   targetPC-x and history-x will be decided while this cmd first come into EX.
  //   Therefore this unit will only update data while excuting BranchTaken
  //   While miss is TRUE or history hit is less than 2, Target PC will be equal to cmdPC(input)
  //   This section is used to update history bit
  //   isBranch denotes the EX.cmd is Branch CMD or not
  //   When it was 1, this section runs
  //   BranchTaken was set to represent the prediction result
  //   In BranchTaken stage, the unit can only revise 2 values, HistoryHit and TargetPC.
  //   Ohterwise, the LRU unit will update counts according to Select input
  //   When input Miss is TRUE, BTB should find out the corresponding table data, and update its targetPC
  //   There are 2 types of LRU. One is while Miss is TRUE, that means LRU have to clear the least frequent item.
  //   If BTB missed, BTB should update the whole line according to LRU,
  //   BranchPC hit
  //   Or while any history hit is 0, corresponding target PC should be updated, with history hit initalize
  //   Miss
endmodule

module BTB_ALU (
  input  [1:0] Bit,
  input  RST,
  input  enable,
  input  ALU_OP,
  output Zero,
  output [1:0] NewBit
);

  wire and_1_out, demultiplexer_1_out0, demultiplexer_1_out1, or_1_out;
  wire [1:0] adder_1_out, multiplexer_1_out, multiplexer_2_out, multiplexer_3_out, multiplexer_4_out,
       multiplexer_5_out, multiplexer_6_out, subtractor_1_out;

  Demultiplexer #(.select(1), .width(1), .tristate("false"), .disabled("Z"), .enable("false")) demultiplexer_1 (
    .out0(demultiplexer_1_out0), .out1(demultiplexer_1_out1), .in(1'b1), .sel(ALU_OP));
  Multiplexer #(.select(1), .width(2), .disabled("Z"), .enable("false")) multiplexer_1 (
    .in0(2'b00), .in1(2'b01), .out(multiplexer_1_out), .sel(demultiplexer_1_out0));
  Multiplexer #(.select(1), .width(2), .disabled("Z"), .enable("false")) multiplexer_2 (
    .in0(2'b00), .in1(2'b01), .out(multiplexer_2_out), .sel(demultiplexer_1_out1));
  Subtractor #(.width(2)) subtractor_1 (.a(Bit), .b(multiplexer_1_out), .out(subtractor_1_out));  // open: bin, bout
  Adder #(.width(2)) adder_1 (.a(multiplexer_2_out), .b(Bit), .out(adder_1_out));  // open: cin, cout
  Multiplexer #(.select(1), .width(2), .disabled("Z"), .enable("false")) multiplexer_3 (
    .in0(subtractor_1_out), .in1(Bit), .out(multiplexer_3_out), .sel(and_1_out));
  and and_1 (and_1_out, subtractor_1_out[0], subtractor_1_out[1]);
  or or_1 (or_1_out, adder_1_out[0], adder_1_out[1]);
  Multiplexer #(.select(1), .width(2), .disabled("Z"), .enable("false")) multiplexer_4 (
    .in0(Bit), .in1(adder_1_out), .out(multiplexer_4_out), .sel(or_1_out));
  Comparator #(.width(2), .mode("unsigned")) comparator_1 (.a(2'b00), .b(Bit), .eq(Zero));  // open: gt, lt
  Multiplexer #(.select(1), .width(2), .disabled("Z"), .enable("false")) multiplexer_5 (
    .in0(multiplexer_3_out), .in1(multiplexer_4_out), .out(multiplexer_5_out), .sel(ALU_OP));
  Multiplexer #(.select(1), .width(2), .disabled("Z"), .enable("false")) multiplexer_6 (
    .in0(multiplexer_5_out), .in1(2'b11), .out(multiplexer_6_out), .sel(RST));
  Multiplexer #(.select(1), .width(2), .disabled("Z"), .enable("false")) multiplexer_7 (
    .in0(Bit), .in1(multiplexer_6_out), .out(NewBit), .sel(enable));

  // Notes on the sheet:
  //   RST represents set NewBit as initial value(11)
  //   RST is allowed when enable is TRUE
  //   ALU_OP=1 -> add  |  ALU_OP=0 -> sub
  //   Only when enable is TRUE will the unit ran, or retrieve input Bit
  //   00-1=11
  //   11+1=00
endmodule
module LRU_Unit (
  input  CLK,
  input  enable,
  input  _0,
  input  _1,
  input  _2,
  input  _3,
  input  _4,
  input  Clear,
  input  _5,
  input  _6,
  input  _7,
  output Out_0,
  output Out_1,
  output Out_2,
  output Out_3,
  output Out_4,
  output Out_5,
  output Out_6,
  output Out_7
);

  wire comparator_1_lt, comparator_2_lt, comparator_3_lt, comparator_4_lt, decoder_1_out0, decoder_1_out1,
       decoder_1_out2, decoder_1_out3, decoder_1_out4, decoder_1_out5, decoder_1_out6, decoder_1_out7,
       or_1_out, or_2_out, or_3_out, or_4_out, or_5_out, or_6_out, or_7_out, or_8_out, register_1_q,
       register_2_q, register_3_q, register_4_q, register_5_q, register_6_q, register_7_q, register_8_q,
       RST_0, RST_1, RST_2, RST_3, RST_4, RST_5, RST_6, RST_7;
  wire [1:0] multiplexer_6_out, multiplexer_8_out;
  wire [2:0] multiplexer_9_out;
  wire [15:0] _000_q, _001_q, _010_q, _011_q, _100_q, _101_q, _110_q, _111_q, multiplexer_1_out,
       multiplexer_2_out, multiplexer_3_out, multiplexer_4_out, multiplexer_5_out, multiplexer_7_out;

  or or_1 (or_1_out, _0, RST_0);
  or or_2 (or_2_out, _1, RST_1);
  or or_3 (or_3_out, _2, RST_2);
  or or_4 (or_4_out, _3, RST_3);
  or or_5 (or_5_out, _4, RST_4);
  or or_6 (or_6_out, _5, RST_5);
  or or_7 (or_7_out, _6, RST_6);
  or or_8 (or_8_out, _7, RST_7);
  Register #(.width(1), .trigger("rising"), .Select("low")) register_1 (
    .D(or_1_out), .Q(register_1_q), .clk(CLK));  // open: en, clr
  Register #(.width(1), .trigger("rising"), .Select("low")) register_2 (
    .D(or_2_out), .Q(register_2_q), .clk(CLK));  // open: en, clr
  Register #(.width(1), .trigger("rising"), .Select("low")) register_3 (
    .D(or_3_out), .Q(register_3_q), .clk(CLK));  // open: en, clr
  Register #(.width(1), .trigger("rising"), .Select("low")) register_4 (
    .D(or_4_out), .Q(register_4_q), .clk(CLK));  // open: en, clr
  Register #(.width(1), .trigger("rising"), .Select("low")) register_5 (
    .D(or_5_out), .Q(register_5_q), .clk(CLK));  // open: en, clr
  Register #(.width(1), .trigger("rising"), .Select("low")) register_6 (
    .D(or_6_out), .Q(register_6_q), .clk(CLK));  // open: en, clr
  Register #(.width(1), .trigger("rising"), .Select("low")) register_7 (
    .D(or_7_out), .Q(register_7_q), .clk(CLK));  // open: en, clr
  Register #(.width(1), .trigger("rising"), .Select("low")) register_8 (
    .D(or_8_out), .Q(register_8_q), .clk(CLK));  // open: en, clr
  Counter #(.width(16), .max('hffff), .ongoal("wrap"), .trigger("rising"), .behavior("new")) _000 (
    .Q(_000_q), .clk(CLK), .clr(register_1_q));  // open: load, D, count, carry, preset, down
  Counter #(.width(16), .max('hffff), .ongoal("wrap"), .trigger("rising"), .behavior("new")) _001 (
    .Q(_001_q), .clk(CLK), .clr(register_2_q));  // open: load, D, count, carry, preset, down
  Counter #(.width(16), .max('hffff), .ongoal("wrap"), .trigger("rising"), .behavior("new")) _010 (
    .Q(_010_q), .clk(CLK), .clr(register_3_q));  // open: load, D, count, carry, preset, down
  Counter #(.width(16), .max('hffff), .ongoal("wrap"), .trigger("rising"), .behavior("new")) _011 (
    .Q(_011_q), .clk(CLK), .clr(register_4_q));  // open: load, D, count, carry, preset, down
  Counter #(.width(16), .max('hffff), .ongoal("wrap"), .trigger("rising"), .behavior("new")) _100 (
    .Q(_100_q), .clk(CLK), .clr(register_5_q));  // open: load, D, count, carry, preset, down
  Counter #(.width(16), .max('hffff), .ongoal("wrap"), .trigger("rising"), .behavior("new")) _101 (
    .Q(_101_q), .clk(CLK), .clr(register_6_q));  // open: load, D, count, carry, preset, down
  Counter #(.width(16), .max('hffff), .ongoal("wrap"), .trigger("rising"), .behavior("new")) _110 (
    .Q(_110_q), .clk(CLK), .clr(register_7_q));  // open: load, D, count, carry, preset, down
  Counter #(.width(16), .max('hffff), .ongoal("wrap"), .trigger("rising"), .behavior("new")) _111 (
    .Q(_111_q), .clk(CLK), .clr(register_8_q));  // open: load, D, count, carry, preset, down
  Comparator #(.width(16), .mode("unsigned")) comparator_1 (
    .a(_000_q), .b(_001_q), .lt(comparator_1_lt));  // open: gt, eq
  Comparator #(.width(16), .mode("unsigned")) comparator_2 (
    .a(_010_q), .b(_011_q), .lt(comparator_2_lt));  // open: gt, eq
  Comparator #(.width(16), .mode("unsigned")) comparator_3 (
    .a(_100_q), .b(_101_q), .lt(comparator_3_lt));  // open: gt, eq
  Comparator #(.width(16), .mode("unsigned")) comparator_4 (
    .a(_110_q), .b(_111_q), .lt(comparator_4_lt));  // open: gt, eq
  Multiplexer #(.select(1), .width(16), .disabled("Z"), .enable("false")) multiplexer_1 (
    .in0(_000_q), .in1(_001_q), .out(multiplexer_1_out), .sel(comparator_1_lt));
  Multiplexer #(.select(1), .width(16), .disabled("Z"), .enable("false")) multiplexer_2 (
    .in0(_010_q), .in1(_011_q), .out(multiplexer_2_out), .sel(comparator_2_lt));
  Multiplexer #(.select(1), .width(16), .disabled("Z"), .enable("false")) multiplexer_3 (
    .in0(_100_q), .in1(_101_q), .out(multiplexer_3_out), .sel(comparator_3_lt));
  Multiplexer #(.select(1), .width(16), .disabled("Z"), .enable("false")) multiplexer_4 (
    .in0(_110_q), .in1(_111_q), .out(multiplexer_4_out), .sel(comparator_4_lt));
  Comparator #(.width(16), .mode("unsigned")) comparator_5 (
    .a(multiplexer_1_out), .b(multiplexer_2_out), .lt(multiplexer_6_out[1]));  // open: gt, eq
  Comparator #(.width(16), .mode("unsigned")) comparator_6 (
    .a(multiplexer_3_out), .b(multiplexer_4_out), .lt(multiplexer_8_out[1]));  // open: gt, eq
  Multiplexer #(.select(1), .width(16), .disabled("Z"), .enable("false")) multiplexer_5 (
    .in0(multiplexer_1_out), .in1(multiplexer_2_out), .out(multiplexer_5_out), .sel(multiplexer_6_out[1]));
  Multiplexer #(.select(1), .width(1), .disabled("Z"), .enable("false")) multiplexer_6 (
    .in0(comparator_1_lt), .in1(comparator_2_lt), .out(multiplexer_6_out[0]), .sel(multiplexer_6_out[1]));
  Multiplexer #(.select(1), .width(16), .disabled("Z"), .enable("false")) multiplexer_7 (
    .in0(multiplexer_3_out), .in1(multiplexer_4_out), .out(multiplexer_7_out), .sel(multiplexer_8_out[1]));
  Multiplexer #(.select(1), .width(1), .disabled("Z"), .enable("false")) multiplexer_8 (
    .in0(comparator_3_lt), .in1(comparator_4_lt), .out(multiplexer_8_out[0]), .sel(multiplexer_8_out[1]));
  Comparator #(.width(16), .mode("unsigned")) comparator_7 (
    .a(multiplexer_5_out), .b(multiplexer_7_out), .lt(multiplexer_9_out[2]));  // open: gt, eq
  Multiplexer #(.select(1), .width(2), .disabled("Z"), .enable("false")) multiplexer_9 (
    .in0(multiplexer_6_out), .in1(multiplexer_8_out), .out(multiplexer_9_out[1:0]), .sel(multiplexer_9_out[2]));
  Decoder #(.select(3), .tristate("false"), .disabled("Z"), .enable("false")) decoder_1 (
    .out0(decoder_1_out0), .out1(decoder_1_out1), .out2(decoder_1_out2), .out3(decoder_1_out3),
    .out4(decoder_1_out4), .out5(decoder_1_out5), .out6(decoder_1_out6), .out7(decoder_1_out7),
    .sel(multiplexer_9_out));
  and and_1 (Out_0, enable, decoder_1_out0);
  and and_2 (Out_1, enable, decoder_1_out1);
  and and_3 (Out_2, enable, decoder_1_out2);
  and and_4 (Out_3, enable, decoder_1_out3);
  and and_5 (Out_4, enable, decoder_1_out4);
  and and_6 (Out_5, enable, decoder_1_out5);
  and and_7 (Out_6, enable, decoder_1_out6);
  and and_8 (Out_7, enable, decoder_1_out7);
  or or_9 (RST_0, Out_0, Clear);
  or or_10 (RST_1, Out_1, Clear);
  or or_11 (RST_2, Out_2, Clear);
  or or_12 (RST_3, Out_3, Clear);
  or or_13 (RST_4, Out_4, Clear);
  or or_14 (RST_5, Out_5, Clear);
  or or_15 (RST_6, Out_6, Clear);
  or or_16 (RST_7, Out_7, Clear);

  // Notes on the sheet:
  //   00x
  //   01x
  //   10x
  //   11x
  //   0xx
  //   1xx
endmodule

module bin (
);

  wire and_1_out, and_2_out, and_3_out, CLK, CLR1, CLR2, CLR3, comparator_1_gt, comparator_2_gt,
       comparator_3_gt, d_ff_1_q, d_ff_2_q, d_ff_3_q, demultiplexer_1_out1, demultiplexer_1_out2,
       demultiplexer_1_out3, ID_URET, INTR1, INTR2, INTR3, IR1, IR2, IR3, or_2_out, or_4_out, or_6_out,
       or_7_out, or_8_out, or_9_out, or_10_out, or_11_out, or_12_out, W1, W2, W3;
  wire [1:0] CUR_INTR;
  wire [7:0] counter_1_q, counter_2_q, counter_3_q;

  Demultiplexer #(.select(2), .width(1), .tristate("false"), .disabled("Z"), .enable("false")) demultiplexer_1 (
    .out1(demultiplexer_1_out1), .out2(demultiplexer_1_out2), .out3(demultiplexer_1_out3), .in(ID_URET),
    .sel(CUR_INTR));  // open: out0
  D_Flip_Flop #(.trigger("rising"), .Pre_Clr_Positions("LEGACY"), .NegatePresetClear("false"), .enable("true"), .NewFFLayout("false")) d_ff_1 (
    .clk(IR1), .D(1'b1), .Q(d_ff_1_q), .reset(INTR1));  // open: Qn, preset, en
  or or_1 (W1, INTR1, d_ff_1_q);
  or or_2 (or_2_out, IR1, demultiplexer_1_out1);
  Counter #(.width(8), .max('hff), .ongoal("wrap"), .trigger("rising"), .behavior("new")) counter_1 (
    .count(or_2_out), .Q(counter_1_q), .clk(CLK), .down(demultiplexer_1_out1));  // open: load, D, carry, clr, preset
  D_Flip_Flop #(.trigger("rising"), .Pre_Clr_Positions("LEGACY"), .NegatePresetClear("false"), .enable("true"), .NewFFLayout("false")) d_ff_2 (
    .clk(IR2), .D(1'b1), .Q(d_ff_2_q), .reset(INTR2));  // open: Qn, preset, en
  or or_3 (W2, INTR2, d_ff_2_q);
  or or_4 (or_4_out, IR2, demultiplexer_1_out2);
  Counter #(.width(8), .max('hff), .ongoal("wrap"), .trigger("rising"), .behavior("new")) counter_2 (
    .count(or_4_out), .Q(counter_2_q), .clk(CLK), .down(demultiplexer_1_out2));  // open: load, D, carry, clr, preset
  D_Flip_Flop #(.trigger("rising"), .Pre_Clr_Positions("LEGACY"), .NegatePresetClear("false"), .enable("true"), .NewFFLayout("false")) d_ff_3 (
    .clk(IR3), .D(1'b1), .Q(d_ff_3_q), .reset(INTR3));  // open: Qn, preset, en
  or or_5 (W3, INTR3, d_ff_3_q);
  or or_6 (or_6_out, IR3, demultiplexer_1_out3);
  Counter #(.width(8), .max('hff), .ongoal("wrap"), .trigger("rising"), .behavior("new")) counter_3 (
    .count(or_6_out), .Q(counter_3_q), .clk(CLK), .down(demultiplexer_1_out3));  // open: load, D, carry, clr, preset
  or or_7 (or_7_out, d_ff_1_q, INTR1);
  or or_8 (or_8_out, d_ff_2_q, INTR2);
  or or_9 (or_9_out, d_ff_3_q, INTR3);
  and and_1 (and_1_out, or_7_out, ~CLR1);  // AND_Gate
  Comparator #(.width(8), .mode("unsigned")) comparator_1 (
    .a(counter_1_q), .b({8{1'b0}}), .gt(comparator_1_gt));  // open: eq, lt
  and and_2 (and_2_out, or_8_out, ~CLR2);  // AND_Gate
  Comparator #(.width(8), .mode("unsigned")) comparator_2 (
    .a(counter_2_q), .b({8{1'b0}}), .gt(comparator_2_gt));  // open: eq, lt
  and and_3 (and_3_out, or_9_out, ~CLR3);  // AND_Gate
  Comparator #(.width(8), .mode("unsigned")) comparator_3 (
    .a(counter_3_q), .b({8{1'b0}}), .gt(comparator_3_gt));  // open: eq, lt
  or or_10 (or_10_out, and_1_out, comparator_1_gt);
  or or_11 (or_11_out, and_2_out, comparator_2_gt);
  or or_12 (or_12_out, and_3_out, comparator_3_gt);
  D_Flip_Flop #(.trigger("rising"), .Pre_Clr_Positions("LEGACY"), .NegatePresetClear("false"), .enable("true"), .NewFFLayout("false")) d_ff_4 (
    .clk(CLK), .D(or_10_out), .Q(INTR1));  // open: Qn, preset, en, reset
  D_Flip_Flop #(.trigger("rising"), .Pre_Clr_Positions("LEGACY"), .NegatePresetClear("false"), .enable("true"), .NewFFLayout("false")) d_ff_5 (
    .clk(CLK), .D(or_11_out), .Q(INTR2));  // open: Qn, preset, en, reset
  D_Flip_Flop #(.trigger("rising"), .Pre_Clr_Positions("LEGACY"), .NegatePresetClear("false"), .enable("true"), .NewFFLayout("false")) d_ff_6 (
    .clk(CLK), .D(or_12_out), .Q(INTR3));  // open: Qn, preset, en, reset
endmodule
